// Logisim project 10_implement_sub_imm.circ as structural Verilog: 2 circuits, main circuit main
module main (
  output ERROR_INS_NOT_IMPLEMENTED,
  output ERROR_DATA_ADDR_OUT_OF_RANGE,
  output ERROR_INS_ADDR_NOT_ALIGNED,
  output ERROR_INS_ADDR_OUT_OF_RANGE,
  output [10:0] opcode_R_or_D_type,
  output [9:0] opcode_I_type,
  output [5:0] opcode_B_type,
  output [7:0] opcode_CB_type,
  output [4:0] Rm,
  output [4:0] Rn,
  output [4:0] Rd_or_Rt,
  output [11:0] ALU_immediate,
  output [8:0] DT_address,
  output [25:0] BR_address,
  output [18:0] COND_BR_address,
  output AND_ins,
  output ORR_ins,
  output EOR_ins,
  output ADD_ins,
  output SUB_ins,
  output AND_imm_ins,
  output ORR_imm_ins,
  output EOR_imm_ins,
  output ADD_imm_ins,
  output SUB_imm_ins,
  output LDUR_ins,
  output STUR_ins,
  output B_ins,
  output CBZ_ins,
  output R_type,
  output I_type,
  output D_type,
  output B_type,
  output CB_type,
  output OPCODE_is_000,
  output OPCODE_is_001,
  output OPCODE_is_010,
  output OPCODE_is_011,
  output OPCODE_is_100,
  output [2:0] OPCODE,
  output USE_R_SRC2,
  output [63:0] D_IN,
  output [4:0] SEL_R_SRC1,
  output [4:0] SEL_R_SRC2,
  output [4:0] SEL_R_DST,
  output BRANCH,
  output BRANCH_IF_ZERO,
  output LOAD_FROM_MEMORY,
  output STORE_TO_MEMORY
);

  wire and_1_out, and_2_out, CLK_out, comparator_1_eq, comparator_2_eq, comparator_17_eq, comparator_18_eq,
       or_10_out, Reset_out;
  wire [1:0] priority_encoder_2_out;
  wire [63:0] adder_1_out, adder_2_out, adder_3_out, and_3_out, bit_extender_1_out, bit_extender_2_out,
       bit_extender_3_out, bit_extender_4_out, DATA_MEMORY_dout, multiplexer_3_out, multiplexer_4_out,
       multiplexer_5_out, multiplexer_6_out, or_11_out, PC_q, regfile_1_read_data0, regfile_1_read_data1,
       shifter_1_out, subtractor_1_out, xor_1_out;

  Clock CLK (.out(CLK_out));
  Button Reset (.out(Reset_out));
  Register #(.width(64)) PC (.D(multiplexer_4_out), .en(1'b1), .clk(CLK_out), .Q(PC_q), .clr(Reset_out));
  // ROM #(.addrWidth(24), .line("quad")) INSTRUCTION_MEMORY: pin names not known; wires that end beside it: PC_q[23:0], BR_address[7:0], {ALU_immediate[5:0], BR_address[9:8]}, {BR_address[23:22], ALU_immediate[11:6]}, {opcode_B_type, BR_address[25:24]}
  Adder #(.width(64)) adder_1 (.a(64'h4), .b(PC_q), .out(adder_1_out), .cin(1'b0));  // open: cout
  Comparator #(.mode("unsigned"), .width(2)) comparator_1 (
    .a(2'b00), .b(PC_q[1:0]), .eq(comparator_1_eq));  // open: gt, lt
  Comparator #(.mode("unsigned"), .width(40)) comparator_2 (
    .a({40{1'b0}}), .b(PC_q[63:24]), .eq(comparator_2_eq));  // open: gt, lt
  not not_1 (ERROR_INS_ADDR_NOT_ALIGNED, comparator_1_eq);
  not not_2 (ERROR_INS_ADDR_OUT_OF_RANGE, comparator_2_eq);
  Comparator #(.mode("unsigned"), .width(11)) comparator_3 (
    .a({opcode_B_type, BR_address[25:22], ALU_immediate[11]}), .b(11'h450), .eq(AND_ins));  // open: gt, lt
  Comparator #(.mode("unsigned"), .width(11)) comparator_4 (
    .a({opcode_B_type, BR_address[25:22], ALU_immediate[11]}), .b(11'h550), .eq(ORR_ins));  // open: gt, lt
  Comparator #(.mode("unsigned"), .width(11)) comparator_5 (
    .a({opcode_B_type, BR_address[25:22], ALU_immediate[11]}), .b(11'h650), .eq(EOR_ins));  // open: gt, lt
  Comparator #(.mode("unsigned"), .width(11)) comparator_6 (
    .a({opcode_B_type, BR_address[25:22], ALU_immediate[11]}), .b(11'h458), .eq(ADD_ins));  // open: gt, lt
  Comparator #(.mode("unsigned"), .width(11)) comparator_7 (
    .a({opcode_B_type, BR_address[25:22], ALU_immediate[11]}), .b(11'h658), .eq(SUB_ins));  // open: gt, lt
  Comparator #(.mode("unsigned"), .width(10)) comparator_8 (
    .a({opcode_B_type, BR_address[25:22]}), .b(10'h248), .eq(AND_imm_ins));  // open: gt, lt
  Comparator #(.mode("unsigned"), .width(10)) comparator_9 (
    .a({opcode_B_type, BR_address[25:22]}), .b(10'h2c8), .eq(ORR_imm_ins));  // open: gt, lt
  Comparator #(.mode("unsigned"), .width(10)) comparator_10 (
    .a({opcode_B_type, BR_address[25:22]}), .b(10'h348), .eq(EOR_imm_ins));  // open: gt, lt
  Comparator #(.mode("unsigned"), .width(10)) comparator_11 (
    .a({opcode_B_type, BR_address[25:22]}), .b(10'h244), .eq(ADD_imm_ins));  // open: gt, lt
  Comparator #(.mode("unsigned"), .width(10)) comparator_12 (
    .a({opcode_B_type, BR_address[25:22]}), .b(10'h344), .eq(SUB_imm_ins));  // open: gt, lt
  Comparator #(.mode("unsigned"), .width(11)) comparator_13 (
    .a({opcode_B_type, BR_address[25:22], ALU_immediate[11]}), .b(11'h7c2), .eq(LDUR_ins));  // open: gt, lt
  Comparator #(.mode("unsigned"), .width(11)) comparator_14 (
    .a({opcode_B_type, BR_address[25:22], ALU_immediate[11]}), .b(11'h7c0), .eq(STORE_TO_MEMORY));  // open: gt, lt
  Comparator #(.mode("unsigned"), .width(6)) comparator_15 (
    .a(opcode_B_type), .b(6'b000101), .eq(B_ins));  // open: gt, lt
  Comparator #(.mode("unsigned")) comparator_16 (
    .a({opcode_B_type, BR_address[25:24]}), .b(8'hb4), .eq(BRANCH_IF_ZERO));  // open: gt, lt
  assign bit_extender_1_out = {{52{1'b0}}, ALU_immediate};  // Bit_Extender bit_extender_1
  assign bit_extender_2_out = {{55{ALU_immediate[10]}}, ALU_immediate[10:2]};  // Bit_Extender bit_extender_2
  assign bit_extender_3_out = {{38{BR_address[25]}}, {BR_address[25:22], ALU_immediate, BR_address[9:0]}};  // Bit_Extender bit_extender_3
  assign bit_extender_4_out = {{45{BR_address[23]}}, {BR_address[23:22], ALU_immediate, BR_address[9:5]}};  // Bit_Extender bit_extender_4
  nor nor_1 (ERROR_INS_NOT_IMPLEMENTED, AND_ins, ORR_ins, EOR_ins, ADD_ins, SUB_ins, AND_imm_ins, ORR_imm_ins, EOR_imm_ins, ADD_imm_ins, SUB_imm_ins, LDUR_ins, STORE_TO_MEMORY, B_ins, BRANCH_IF_ZERO);
  or or_1 (R_type, AND_ins, ORR_ins, EOR_ins, ADD_ins, SUB_ins);
  or or_2 (I_type, AND_imm_ins, ORR_imm_ins, EOR_imm_ins, ADD_imm_ins, SUB_imm_ins);
  or or_3 (D_type, LDUR_ins, STORE_TO_MEMORY);
  or or_4 (OPCODE_is_000, AND_ins, AND_imm_ins);
  or or_5 (OPCODE_is_001, ORR_ins, ORR_imm_ins);
  or or_6 (OPCODE_is_010, EOR_ins, EOR_imm_ins);
  or or_7 (OPCODE_is_011, ADD_ins, ADD_imm_ins);
  or or_8 (OPCODE_is_100, SUB_ins, SUB_imm_ins);
  or or_9 (USE_R_SRC2, AND_ins, ORR_ins, EOR_ins, ADD_ins, SUB_ins);
  and and_1 (and_1_out, ~STORE_TO_MEMORY, ~BRANCH_IF_ZERO, ~B_ins);  // AND_Gate
  Multiplexer #(.enable("false"), .width(5)) multiplexer_1 (
    .in0(ALU_immediate[10:6]), .in1(BR_address[4:0]), .out(SEL_R_SRC2), .sel(STORE_TO_MEMORY));
  Priority_Encoder priority_encoder_1 (
    .in0(OPCODE_is_000), .in1(OPCODE_is_001), .in2(OPCODE_is_010), .in3(OPCODE_is_011), .in4(OPCODE_is_100),
    .out(OPCODE), .en_in(1'b1));  // open: in5, in6, in7, gs, en_out
  Priority_Encoder #(.select(2)) priority_encoder_2 (
    .in0(I_type), .in1(D_type), .in2(B_ins), .in3(BRANCH_IF_ZERO), .out(priority_encoder_2_out), .en_in(1'b1));  // open: gs, en_out
  Multiplexer #(.enable("false"), .select(2), .width(64)) multiplexer_2 (
    .in0(bit_extender_1_out), .in1(bit_extender_2_out), .in2(bit_extender_3_out), .in3(bit_extender_4_out),
    .out(D_IN), .sel(priority_encoder_2_out));
  Shifter #(.width(64)) shifter_1 (.in(D_IN), .\dist (6'b000010), .out(shifter_1_out));
  regfile regfile_1 (
    .READ_ADDR0(BR_address[9:5]), .READ_ADDR1(SEL_R_SRC2), .WRITE_ADDR(BR_address[4:0]),
    .WRITE_DATA(multiplexer_6_out), .WRITE_ENABLE(and_1_out), .CLOCK(CLK_out), .RESET(Reset_out),
    .READ_DATA0(regfile_1_read_data0), .READ_DATA1(regfile_1_read_data1));
  Multiplexer #(.enable("false"), .width(64)) multiplexer_3 (
    .in0(D_IN), .in1(regfile_1_read_data1), .out(multiplexer_3_out), .sel(OPCODE_is_010));
  Adder #(.width(64)) adder_2 (.a(PC_q), .b(shifter_1_out), .out(adder_2_out), .cin(1'b0));  // open: cout
  Multiplexer #(.enable("false"), .width(64)) multiplexer_4 (
    .in0(adder_1_out), .in1(adder_2_out), .out(multiplexer_4_out), .sel(or_10_out));
  or or_10 (or_10_out, B_ins, and_2_out);
  and and_2 (and_2_out, BRANCH_IF_ZERO, comparator_17_eq);
  Comparator #(.mode("unsigned"), .width(64)) comparator_17 (
    .a({64{1'b0}}), .b(regfile_1_read_data0), .eq(comparator_17_eq));  // open: gt, lt
  assign and_3_out = regfile_1_read_data0 & multiplexer_3_out;  // AND_Gate and_3, 64 bits wide
  assign or_11_out = regfile_1_read_data0 | multiplexer_3_out;  // OR_Gate or_11, 64 bits wide
  assign xor_1_out = regfile_1_read_data0 ^ multiplexer_3_out;  // XOR_Gate xor_1, 64 bits wide
  Adder #(.width(64)) adder_3 (
    .a(regfile_1_read_data0), .b(multiplexer_3_out), .out(adder_3_out), .cin(1'b0));  // open: cout
  Subtractor #(.width(64)) subtractor_1 (
    .a(regfile_1_read_data0), .b(multiplexer_3_out), .out(subtractor_1_out), .bin(1'b0));  // open: bout
  RAM #(.addrWidth(24), .dataWidth(64)) DATA_MEMORY (
    .addr(regfile_1_read_data0[23:0]), .we(STORE_TO_MEMORY), .oe(LDUR_ins), .clk(CLK_out),
    .din(regfile_1_read_data1), .dout(DATA_MEMORY_dout));
  Multiplexer #(.enable("false"), .select(3), .width(64)) multiplexer_5 (
    .in0(and_3_out), .in1(or_11_out), .in2(xor_1_out), .in3(adder_3_out), .in4(subtractor_1_out),
    .out(multiplexer_5_out), .sel(OPCODE));  // open: in5, in6, in7
  Comparator #(.mode("unsigned"), .width(40)) comparator_18 (
    .a({40{1'b0}}), .b(regfile_1_read_data0[63:24]), .eq(comparator_18_eq));  // open: gt, lt
  not not_3 (ERROR_DATA_ADDR_OUT_OF_RANGE, comparator_18_eq);
  Multiplexer #(.enable("false"), .width(64)) multiplexer_6 (
    .in0(multiplexer_5_out), .in1(DATA_MEMORY_dout), .out(multiplexer_6_out), .sel(LDUR_ins));

  assign B_type = B_ins;
  assign BR_address[21:10] = ALU_immediate;
  assign BRANCH = B_ins;
  assign CB_type = BRANCH_IF_ZERO;
  assign CBZ_ins = BRANCH_IF_ZERO;
  assign COND_BR_address = {BR_address[23:22], ALU_immediate, BR_address[9:5]};
  assign DT_address = ALU_immediate[10:2];
  assign LOAD_FROM_MEMORY = LDUR_ins;
  assign opcode_CB_type = {opcode_B_type, BR_address[25:24]};
  assign opcode_I_type = {opcode_B_type, BR_address[25:22]};
  assign opcode_R_or_D_type = {opcode_B_type, BR_address[25:22], ALU_immediate[11]};
  assign Rd_or_Rt = BR_address[4:0];
  assign Rm = ALU_immediate[10:6];
  assign Rn = BR_address[9:5];
  assign SEL_R_DST = BR_address[4:0];
  assign SEL_R_SRC1 = BR_address[9:5];
  assign STUR_ins = STORE_TO_MEMORY;
endmodule

module regfile (
  input  [4:0] READ_ADDR0,
  input  [4:0] READ_ADDR1,
  input  [4:0] WRITE_ADDR,
  input  [63:0] WRITE_DATA,
  input  WRITE_ENABLE,
  input  CLOCK,
  input  RESET,
  output [63:0] READ_DATA0,
  output [63:0] READ_DATA1
);

  wire decoder_1_out0, decoder_1_out1, decoder_1_out2, decoder_1_out3, decoder_1_out4, decoder_1_out5,
       decoder_1_out6, decoder_1_out7, decoder_1_out8, decoder_1_out9, decoder_1_out10, decoder_1_out11,
       decoder_1_out12, decoder_1_out13, decoder_1_out14, decoder_1_out15, decoder_1_out16, decoder_1_out17,
       decoder_1_out18, decoder_1_out19, decoder_1_out20, decoder_1_out21, decoder_1_out22, decoder_1_out23,
       decoder_1_out24, decoder_1_out25, decoder_1_out26, decoder_1_out27, decoder_1_out28, decoder_1_out29,
       decoder_1_out30, decoder_1_out31;
  wire [63:0] X0_q, X1_q, X2_q, X3_q, X4_q, X5_q, X6_q, X7_q, X8_q, X9_q, X10_q, X11_q, X12_q, X13_q, X14_q,
       X15_q, X16_q, X17_q, X18_q, X19_q, X20_q, X21_q, X22_q, X23_q, X24_q, X25_q, X26_q, X27_q, X28_q,
       X29_q, X30_q;

  Decoder #(.select(5)) decoder_1 (
    .out0(decoder_1_out0), .out1(decoder_1_out1), .out2(decoder_1_out2), .out3(decoder_1_out3),
    .out4(decoder_1_out4), .out5(decoder_1_out5), .out6(decoder_1_out6), .out7(decoder_1_out7),
    .out8(decoder_1_out8), .out9(decoder_1_out9), .out10(decoder_1_out10), .out11(decoder_1_out11),
    .out12(decoder_1_out12), .out13(decoder_1_out13), .out14(decoder_1_out14), .out15(decoder_1_out15),
    .out16(decoder_1_out16), .out17(decoder_1_out17), .out18(decoder_1_out18), .out19(decoder_1_out19),
    .out20(decoder_1_out20), .out21(decoder_1_out21), .out22(decoder_1_out22), .out23(decoder_1_out23),
    .out24(decoder_1_out24), .out25(decoder_1_out25), .out26(decoder_1_out26), .out27(decoder_1_out27),
    .out28(decoder_1_out28), .out29(decoder_1_out29), .out30(decoder_1_out30), .out31(decoder_1_out31),
    .sel(WRITE_ADDR), .en(WRITE_ENABLE));
  // NoConnect on decoder_1_out31
  Register #(.width(64)) X0 (.D(WRITE_DATA), .en(decoder_1_out0), .clk(CLOCK), .Q(X0_q), .clr(RESET));
  Register #(.width(64)) X1 (.D(WRITE_DATA), .en(decoder_1_out1), .clk(CLOCK), .Q(X1_q), .clr(RESET));
  Register #(.width(64)) X2 (.D(WRITE_DATA), .en(decoder_1_out2), .clk(CLOCK), .Q(X2_q), .clr(RESET));
  Register #(.width(64)) X3 (.D(WRITE_DATA), .en(decoder_1_out3), .clk(CLOCK), .Q(X3_q), .clr(RESET));
  Register #(.width(64)) X4 (.D(WRITE_DATA), .en(decoder_1_out4), .clk(CLOCK), .Q(X4_q), .clr(RESET));
  Register #(.width(64)) X5 (.D(WRITE_DATA), .en(decoder_1_out5), .clk(CLOCK), .Q(X5_q), .clr(RESET));
  Register #(.width(64)) X6 (.D(WRITE_DATA), .en(decoder_1_out6), .clk(CLOCK), .Q(X6_q), .clr(RESET));
  Register #(.width(64)) X7 (.D(WRITE_DATA), .en(decoder_1_out7), .clk(CLOCK), .Q(X7_q), .clr(RESET));
  Register #(.width(64)) X8 (.D(WRITE_DATA), .en(decoder_1_out8), .clk(CLOCK), .Q(X8_q), .clr(RESET));
  Register #(.width(64)) X9 (.D(WRITE_DATA), .en(decoder_1_out9), .clk(CLOCK), .Q(X9_q), .clr(RESET));
  Register #(.width(64)) X10 (.D(WRITE_DATA), .en(decoder_1_out10), .clk(CLOCK), .Q(X10_q), .clr(RESET));
  Register #(.width(64)) X11 (.D(WRITE_DATA), .en(decoder_1_out11), .clk(CLOCK), .Q(X11_q), .clr(RESET));
  Register #(.width(64)) X12 (.D(WRITE_DATA), .en(decoder_1_out12), .clk(CLOCK), .Q(X12_q), .clr(RESET));
  Register #(.width(64)) X13 (.D(WRITE_DATA), .en(decoder_1_out13), .clk(CLOCK), .Q(X13_q), .clr(RESET));
  Register #(.width(64)) X14 (.D(WRITE_DATA), .en(decoder_1_out14), .clk(CLOCK), .Q(X14_q), .clr(RESET));
  Register #(.width(64)) X15 (.D(WRITE_DATA), .en(decoder_1_out15), .clk(CLOCK), .Q(X15_q), .clr(RESET));
  Register #(.width(64)) X16 (.D(WRITE_DATA), .en(decoder_1_out16), .clk(CLOCK), .Q(X16_q), .clr(RESET));
  Register #(.width(64)) X17 (.D(WRITE_DATA), .en(decoder_1_out17), .clk(CLOCK), .Q(X17_q), .clr(RESET));
  Register #(.width(64)) X18 (.D(WRITE_DATA), .en(decoder_1_out18), .clk(CLOCK), .Q(X18_q), .clr(RESET));
  Register #(.width(64)) X19 (.D(WRITE_DATA), .en(decoder_1_out19), .clk(CLOCK), .Q(X19_q), .clr(RESET));
  Register #(.width(64)) X20 (.D(WRITE_DATA), .en(decoder_1_out20), .clk(CLOCK), .Q(X20_q), .clr(RESET));
  Register #(.width(64)) X21 (.D(WRITE_DATA), .en(decoder_1_out21), .clk(CLOCK), .Q(X21_q), .clr(RESET));
  Register #(.width(64)) X22 (.D(WRITE_DATA), .en(decoder_1_out22), .clk(CLOCK), .Q(X22_q), .clr(RESET));
  Register #(.width(64)) X23 (.D(WRITE_DATA), .en(decoder_1_out23), .clk(CLOCK), .Q(X23_q), .clr(RESET));
  Register #(.width(64)) X24 (.D(WRITE_DATA), .en(decoder_1_out24), .clk(CLOCK), .Q(X24_q), .clr(RESET));
  Register #(.width(64)) X25 (.D(WRITE_DATA), .en(decoder_1_out25), .clk(CLOCK), .Q(X25_q), .clr(RESET));
  Register #(.width(64)) X26 (.D(WRITE_DATA), .en(decoder_1_out26), .clk(CLOCK), .Q(X26_q), .clr(RESET));
  Register #(.width(64)) X27 (.D(WRITE_DATA), .en(decoder_1_out27), .clk(CLOCK), .Q(X27_q), .clr(RESET));
  Register #(.width(64)) X28 (.D(WRITE_DATA), .en(decoder_1_out28), .clk(CLOCK), .Q(X28_q), .clr(RESET));
  Register #(.width(64)) X29 (.D(WRITE_DATA), .en(decoder_1_out29), .clk(CLOCK), .Q(X29_q), .clr(RESET));
  Register #(.width(64)) X30 (.D(WRITE_DATA), .en(decoder_1_out30), .clk(CLOCK), .Q(X30_q), .clr(RESET));
  Multiplexer #(.enable("false"), .select(5), .width(64)) multiplexer_1 (
    .in0(X0_q), .in1(X1_q), .in2(X2_q), .in3(X3_q), .in4(X4_q), .in5(X5_q), .in6(X6_q), .in7(X7_q),
    .in8(X8_q), .in9(X9_q), .in10(X10_q), .in11(X11_q), .in12(X12_q), .in13(X13_q), .in14(X14_q),
    .in15(X15_q), .in16(X16_q), .in17(X17_q), .in18(X18_q), .in19(X19_q), .in20(X20_q), .in21(X21_q),
    .in22(X22_q), .in23(X23_q), .in24(X24_q), .in25(X25_q), .in26(X26_q), .in27(X27_q), .in28(X28_q),
    .in29(X29_q), .in30(X30_q), .in31({64{1'b0}}), .out(READ_DATA0), .sel(READ_ADDR0));
  Multiplexer #(.enable("false"), .select(5), .width(64)) multiplexer_2 (
    .in0(X0_q), .in1(X1_q), .in2(X2_q), .in3(X3_q), .in4(X4_q), .in5(X5_q), .in6(X6_q), .in7(X7_q),
    .in8(X8_q), .in9(X9_q), .in10(X10_q), .in11(X11_q), .in12(X12_q), .in13(X13_q), .in14(X14_q),
    .in15(X15_q), .in16(X16_q), .in17(X17_q), .in18(X18_q), .in19(X19_q), .in20(X20_q), .in21(X21_q),
    .in22(X22_q), .in23(X23_q), .in24(X24_q), .in25(X25_q), .in26(X26_q), .in27(X27_q), .in28(X28_q),
    .in29(X29_q), .in30(X30_q), .in31({64{1'b0}}), .out(READ_DATA1), .sel(READ_ADDR1));
endmodule
