// Logisim project 1_use64bitregs.circ as structural Verilog: 1 circuit, main circuit main
module main (
  output ERROR_DATA_ADDR_OUT_OF_RANGE,
  output ERROR_INS_ADDR_OUT_OF_RANGE,
  output [1:0] SEL_OP,
  output USE_R_SRC2,
  output [3:0] D_IN,
  output [1:0] SEL_R_SRC1,
  output [1:0] SEL_R_SRC2,
  output [1:0] SEL_R_DST,
  output BRANCH,
  output BRANCH_IF_ZERO,
  output LOAD_FROM_MEMORY,
  output STORE_TO_MEMORY
);

  wire and_1_out, and_2_out, CLK_out, comparator_1_eq, comparator_2_eq, comparator_3_eq, decoder_1_out0,
       decoder_1_out1, decoder_1_out2, decoder_1_out3, or_1_out, Reset_out;
  wire [23:0] multiplexer_1_out;
  wire [39:0] multiplexer_1_out_2;
  wire [63:0] adder_1_out, adder_2_out, adder_3_out, and_3_out, bit_extender_1_out, bit_extender_2_out,
       DATA_MEMORY_dout, multiplexer_2_out, multiplexer_3_out, multiplexer_4_out, multiplexer_5_out,
       multiplexer_6_out, or_2_out, PC_q, REG0_q, REG1_q, REG2_q, REG3_q, xor_1_out;

  Clock CLK (.out(CLK_out));
  Button Reset (.out(Reset_out));
  Register #(.width(64)) PC (.D(multiplexer_4_out), .en(1'b1), .clk(CLK_out), .Q(PC_q), .clr(Reset_out));
  ROM #(.addrWidth(24), .dataWidth(17)) INSTRUCTION_MEMORY (
    .addr(PC_q[23:0]),
    .data({STORE_TO_MEMORY, LOAD_FROM_MEMORY, BRANCH_IF_ZERO, BRANCH, SEL_R_DST, SEL_R_SRC2, SEL_R_SRC1, D_IN, USE_R_SRC2, SEL_OP}));
  Adder #(.width(64)) adder_1 (.a(64'h1), .b(PC_q), .out(adder_1_out), .cin(1'b0));  // open: cout
  not not_1 (ERROR_INS_ADDR_OUT_OF_RANGE, comparator_1_eq);
  Comparator #(.mode("unsigned"), .width(40)) comparator_1 (
    .a({40{1'b0}}), .b(PC_q[63:24]), .eq(comparator_1_eq));  // open: gt, lt
  and and_1 (and_1_out, ~STORE_TO_MEMORY, ~BRANCH_IF_ZERO, ~BRANCH);  // AND_Gate
  Decoder #(.select(2)) decoder_1 (
    .out0(decoder_1_out0), .out1(decoder_1_out1), .out2(decoder_1_out2), .out3(decoder_1_out3),
    .sel(SEL_R_DST), .en(and_1_out));
  assign bit_extender_1_out = {{60{D_IN[3]}}, D_IN};  // Bit_Extender bit_extender_1
  Register #(.width(64)) REG0 (.D(multiplexer_6_out), .en(decoder_1_out0), .clk(CLK_out), .Q(REG0_q), .clr(Reset_out));
  Register #(.width(64)) REG1 (.D(multiplexer_6_out), .en(decoder_1_out1), .clk(CLK_out), .Q(REG1_q), .clr(Reset_out));
  Register #(.width(64)) REG2 (.D(multiplexer_6_out), .en(decoder_1_out2), .clk(CLK_out), .Q(REG2_q), .clr(Reset_out));
  Register #(.width(64)) REG3 (.D(multiplexer_6_out), .en(decoder_1_out3), .clk(CLK_out), .Q(REG3_q), .clr(Reset_out));
  Adder #(.width(64)) adder_2 (.a(PC_q), .b(bit_extender_1_out), .out(adder_2_out), .cin(1'b0));  // open: cout
  Multiplexer #(.enable("false"), .select(2), .width(64)) multiplexer_1 (
    .in0(REG0_q), .in1(REG1_q), .in2(REG2_q), .in3(REG3_q), .out({multiplexer_1_out_2, multiplexer_1_out}),
    .sel(SEL_R_SRC1));
  Multiplexer #(.enable("false"), .select(2), .width(64)) multiplexer_2 (
    .in0(REG0_q), .in1(REG1_q), .in2(REG2_q), .in3(REG3_q), .out(multiplexer_2_out), .sel(SEL_R_SRC2));
  assign bit_extender_2_out = {{60{1'b0}}, D_IN};  // Bit_Extender bit_extender_2
  Multiplexer #(.enable("false"), .width(64)) multiplexer_3 (
    .in0(bit_extender_2_out), .in1(multiplexer_2_out), .out(multiplexer_3_out), .sel(USE_R_SRC2));
  Multiplexer #(.enable("false"), .width(64)) multiplexer_4 (
    .in0(adder_1_out), .in1(adder_2_out), .out(multiplexer_4_out), .sel(or_1_out));
  or or_1 (or_1_out, BRANCH, and_2_out);
  and and_2 (and_2_out, BRANCH_IF_ZERO, comparator_2_eq);
  Comparator #(.mode("unsigned"), .width(64)) comparator_2 (
    .a({64{1'b0}}), .b({multiplexer_1_out_2, multiplexer_1_out}), .eq(comparator_2_eq));  // open: gt, lt
  assign and_3_out = {multiplexer_1_out_2, multiplexer_1_out} & multiplexer_3_out;  // AND_Gate and_3, 64 bits wide
  assign or_2_out = {multiplexer_1_out_2, multiplexer_1_out} | multiplexer_3_out;  // OR_Gate or_2, 64 bits wide
  assign xor_1_out = {multiplexer_1_out_2, multiplexer_1_out} ^ multiplexer_3_out;  // XOR_Gate xor_1, 64 bits wide
  Adder #(.width(64)) adder_3 (
    .a({multiplexer_1_out_2, multiplexer_1_out}), .b(multiplexer_3_out), .out(adder_3_out), .cin(1'b0));  // open: cout
  RAM #(.addrWidth(24), .dataWidth(64)) DATA_MEMORY (
    .addr(multiplexer_1_out), .we(STORE_TO_MEMORY), .oe(LOAD_FROM_MEMORY), .clk(CLK_out),
    .din(multiplexer_2_out), .dout(DATA_MEMORY_dout));
  Multiplexer #(.enable("false"), .select(2), .width(64)) multiplexer_5 (
    .in0(and_3_out), .in1(or_2_out), .in2(xor_1_out), .in3(adder_3_out), .out(multiplexer_5_out), .sel(SEL_OP));
  Comparator #(.mode("unsigned"), .width(40)) comparator_3 (
    .a({40{1'b0}}), .b(multiplexer_1_out_2), .eq(comparator_3_eq));  // open: gt, lt
  not not_2 (ERROR_DATA_ADDR_OUT_OF_RANGE, comparator_3_eq);
  Multiplexer #(.enable("false"), .width(64)) multiplexer_6 (
    .in0(multiplexer_5_out), .in1(DATA_MEMORY_dout), .out(multiplexer_6_out), .sel(LOAD_FROM_MEMORY));

  // Notes on the sheet:
  //   contents of INSTRUCTION_MEMORY (hex, n*v repeats v):
  //   2018 9*0 2078
endmodule
