// Logisim project 4_use32regs.circ as structural Verilog: 1 circuit, main circuit main
module main (
  output ERROR_DATA_ADDR_OUT_OF_RANGE,
  output ERROR_INS_ADDR_OUT_OF_RANGE,
  output [1:0] SEL_OP,
  output USE_R_SRC2,
  output [3:0] D_IN,
  output [4:0] SEL_R_SRC1,
  output [4:0] SEL_R_SRC2,
  output [4:0] SEL_R_DST,
  output BRANCH,
  output BRANCH_IF_ZERO,
  output LOAD_FROM_MEMORY,
  output STORE_TO_MEMORY
);

  wire and_1_out, and_2_out, CLK_out, comparator_1_eq, comparator_2_eq, comparator_3_eq, decoder_1_out0,
       decoder_1_out1, decoder_1_out2, decoder_1_out3, decoder_1_out4, decoder_1_out5, decoder_1_out6,
       decoder_1_out7, decoder_1_out8, decoder_1_out9, decoder_1_out10, decoder_1_out11, decoder_1_out12,
       decoder_1_out13, decoder_1_out14, decoder_1_out15, decoder_1_out16, decoder_1_out17, decoder_1_out18,
       decoder_1_out19, decoder_1_out20, decoder_1_out21, decoder_1_out22, decoder_1_out23, decoder_1_out24,
       decoder_1_out25, decoder_1_out26, decoder_1_out27, decoder_1_out28, decoder_1_out29, decoder_1_out30,
       decoder_1_out31, or_1_out, Reset_out;
  wire [63:0] adder_1_out, adder_2_out, adder_3_out, and_3_out, bit_extender_1_out, bit_extender_2_out,
       DATA_MEMORY_dout, multiplexer_1_out, multiplexer_2_out, multiplexer_3_out, multiplexer_4_out,
       multiplexer_5_out, multiplexer_6_out, or_2_out, PC_q, X0_q, X1_q, X2_q, X3_q, X4_q, X5_q, X6_q, X7_q,
       X8_q, X9_q, X10_q, X11_q, X12_q, X13_q, X14_q, X15_q, X16_q, X17_q, X18_q, X19_q, X20_q, X21_q, X22_q,
       X23_q, X24_q, X25_q, X26_q, X27_q, X28_q, X29_q, X30_q, xor_1_out;

  Register #(.width(64)) PC (.D(multiplexer_4_out), .en(1'b1), .clk(CLK_out), .Q(PC_q), .clr(Reset_out));
  Clock CLK (.out(CLK_out));
  Button Reset (.out(Reset_out));
  ROM #(.addrWidth(24), .dataWidth(26)) INSTRUCTION_MEMORY (
    .addr(PC_q[23:0]),
    .data({STORE_TO_MEMORY, LOAD_FROM_MEMORY, BRANCH_IF_ZERO, BRANCH, SEL_R_DST, SEL_R_SRC2, SEL_R_SRC1, D_IN, USE_R_SRC2, SEL_OP}));
  Adder #(.width(64)) adder_1 (.a(64'h1), .b(PC_q), .out(adder_1_out), .cin(1'b0));  // open: cout
  Comparator #(.mode("unsigned"), .width(40)) comparator_1 (
    .a({40{1'b0}}), .b(PC_q[63:24]), .eq(comparator_1_eq));  // open: gt, lt
  not not_1 (ERROR_INS_ADDR_OUT_OF_RANGE, comparator_1_eq);
  and and_1 (and_1_out, ~STORE_TO_MEMORY, ~BRANCH_IF_ZERO, ~BRANCH);  // AND_Gate
  Decoder #(.select(5)) decoder_1 (
    .out0(decoder_1_out0), .out1(decoder_1_out1), .out2(decoder_1_out2), .out3(decoder_1_out3),
    .out4(decoder_1_out4), .out5(decoder_1_out5), .out6(decoder_1_out6), .out7(decoder_1_out7),
    .out8(decoder_1_out8), .out9(decoder_1_out9), .out10(decoder_1_out10), .out11(decoder_1_out11),
    .out12(decoder_1_out12), .out13(decoder_1_out13), .out14(decoder_1_out14), .out15(decoder_1_out15),
    .out16(decoder_1_out16), .out17(decoder_1_out17), .out18(decoder_1_out18), .out19(decoder_1_out19),
    .out20(decoder_1_out20), .out21(decoder_1_out21), .out22(decoder_1_out22), .out23(decoder_1_out23),
    .out24(decoder_1_out24), .out25(decoder_1_out25), .out26(decoder_1_out26), .out27(decoder_1_out27),
    .out28(decoder_1_out28), .out29(decoder_1_out29), .out30(decoder_1_out30), .out31(decoder_1_out31),
    .sel(SEL_R_DST), .en(and_1_out));
  // NoConnect on decoder_1_out31
  assign bit_extender_1_out = {{60{D_IN[3]}}, D_IN};  // Bit_Extender bit_extender_1
  Register #(.width(64)) X0 (.D(multiplexer_6_out), .en(decoder_1_out0), .clk(CLK_out), .Q(X0_q), .clr(Reset_out));
  Register #(.width(64)) X1 (.D(multiplexer_6_out), .en(decoder_1_out1), .clk(CLK_out), .Q(X1_q), .clr(Reset_out));
  Register #(.width(64)) X2 (.D(multiplexer_6_out), .en(decoder_1_out2), .clk(CLK_out), .Q(X2_q), .clr(Reset_out));
  Register #(.width(64)) X3 (.D(multiplexer_6_out), .en(decoder_1_out3), .clk(CLK_out), .Q(X3_q), .clr(Reset_out));
  Register #(.width(64)) X4 (.D(multiplexer_6_out), .en(decoder_1_out4), .clk(CLK_out), .Q(X4_q), .clr(Reset_out));
  Register #(.width(64)) X5 (.D(multiplexer_6_out), .en(decoder_1_out5), .clk(CLK_out), .Q(X5_q), .clr(Reset_out));
  Register #(.width(64)) X6 (.D(multiplexer_6_out), .en(decoder_1_out6), .clk(CLK_out), .Q(X6_q), .clr(Reset_out));
  Register #(.width(64)) X7 (.D(multiplexer_6_out), .en(decoder_1_out7), .clk(CLK_out), .Q(X7_q), .clr(Reset_out));
  Register #(.width(64)) X8 (.D(multiplexer_6_out), .en(decoder_1_out8), .clk(CLK_out), .Q(X8_q), .clr(Reset_out));
  Register #(.width(64)) X9 (.D(multiplexer_6_out), .en(decoder_1_out9), .clk(CLK_out), .Q(X9_q), .clr(Reset_out));
  Register #(.width(64)) X10 (.D(multiplexer_6_out), .en(decoder_1_out10), .clk(CLK_out), .Q(X10_q), .clr(Reset_out));
  Register #(.width(64)) X11 (.D(multiplexer_6_out), .en(decoder_1_out11), .clk(CLK_out), .Q(X11_q), .clr(Reset_out));
  Register #(.width(64)) X12 (.D(multiplexer_6_out), .en(decoder_1_out12), .clk(CLK_out), .Q(X12_q), .clr(Reset_out));
  Register #(.width(64)) X13 (.D(multiplexer_6_out), .en(decoder_1_out13), .clk(CLK_out), .Q(X13_q), .clr(Reset_out));
  Register #(.width(64)) X14 (.D(multiplexer_6_out), .en(decoder_1_out14), .clk(CLK_out), .Q(X14_q), .clr(Reset_out));
  Register #(.width(64)) X15 (.D(multiplexer_6_out), .en(decoder_1_out15), .clk(CLK_out), .Q(X15_q), .clr(Reset_out));
  Register #(.width(64)) X16 (.D(multiplexer_6_out), .en(decoder_1_out16), .clk(CLK_out), .Q(X16_q), .clr(Reset_out));
  Register #(.width(64)) X17 (.D(multiplexer_6_out), .en(decoder_1_out17), .clk(CLK_out), .Q(X17_q), .clr(Reset_out));
  Register #(.width(64)) X18 (.D(multiplexer_6_out), .en(decoder_1_out18), .clk(CLK_out), .Q(X18_q), .clr(Reset_out));
  Register #(.width(64)) X19 (.D(multiplexer_6_out), .en(decoder_1_out19), .clk(CLK_out), .Q(X19_q), .clr(Reset_out));
  Register #(.width(64)) X20 (.D(multiplexer_6_out), .en(decoder_1_out20), .clk(CLK_out), .Q(X20_q), .clr(Reset_out));
  Register #(.width(64)) X21 (.D(multiplexer_6_out), .en(decoder_1_out21), .clk(CLK_out), .Q(X21_q), .clr(Reset_out));
  Register #(.width(64)) X22 (.D(multiplexer_6_out), .en(decoder_1_out22), .clk(CLK_out), .Q(X22_q), .clr(Reset_out));
  Register #(.width(64)) X23 (.D(multiplexer_6_out), .en(decoder_1_out23), .clk(CLK_out), .Q(X23_q), .clr(Reset_out));
  Register #(.width(64)) X24 (.D(multiplexer_6_out), .en(decoder_1_out24), .clk(CLK_out), .Q(X24_q), .clr(Reset_out));
  Register #(.width(64)) X25 (.D(multiplexer_6_out), .en(decoder_1_out25), .clk(CLK_out), .Q(X25_q), .clr(Reset_out));
  Register #(.width(64)) X26 (.D(multiplexer_6_out), .en(decoder_1_out26), .clk(CLK_out), .Q(X26_q), .clr(Reset_out));
  Register #(.width(64)) X27 (.D(multiplexer_6_out), .en(decoder_1_out27), .clk(CLK_out), .Q(X27_q), .clr(Reset_out));
  Register #(.width(64)) X28 (.D(multiplexer_6_out), .en(decoder_1_out28), .clk(CLK_out), .Q(X28_q), .clr(Reset_out));
  Register #(.width(64)) X29 (.D(multiplexer_6_out), .en(decoder_1_out29), .clk(CLK_out), .Q(X29_q), .clr(Reset_out));
  Register #(.width(64)) X30 (.D(multiplexer_6_out), .en(decoder_1_out30), .clk(CLK_out), .Q(X30_q), .clr(Reset_out));
  Adder #(.width(64)) adder_2 (.a(PC_q), .b(bit_extender_1_out), .out(adder_2_out), .cin(1'b0));  // open: cout
  Multiplexer #(.enable("false"), .select(5), .width(64)) multiplexer_1 (
    .in0(X0_q), .in1(X1_q), .in2(X2_q), .in3(X3_q), .in4(X4_q), .in5(X5_q), .in6(X6_q), .in7(X7_q),
    .in8(X8_q), .in9(X9_q), .in10(X10_q), .in11(X11_q), .in12(X12_q), .in13(X13_q), .in14(X14_q),
    .in15(X15_q), .in16(X16_q), .in17(X17_q), .in18(X18_q), .in19(X19_q), .in20(X20_q), .in21(X21_q),
    .in22(X22_q), .in23(X23_q), .in24(X24_q), .in25(X25_q), .in26(X26_q), .in27(X27_q), .in28(X28_q),
    .in29(X29_q), .in30(X30_q), .in31({64{1'b0}}), .out(multiplexer_1_out), .sel(SEL_R_SRC1));
  Multiplexer #(.enable("false"), .select(5), .width(64)) multiplexer_2 (
    .in0(X0_q), .in1(X1_q), .in2(X2_q), .in3(X3_q), .in4(X4_q), .in5(X5_q), .in6(X6_q), .in7(X7_q),
    .in8(X8_q), .in9(X9_q), .in10(X10_q), .in11(X11_q), .in12(X12_q), .in13(X13_q), .in14(X14_q),
    .in15(X15_q), .in16(X16_q), .in17(X17_q), .in18(X18_q), .in19(X19_q), .in20(X20_q), .in21(X21_q),
    .in22(X22_q), .in23(X23_q), .in24(X24_q), .in25(X25_q), .in26(X26_q), .in27(X27_q), .in28(X28_q),
    .in29(X29_q), .in30(X30_q), .in31({64{1'b0}}), .out(multiplexer_2_out), .sel(SEL_R_SRC2));
  assign bit_extender_2_out = {{60{1'b0}}, D_IN};  // Bit_Extender bit_extender_2
  Multiplexer #(.enable("false"), .width(64)) multiplexer_3 (
    .in0(bit_extender_2_out), .in1(multiplexer_2_out), .out(multiplexer_3_out), .sel(USE_R_SRC2));
  or or_1 (or_1_out, BRANCH, and_2_out);
  Multiplexer #(.enable("false"), .width(64)) multiplexer_4 (
    .in0(adder_1_out), .in1(adder_2_out), .out(multiplexer_4_out), .sel(or_1_out));
  and and_2 (and_2_out, BRANCH_IF_ZERO, comparator_2_eq);
  Comparator #(.mode("unsigned"), .width(64)) comparator_2 (
    .a({64{1'b0}}), .b(multiplexer_1_out), .eq(comparator_2_eq));  // open: gt, lt
  assign and_3_out = multiplexer_1_out & multiplexer_3_out;  // AND_Gate and_3, 64 bits wide
  assign or_2_out = multiplexer_1_out | multiplexer_3_out;  // OR_Gate or_2, 64 bits wide
  assign xor_1_out = multiplexer_1_out ^ multiplexer_3_out;  // XOR_Gate xor_1, 64 bits wide
  Adder #(.width(64)) adder_3 (
    .a(multiplexer_1_out), .b(multiplexer_3_out), .out(adder_3_out), .cin(1'b0));  // open: cout
  RAM #(.addrWidth(24), .dataWidth(64)) DATA_MEMORY (
    .addr(multiplexer_1_out[23:0]), .we(STORE_TO_MEMORY), .oe(LOAD_FROM_MEMORY), .clk(CLK_out),
    .din(multiplexer_2_out), .dout(DATA_MEMORY_dout));
  Multiplexer #(.enable("false"), .select(2), .width(64)) multiplexer_5 (
    .in0(and_3_out), .in1(or_2_out), .in2(xor_1_out), .in3(adder_3_out), .out(multiplexer_5_out), .sel(SEL_OP));
  not not_2 (ERROR_DATA_ADDR_OUT_OF_RANGE, comparator_3_eq);
  Comparator #(.mode("unsigned"), .width(40)) comparator_3 (
    .a({40{1'b0}}), .b(multiplexer_1_out[63:24]), .eq(comparator_3_eq));  // open: gt, lt
  Multiplexer #(.enable("false"), .width(64)) multiplexer_6 (
    .in0(multiplexer_5_out), .in1(DATA_MEMORY_dout), .out(multiplexer_6_out), .sel(LOAD_FROM_MEMORY));
endmodule
