// Logisim project acc4.circ as structural Verilog: 1 circuit, main circuit main
module main (
  input  SEL1,
  input  SEL0,
  input  IN3,
  input  IN2,
  input  IN1,
  input  IN0
);

  wire ACC0_q, ACC1_q, ACC2_q, ACC3_q, and_1_out, and_2_out, and_3_out, and_4_out, and_5_out, and_6_out,
       and_7_out, and_8_out, and_9_out, and_10_out, and_11_out, and_12_out, and_13_out, and_14_out,
       and_15_out, and_16_out, and_17_out, and_18_out, and_19_out, and_20_out, and_21_out, and_22_out,
       and_23_out, and_24_out, and_25_out, and_26_out, CLK_out, or_1_out, or_2_out, or_3_out, or_4_out,
       or_5_out, or_6_out, or_7_out, or_8_out, or_9_out, or_10_out, Reset_out, xor_1_out, xor_2_out,
       xor_3_out, xor_4_out, xor_5_out, xor_6_out, xor_7_out;

  Clock CLK (.out(CLK_out));
  Button Reset (.out(Reset_out));
  D_Flip_Flop ACC3 (.D(or_7_out), .clk(CLK_out), .Q(ACC3_q), .reset(Reset_out));  // open: Qn, preset
  D_Flip_Flop ACC2 (.D(or_8_out), .clk(CLK_out), .Q(ACC2_q), .reset(Reset_out));  // open: Qn, preset
  D_Flip_Flop ACC1 (.D(or_9_out), .clk(CLK_out), .Q(ACC1_q), .reset(Reset_out));  // open: Qn, preset
  D_Flip_Flop ACC0 (.D(or_10_out), .clk(CLK_out), .Q(ACC0_q), .reset(Reset_out));  // open: Qn, preset
  and and_1 (and_1_out, IN3, ACC3_q);
  and and_2 (and_2_out, IN2, ACC2_q);
  and and_3 (and_3_out, IN1, ACC1_q);
  and and_4 (and_4_out, IN0, ACC0_q);
  or or_1 (or_1_out, IN3, ACC3_q);
  or or_2 (or_2_out, IN2, ACC2_q);
  or or_3 (or_3_out, IN1, ACC1_q);
  or or_4 (or_4_out, IN0, ACC0_q);
  xor xor_1 (xor_1_out, IN3, ACC3_q);
  xor xor_2 (xor_2_out, IN2, ACC2_q);
  xor xor_3 (xor_3_out, IN1, ACC1_q);
  xor xor_4 (xor_4_out, IN0, ACC0_q);
  or or_5 (or_5_out, and_3_out, and_5_out);
  and and_5 (and_5_out, and_4_out, xor_3_out);
  xor xor_5 (xor_5_out, and_4_out, xor_3_out);
  and and_6 (and_6_out, ~SEL0, ~SEL1);  // AND_Gate
  or or_6 (or_6_out, and_2_out, and_7_out);
  and and_7 (and_7_out, xor_2_out, or_5_out);
  xor xor_6 (xor_6_out, or_5_out, xor_2_out);
  and and_8 (and_8_out, SEL0, ~SEL1);  // AND_Gate
  and and_9 (and_9_out, ~SEL0, SEL1);  // AND_Gate
  xor xor_7 (xor_7_out, or_6_out, xor_1_out);
  and and_10 (and_10_out, SEL0, SEL1);
  and and_11 (and_11_out, and_1_out, and_6_out);
  and and_12 (and_12_out, and_2_out, and_6_out);
  and and_13 (and_13_out, and_3_out, and_6_out);
  and and_14 (and_14_out, and_4_out, and_6_out);
  and and_15 (and_15_out, or_1_out, and_8_out);
  and and_16 (and_16_out, or_2_out, and_8_out);
  and and_17 (and_17_out, or_3_out, and_8_out);
  and and_18 (and_18_out, or_4_out, and_8_out);
  and and_19 (and_19_out, xor_1_out, and_9_out);
  and and_20 (and_20_out, xor_2_out, and_9_out);
  and and_21 (and_21_out, xor_3_out, and_9_out);
  and and_22 (and_22_out, xor_4_out, and_9_out);
  and and_23 (and_23_out, xor_7_out, and_10_out);
  and and_24 (and_24_out, xor_6_out, and_10_out);
  and and_25 (and_25_out, xor_5_out, and_10_out);
  and and_26 (and_26_out, xor_4_out, and_10_out);
  or or_7 (or_7_out, and_11_out, and_15_out, and_19_out, and_23_out);
  or or_8 (or_8_out, and_12_out, and_16_out, and_20_out, and_24_out);
  or or_9 (or_9_out, and_13_out, and_17_out, and_21_out, and_25_out);
  or or_10 (or_10_out, and_14_out, and_18_out, and_22_out, and_26_out);
endmodule
