// Logisim project acc4_4regs.circ as structural Verilog: 1 circuit, main circuit main
module main (
  input  [1:0] SEL_OP,
  input  [1:0] SEL_R,
  input  [3:0] D_IN
);

  wire CLK_out, decoder_1_out0, decoder_1_out1, decoder_1_out2, decoder_1_out3, Reset_out;
  wire [3:0] adder_1_out, and_1_out, multiplexer_1_out, multiplexer_2_out, or_1_out, REG0_q, REG1_q, REG2_q,
       REG3_q, xor_1_out;

  Clock CLK (.out(CLK_out));
  Button Reset (.out(Reset_out));
  Decoder #(.select(2)) decoder_1 (
    .out0(decoder_1_out0), .out1(decoder_1_out1), .out2(decoder_1_out2), .out3(decoder_1_out3), .sel(SEL_R),
    .en(1'b1));
  Register #(.width(4)) REG0 (.D(multiplexer_2_out), .en(decoder_1_out0), .clk(CLK_out), .Q(REG0_q), .clr(Reset_out));
  Register #(.width(4)) REG1 (.D(multiplexer_2_out), .en(decoder_1_out1), .clk(CLK_out), .Q(REG1_q), .clr(Reset_out));
  Register #(.width(4)) REG2 (.D(multiplexer_2_out), .en(decoder_1_out2), .clk(CLK_out), .Q(REG2_q), .clr(Reset_out));
  Register #(.width(4)) REG3 (.D(multiplexer_2_out), .en(decoder_1_out3), .clk(CLK_out), .Q(REG3_q), .clr(Reset_out));
  Multiplexer #(.enable("false"), .select(2), .width(4)) multiplexer_1 (
    .in0(REG0_q), .in1(REG1_q), .in2(REG2_q), .in3(REG3_q), .out(multiplexer_1_out), .sel(SEL_R));
  assign and_1_out = D_IN & multiplexer_1_out;  // AND_Gate and_1, 4 bits wide
  assign or_1_out = D_IN | multiplexer_1_out;  // OR_Gate or_1, 4 bits wide
  assign xor_1_out = D_IN ^ multiplexer_1_out;  // XOR_Gate xor_1, 4 bits wide
  Adder #(.width(4)) adder_1 (.a(D_IN), .b(multiplexer_1_out), .out(adder_1_out), .cin(1'b0));  // open: cout
  Multiplexer #(.enable("false"), .select(2), .width(4)) multiplexer_2 (
    .in0(and_1_out), .in1(or_1_out), .in2(xor_1_out), .in3(adder_1_out), .out(multiplexer_2_out), .sel(SEL_OP));
endmodule
