// Logisim project acc4_simplified.circ as structural Verilog: 1 circuit, main circuit main
module main (
  input  [1:0] SEL,
  input  [3:0] D_IN
);

  wire CLK_out, Reset_out;
  wire [3:0] ACC_q, adder_1_out, and_1_out, multiplexer_1_out, or_1_out, xor_1_out;

  Clock CLK (.out(CLK_out));
  Button Reset (.out(Reset_out));
  Register #(.width(4)) ACC (.D(multiplexer_1_out), .en(1'b1), .clk(CLK_out), .Q(ACC_q), .clr(Reset_out));
  assign and_1_out = D_IN & ACC_q;  // AND_Gate and_1, 4 bits wide
  assign or_1_out = D_IN | ACC_q;  // OR_Gate or_1, 4 bits wide
  assign xor_1_out = D_IN ^ ACC_q;  // XOR_Gate xor_1, 4 bits wide
  Adder #(.width(4)) adder_1 (.a(D_IN), .b(ACC_q), .out(adder_1_out), .cin(1'b0));  // open: cout
  Multiplexer #(.enable("false"), .select(2), .width(4)) multiplexer_1 (
    .in0(and_1_out), .in1(or_1_out), .in2(xor_1_out), .in3(adder_1_out), .out(multiplexer_1_out), .sel(SEL));
endmodule
