// Logisim project added_imms_mul_div_accesssize_varshift.circ as structural Verilog: 11 circuits, main circuit main
module main (
);

  wire and_1_out, and_2_out, arithmeticlogicunit_1_c, arithmeticlogicunit_1_n, arithmeticlogicunit_1_padd,
       arithmeticlogicunit_1_pand, arithmeticlogicunit_1_peor, arithmeticlogicunit_1_plsl,
       arithmeticlogicunit_1_plslv, arithmeticlogicunit_1_plsr, arithmeticlogicunit_1_plsrv,
       arithmeticlogicunit_1_pmul, arithmeticlogicunit_1_por, arithmeticlogicunit_1_ppass_b,
       arithmeticlogicunit_1_psmulh, arithmeticlogicunit_1_psub, arithmeticlogicunit_1_pumulh,
       arithmeticlogicunit_1_sdiv, arithmeticlogicunit_1_udiv, arithmeticlogicunit_1_v,
       arithmeticlogicunit_1_z, arithmeticlogicunit_1_zero, buffer_1_out, buffer_2_out, buffer_3_out,
       CLK_out, controlunit_1_alusrc, controlunit_1_b, controlunit_1_bcond_true, controlunit_1_bl,
       controlunit_1_br, controlunit_1_cbnz, controlunit_1_cbz, controlunit_1_insadd, controlunit_1_insaddi,
       controlunit_1_insaddis, controlunit_1_insadds, controlunit_1_insand, controlunit_1_insandi,
       controlunit_1_insandis, controlunit_1_insands, controlunit_1_insb, controlunit_1_insbcond,
       controlunit_1_insbl, controlunit_1_insbr, controlunit_1_inscbnz, controlunit_1_inscbz,
       controlunit_1_inseor, controlunit_1_inseori, controlunit_1_insldur, controlunit_1_inslsl,
       controlunit_1_inslslv, controlunit_1_inslsr, controlunit_1_inslsrv, controlunit_1_insmovk,
       controlunit_1_insmovn, controlunit_1_insmovz, controlunit_1_insmul, controlunit_1_insnot_implemented,
       controlunit_1_insorr, controlunit_1_insorri, controlunit_1_inssdiv, controlunit_1_inssmulh,
       controlunit_1_insstur, controlunit_1_inssub, controlunit_1_inssubi, controlunit_1_inssubis,
       controlunit_1_inssubs, controlunit_1_insudiv, controlunit_1_insumulh, controlunit_1_memread,
       controlunit_1_memtoreg, controlunit_1_memwrite, controlunit_1_movk, controlunit_1_movn,
       controlunit_1_movz, controlunit_1_rdsp, controlunit_1_reg2loc, controlunit_1_regwrite,
       controlunit_1_rnsp, controlunit_1_setflags, immediateextend_1_imm9, immediateextend_1_imm12,
       immediateextend_1_imm13, immediateextend_1_imm16, immediateextend_1_imm19, immediateextend_1_imm26,
       immediateextend_1_sign_extend, immediateextend_1_zero_extend, insaddralignment_1_aligned,
       insaddralignment_1_not_aligned, insaddrrange_1_in_range, insaddrrange_1_out_of_range,
       memorycontroller_1_a0, memorycontroller_1_a1, memorycontroller_1_a2, memorycontroller_1_a3,
       memorycontroller_1_address_out_of_range, memorycontroller_1_data_memory_access,
       memorycontroller_1_data_memory_read, memorycontroller_1_data_memory_write,
       memorycontroller_1_gpio_access, memorycontroller_1_gpio_access_size_invalid,
       memorycontroller_1_gpio_address_not_aligned, memorycontroller_1_gpio_read,
       memorycontroller_1_gpio_write, memorycontroller_1_peripheral_access,
       memorycontroller_1_peripheral_not_implemented, memorycontroller_1_r, memorycontroller_1_w, or_1_out,
       or_2_out, registerfile_1_we, Reset_out, xor_1_out;
  wire [1:0] controlunit_1_accesssize;
  wire [2:0] controlunit_1_immsel;
  wire [3:0] arithmeticlogicunit_1_flags, controlunit_1_aluop, FLAGS_q;
  wire [4:0] multiplexer_2_out, multiplexer_3_out, registerfile_1_ra1, registerfile_1_ra2, registerfile_1_wa;
  wire [5:0] arithmeticlogicunit_1_shamt, controlunit_1_shamt;
  wire [7:0] INSTRUCTION_MEMORY_p2, INSTRUCTION_MEMORY_p3, INSTRUCTION_MEMORY_p4, INSTRUCTION_MEMORY_p5,
       memorycontroller_1_data_memory_byte_enable, memorycontroller_1_gpio_address, ram_1_p12, ram_1_p13,
       ram_1_p14, ram_1_p15, ram_1_p16, ram_1_p17, ram_1_p18, ram_1_p19;
  wire [23:0] memorycontroller_1_data_memory_address;
  wire [53:0] gpio_1_gpio_out;
  wire [63:0] adder_1_out, adder_2_out, and_3_out, arithmeticlogicunit_1_o11, arithmeticlogicunit_1_o12,
       arithmeticlogicunit_1_o13, arithmeticlogicunit_1_o21, arithmeticlogicunit_1_o22,
       arithmeticlogicunit_1_o23, arithmeticlogicunit_1_r1, arithmeticlogicunit_1_r2,
       arithmeticlogicunit_1_r3, arithmeticlogicunit_1_result, controlled_buffer_1_out, gpio_1_data_out,
       immediateextend_1_extended1, immediateextend_1_extended2, immediateextend_1_extended3,
       immediateextend_1_immediate, memorycontroller_1_access_mask, memorycontroller_1_data_out,
       multiplexer_1_out, multiplexer_4_out, multiplexer_5_out, multiplexer_6_out, multiplexer_7_out,
       multiplexer_8_out, PC_q, registerfile_1_rd11, registerfile_1_rd12, registerfile_1_rd13,
       registerfile_1_rd21, registerfile_1_rd22, registerfile_1_rd23, registerfile_1_read_data1,
       registerfile_1_read_data2, registerfile_1_wd1, registerfile_1_wd2, registerfile_1_wd3, shifter_1_out,
       wideimmediate_1_imm_out;

  Button Reset (.out(Reset_out));
  buf buffer_1 (buffer_1_out, Reset_out);
  Clock CLK (.out(CLK_out));
  buf buffer_2 (buffer_2_out, buffer_1_out);
  buf buffer_3 (buffer_3_out, buffer_2_out);
  Register #(.width(64)) PC (.D(multiplexer_1_out), .en(1'b1), .clk(xor_1_out), .Q(PC_q));  // open: clr
  Multiplexer #(.enable("false"), .width(64)) multiplexer_1 (
    .in0(multiplexer_6_out), .in1(64'h80000), .out(multiplexer_1_out), .sel(or_1_out));
  or or_1 (or_1_out, Reset_out, buffer_3_out);
  xor xor_1 (xor_1_out, buffer_3_out, CLK_out);
  // ROM #(.addrWidth(24), .line("quad")) INSTRUCTION_MEMORY: pin names not known; wires that end beside it: PC_q[23:0], INSTRUCTION_MEMORY_p2, INSTRUCTION_MEMORY_p3, INSTRUCTION_MEMORY_p4, INSTRUCTION_MEMORY_p5
  Adder #(.width(64)) adder_1 (.a(64'h4), .b(PC_q), .out(adder_1_out), .cin(1'b0));  // open: cout
  LED led_1 (.in(insaddralignment_1_aligned));
  LED led_2 (.in(insaddralignment_1_not_aligned));
  LED led_3 (.in(insaddrrange_1_in_range));
  LED led_4 (.in(insaddrrange_1_out_of_range));
  InsAddrAlignment insaddralignment_1 (
    .ALIGNED(insaddralignment_1_aligned), .NOT_ALIGNED(insaddralignment_1_not_aligned), .ADDR(PC_q));
  InsAddrRange insaddrrange_1 (
    .IN_RANGE(insaddrrange_1_in_range), .OUT_OF_RANGE(insaddrrange_1_out_of_range), .ADDR(PC_q));
  LED led_5 (.in(controlunit_1_insnot_implemented));
  LED led_6 (.in(controlunit_1_insb));
  LED led_7 (.in(controlunit_1_insbl));
  LED led_8 (.in(controlunit_1_insbr));
  LED led_9 (.in(controlunit_1_insldur));
  LED led_10 (.in(controlunit_1_insand));
  LED led_11 (.in(controlunit_1_insorr));
  LED led_12 (.in(controlunit_1_inseor));
  LED led_13 (.in(controlunit_1_insadd));
  LED led_14 (.in(controlunit_1_inssub));
  LED led_15 (.in(controlunit_1_insands));
  LED led_16 (.in(controlunit_1_insadds));
  LED led_17 (.in(controlunit_1_inssubs));
  LED led_18 (.in(controlunit_1_inslsl));
  LED led_19 (.in(controlunit_1_inslsr));
  LED led_20 (.in(controlunit_1_insmovk));
  LED led_21 (.in(controlunit_1_insmovn));
  LED led_22 (.in(controlunit_1_insumulh));
  LED led_23 (.in(controlunit_1_insudiv));
  LED led_24 (.in(controlunit_1_insbcond));
  LED led_25 (.in(controlunit_1_inscbz));
  LED led_26 (.in(controlunit_1_inscbnz));
  LED led_27 (.in(controlunit_1_insstur));
  LED led_28 (.in(controlunit_1_insandi));
  LED led_29 (.in(controlunit_1_insorri));
  LED led_30 (.in(controlunit_1_inseori));
  LED led_31 (.in(controlunit_1_insaddi));
  LED led_32 (.in(controlunit_1_inssubi));
  LED led_33 (.in(controlunit_1_insandis));
  LED led_34 (.in(controlunit_1_insaddis));
  LED led_35 (.in(controlunit_1_inssubis));
  LED led_36 (.in(controlunit_1_inslslv));
  LED led_37 (.in(controlunit_1_inslsrv));
  LED led_38 (.in(controlunit_1_insmovz));
  LED led_39 (.in(controlunit_1_insmul));
  LED led_40 (.in(controlunit_1_inssmulh));
  LED led_41 (.in(controlunit_1_inssdiv));
  ControlUnit controlunit_1 (
    .insB(controlunit_1_insb), .insBL(controlunit_1_insbl), .insBR(controlunit_1_insbr),
    .insCBZ(controlunit_1_inscbz), .insCBNZ(controlunit_1_inscbnz), .insBCOND(controlunit_1_insbcond),
    .insSTUR(controlunit_1_insstur), .insLDUR(controlunit_1_insldur), .insAND(controlunit_1_insand),
    .insORR(controlunit_1_insorr), .insEOR(controlunit_1_inseor), .insADD(controlunit_1_insadd),
    .insSUB(controlunit_1_inssub), .insANDI(controlunit_1_insandi), .insORRI(controlunit_1_insorri),
    .insEORI(controlunit_1_inseori), .insADDI(controlunit_1_insaddi), .insSUBI(controlunit_1_inssubi),
    .insANDS(controlunit_1_insands), .insADDS(controlunit_1_insadds), .insSUBS(controlunit_1_inssubs),
    .insANDIS(controlunit_1_insandis), .insADDIS(controlunit_1_insaddis), .insSUBIS(controlunit_1_inssubis),
    .insLSL(controlunit_1_inslsl), .insLSR(controlunit_1_inslsr), .insMOVK(controlunit_1_insmovk),
    .insMOVZ(controlunit_1_insmovz), .insMOVN(controlunit_1_insmovn), .insLSLV(controlunit_1_inslslv),
    .insLSRV(controlunit_1_inslsrv), .insMUL(controlunit_1_insmul), .insUMULH(controlunit_1_insumulh),
    .insSMULH(controlunit_1_inssmulh), .insUDIV(controlunit_1_insudiv), .insSDIV(controlunit_1_inssdiv),
    .insNOT_IMPLEMENTED(controlunit_1_insnot_implemented), .AccessSize(controlunit_1_accesssize),
    .B(controlunit_1_b), .BL(controlunit_1_bl), .BR(controlunit_1_br), .CBZ(controlunit_1_cbz),
    .CBNZ(controlunit_1_cbnz), .MOVK(controlunit_1_movk), .MOVZ(controlunit_1_movz),
    .MOVN(controlunit_1_movn), .Reg2Loc(controlunit_1_reg2loc), .RegWrite(controlunit_1_regwrite),
    .MemRead(controlunit_1_memread), .MemWrite(controlunit_1_memwrite), .ALUSrc(controlunit_1_alusrc),
    .MemtoReg(controlunit_1_memtoreg), .ALUop(controlunit_1_aluop), .ImmSel(controlunit_1_immsel),
    .SetFlags(controlunit_1_setflags), .RdSP(controlunit_1_rdsp), .RnSP(controlunit_1_rnsp),
    .Shamt(controlunit_1_shamt), .BCOND_TRUE(controlunit_1_bcond_true), .FLAGS(FLAGS_q),
    .INS({INSTRUCTION_MEMORY_p5, INSTRUCTION_MEMORY_p4, INSTRUCTION_MEMORY_p3, INSTRUCTION_MEMORY_p2}));
  Multiplexer #(.enable("false"), .width(5)) multiplexer_2 (
    .in0(INSTRUCTION_MEMORY_p4[4:0]), .in1(INSTRUCTION_MEMORY_p2[4:0]), .out(multiplexer_2_out),
    .sel(controlunit_1_reg2loc));
  Multiplexer #(.enable("false"), .width(5)) multiplexer_3 (
    .in0(INSTRUCTION_MEMORY_p2[4:0]), .in1(5'b11110), .out(multiplexer_3_out), .sel(controlunit_1_bl));
  // Probe on registerfile_1_ra1
  // Probe on registerfile_1_ra2
  // Probe on registerfile_1_wa
  LED led_42 (.in(registerfile_1_we));
  LED led_43 (.in(immediateextend_1_zero_extend));
  LED led_44 (.in(immediateextend_1_imm9));
  LED led_45 (.in(immediateextend_1_imm12));
  LED led_46 (.in(immediateextend_1_imm13));
  // Probe on immediateextend_1_extended2
  // Probe on immediateextend_1_extended3
  // Probe on registerfile_1_rd11
  // Probe on registerfile_1_rd12
  // Probe on registerfile_1_rd13
  // Probe on registerfile_1_rd23
  // Probe on registerfile_1_rd22
  // Probe on registerfile_1_rd21
  // Probe on registerfile_1_wd1
  // Probe on registerfile_1_wd3
  // Probe on registerfile_1_wd2
  LED led_47 (.in(immediateextend_1_sign_extend));
  LED led_48 (.in(immediateextend_1_imm16));
  LED led_49 (.in(immediateextend_1_imm19));
  LED led_50 (.in(immediateextend_1_imm26));
  // Probe on immediateextend_1_extended1
  RegisterFile registerfile_1 (
    .RD11(registerfile_1_rd11), .RD12(registerfile_1_rd12), .RD13(registerfile_1_rd13),
    .RD21(registerfile_1_rd21), .RD22(registerfile_1_rd22), .RD23(registerfile_1_rd23),
    .READ_DATA1(registerfile_1_read_data1), .READ_DATA2(registerfile_1_read_data2), .WE(registerfile_1_we),
    .RA1(registerfile_1_ra1), .RA2(registerfile_1_ra2), .WA(registerfile_1_wa), .WD1(registerfile_1_wd1),
    .WD2(registerfile_1_wd2), .WD3(registerfile_1_wd3), .WRITE_USE_SP(controlunit_1_rdsp),
    .READ1_USE_SP(controlunit_1_rnsp), .WRITE_ENABLE(controlunit_1_regwrite), .CLOCK(CLK_out),
    .READ_ADDR1({INSTRUCTION_MEMORY_p3[1:0], INSTRUCTION_MEMORY_p2[7:5]}), .READ_ADDR2(multiplexer_2_out),
    .WRITE_ADDR(multiplexer_3_out), .WRITE_DATA(multiplexer_8_out));
  ImmediateExtend immediateextend_1 (
    .SIGN_EXTEND(immediateextend_1_sign_extend), .IMM12(immediateextend_1_imm12),
    .IMM9(immediateextend_1_imm9), .IMM26(immediateextend_1_imm26), .IMM19(immediateextend_1_imm19),
    .IMM16(immediateextend_1_imm16), .IMM13(immediateextend_1_imm13),
    .IMMEDIATE(immediateextend_1_immediate), .ZERO_EXTEND(immediateextend_1_zero_extend),
    .EXTENDED1(immediateextend_1_extended1), .EXTENDED2(immediateextend_1_extended2),
    .EXTENDED3(immediateextend_1_extended3), .CTRL(controlunit_1_immsel),
    .INS({INSTRUCTION_MEMORY_p5, INSTRUCTION_MEMORY_p4, INSTRUCTION_MEMORY_p3, INSTRUCTION_MEMORY_p2}));
  Shifter #(.width(64)) shifter_1 (.in(immediateextend_1_immediate), .\dist (6'b000010), .out(shifter_1_out));
  WideImmediate wideimmediate_1 (
    .IMM_OUT(wideimmediate_1_imm_out), .MOVK(controlunit_1_movk), .MOVZ(controlunit_1_movz),
    .MOVN(controlunit_1_movn), .REG_DATA(registerfile_1_read_data2), .SHAMT(controlunit_1_shamt),
    .IMM_IN(immediateextend_1_immediate));
  Adder #(.width(64)) adder_2 (.a(PC_q), .b(shifter_1_out), .out(adder_2_out), .cin(1'b0));  // open: cout
  Multiplexer #(.enable("false"), .width(64)) multiplexer_4 (
    .in0(registerfile_1_read_data2), .in1(wideimmediate_1_imm_out), .out(multiplexer_4_out),
    .sel(controlunit_1_alusrc));
  Multiplexer #(.enable("false"), .width(64)) multiplexer_5 (
    .in0(adder_2_out), .in1(registerfile_1_read_data1), .out(multiplexer_5_out), .sel(controlunit_1_br));
  LED led_51 (.in(arithmeticlogicunit_1_pand));
  LED led_52 (.in(arithmeticlogicunit_1_por));
  LED led_53 (.in(arithmeticlogicunit_1_peor));
  LED led_54 (.in(arithmeticlogicunit_1_padd));
  LED led_55 (.in(arithmeticlogicunit_1_psub));
  LED led_56 (.in(arithmeticlogicunit_1_plsl));
  LED led_57 (.in(arithmeticlogicunit_1_plsr));
  LED led_58 (.in(arithmeticlogicunit_1_plslv));
  LED led_59 (.in(arithmeticlogicunit_1_plsrv));
  LED led_60 (.in(arithmeticlogicunit_1_pmul));
  LED led_61 (.in(arithmeticlogicunit_1_pumulh));
  LED led_62 (.in(arithmeticlogicunit_1_psmulh));
  LED led_63 (.in(arithmeticlogicunit_1_udiv));
  LED led_64 (.in(arithmeticlogicunit_1_sdiv));
  LED led_65 (.in(arithmeticlogicunit_1_ppass_b));
  // Probe on arithmeticlogicunit_1_o12
  // Probe on arithmeticlogicunit_1_o13
  // Probe on arithmeticlogicunit_1_o22
  // Probe on arithmeticlogicunit_1_o23
  // Probe on arithmeticlogicunit_1_r2
  // Probe on arithmeticlogicunit_1_r3
  // Probe on arithmeticlogicunit_1_shamt
  // Probe on arithmeticlogicunit_1_o11
  // Probe on arithmeticlogicunit_1_o21
  // Probe on arithmeticlogicunit_1_r1
  LED led_66 (.in(arithmeticlogicunit_1_z));
  LED led_67 (.in(arithmeticlogicunit_1_n));
  LED led_68 (.in(arithmeticlogicunit_1_c));
  LED led_69 (.in(arithmeticlogicunit_1_v));
  ArithmeticLogicUnit arithmeticlogicunit_1 (
    .pAND(arithmeticlogicunit_1_pand), .pOR(arithmeticlogicunit_1_por), .pEOR(arithmeticlogicunit_1_peor),
    .pADD(arithmeticlogicunit_1_padd), .pSUB(arithmeticlogicunit_1_psub), .pLSL(arithmeticlogicunit_1_plsl),
    .pLSR(arithmeticlogicunit_1_plsr), .pLSLV(arithmeticlogicunit_1_plslv),
    .pLSRV(arithmeticlogicunit_1_plsrv), .pMUL(arithmeticlogicunit_1_pmul),
    .pUMULH(arithmeticlogicunit_1_pumulh), .pSMULH(arithmeticlogicunit_1_psmulh),
    .UDIV(arithmeticlogicunit_1_udiv), .SDIV(arithmeticlogicunit_1_sdiv),
    .pPASS_B(arithmeticlogicunit_1_ppass_b), .R1(arithmeticlogicunit_1_r1), .R2(arithmeticlogicunit_1_r2),
    .R3(arithmeticlogicunit_1_r3), .RESULT(arithmeticlogicunit_1_result), .ZERO(arithmeticlogicunit_1_zero),
    .Z(arithmeticlogicunit_1_z), .N(arithmeticlogicunit_1_n), .FLAGS(arithmeticlogicunit_1_flags),
    .C(arithmeticlogicunit_1_c), .V(arithmeticlogicunit_1_v), .SHAMT(arithmeticlogicunit_1_shamt),
    .O11(arithmeticlogicunit_1_o11), .O12(arithmeticlogicunit_1_o12), .O13(arithmeticlogicunit_1_o13),
    .O21(arithmeticlogicunit_1_o21), .O22(arithmeticlogicunit_1_o22), .O23(arithmeticlogicunit_1_o23),
    .SHIFT_AMOUNT(controlunit_1_shamt), .OPERAND1(registerfile_1_read_data1), .OPERAND2(multiplexer_4_out),
    .ALU_OP(controlunit_1_aluop));
  and and_1 (and_1_out, controlunit_1_cbz, arithmeticlogicunit_1_zero);
  and and_2 (and_2_out, controlunit_1_cbnz, ~arithmeticlogicunit_1_zero);  // AND_Gate
  Register #(.width(4)) FLAGS (
    .D(arithmeticlogicunit_1_flags), .en(controlunit_1_setflags), .clk(CLK_out), .Q(FLAGS_q));  // open: clr
  Multiplexer #(.enable("false"), .width(64)) multiplexer_6 (
    .in0(adder_1_out), .in1(multiplexer_5_out), .out(multiplexer_6_out), .sel(or_2_out));
  or or_2 (or_2_out, controlunit_1_b, controlunit_1_bl, controlunit_1_br, controlunit_1_bcond_true, and_1_out, and_2_out);
  LED led_70 (.in(memorycontroller_1_r));
  LED led_71 (.in(memorycontroller_1_a0));
  LED led_72 (.in(memorycontroller_1_a2));
  LED led_73 (.in(memorycontroller_1_gpio_access));
  LED led_74 (.in(memorycontroller_1_gpio_address_not_aligned));
  LED led_75 (.in(memorycontroller_1_gpio_access_size_invalid));
  LED led_76 (.in(memorycontroller_1_w));
  LED led_77 (.in(memorycontroller_1_a1));
  LED led_78 (.in(memorycontroller_1_a3));
  LED led_79 (.in(memorycontroller_1_data_memory_access));
  LED led_80 (.in(memorycontroller_1_peripheral_access));
  LED led_81 (.in(memorycontroller_1_peripheral_not_implemented));
  LED led_82 (.in(memorycontroller_1_address_out_of_range));
  MemoryController memorycontroller_1 (
    .A1(memorycontroller_1_a1), .A2(memorycontroller_1_a2), .R(memorycontroller_1_r),
    .W(memorycontroller_1_w), .A3(memorycontroller_1_a3),
    .GPIO_ACCESS_SIZE_INVALID(memorycontroller_1_gpio_access_size_invalid),
    .GPIO_READ(memorycontroller_1_gpio_read), .GPIO_WRITE(memorycontroller_1_gpio_write),
    .PERIPHERAL_NOT_IMPLEMENTED(memorycontroller_1_peripheral_not_implemented),
    .PERIPHERAL_ACCESS(memorycontroller_1_peripheral_access),
    .ADDRESS_OUT_OF_RANGE(memorycontroller_1_address_out_of_range),
    .DATA_MEMORY_ADDRESS(memorycontroller_1_data_memory_address),
    .DATA_MEMORY_READ(memorycontroller_1_data_memory_read), .DATA_OUT(memorycontroller_1_data_out),
    .DATA_MEMORY_WRITE(memorycontroller_1_data_memory_write), .A0(memorycontroller_1_a0),
    .DATA_MEMORY_BYTE_ENABLE(memorycontroller_1_data_memory_byte_enable),
    .DATA_MEMORY_ACCESS(memorycontroller_1_data_memory_access), .GPIO_ACCESS(memorycontroller_1_gpio_access),
    .GPIO_ADDRESS(memorycontroller_1_gpio_address),
    .GPIO_ADDRESS_NOT_ALIGNED(memorycontroller_1_gpio_address_not_aligned),
    .ACCESS_MASK(memorycontroller_1_access_mask), .ADDRESS(arithmeticlogicunit_1_result),
    .DATA_IN(registerfile_1_read_data2), .ACCESS_SIZE(controlunit_1_accesssize),
    .MEM_READ(controlunit_1_memread), .MEM_WRITE(controlunit_1_memwrite));
  // RAM #(.addrWidth(24), .enables("line"), .line("octo"), .misaligned("true")) ram_1: pin names not known; wires that end beside it: memorycontroller_1_data_memory_address, memorycontroller_1_data_memory_write, CLK_out, memorycontroller_1_data_out[7:0], memorycontroller_1_data_out[15:8], memorycontroller_1_data_out[23:16], memorycontroller_1_data_out[31:24], memorycontroller_1_data_out[39:32], memorycontroller_1_data_out[47:40], memorycontroller_1_data_out[55:48], memorycontroller_1_data_out[63:56], ram_1_p12, ram_1_p13, ram_1_p14, ram_1_p15, ram_1_p16, ram_1_p17, ram_1_p18, ram_1_p19
  GPIO gpio_1 (
    .GPIO_OUT(gpio_1_gpio_out), .DATA_OUT(gpio_1_data_out), .CLK(CLK_out),
    .WRITE(memorycontroller_1_gpio_write), .ADDR(memorycontroller_1_gpio_address),
    .DATA_IN(memorycontroller_1_data_out));  // open: GPIO_IN
  assign controlled_buffer_1_out = memorycontroller_1_data_memory_read ? {ram_1_p19, ram_1_p18, ram_1_p17, ram_1_p16, ram_1_p15, ram_1_p14, ram_1_p13, ram_1_p12} : 64'bz;  // Controlled_Buffer controlled_buffer_1
  assign controlled_buffer_1_out = memorycontroller_1_gpio_read ? gpio_1_data_out : 64'bz;  // Controlled_Buffer controlled_buffer_2
  LED RED_LED (.in(gpio_1_gpio_out[5]));
  LED GREEN_LED (.in(gpio_1_gpio_out[6]));
  assign and_3_out = controlled_buffer_1_out & memorycontroller_1_access_mask;  // AND_Gate and_3, 64 bits wide
  Multiplexer #(.enable("false"), .width(64)) multiplexer_7 (
    .in0(arithmeticlogicunit_1_result), .in1(and_3_out), .out(multiplexer_7_out), .sel(controlunit_1_memtoreg));
  Multiplexer #(.enable("false"), .width(64)) multiplexer_8 (
    .in0(multiplexer_7_out), .in1(adder_1_out), .out(multiplexer_8_out), .sel(controlunit_1_bl));
endmodule

module GPIO (
  input  [63:0] DATA_IN,
  input  [53:0] GPIO_IN,
  input  CLK,
  input  WRITE,
  input  [7:0] ADDR,
  output [63:0] DATA_OUT,
  output [53:0] GPIO_OUT
);

  wire and_1_out, and_2_out, and_3_out, and_4_out, and_5_out, and_6_out, and_7_out, and_8_out, and_9_out,
       and_10_out, comparator_1_eq, comparator_2_eq, comparator_3_eq, comparator_4_eq, comparator_5_eq,
       comparator_6_eq, comparator_7_eq, comparator_8_eq, comparator_9_eq, comparator_10_eq,
       comparator_11_eq, comparator_12_eq, comparator_13_eq, comparator_14_eq, comparator_15_eq,
       comparator_16_eq, d_ff_1_q, d_ff_2_q, d_ff_3_q, d_ff_4_q, or_1_out, s_r_ff_1_q, s_r_ff_2_q,
       s_r_ff_3_q, s_r_ff_4_q, s_r_ff_5_q, s_r_ff_6_q, s_r_ff_7_q, s_r_ff_8_q, s_r_ff_9_q, s_r_ff_10_q,
       s_r_ff_11_q, s_r_ff_12_q, s_r_ff_13_q, s_r_ff_14_q, s_r_ff_15_q, s_r_ff_16_q, s_r_ff_17_q,
       s_r_ff_18_q, s_r_ff_19_q, s_r_ff_20_q, s_r_ff_21_q, s_r_ff_22_q, s_r_ff_23_q, s_r_ff_24_q,
       s_r_ff_25_q, s_r_ff_26_q, s_r_ff_27_q, s_r_ff_28_q, s_r_ff_29_q, s_r_ff_30_q, s_r_ff_31_q,
       s_r_ff_32_q, s_r_ff_33_q, s_r_ff_34_q, s_r_ff_35_q, s_r_ff_36_q, s_r_ff_37_q, s_r_ff_38_q,
       s_r_ff_39_q, s_r_ff_40_q, s_r_ff_41_q, s_r_ff_42_q, s_r_ff_43_q, s_r_ff_44_q, s_r_ff_45_q,
       s_r_ff_46_q, s_r_ff_47_q, s_r_ff_48_q, s_r_ff_49_q, s_r_ff_50_q, s_r_ff_51_q, s_r_ff_52_q,
       s_r_ff_53_q, s_r_ff_54_q;
  wire [21:0] GPCLR1_q, GPSET1_q, register_33_q;
  wire [31:0] controlled_buffer_1_out, GPCLR0_q, GPFSEL0_q, GPFSEL1_q, GPFSEL2_q, GPFSEL3_q, GPFSEL4_q,
       GPFSEL5_q, GPSET0_q, register_1_q;
  wire [53:0] and_11_out, and_65_out;

  Comparator comparator_1 (.a(ADDR), .b({8{1'b0}}), .eq(comparator_1_eq));  // open: gt, lt
  Comparator comparator_2 (.a(ADDR), .b(8'h4), .eq(comparator_2_eq));  // open: gt, lt
  Comparator comparator_3 (.a(ADDR), .b(8'h8), .eq(comparator_3_eq));  // open: gt, lt
  Comparator comparator_4 (.a(ADDR), .b(8'hc), .eq(comparator_4_eq));  // open: gt, lt
  Comparator comparator_5 (.a(ADDR), .b(8'h10), .eq(comparator_5_eq));  // open: gt, lt
  Comparator comparator_6 (.a(ADDR), .b(8'h14), .eq(comparator_6_eq));  // open: gt, lt
  Comparator comparator_7 (.a(ADDR), .b(8'h1c), .eq(comparator_7_eq));  // open: gt, lt
  Comparator comparator_8 (.a(ADDR), .b(8'h20), .eq(comparator_8_eq));  // open: gt, lt
  Comparator comparator_9 (.a(ADDR), .b(8'h28), .eq(comparator_9_eq));  // open: gt, lt
  Comparator comparator_10 (.a(ADDR), .b(8'h2c), .eq(comparator_10_eq));  // open: gt, lt
  Comparator comparator_11 (.a(ADDR), .b(8'h34), .eq(comparator_11_eq));  // open: gt, lt
  Comparator comparator_12 (.a(ADDR), .b(8'h38), .eq(comparator_12_eq));  // open: gt, lt
  Comparator comparator_13 (.a(ADDR), .b(8'h1c), .eq(comparator_13_eq));  // open: gt, lt
  Comparator comparator_14 (.a(ADDR), .b(8'h20), .eq(comparator_14_eq));  // open: gt, lt
  Comparator comparator_15 (.a(ADDR), .b(8'h28), .eq(comparator_15_eq));  // open: gt, lt
  Comparator comparator_16 (.a(ADDR), .b(8'h2c), .eq(comparator_16_eq));  // open: gt, lt
  and and_1 (and_1_out, comparator_1_eq, WRITE);
  and and_2 (and_2_out, comparator_2_eq, WRITE);
  and and_3 (and_3_out, comparator_3_eq, WRITE);
  and and_4 (and_4_out, comparator_4_eq, WRITE);
  and and_5 (and_5_out, comparator_5_eq, WRITE);
  and and_6 (and_6_out, comparator_6_eq, WRITE);
  and and_7 (and_7_out, comparator_7_eq, WRITE);
  and and_8 (and_8_out, comparator_8_eq, WRITE);
  and and_9 (and_9_out, comparator_9_eq, WRITE);
  and and_10 (and_10_out, comparator_10_eq, WRITE);
  Register #(.width(32)) GPFSEL0 (.D(DATA_IN[31:0]), .en(and_1_out), .clk(CLK), .Q(GPFSEL0_q));  // open: clr
  Register #(.width(32)) GPFSEL1 (.D(DATA_IN[31:0]), .en(and_2_out), .clk(CLK), .Q(GPFSEL1_q));  // open: clr
  Register #(.width(32)) GPFSEL2 (.D(DATA_IN[31:0]), .en(and_3_out), .clk(CLK), .Q(GPFSEL2_q));  // open: clr
  Register #(.width(32)) GPFSEL3 (.D(DATA_IN[31:0]), .en(and_4_out), .clk(CLK), .Q(GPFSEL3_q));  // open: clr
  Register #(.width(32)) GPFSEL4 (.D(DATA_IN[31:0]), .en(and_5_out), .clk(CLK), .Q(GPFSEL4_q));  // open: clr
  Register #(.width(32)) GPFSEL5 (.D(DATA_IN[31:0]), .en(and_6_out), .clk(CLK), .Q(GPFSEL5_q));  // open: clr
  Register #(.trigger("high"), .width(32)) GPSET0 (
    .D(DATA_IN[31:0]), .en(and_7_out), .clk(CLK), .Q(GPSET0_q), .clr(d_ff_1_q));
  D_Flip_Flop d_ff_1 (.D(and_7_out), .clk(CLK), .Q(d_ff_1_q));  // open: Qn, preset, reset
  Register #(.trigger("high"), .width(22)) GPSET1 (
    .D(DATA_IN[21:0]), .en(and_8_out), .clk(CLK), .Q(GPSET1_q), .clr(d_ff_2_q));
  D_Flip_Flop d_ff_2 (.D(and_8_out), .clk(CLK), .Q(d_ff_2_q));  // open: Qn, preset, reset
  Register #(.trigger("high"), .width(32)) GPCLR0 (
    .D(DATA_IN[31:0]), .en(and_9_out), .clk(CLK), .Q(GPCLR0_q), .clr(d_ff_3_q));
  D_Flip_Flop d_ff_3 (.D(and_9_out), .clk(CLK), .Q(d_ff_3_q));  // open: Qn, preset, reset
  Register #(.trigger("high"), .width(22)) GPCLR1 (
    .D(DATA_IN[21:0]), .en(and_10_out), .clk(CLK), .Q(GPCLR1_q), .clr(d_ff_4_q));
  D_Flip_Flop d_ff_4 (.D(and_10_out), .clk(CLK), .Q(d_ff_4_q));  // open: Qn, preset, reset
  or or_1 (or_1_out, comparator_13_eq, comparator_14_eq, comparator_15_eq, comparator_16_eq);
  assign controlled_buffer_1_out = comparator_1_eq ? GPFSEL0_q : 32'bz;  // Controlled_Buffer controlled_buffer_1
  assign controlled_buffer_1_out = comparator_2_eq ? GPFSEL1_q : 32'bz;  // Controlled_Buffer controlled_buffer_2
  assign controlled_buffer_1_out = comparator_3_eq ? GPFSEL2_q : 32'bz;  // Controlled_Buffer controlled_buffer_3
  assign controlled_buffer_1_out = comparator_4_eq ? GPFSEL3_q : 32'bz;  // Controlled_Buffer controlled_buffer_4
  assign controlled_buffer_1_out = comparator_5_eq ? GPFSEL4_q : 32'bz;  // Controlled_Buffer controlled_buffer_5
  assign controlled_buffer_1_out = comparator_6_eq ? GPFSEL5_q : 32'bz;  // Controlled_Buffer controlled_buffer_6
  assign controlled_buffer_1_out = or_1_out ? 32'h6770696f : 32'bz;  // Controlled_Buffer controlled_buffer_7
  and and_11 (and_11_out[0], GPFSEL0_q[0], ~GPFSEL0_q[1], ~GPFSEL0_q[2]);  // AND_Gate
  and and_12 (and_11_out[1], GPFSEL0_q[3], ~GPFSEL0_q[4], ~GPFSEL0_q[5]);  // AND_Gate
  and and_13 (and_11_out[2], GPFSEL0_q[6], ~GPFSEL0_q[7], ~GPFSEL0_q[8]);  // AND_Gate
  and and_14 (and_11_out[3], GPFSEL0_q[9], ~GPFSEL0_q[10], ~GPFSEL0_q[11]);  // AND_Gate
  and and_15 (and_11_out[4], GPFSEL0_q[12], ~GPFSEL0_q[13], ~GPFSEL0_q[14]);  // AND_Gate
  and and_16 (and_11_out[5], GPFSEL0_q[15], ~GPFSEL0_q[16], ~GPFSEL0_q[17]);  // AND_Gate
  and and_17 (and_11_out[6], GPFSEL0_q[18], ~GPFSEL0_q[19], ~GPFSEL0_q[20]);  // AND_Gate
  and and_18 (and_11_out[7], GPFSEL0_q[21], ~GPFSEL0_q[22], ~GPFSEL0_q[23]);  // AND_Gate
  and and_19 (and_11_out[8], GPFSEL0_q[24], ~GPFSEL0_q[25], ~GPFSEL0_q[26]);  // AND_Gate
  and and_20 (and_11_out[9], GPFSEL0_q[27], ~GPFSEL0_q[28], ~GPFSEL0_q[29]);  // AND_Gate
  and and_21 (and_11_out[10], GPFSEL1_q[0], ~GPFSEL1_q[1], ~GPFSEL1_q[2]);  // AND_Gate
  and and_22 (and_11_out[11], GPFSEL1_q[3], ~GPFSEL1_q[4], ~GPFSEL1_q[5]);  // AND_Gate
  and and_23 (and_11_out[12], GPFSEL1_q[6], ~GPFSEL1_q[7], ~GPFSEL1_q[8]);  // AND_Gate
  and and_24 (and_11_out[13], GPFSEL1_q[9], ~GPFSEL1_q[10], ~GPFSEL1_q[11]);  // AND_Gate
  and and_25 (and_11_out[14], GPFSEL1_q[12], ~GPFSEL1_q[13], ~GPFSEL1_q[14]);  // AND_Gate
  and and_26 (and_11_out[15], GPFSEL1_q[15], ~GPFSEL1_q[16], ~GPFSEL1_q[17]);  // AND_Gate
  and and_27 (and_11_out[16], GPFSEL1_q[18], ~GPFSEL1_q[19], ~GPFSEL1_q[20]);  // AND_Gate
  and and_28 (and_11_out[17], GPFSEL1_q[21], ~GPFSEL1_q[22], ~GPFSEL1_q[23]);  // AND_Gate
  and and_29 (and_11_out[18], GPFSEL1_q[24], ~GPFSEL1_q[25], ~GPFSEL1_q[26]);  // AND_Gate
  and and_30 (and_11_out[19], GPFSEL1_q[27], ~GPFSEL1_q[28], ~GPFSEL1_q[29]);  // AND_Gate
  and and_31 (and_11_out[20], GPFSEL2_q[0], ~GPFSEL2_q[1], ~GPFSEL2_q[2]);  // AND_Gate
  and and_32 (and_11_out[21], GPFSEL2_q[3], ~GPFSEL2_q[4], ~GPFSEL2_q[5]);  // AND_Gate
  and and_33 (and_11_out[22], GPFSEL2_q[6], ~GPFSEL2_q[7], ~GPFSEL2_q[8]);  // AND_Gate
  and and_34 (and_11_out[23], GPFSEL2_q[9], ~GPFSEL2_q[10], ~GPFSEL2_q[11]);  // AND_Gate
  and and_35 (and_11_out[24], GPFSEL2_q[12], ~GPFSEL2_q[13], ~GPFSEL2_q[14]);  // AND_Gate
  and and_36 (and_11_out[25], GPFSEL2_q[15], ~GPFSEL2_q[16], ~GPFSEL2_q[17]);  // AND_Gate
  and and_37 (and_11_out[26], GPFSEL2_q[18], ~GPFSEL2_q[19], ~GPFSEL2_q[20]);  // AND_Gate
  and and_38 (and_11_out[27], GPFSEL2_q[21], ~GPFSEL2_q[22], ~GPFSEL2_q[23]);  // AND_Gate
  and and_39 (and_11_out[28], GPFSEL2_q[24], ~GPFSEL2_q[25], ~GPFSEL2_q[26]);  // AND_Gate
  and and_40 (and_11_out[29], GPFSEL2_q[27], ~GPFSEL2_q[28], ~GPFSEL2_q[29]);  // AND_Gate
  and and_41 (and_11_out[30], GPFSEL3_q[0], ~GPFSEL3_q[1], ~GPFSEL3_q[2]);  // AND_Gate
  and and_42 (and_11_out[31], GPFSEL3_q[3], ~GPFSEL3_q[4], ~GPFSEL3_q[5]);  // AND_Gate
  and and_43 (and_11_out[32], GPFSEL3_q[6], ~GPFSEL3_q[7], ~GPFSEL3_q[8]);  // AND_Gate
  and and_44 (and_11_out[33], GPFSEL3_q[9], ~GPFSEL3_q[10], ~GPFSEL3_q[11]);  // AND_Gate
  and and_45 (and_11_out[34], GPFSEL3_q[12], ~GPFSEL3_q[13], ~GPFSEL3_q[14]);  // AND_Gate
  and and_46 (and_11_out[35], GPFSEL3_q[15], ~GPFSEL3_q[16], ~GPFSEL3_q[17]);  // AND_Gate
  and and_47 (and_11_out[36], GPFSEL3_q[18], ~GPFSEL3_q[19], ~GPFSEL3_q[20]);  // AND_Gate
  and and_48 (and_11_out[37], GPFSEL3_q[21], ~GPFSEL3_q[22], ~GPFSEL3_q[23]);  // AND_Gate
  and and_49 (and_11_out[38], GPFSEL3_q[24], ~GPFSEL3_q[25], ~GPFSEL3_q[26]);  // AND_Gate
  and and_50 (and_11_out[39], GPFSEL3_q[27], ~GPFSEL3_q[28], ~GPFSEL3_q[29]);  // AND_Gate
  and and_51 (and_11_out[40], GPFSEL4_q[0], ~GPFSEL4_q[1], ~GPFSEL4_q[2]);  // AND_Gate
  and and_52 (and_11_out[41], GPFSEL4_q[3], ~GPFSEL4_q[4], ~GPFSEL4_q[5]);  // AND_Gate
  and and_53 (and_11_out[42], GPFSEL4_q[6], ~GPFSEL4_q[7], ~GPFSEL4_q[8]);  // AND_Gate
  and and_54 (and_11_out[43], GPFSEL4_q[9], ~GPFSEL4_q[10], ~GPFSEL4_q[11]);  // AND_Gate
  and and_55 (and_11_out[44], GPFSEL4_q[12], ~GPFSEL4_q[13], ~GPFSEL4_q[14]);  // AND_Gate
  and and_56 (and_11_out[45], GPFSEL4_q[15], ~GPFSEL4_q[16], ~GPFSEL4_q[17]);  // AND_Gate
  and and_57 (and_11_out[46], GPFSEL4_q[18], ~GPFSEL4_q[19], ~GPFSEL4_q[20]);  // AND_Gate
  and and_58 (and_11_out[47], GPFSEL4_q[21], ~GPFSEL4_q[22], ~GPFSEL4_q[23]);  // AND_Gate
  and and_59 (and_11_out[48], GPFSEL4_q[24], ~GPFSEL4_q[25], ~GPFSEL4_q[26]);  // AND_Gate
  and and_60 (and_11_out[49], GPFSEL4_q[27], ~GPFSEL4_q[28], ~GPFSEL4_q[29]);  // AND_Gate
  and and_61 (and_11_out[50], GPFSEL5_q[0], ~GPFSEL5_q[1], ~GPFSEL5_q[2]);  // AND_Gate
  and and_62 (and_11_out[51], GPFSEL5_q[3], ~GPFSEL5_q[4], ~GPFSEL5_q[5]);  // AND_Gate
  and and_63 (and_11_out[52], GPFSEL5_q[6], ~GPFSEL5_q[7], ~GPFSEL5_q[8]);  // AND_Gate
  and and_64 (and_11_out[53], GPFSEL5_q[9], ~GPFSEL5_q[10], ~GPFSEL5_q[11]);  // AND_Gate
  and and_65 (and_65_out[0], ~GPFSEL0_q[0], ~GPFSEL0_q[1], ~GPFSEL0_q[2]);  // AND_Gate
  and and_66 (and_65_out[1], ~GPFSEL0_q[3], ~GPFSEL0_q[4], ~GPFSEL0_q[5]);  // AND_Gate
  and and_67 (and_65_out[2], ~GPFSEL0_q[6], ~GPFSEL0_q[7], ~GPFSEL0_q[8]);  // AND_Gate
  and and_68 (and_65_out[3], ~GPFSEL0_q[9], ~GPFSEL0_q[10], ~GPFSEL0_q[11]);  // AND_Gate
  and and_69 (and_65_out[4], ~GPFSEL0_q[12], ~GPFSEL0_q[13], ~GPFSEL0_q[14]);  // AND_Gate
  and and_70 (and_65_out[5], ~GPFSEL0_q[15], ~GPFSEL0_q[16], ~GPFSEL0_q[17]);  // AND_Gate
  and and_71 (and_65_out[6], ~GPFSEL0_q[18], ~GPFSEL0_q[19], ~GPFSEL0_q[20]);  // AND_Gate
  and and_72 (and_65_out[7], ~GPFSEL0_q[21], ~GPFSEL0_q[22], ~GPFSEL0_q[23]);  // AND_Gate
  and and_73 (and_65_out[8], ~GPFSEL0_q[24], ~GPFSEL0_q[25], ~GPFSEL0_q[26]);  // AND_Gate
  and and_74 (and_65_out[9], ~GPFSEL0_q[27], ~GPFSEL0_q[28], ~GPFSEL0_q[29]);  // AND_Gate
  and and_75 (and_65_out[10], ~GPFSEL1_q[0], ~GPFSEL1_q[1], ~GPFSEL1_q[2]);  // AND_Gate
  and and_76 (and_65_out[11], ~GPFSEL1_q[3], ~GPFSEL1_q[4], ~GPFSEL1_q[5]);  // AND_Gate
  and and_77 (and_65_out[12], ~GPFSEL1_q[6], ~GPFSEL1_q[7], ~GPFSEL1_q[8]);  // AND_Gate
  and and_78 (and_65_out[13], ~GPFSEL1_q[9], ~GPFSEL1_q[10], ~GPFSEL1_q[11]);  // AND_Gate
  and and_79 (and_65_out[14], ~GPFSEL1_q[12], ~GPFSEL1_q[13], ~GPFSEL1_q[14]);  // AND_Gate
  and and_80 (and_65_out[15], ~GPFSEL1_q[15], ~GPFSEL1_q[16], ~GPFSEL1_q[17]);  // AND_Gate
  and and_81 (and_65_out[16], ~GPFSEL1_q[18], ~GPFSEL1_q[19], ~GPFSEL1_q[20]);  // AND_Gate
  and and_82 (and_65_out[17], ~GPFSEL1_q[21], ~GPFSEL1_q[22], ~GPFSEL1_q[23]);  // AND_Gate
  and and_83 (and_65_out[18], ~GPFSEL1_q[24], ~GPFSEL1_q[25], ~GPFSEL1_q[26]);  // AND_Gate
  and and_84 (and_65_out[19], ~GPFSEL1_q[27], ~GPFSEL1_q[28], ~GPFSEL1_q[29]);  // AND_Gate
  and and_85 (and_65_out[20], ~GPFSEL2_q[0], ~GPFSEL2_q[1], ~GPFSEL2_q[2]);  // AND_Gate
  and and_86 (and_65_out[21], ~GPFSEL2_q[3], ~GPFSEL2_q[4], ~GPFSEL2_q[5]);  // AND_Gate
  and and_87 (and_65_out[22], ~GPFSEL2_q[6], ~GPFSEL2_q[7], ~GPFSEL2_q[8]);  // AND_Gate
  and and_88 (and_65_out[23], ~GPFSEL2_q[9], ~GPFSEL2_q[10], ~GPFSEL2_q[11]);  // AND_Gate
  and and_89 (and_65_out[24], ~GPFSEL2_q[12], ~GPFSEL2_q[13], ~GPFSEL2_q[14]);  // AND_Gate
  and and_90 (and_65_out[25], ~GPFSEL2_q[15], ~GPFSEL2_q[16], ~GPFSEL2_q[17]);  // AND_Gate
  and and_91 (and_65_out[26], ~GPFSEL2_q[18], ~GPFSEL2_q[19], ~GPFSEL2_q[20]);  // AND_Gate
  and and_92 (and_65_out[27], ~GPFSEL2_q[21], ~GPFSEL2_q[22], ~GPFSEL2_q[23]);  // AND_Gate
  and and_93 (and_65_out[28], ~GPFSEL2_q[24], ~GPFSEL2_q[25], ~GPFSEL2_q[26]);  // AND_Gate
  and and_94 (and_65_out[29], ~GPFSEL2_q[27], ~GPFSEL2_q[28], ~GPFSEL2_q[29]);  // AND_Gate
  and and_95 (and_65_out[30], ~GPFSEL3_q[0], ~GPFSEL3_q[1], ~GPFSEL3_q[2]);  // AND_Gate
  and and_96 (and_65_out[31], ~GPFSEL3_q[3], ~GPFSEL3_q[4], ~GPFSEL3_q[5]);  // AND_Gate
  and and_97 (and_65_out[32], ~GPFSEL3_q[6], ~GPFSEL3_q[7], ~GPFSEL3_q[8]);  // AND_Gate
  and and_98 (and_65_out[33], ~GPFSEL3_q[9], ~GPFSEL3_q[10], ~GPFSEL3_q[11]);  // AND_Gate
  and and_99 (and_65_out[34], ~GPFSEL3_q[12], ~GPFSEL3_q[13], ~GPFSEL3_q[14]);  // AND_Gate
  and and_100 (and_65_out[35], ~GPFSEL3_q[15], ~GPFSEL3_q[16], ~GPFSEL3_q[17]);  // AND_Gate
  and and_101 (and_65_out[36], ~GPFSEL3_q[18], ~GPFSEL3_q[19], ~GPFSEL3_q[20]);  // AND_Gate
  and and_102 (and_65_out[37], ~GPFSEL3_q[21], ~GPFSEL3_q[22], ~GPFSEL3_q[23]);  // AND_Gate
  and and_103 (and_65_out[38], ~GPFSEL3_q[24], ~GPFSEL3_q[25], ~GPFSEL3_q[26]);  // AND_Gate
  and and_104 (and_65_out[39], ~GPFSEL3_q[27], ~GPFSEL3_q[28], ~GPFSEL3_q[29]);  // AND_Gate
  and and_105 (and_65_out[40], ~GPFSEL4_q[0], ~GPFSEL4_q[1], ~GPFSEL4_q[2]);  // AND_Gate
  and and_106 (and_65_out[41], ~GPFSEL4_q[3], ~GPFSEL4_q[4], ~GPFSEL4_q[5]);  // AND_Gate
  and and_107 (and_65_out[42], ~GPFSEL4_q[6], ~GPFSEL4_q[7], ~GPFSEL4_q[8]);  // AND_Gate
  and and_108 (and_65_out[43], ~GPFSEL4_q[9], ~GPFSEL4_q[10], ~GPFSEL4_q[11]);  // AND_Gate
  and and_109 (and_65_out[44], ~GPFSEL4_q[12], ~GPFSEL4_q[13], ~GPFSEL4_q[14]);  // AND_Gate
  and and_110 (and_65_out[45], ~GPFSEL4_q[15], ~GPFSEL4_q[16], ~GPFSEL4_q[17]);  // AND_Gate
  and and_111 (and_65_out[46], ~GPFSEL4_q[18], ~GPFSEL4_q[19], ~GPFSEL4_q[20]);  // AND_Gate
  and and_112 (and_65_out[47], ~GPFSEL4_q[21], ~GPFSEL4_q[22], ~GPFSEL4_q[23]);  // AND_Gate
  and and_113 (and_65_out[48], ~GPFSEL4_q[24], ~GPFSEL4_q[25], ~GPFSEL4_q[26]);  // AND_Gate
  and and_114 (and_65_out[49], ~GPFSEL4_q[27], ~GPFSEL4_q[28], ~GPFSEL4_q[29]);  // AND_Gate
  and and_115 (and_65_out[50], ~GPFSEL5_q[0], ~GPFSEL5_q[1], ~GPFSEL5_q[2]);  // AND_Gate
  and and_116 (and_65_out[51], ~GPFSEL5_q[3], ~GPFSEL5_q[4], ~GPFSEL5_q[5]);  // AND_Gate
  and and_117 (and_65_out[52], ~GPFSEL5_q[6], ~GPFSEL5_q[7], ~GPFSEL5_q[8]);  // AND_Gate
  and and_118 (and_65_out[53], ~GPFSEL5_q[9], ~GPFSEL5_q[10], ~GPFSEL5_q[11]);  // AND_Gate
  S_R_Flip_Flop s_r_ff_1 (.S(GPSET0_q[0]), .R(GPCLR0_q[0]), .clk(CLK), .Q(s_r_ff_1_q));  // open: reset, Qn, preset
  S_R_Flip_Flop s_r_ff_2 (.S(GPSET0_q[1]), .R(GPCLR0_q[1]), .clk(CLK), .Q(s_r_ff_2_q));  // open: reset, Qn, preset
  S_R_Flip_Flop s_r_ff_3 (.S(GPSET0_q[2]), .R(GPCLR0_q[2]), .clk(CLK), .Q(s_r_ff_3_q));  // open: reset, Qn, preset
  S_R_Flip_Flop s_r_ff_4 (.S(GPSET0_q[3]), .R(GPCLR0_q[3]), .clk(CLK), .Q(s_r_ff_4_q));  // open: reset, Qn, preset
  S_R_Flip_Flop s_r_ff_5 (.S(GPSET0_q[4]), .R(GPCLR0_q[4]), .clk(CLK), .Q(s_r_ff_5_q));  // open: reset, Qn, preset
  S_R_Flip_Flop s_r_ff_6 (.S(GPSET0_q[5]), .R(GPCLR0_q[5]), .clk(CLK), .Q(s_r_ff_6_q));  // open: reset, Qn, preset
  S_R_Flip_Flop s_r_ff_7 (.S(GPSET0_q[6]), .R(GPCLR0_q[6]), .clk(CLK), .Q(s_r_ff_7_q));  // open: reset, Qn, preset
  S_R_Flip_Flop s_r_ff_8 (.S(GPSET0_q[7]), .R(GPCLR0_q[7]), .clk(CLK), .Q(s_r_ff_8_q));  // open: reset, Qn, preset
  S_R_Flip_Flop s_r_ff_9 (.S(GPSET0_q[8]), .R(GPCLR0_q[8]), .clk(CLK), .Q(s_r_ff_9_q));  // open: reset, Qn, preset
  S_R_Flip_Flop s_r_ff_10 (.S(GPSET0_q[9]), .R(GPCLR0_q[9]), .clk(CLK), .Q(s_r_ff_10_q));  // open: reset, Qn, preset
  S_R_Flip_Flop s_r_ff_11 (.S(GPSET0_q[10]), .R(GPCLR0_q[10]), .clk(CLK), .Q(s_r_ff_11_q));  // open: reset, Qn, preset
  S_R_Flip_Flop s_r_ff_12 (.S(GPSET0_q[11]), .R(GPCLR0_q[11]), .clk(CLK), .Q(s_r_ff_12_q));  // open: reset, Qn, preset
  S_R_Flip_Flop s_r_ff_13 (.S(GPSET0_q[12]), .R(GPCLR0_q[12]), .clk(CLK), .Q(s_r_ff_13_q));  // open: reset, Qn, preset
  S_R_Flip_Flop s_r_ff_14 (.S(GPSET0_q[13]), .R(GPCLR0_q[13]), .clk(CLK), .Q(s_r_ff_14_q));  // open: reset, Qn, preset
  S_R_Flip_Flop s_r_ff_15 (.S(GPSET0_q[14]), .R(GPCLR0_q[14]), .clk(CLK), .Q(s_r_ff_15_q));  // open: reset, Qn, preset
  S_R_Flip_Flop s_r_ff_16 (.S(GPSET0_q[15]), .R(GPCLR0_q[15]), .clk(CLK), .Q(s_r_ff_16_q));  // open: reset, Qn, preset
  S_R_Flip_Flop s_r_ff_17 (.S(GPSET0_q[16]), .R(GPCLR0_q[16]), .clk(CLK), .Q(s_r_ff_17_q));  // open: reset, Qn, preset
  S_R_Flip_Flop s_r_ff_18 (.S(GPSET0_q[17]), .R(GPCLR0_q[17]), .clk(CLK), .Q(s_r_ff_18_q));  // open: reset, Qn, preset
  S_R_Flip_Flop s_r_ff_19 (.S(GPSET0_q[18]), .R(GPCLR0_q[18]), .clk(CLK), .Q(s_r_ff_19_q));  // open: reset, Qn, preset
  S_R_Flip_Flop s_r_ff_20 (.S(GPSET0_q[19]), .R(GPCLR0_q[19]), .clk(CLK), .Q(s_r_ff_20_q));  // open: reset, Qn, preset
  S_R_Flip_Flop s_r_ff_21 (.S(GPSET0_q[20]), .R(GPCLR0_q[20]), .clk(CLK), .Q(s_r_ff_21_q));  // open: reset, Qn, preset
  S_R_Flip_Flop s_r_ff_22 (.S(GPSET0_q[21]), .R(GPCLR0_q[21]), .clk(CLK), .Q(s_r_ff_22_q));  // open: reset, Qn, preset
  S_R_Flip_Flop s_r_ff_23 (.S(GPSET0_q[22]), .R(GPCLR0_q[22]), .clk(CLK), .Q(s_r_ff_23_q));  // open: reset, Qn, preset
  S_R_Flip_Flop s_r_ff_24 (.S(GPSET0_q[23]), .R(GPCLR0_q[23]), .clk(CLK), .Q(s_r_ff_24_q));  // open: reset, Qn, preset
  S_R_Flip_Flop s_r_ff_25 (.S(GPSET0_q[24]), .R(GPCLR0_q[24]), .clk(CLK), .Q(s_r_ff_25_q));  // open: reset, Qn, preset
  S_R_Flip_Flop s_r_ff_26 (.S(GPSET0_q[25]), .R(GPCLR0_q[25]), .clk(CLK), .Q(s_r_ff_26_q));  // open: reset, Qn, preset
  S_R_Flip_Flop s_r_ff_27 (.S(GPSET0_q[26]), .R(GPCLR0_q[26]), .clk(CLK), .Q(s_r_ff_27_q));  // open: reset, Qn, preset
  S_R_Flip_Flop s_r_ff_28 (.S(GPSET0_q[27]), .R(GPCLR0_q[27]), .clk(CLK), .Q(s_r_ff_28_q));  // open: reset, Qn, preset
  S_R_Flip_Flop s_r_ff_29 (.S(GPSET0_q[28]), .R(GPCLR0_q[28]), .clk(CLK), .Q(s_r_ff_29_q));  // open: reset, Qn, preset
  S_R_Flip_Flop s_r_ff_30 (.S(GPSET0_q[29]), .R(GPCLR0_q[29]), .clk(CLK), .Q(s_r_ff_30_q));  // open: reset, Qn, preset
  S_R_Flip_Flop s_r_ff_31 (.S(GPSET0_q[30]), .R(GPCLR0_q[30]), .clk(CLK), .Q(s_r_ff_31_q));  // open: reset, Qn, preset
  S_R_Flip_Flop s_r_ff_32 (.S(GPSET0_q[31]), .R(GPCLR0_q[31]), .clk(CLK), .Q(s_r_ff_32_q));  // open: reset, Qn, preset
  S_R_Flip_Flop s_r_ff_33 (.S(GPSET1_q[0]), .R(GPCLR1_q[0]), .clk(CLK), .Q(s_r_ff_33_q));  // open: reset, Qn, preset
  S_R_Flip_Flop s_r_ff_34 (.S(GPSET1_q[1]), .R(GPCLR1_q[1]), .clk(CLK), .Q(s_r_ff_34_q));  // open: reset, Qn, preset
  S_R_Flip_Flop s_r_ff_35 (.S(GPSET1_q[2]), .R(GPCLR1_q[2]), .clk(CLK), .Q(s_r_ff_35_q));  // open: reset, Qn, preset
  S_R_Flip_Flop s_r_ff_36 (.S(GPSET1_q[3]), .R(GPCLR1_q[3]), .clk(CLK), .Q(s_r_ff_36_q));  // open: reset, Qn, preset
  S_R_Flip_Flop s_r_ff_37 (.S(GPSET1_q[4]), .R(GPCLR1_q[4]), .clk(CLK), .Q(s_r_ff_37_q));  // open: reset, Qn, preset
  S_R_Flip_Flop s_r_ff_38 (.S(GPSET1_q[5]), .R(GPCLR1_q[5]), .clk(CLK), .Q(s_r_ff_38_q));  // open: reset, Qn, preset
  S_R_Flip_Flop s_r_ff_39 (.S(GPSET1_q[6]), .R(GPCLR1_q[6]), .clk(CLK), .Q(s_r_ff_39_q));  // open: reset, Qn, preset
  S_R_Flip_Flop s_r_ff_40 (.S(GPSET1_q[7]), .R(GPCLR1_q[7]), .clk(CLK), .Q(s_r_ff_40_q));  // open: reset, Qn, preset
  S_R_Flip_Flop s_r_ff_41 (.S(GPSET1_q[8]), .R(GPCLR1_q[8]), .clk(CLK), .Q(s_r_ff_41_q));  // open: reset, Qn, preset
  S_R_Flip_Flop s_r_ff_42 (.S(GPSET1_q[9]), .R(GPCLR1_q[9]), .clk(CLK), .Q(s_r_ff_42_q));  // open: reset, Qn, preset
  S_R_Flip_Flop s_r_ff_43 (.S(GPSET1_q[10]), .R(GPCLR1_q[10]), .clk(CLK), .Q(s_r_ff_43_q));  // open: reset, Qn, preset
  S_R_Flip_Flop s_r_ff_44 (.S(GPSET1_q[11]), .R(GPCLR1_q[11]), .clk(CLK), .Q(s_r_ff_44_q));  // open: reset, Qn, preset
  S_R_Flip_Flop s_r_ff_45 (.S(GPSET1_q[12]), .R(GPCLR1_q[12]), .clk(CLK), .Q(s_r_ff_45_q));  // open: reset, Qn, preset
  S_R_Flip_Flop s_r_ff_46 (.S(GPSET1_q[13]), .R(GPCLR1_q[13]), .clk(CLK), .Q(s_r_ff_46_q));  // open: reset, Qn, preset
  S_R_Flip_Flop s_r_ff_47 (.S(GPSET1_q[14]), .R(GPCLR1_q[14]), .clk(CLK), .Q(s_r_ff_47_q));  // open: reset, Qn, preset
  S_R_Flip_Flop s_r_ff_48 (.S(GPSET1_q[15]), .R(GPCLR1_q[15]), .clk(CLK), .Q(s_r_ff_48_q));  // open: reset, Qn, preset
  S_R_Flip_Flop s_r_ff_49 (.S(GPSET1_q[16]), .R(GPCLR1_q[16]), .clk(CLK), .Q(s_r_ff_49_q));  // open: reset, Qn, preset
  S_R_Flip_Flop s_r_ff_50 (.S(GPSET1_q[17]), .R(GPCLR1_q[17]), .clk(CLK), .Q(s_r_ff_50_q));  // open: reset, Qn, preset
  S_R_Flip_Flop s_r_ff_51 (.S(GPSET1_q[18]), .R(GPCLR1_q[18]), .clk(CLK), .Q(s_r_ff_51_q));  // open: reset, Qn, preset
  S_R_Flip_Flop s_r_ff_52 (.S(GPSET1_q[19]), .R(GPCLR1_q[19]), .clk(CLK), .Q(s_r_ff_52_q));  // open: reset, Qn, preset
  S_R_Flip_Flop s_r_ff_53 (.S(GPSET1_q[20]), .R(GPCLR1_q[20]), .clk(CLK), .Q(s_r_ff_53_q));  // open: reset, Qn, preset
  S_R_Flip_Flop s_r_ff_54 (.S(GPSET1_q[21]), .R(GPCLR1_q[21]), .clk(CLK), .Q(s_r_ff_54_q));  // open: reset, Qn, preset
  assign GPIO_OUT[0] = and_11_out[0] ? s_r_ff_1_q : 1'bz;  // Controlled_Buffer controlled_buffer_8
  assign GPIO_OUT[1] = and_11_out[1] ? s_r_ff_2_q : 1'bz;  // Controlled_Buffer controlled_buffer_9
  assign GPIO_OUT[2] = and_11_out[2] ? s_r_ff_3_q : 1'bz;  // Controlled_Buffer controlled_buffer_10
  assign GPIO_OUT[3] = and_11_out[3] ? s_r_ff_4_q : 1'bz;  // Controlled_Buffer controlled_buffer_11
  assign GPIO_OUT[4] = and_11_out[4] ? s_r_ff_5_q : 1'bz;  // Controlled_Buffer controlled_buffer_12
  assign GPIO_OUT[5] = and_11_out[5] ? s_r_ff_6_q : 1'bz;  // Controlled_Buffer controlled_buffer_13
  assign GPIO_OUT[6] = and_11_out[6] ? s_r_ff_7_q : 1'bz;  // Controlled_Buffer controlled_buffer_14
  assign GPIO_OUT[7] = and_11_out[7] ? s_r_ff_8_q : 1'bz;  // Controlled_Buffer controlled_buffer_15
  assign GPIO_OUT[8] = and_11_out[8] ? s_r_ff_9_q : 1'bz;  // Controlled_Buffer controlled_buffer_16
  assign GPIO_OUT[9] = and_11_out[9] ? s_r_ff_10_q : 1'bz;  // Controlled_Buffer controlled_buffer_17
  assign GPIO_OUT[10] = and_11_out[10] ? s_r_ff_11_q : 1'bz;  // Controlled_Buffer controlled_buffer_18
  assign GPIO_OUT[11] = and_11_out[11] ? s_r_ff_12_q : 1'bz;  // Controlled_Buffer controlled_buffer_19
  assign GPIO_OUT[12] = and_11_out[12] ? s_r_ff_13_q : 1'bz;  // Controlled_Buffer controlled_buffer_20
  assign GPIO_OUT[13] = and_11_out[13] ? s_r_ff_14_q : 1'bz;  // Controlled_Buffer controlled_buffer_21
  assign GPIO_OUT[14] = and_11_out[14] ? s_r_ff_15_q : 1'bz;  // Controlled_Buffer controlled_buffer_22
  assign GPIO_OUT[15] = and_11_out[15] ? s_r_ff_16_q : 1'bz;  // Controlled_Buffer controlled_buffer_23
  assign GPIO_OUT[16] = and_11_out[16] ? s_r_ff_17_q : 1'bz;  // Controlled_Buffer controlled_buffer_24
  assign GPIO_OUT[17] = and_11_out[17] ? s_r_ff_18_q : 1'bz;  // Controlled_Buffer controlled_buffer_25
  assign GPIO_OUT[18] = and_11_out[18] ? s_r_ff_19_q : 1'bz;  // Controlled_Buffer controlled_buffer_26
  assign GPIO_OUT[19] = and_11_out[19] ? s_r_ff_20_q : 1'bz;  // Controlled_Buffer controlled_buffer_27
  assign GPIO_OUT[20] = and_11_out[20] ? s_r_ff_21_q : 1'bz;  // Controlled_Buffer controlled_buffer_28
  assign GPIO_OUT[21] = and_11_out[21] ? s_r_ff_22_q : 1'bz;  // Controlled_Buffer controlled_buffer_29
  assign GPIO_OUT[22] = and_11_out[22] ? s_r_ff_23_q : 1'bz;  // Controlled_Buffer controlled_buffer_30
  assign GPIO_OUT[23] = and_11_out[23] ? s_r_ff_24_q : 1'bz;  // Controlled_Buffer controlled_buffer_31
  assign GPIO_OUT[24] = and_11_out[24] ? s_r_ff_25_q : 1'bz;  // Controlled_Buffer controlled_buffer_32
  assign GPIO_OUT[25] = and_11_out[25] ? s_r_ff_26_q : 1'bz;  // Controlled_Buffer controlled_buffer_33
  assign GPIO_OUT[26] = and_11_out[26] ? s_r_ff_27_q : 1'bz;  // Controlled_Buffer controlled_buffer_34
  assign GPIO_OUT[27] = and_11_out[27] ? s_r_ff_28_q : 1'bz;  // Controlled_Buffer controlled_buffer_35
  assign GPIO_OUT[28] = and_11_out[28] ? s_r_ff_29_q : 1'bz;  // Controlled_Buffer controlled_buffer_36
  assign GPIO_OUT[29] = and_11_out[29] ? s_r_ff_30_q : 1'bz;  // Controlled_Buffer controlled_buffer_37
  assign GPIO_OUT[30] = and_11_out[30] ? s_r_ff_31_q : 1'bz;  // Controlled_Buffer controlled_buffer_38
  assign GPIO_OUT[31] = and_11_out[31] ? s_r_ff_32_q : 1'bz;  // Controlled_Buffer controlled_buffer_39
  assign GPIO_OUT[32] = and_11_out[32] ? s_r_ff_33_q : 1'bz;  // Controlled_Buffer controlled_buffer_40
  assign GPIO_OUT[33] = and_11_out[33] ? s_r_ff_34_q : 1'bz;  // Controlled_Buffer controlled_buffer_41
  assign GPIO_OUT[34] = and_11_out[34] ? s_r_ff_35_q : 1'bz;  // Controlled_Buffer controlled_buffer_42
  assign GPIO_OUT[35] = and_11_out[35] ? s_r_ff_36_q : 1'bz;  // Controlled_Buffer controlled_buffer_43
  assign GPIO_OUT[36] = and_11_out[36] ? s_r_ff_37_q : 1'bz;  // Controlled_Buffer controlled_buffer_44
  assign GPIO_OUT[37] = and_11_out[37] ? s_r_ff_38_q : 1'bz;  // Controlled_Buffer controlled_buffer_45
  assign GPIO_OUT[38] = and_11_out[38] ? s_r_ff_39_q : 1'bz;  // Controlled_Buffer controlled_buffer_46
  assign GPIO_OUT[39] = and_11_out[39] ? s_r_ff_40_q : 1'bz;  // Controlled_Buffer controlled_buffer_47
  assign GPIO_OUT[40] = and_11_out[40] ? s_r_ff_41_q : 1'bz;  // Controlled_Buffer controlled_buffer_48
  assign GPIO_OUT[41] = and_11_out[41] ? s_r_ff_42_q : 1'bz;  // Controlled_Buffer controlled_buffer_49
  assign GPIO_OUT[42] = and_11_out[42] ? s_r_ff_43_q : 1'bz;  // Controlled_Buffer controlled_buffer_50
  assign GPIO_OUT[43] = and_11_out[43] ? s_r_ff_44_q : 1'bz;  // Controlled_Buffer controlled_buffer_51
  assign GPIO_OUT[44] = and_11_out[44] ? s_r_ff_45_q : 1'bz;  // Controlled_Buffer controlled_buffer_52
  assign GPIO_OUT[45] = and_11_out[45] ? s_r_ff_46_q : 1'bz;  // Controlled_Buffer controlled_buffer_53
  assign GPIO_OUT[46] = and_11_out[46] ? s_r_ff_47_q : 1'bz;  // Controlled_Buffer controlled_buffer_54
  assign GPIO_OUT[47] = and_11_out[47] ? s_r_ff_48_q : 1'bz;  // Controlled_Buffer controlled_buffer_55
  assign GPIO_OUT[48] = and_11_out[48] ? s_r_ff_49_q : 1'bz;  // Controlled_Buffer controlled_buffer_56
  assign GPIO_OUT[49] = and_11_out[49] ? s_r_ff_50_q : 1'bz;  // Controlled_Buffer controlled_buffer_57
  assign GPIO_OUT[50] = and_11_out[50] ? s_r_ff_51_q : 1'bz;  // Controlled_Buffer controlled_buffer_58
  assign GPIO_OUT[51] = and_11_out[51] ? s_r_ff_52_q : 1'bz;  // Controlled_Buffer controlled_buffer_59
  assign GPIO_OUT[52] = and_11_out[52] ? s_r_ff_53_q : 1'bz;  // Controlled_Buffer controlled_buffer_60
  assign GPIO_OUT[53] = and_11_out[53] ? s_r_ff_54_q : 1'bz;  // Controlled_Buffer controlled_buffer_61
  Register #(.width(1)) register_1 (.D(GPIO_IN[0]), .en(and_65_out[0]), .clk(CLK), .Q(register_1_q[0]));  // open: clr
  Register #(.width(1)) register_2 (.D(GPIO_IN[1]), .en(and_65_out[1]), .clk(CLK), .Q(register_1_q[1]));  // open: clr
  Register #(.width(1)) register_3 (.D(GPIO_IN[2]), .en(and_65_out[2]), .clk(CLK), .Q(register_1_q[2]));  // open: clr
  Register #(.width(1)) register_4 (.D(GPIO_IN[3]), .en(and_65_out[3]), .clk(CLK), .Q(register_1_q[3]));  // open: clr
  Register #(.width(1)) register_5 (.D(GPIO_IN[4]), .en(and_65_out[4]), .clk(CLK), .Q(register_1_q[4]));  // open: clr
  Register #(.width(1)) register_6 (.D(GPIO_IN[5]), .en(and_65_out[5]), .clk(CLK), .Q(register_1_q[5]));  // open: clr
  Register #(.width(1)) register_7 (.D(GPIO_IN[6]), .en(and_65_out[6]), .clk(CLK), .Q(register_1_q[6]));  // open: clr
  Register #(.width(1)) register_8 (.D(GPIO_IN[7]), .en(and_65_out[7]), .clk(CLK), .Q(register_1_q[7]));  // open: clr
  Register #(.width(1)) register_9 (.D(GPIO_IN[8]), .en(and_65_out[8]), .clk(CLK), .Q(register_1_q[8]));  // open: clr
  Register #(.width(1)) register_10 (.D(GPIO_IN[9]), .en(and_65_out[9]), .clk(CLK), .Q(register_1_q[9]));  // open: clr
  Register #(.width(1)) register_11 (
    .D(GPIO_IN[10]), .en(and_65_out[10]), .clk(CLK), .Q(register_1_q[10]));  // open: clr
  Register #(.width(1)) register_12 (
    .D(GPIO_IN[11]), .en(and_65_out[11]), .clk(CLK), .Q(register_1_q[11]));  // open: clr
  Register #(.width(1)) register_13 (
    .D(GPIO_IN[12]), .en(and_65_out[12]), .clk(CLK), .Q(register_1_q[12]));  // open: clr
  Register #(.width(1)) register_14 (
    .D(GPIO_IN[13]), .en(and_65_out[13]), .clk(CLK), .Q(register_1_q[13]));  // open: clr
  Register #(.width(1)) register_15 (
    .D(GPIO_IN[14]), .en(and_65_out[14]), .clk(CLK), .Q(register_1_q[14]));  // open: clr
  Register #(.width(1)) register_16 (
    .D(GPIO_IN[15]), .en(and_65_out[15]), .clk(CLK), .Q(register_1_q[15]));  // open: clr
  Register #(.width(1)) register_17 (
    .D(GPIO_IN[16]), .en(and_65_out[16]), .clk(CLK), .Q(register_1_q[16]));  // open: clr
  Register #(.width(1)) register_18 (
    .D(GPIO_IN[17]), .en(and_65_out[17]), .clk(CLK), .Q(register_1_q[17]));  // open: clr
  Register #(.width(1)) register_19 (
    .D(GPIO_IN[18]), .en(and_65_out[18]), .clk(CLK), .Q(register_1_q[18]));  // open: clr
  Register #(.width(1)) register_20 (
    .D(GPIO_IN[19]), .en(and_65_out[19]), .clk(CLK), .Q(register_1_q[19]));  // open: clr
  Register #(.width(1)) register_21 (
    .D(GPIO_IN[20]), .en(and_65_out[20]), .clk(CLK), .Q(register_1_q[20]));  // open: clr
  Register #(.width(1)) register_22 (
    .D(GPIO_IN[21]), .en(and_65_out[21]), .clk(CLK), .Q(register_1_q[21]));  // open: clr
  Register #(.width(1)) register_23 (
    .D(GPIO_IN[22]), .en(and_65_out[22]), .clk(CLK), .Q(register_1_q[22]));  // open: clr
  Register #(.width(1)) register_24 (
    .D(GPIO_IN[23]), .en(and_65_out[23]), .clk(CLK), .Q(register_1_q[23]));  // open: clr
  Register #(.width(1)) register_25 (
    .D(GPIO_IN[24]), .en(and_65_out[24]), .clk(CLK), .Q(register_1_q[24]));  // open: clr
  Register #(.width(1)) register_26 (
    .D(GPIO_IN[25]), .en(and_65_out[25]), .clk(CLK), .Q(register_1_q[25]));  // open: clr
  Register #(.width(1)) register_27 (
    .D(GPIO_IN[26]), .en(and_65_out[26]), .clk(CLK), .Q(register_1_q[26]));  // open: clr
  Register #(.width(1)) register_28 (
    .D(GPIO_IN[27]), .en(and_65_out[27]), .clk(CLK), .Q(register_1_q[27]));  // open: clr
  Register #(.width(1)) register_29 (
    .D(GPIO_IN[28]), .en(and_65_out[28]), .clk(CLK), .Q(register_1_q[28]));  // open: clr
  Register #(.width(1)) register_30 (
    .D(GPIO_IN[29]), .en(and_65_out[29]), .clk(CLK), .Q(register_1_q[29]));  // open: clr
  Register #(.width(1)) register_31 (
    .D(GPIO_IN[30]), .en(and_65_out[30]), .clk(CLK), .Q(register_1_q[30]));  // open: clr
  Register #(.width(1)) register_32 (
    .D(GPIO_IN[31]), .en(and_65_out[31]), .clk(CLK), .Q(register_1_q[31]));  // open: clr
  Register #(.width(1)) register_33 (
    .D(GPIO_IN[32]), .en(and_65_out[32]), .clk(CLK), .Q(register_33_q[0]));  // open: clr
  Register #(.width(1)) register_34 (
    .D(GPIO_IN[33]), .en(and_65_out[33]), .clk(CLK), .Q(register_33_q[1]));  // open: clr
  Register #(.width(1)) register_35 (
    .D(GPIO_IN[34]), .en(and_65_out[34]), .clk(CLK), .Q(register_33_q[2]));  // open: clr
  Register #(.width(1)) register_36 (
    .D(GPIO_IN[35]), .en(and_65_out[35]), .clk(CLK), .Q(register_33_q[3]));  // open: clr
  Register #(.width(1)) register_37 (
    .D(GPIO_IN[36]), .en(and_65_out[36]), .clk(CLK), .Q(register_33_q[4]));  // open: clr
  Register #(.width(1)) register_38 (
    .D(GPIO_IN[37]), .en(and_65_out[37]), .clk(CLK), .Q(register_33_q[5]));  // open: clr
  Register #(.width(1)) register_39 (
    .D(GPIO_IN[38]), .en(and_65_out[38]), .clk(CLK), .Q(register_33_q[6]));  // open: clr
  Register #(.width(1)) register_40 (
    .D(GPIO_IN[39]), .en(and_65_out[39]), .clk(CLK), .Q(register_33_q[7]));  // open: clr
  Register #(.width(1)) register_41 (
    .D(GPIO_IN[40]), .en(and_65_out[40]), .clk(CLK), .Q(register_33_q[8]));  // open: clr
  Register #(.width(1)) register_42 (
    .D(GPIO_IN[41]), .en(and_65_out[41]), .clk(CLK), .Q(register_33_q[9]));  // open: clr
  Register #(.width(1)) register_43 (
    .D(GPIO_IN[42]), .en(and_65_out[42]), .clk(CLK), .Q(register_33_q[10]));  // open: clr
  Register #(.width(1)) register_44 (
    .D(GPIO_IN[43]), .en(and_65_out[43]), .clk(CLK), .Q(register_33_q[11]));  // open: clr
  Register #(.width(1)) register_45 (
    .D(GPIO_IN[44]), .en(and_65_out[44]), .clk(CLK), .Q(register_33_q[12]));  // open: clr
  Register #(.width(1)) register_46 (
    .D(GPIO_IN[45]), .en(and_65_out[45]), .clk(CLK), .Q(register_33_q[13]));  // open: clr
  Register #(.width(1)) register_47 (
    .D(GPIO_IN[46]), .en(and_65_out[46]), .clk(CLK), .Q(register_33_q[14]));  // open: clr
  Register #(.width(1)) register_48 (
    .D(GPIO_IN[47]), .en(and_65_out[47]), .clk(CLK), .Q(register_33_q[15]));  // open: clr
  Register #(.width(1)) register_49 (
    .D(GPIO_IN[48]), .en(and_65_out[48]), .clk(CLK), .Q(register_33_q[16]));  // open: clr
  Register #(.width(1)) register_50 (
    .D(GPIO_IN[49]), .en(and_65_out[49]), .clk(CLK), .Q(register_33_q[17]));  // open: clr
  Register #(.width(1)) register_51 (
    .D(GPIO_IN[50]), .en(and_65_out[50]), .clk(CLK), .Q(register_33_q[18]));  // open: clr
  Register #(.width(1)) register_52 (
    .D(GPIO_IN[51]), .en(and_65_out[51]), .clk(CLK), .Q(register_33_q[19]));  // open: clr
  Register #(.width(1)) register_53 (
    .D(GPIO_IN[52]), .en(and_65_out[52]), .clk(CLK), .Q(register_33_q[20]));  // open: clr
  Register #(.width(1)) register_54 (
    .D(GPIO_IN[53]), .en(and_65_out[53]), .clk(CLK), .Q(register_33_q[21]));  // open: clr
  assign controlled_buffer_1_out = comparator_11_eq ? register_1_q : 32'bz;  // Controlled_Buffer controlled_buffer_62
  assign controlled_buffer_1_out = comparator_12_eq ? {{10{1'b0}}, register_33_q} : 32'bz;  // Controlled_Buffer controlled_buffer_63
  assign DATA_OUT = {{32{1'b0}}, controlled_buffer_1_out};  // Bit_Extender bit_extender_1
endmodule

module InsAddrAlignment (
  input  [63:0] ADDR,
  output ALIGNED,
  output NOT_ALIGNED
);

  Comparator #(.mode("unsigned"), .width(2)) comparator_1 (.a(2'b00), .b(ADDR[1:0]), .eq(ALIGNED));  // open: gt, lt
  not not_1 (NOT_ALIGNED, ALIGNED);
endmodule

module InsAddrRange (
  input  [63:0] ADDR,
  output IN_RANGE,
  output OUT_OF_RANGE
);

  Comparator #(.mode("unsigned"), .width(40)) comparator_1 (
    .a({40{1'b0}}), .b(ADDR[63:24]), .eq(IN_RANGE));  // open: gt, lt
  not not_1 (OUT_OF_RANGE, IN_RANGE);
endmodule

module ControlUnit (
  input  [31:0] INS,
  input  [3:0] FLAGS,
  output insB,
  output insBL,
  output insBR,
  output insCBZ,
  output insCBNZ,
  output insBCOND,
  output insSTUR,
  output insLDUR,
  output insAND,
  output insORR,
  output insEOR,
  output insADD,
  output insSUB,
  output insANDI,
  output insORRI,
  output insEORI,
  output insADDI,
  output insSUBI,
  output insANDS,
  output insADDS,
  output insSUBS,
  output insANDIS,
  output insADDIS,
  output insSUBIS,
  output insLSL,
  output insLSR,
  output insMOVK,
  output insMOVZ,
  output insMOVN,
  output insLSLV,
  output insLSRV,
  output insMUL,
  output insUMULH,
  output insSMULH,
  output insUDIV,
  output insSDIV,
  output insNOT_IMPLEMENTED,
  output [1:0] AccessSize,
  output RdSP,
  output RnSP,
  output [5:0] Shamt,
  output B,
  output BL,
  output BR,
  output CBZ,
  output CBNZ,
  output MOVK,
  output MOVZ,
  output MOVN,
  output BCOND_TRUE,
  output Reg2Loc,
  output RegWrite,
  output MemRead,
  output MemWrite,
  output ALUSrc,
  output MemtoReg,
  output [2:0] ImmSel,
  output [3:0] ALUop,
  output SetFlags
);

  wire and_1_out, and_2_out, decoder_1_out0, decoder_1_out1, decoder_1_out2, decoder_1_out3, decoder_1_out4,
       decoder_1_out5, decoder_1_out6, decoder_1_out7, decoder_1_out8, decoder_1_out9, decoder_1_out10,
       decoder_1_out11, decoder_1_out12, decoder_1_out13, decoder_1_out14, gADDop_out, gALUimm_out,
       gANDop_out, gBRAddr_out, gCONDBRAddr_out, gDTAddr_out, gEORop_out, gEQ_out, gGE_out, gGT_out, gHI_out,
       gHS_out, gLE_out, gLO_out, gLogicalImm_out, gLS_out, gLT_out, gMI_out, gMOVImm_out, gNE_out,
       gORop_out, gPASSBop_out, gPL_out, gSUBop_out, gVC_out, gVS_out, or_1_out, or_2_out, or_3_out,
       or_4_out, or_5_out, or_6_out, xnor_1_out, xnor_2_out, xor_1_out, xor_2_out;
  wire [5:0] subtractor_1_out;

  Subtractor #(.width(6)) subtractor_1 (
    .a({6{1'b1}}), .b(INS[15:10]), .out(subtractor_1_out), .bin(1'b0));  // open: bout
  Decoder #(.select(4)) decoder_1 (
    .out0(decoder_1_out0), .out1(decoder_1_out1), .out2(decoder_1_out2), .out3(decoder_1_out3),
    .out4(decoder_1_out4), .out5(decoder_1_out5), .out6(decoder_1_out6), .out7(decoder_1_out7),
    .out8(decoder_1_out8), .out9(decoder_1_out9), .out10(decoder_1_out10), .out11(decoder_1_out11),
    .out12(decoder_1_out12), .out13(decoder_1_out13), .out14(decoder_1_out14), .sel(INS[3:0]), .en(insBCOND));  // open: out15
  and gB (B, ~INS[31], ~INS[30], ~INS[29], INS[28], ~INS[27], INS[26]);  // AND_Gate
  and gBL (BL, INS[31], ~INS[30], ~INS[29], INS[28], ~INS[27], INS[26]);  // AND_Gate
  and gBR (BR, INS[31], INS[30], ~INS[29], INS[28], ~INS[27], INS[26], INS[25], ~INS[24], ~INS[23], ~INS[22], ~INS[21]);  // AND_Gate
  and gCBZ (CBZ, INS[31], ~INS[30], INS[29], INS[28], ~INS[27], INS[26], ~INS[25], ~INS[24]);  // AND_Gate
  and gCBNZ (CBNZ, INS[31], ~INS[30], INS[29], INS[28], ~INS[27], INS[26], ~INS[25], INS[24]);  // AND_Gate
  and gBCOND (insBCOND, ~INS[31], INS[30], ~INS[29], INS[28], ~INS[27], INS[26], ~INS[25], ~INS[24]);  // AND_Gate
  and gSTUR (insSTUR, INS[29], INS[28], INS[27], ~INS[26], ~INS[25], ~INS[24], ~INS[23], ~INS[22], ~INS[21]);  // AND_Gate
  and gLDUR (insLDUR, INS[29], INS[28], INS[27], ~INS[26], ~INS[25], ~INS[24], ~INS[23], INS[22], ~INS[21]);  // AND_Gate
  and gAND (insAND, INS[31], ~INS[30], ~INS[29], ~INS[28], INS[27], ~INS[26], INS[25], ~INS[24], ~INS[23], ~INS[22], ~INS[21]);  // AND_Gate
  and gORR (insORR, INS[31], ~INS[30], INS[29], ~INS[28], INS[27], ~INS[26], INS[25], ~INS[24], ~INS[23], ~INS[22], ~INS[21]);  // AND_Gate
  and gEOR (insEOR, INS[31], INS[30], ~INS[29], ~INS[28], INS[27], ~INS[26], INS[25], ~INS[24], ~INS[23], ~INS[22], ~INS[21]);  // AND_Gate
  and gADD (insADD, INS[31], ~INS[30], ~INS[29], ~INS[28], INS[27], ~INS[26], INS[25], INS[24], ~INS[23], ~INS[22]);  // AND_Gate
  and gSUB (insSUB, INS[31], INS[30], ~INS[29], ~INS[28], INS[27], ~INS[26], INS[25], INS[24], ~INS[23], ~INS[22]);  // AND_Gate
  and gANDI (insANDI, INS[31], ~INS[30], ~INS[29], INS[28], ~INS[27], ~INS[26], INS[25], ~INS[24], ~INS[23]);  // AND_Gate
  and gORRI (insORRI, INS[31], ~INS[30], INS[29], INS[28], ~INS[27], ~INS[26], INS[25], ~INS[24], ~INS[23]);  // AND_Gate
  and gEORI (insEORI, INS[31], INS[30], ~INS[29], INS[28], ~INS[27], ~INS[26], INS[25], ~INS[24], ~INS[23]);  // AND_Gate
  and gADDI (insADDI, INS[31], ~INS[30], ~INS[29], INS[28], ~INS[27], ~INS[26], ~INS[25], INS[24], ~INS[23], ~INS[22]);  // AND_Gate
  and gSUBI (insSUBI, INS[31], INS[30], ~INS[29], INS[28], ~INS[27], ~INS[26], ~INS[25], INS[24], ~INS[23], ~INS[22]);  // AND_Gate
  and gANDS (insANDS, INS[31], INS[30], INS[29], ~INS[28], INS[27], ~INS[26], INS[25], ~INS[24], ~INS[23], ~INS[22], ~INS[21]);  // AND_Gate
  and gADDS (insADDS, INS[31], ~INS[30], INS[29], ~INS[28], INS[27], ~INS[26], INS[25], INS[24], ~INS[23], ~INS[22]);  // AND_Gate
  and gSUBS (insSUBS, INS[31], INS[30], INS[29], ~INS[28], INS[27], ~INS[26], INS[25], INS[24], ~INS[23], ~INS[22]);  // AND_Gate
  and gANDIS (insANDIS, INS[31], INS[30], INS[29], INS[28], ~INS[27], ~INS[26], INS[25], ~INS[24], ~INS[23]);  // AND_Gate
  and gADDIS (insADDIS, INS[31], ~INS[30], INS[29], INS[28], ~INS[27], ~INS[26], ~INS[25], INS[24], ~INS[23], ~INS[22]);  // AND_Gate
  and gSUBIS (insSUBIS, INS[31], INS[30], INS[29], INS[28], ~INS[27], ~INS[26], ~INS[25], INS[24], ~INS[23], ~INS[22]);  // AND_Gate
  and gLSL (insLSL, INS[31], INS[30], ~INS[29], INS[28], ~INS[27], ~INS[26], INS[25], INS[24], ~INS[23], INS[22], ~insLSR);  // AND_Gate
  and gLSR (insLSR, INS[31], INS[30], ~INS[29], INS[28], ~INS[27], ~INS[26], INS[25], INS[24], ~INS[22], INS[21], INS[15], INS[14], INS[13], INS[12], INS[11], INS[10]);  // AND_Gate
  and gMOVK (insMOVK, INS[31], INS[30], INS[29], INS[28], ~INS[27], ~INS[26], INS[25], ~INS[24], INS[23]);  // AND_Gate
  and gMOVZ (insMOVZ, INS[31], INS[30], ~INS[29], INS[28], ~INS[27], ~INS[26], INS[25], ~INS[24], INS[23]);  // AND_Gate
  and gMOVN (insMOVN, INS[31], ~INS[30], ~INS[29], INS[28], ~INS[27], ~INS[26], INS[25], ~INS[24], INS[23]);  // AND_Gate
  and gLSLV (insLSLV, INS[31], ~INS[30], ~INS[29], INS[28], INS[27], ~INS[26], INS[25], ~INS[24], INS[23], INS[22], ~INS[21], ~INS[15], ~INS[14], INS[13], ~INS[12], ~INS[11], ~INS[10]);  // AND_Gate
  and gLSRV (insLSRV, INS[31], ~INS[30], ~INS[29], INS[28], INS[27], ~INS[26], INS[25], ~INS[24], INS[23], INS[22], ~INS[21], ~INS[15], ~INS[14], INS[13], ~INS[12], ~INS[11], INS[10]);  // AND_Gate
  and gMUL (insMUL, INS[31], ~INS[30], ~INS[29], INS[28], INS[27], ~INS[26], INS[25], INS[24], ~INS[23], ~INS[22], ~INS[21], ~INS[15], INS[14], INS[13], INS[12], INS[11], INS[10]);  // AND_Gate
  and gUMULH (insUMULH, INS[31], ~INS[30], ~INS[29], INS[28], INS[27], ~INS[26], INS[25], INS[24], INS[23], INS[22], ~INS[21]);  // AND_Gate
  and gSMULH (insSMULH, INS[31], ~INS[30], ~INS[29], INS[28], INS[27], ~INS[26], INS[25], INS[24], ~INS[23], INS[22], ~INS[21]);  // AND_Gate
  and UDIV (insUDIV, INS[31], ~INS[30], ~INS[29], INS[28], INS[27], ~INS[26], INS[25], ~INS[24], INS[23], INS[22], ~INS[21], ~INS[15], ~INS[14], ~INS[13], ~INS[12], INS[11], INS[10]);  // AND_Gate
  and gSDIV (insSDIV, INS[31], ~INS[30], ~INS[29], INS[28], INS[27], ~INS[26], INS[25], ~INS[24], INS[23], INS[22], ~INS[21], ~INS[15], ~INS[14], ~INS[13], ~INS[12], INS[11], ~INS[10]);  // AND_Gate
  nor nor_1 (insNOT_IMPLEMENTED, B, BL, BR, CBZ, CBNZ, insBCOND, insSTUR, insLDUR, insAND, insORR, insEOR, insADD, insSUB, insANDI, insORRI, insEORI, insADDI, insSUBI, insANDS, insADDS, insSUBS, insANDIS, insADDIS, insSUBIS, insLSL, insLSR, insMOVK, insMOVZ, insMOVN, insLSLV, insLSRV, insMUL, insUMULH, insSMULH, insUDIV, insSDIV);
  or or_1 (or_1_out, insSTUR, insLDUR);
  assign AccessSize = or_1_out ? INS[31:30] : 2'bz;  // Controlled_Buffer controlled_buffer_1
  and and_1 (and_1_out, INS[21], or_2_out);
  or or_2 (or_2_out, insADD, insSUB);
  and and_2 (and_2_out, INS[21], or_3_out);
  or or_3 (or_3_out, insADDS, insSUBS);
  assign Shamt = insLSL ? subtractor_1_out : 6'bz;  // Controlled_Buffer controlled_buffer_2
  assign Shamt = insLSR ? INS[21:16] : 6'bz;  // Controlled_Buffer controlled_buffer_3
  or or_4 (or_4_out, insMOVK, insMOVZ, insMOVN);
  assign Shamt = or_4_out ? {INS[22:21], 4'b0000} : 6'bz;  // Controlled_Buffer controlled_buffer_4
  and gEQ (gEQ_out, decoder_1_out0, FLAGS[0]);
  and gNE (gNE_out, decoder_1_out1, ~FLAGS[0]);  // AND_Gate
  and gHS (gHS_out, decoder_1_out2, FLAGS[2]);
  and gLO (gLO_out, decoder_1_out3, ~FLAGS[2]);  // AND_Gate
  and gMI (gMI_out, decoder_1_out4, FLAGS[1]);
  and gPL (gPL_out, decoder_1_out5, ~FLAGS[1]);  // AND_Gate
  and gVS (gVS_out, decoder_1_out6, FLAGS[3]);
  and gVC (gVC_out, decoder_1_out7, ~FLAGS[3]);  // AND_Gate
  and gHI (gHI_out, decoder_1_out8, ~FLAGS[0], FLAGS[2]);  // AND_Gate
  or or_5 (or_5_out, FLAGS[0], ~FLAGS[2]);  // OR_Gate
  xnor xnor_1 (xnor_1_out, FLAGS[1], FLAGS[3]);
  xor xor_1 (xor_1_out, FLAGS[1], FLAGS[3]);
  xnor xnor_2 (xnor_2_out, FLAGS[1], FLAGS[3]);
  or or_6 (or_6_out, FLAGS[0], xor_2_out);
  xor xor_2 (xor_2_out, FLAGS[1], FLAGS[3]);
  or or_7 (Reg2Loc, CBZ, CBNZ, insSTUR, insMOVZ);
  or or_8 (RegWrite, BL, insLDUR, insAND, insORR, insEOR, insADD, insSUB, insANDI, insORRI, insEORI, insADDI, insSUBI, insANDS, insADDS, insSUBS, insANDIS, insADDIS, insSUBIS, insLSL, insLSR, insMOVK, insMOVZ, insMOVN, insLSLV, insLSRV, insMUL, insUMULH, insSMULH, insUDIV, insSDIV);
  or or_9 (ALUSrc, insSTUR, insLDUR, insANDI, insORRI, insEORI, insADDI, insSUBI, insANDIS, insADDIS, insSUBIS, insMOVK, insMOVZ, insMOVN);
  or gALUimm (gALUimm_out, insADDI, insSUBI, insADDIS, insSUBIS);
  or gDTAddr (gDTAddr_out, insSTUR, insLDUR);
  or gBRAddr (gBRAddr_out, B, BL);
  or gCONDBRAddr (gCONDBRAddr_out, CBZ, CBNZ, insBCOND);
  or gMOVImm (gMOVImm_out, insMOVK, insMOVZ, insMOVN);
  or gLogicalImm (gLogicalImm_out, insANDI, insORRI, insEORI, insANDIS);
  or gANDop (gANDop_out, insAND, insANDI, insANDS, insANDIS);
  or gORop (gORop_out, insORR, insORRI);
  or gEORop (gEORop_out, insEOR, insEORI);
  or gADDop (gADDop_out, insSTUR, insLDUR, insADD, insADDI, insADDS, insADDIS);
  or gSUBop (gSUBop_out, insSUB, insSUBI, insSUBS, insSUBIS);
  or gPASSBop (gPASSBop_out, CBZ, CBNZ, insMOVK, insMOVZ, insMOVN);
  or or_10 (SetFlags, insANDS, insADDS, insSUBS, insANDIS, insADDIS, insSUBIS);
  or or_11 (RdSP, and_1_out, insANDI, insORRI, insEORI, insADDI, insSUBI);
  or or_12 (RnSP, and_1_out, and_2_out, insSTUR, insLDUR, insADDI, insSUBI, insADDIS, insSUBIS);
  and gLS (gLS_out, decoder_1_out9, or_5_out);
  and gGE (gGE_out, decoder_1_out10, xnor_1_out);
  and gLT (gLT_out, decoder_1_out11, xor_1_out);
  and gGT (gGT_out, decoder_1_out12, ~FLAGS[0], xnor_2_out);  // AND_Gate
  and gLE (gLE_out, decoder_1_out13, or_6_out);
  Priority_Encoder priority_encoder_1 (
    .in0(gALUimm_out), .in1(gDTAddr_out), .in2(gBRAddr_out), .in3(gCONDBRAddr_out), .in4(gMOVImm_out),
    .in5(gLogicalImm_out), .out(ImmSel), .en_in(1'b1));  // open: in6, in7, gs, en_out
  Priority_Encoder #(.select(4)) priority_encoder_2 (
    .in0(gANDop_out), .in1(gORop_out), .in2(gEORop_out), .in3(gADDop_out), .in4(gSUBop_out), .in5(insLSL),
    .in6(insLSR), .in7(insLSLV), .in8(insLSRV), .in9(insMUL), .in10(insUMULH), .in11(insSMULH),
    .in12(insUDIV), .in13(insSDIV), .in14(gPASSBop_out), .out(ALUop), .en_in(1'b1));  // open: in15, gs, en_out
  or or_13 (BCOND_TRUE, gEQ_out, gNE_out, gHS_out, gLO_out, gMI_out, gPL_out, gVS_out, gVC_out, gHI_out, gLS_out, gGE_out, gLT_out, gGT_out, gLE_out, decoder_1_out14);

  assign insB = B;
  assign insBL = BL;
  assign insBR = BR;
  assign insCBNZ = CBNZ;
  assign insCBZ = CBZ;
  assign MemRead = insLDUR;
  assign MemtoReg = insLDUR;
  assign MemWrite = insSTUR;
  assign MOVK = insMOVK;
  assign MOVN = insMOVN;
  assign MOVZ = insMOVZ;
endmodule

module ImmediateExtend (
  input  [2:0] CTRL,
  input  [31:0] INS,
  output ZERO_EXTEND,
  output SIGN_EXTEND,
  output IMM12,
  output IMM9,
  output IMM26,
  output IMM19,
  output IMM16,
  output IMM13,
  output [63:0] IMMEDIATE,
  output [63:0] EXTENDED1,
  output [63:0] EXTENDED2,
  output [63:0] EXTENDED3
);

  wire [63:0] bit_extender_1_out, bit_extender_2_out, bit_extender_3_out, bit_extender_4_out,
       bit_extender_5_out, bitmaskimmediate_1_out_2;

  assign bit_extender_1_out = {{52{1'b0}}, INS[21:10]};  // Bit_Extender bit_extender_1
  assign bit_extender_2_out = {{55{INS[20]}}, INS[20:12]};  // Bit_Extender bit_extender_2
  assign bit_extender_3_out = {{38{INS[25]}}, INS[25:0]};  // Bit_Extender bit_extender_3
  assign bit_extender_4_out = {{45{INS[23]}}, INS[23:5]};  // Bit_Extender bit_extender_4
  assign bit_extender_5_out = {{48{1'b0}}, INS[20:5]};  // Bit_Extender bit_extender_5
  BitmaskImmediate bitmaskimmediate_1 (.out_2(bitmaskimmediate_1_out_2), .in_1(INS[22:10]));
  Decoder #(.enable("false"), .select(3)) decoder_1 (
    .out0(IMM12), .out1(IMM9), .out2(IMM26), .out3(IMM19), .out4(IMM16), .out5(IMM13), .sel(CTRL));  // open: out6, out7
  Multiplexer #(.enable("false"), .select(3), .width(64)) multiplexer_1 (
    .in0(bit_extender_1_out), .in1(bit_extender_2_out), .in2(bit_extender_3_out), .in3(bit_extender_4_out),
    .in4(bit_extender_5_out), .in5(bitmaskimmediate_1_out_2), .out(EXTENDED1), .sel(CTRL));  // open: in6, in7
  or or_1 (ZERO_EXTEND, IMM12, IMM16);
  or or_2 (SIGN_EXTEND, IMM9, IMM26, IMM19);

  assign EXTENDED2 = EXTENDED1;
  assign EXTENDED3 = EXTENDED1;
  assign IMMEDIATE = EXTENDED1;
endmodule

module RegisterFile (
  input  [4:0] READ_ADDR1,
  input  [4:0] READ_ADDR2,
  input  [4:0] WRITE_ADDR,
  input  [63:0] WRITE_DATA,
  input  WRITE_ENABLE,
  input  CLOCK,
  input  WRITE_USE_SP,
  input  READ1_USE_SP,
  output [63:0] RD11,
  output [63:0] RD12,
  output [63:0] RD13,
  output [4:0] RA1,
  output [63:0] RD21,
  output [63:0] WD1,
  output [4:0] RA2,
  output [63:0] RD22,
  output [63:0] WD2,
  output [63:0] RD23,
  output [4:0] WA,
  output [63:0] WD3,
  output [63:0] READ_DATA1,
  output [63:0] READ_DATA2,
  output WE
);

  wire and_1_out, and_2_out, and_3_out, decoder_1_out0, decoder_1_out1, decoder_1_out2, decoder_1_out3,
       decoder_1_out4, decoder_1_out5, decoder_1_out6, decoder_1_out7, decoder_1_out8, decoder_1_out9,
       decoder_1_out10, decoder_1_out11, decoder_1_out12, decoder_1_out13, decoder_1_out14, decoder_1_out15,
       decoder_1_out16, decoder_1_out17, decoder_1_out18, decoder_1_out19, decoder_1_out20, decoder_1_out21,
       decoder_1_out22, decoder_1_out23, decoder_1_out24, decoder_1_out25, decoder_1_out26, decoder_1_out27,
       decoder_1_out28, decoder_1_out29, decoder_1_out30, decoder_1_out31, decoder_2_out0, decoder_2_out1,
       decoder_2_out2, decoder_2_out3, decoder_2_out4, decoder_2_out5, decoder_2_out6, decoder_2_out7,
       decoder_2_out8, decoder_2_out9, decoder_2_out10, decoder_2_out11, decoder_2_out12, decoder_2_out13,
       decoder_2_out14, decoder_2_out15, decoder_2_out16, decoder_2_out17, decoder_2_out18, decoder_2_out19,
       decoder_2_out20, decoder_2_out21, decoder_2_out22, decoder_2_out23, decoder_2_out24, decoder_2_out25,
       decoder_2_out26, decoder_2_out27, decoder_2_out28, decoder_2_out29, decoder_2_out30, decoder_2_out31,
       decoder_3_out0, decoder_3_out1, decoder_3_out2, decoder_3_out3, decoder_3_out4, decoder_3_out5,
       decoder_3_out6, decoder_3_out7, decoder_3_out8, decoder_3_out9, decoder_3_out10, decoder_3_out11,
       decoder_3_out12, decoder_3_out13, decoder_3_out14, decoder_3_out15, decoder_3_out16, decoder_3_out17,
       decoder_3_out18, decoder_3_out19, decoder_3_out20, decoder_3_out21, decoder_3_out22, decoder_3_out23,
       decoder_3_out24, decoder_3_out25, decoder_3_out26, decoder_3_out27, decoder_3_out28, decoder_3_out29,
       decoder_3_out30, decoder_3_out31;
  wire [63:0] SP_q, X0_q, X1_q, X2_q, X3_q, X4_q, X5_q, X6_q, X7_q, X8_q, X9_q, X10_q, X11_q, X12_q, X13_q,
       X14_q, X15_q, X16_q, X17_q, X18_q, X19_q, X20_q, X21_q, X22_q, X23_q, X24_q, X25_q, X26_q, X27_q,
       X28_q, X29_q, X30_q;

  Decoder #(.select(5)) decoder_1 (
    .out0(decoder_1_out0), .out1(decoder_1_out1), .out2(decoder_1_out2), .out3(decoder_1_out3),
    .out4(decoder_1_out4), .out5(decoder_1_out5), .out6(decoder_1_out6), .out7(decoder_1_out7),
    .out8(decoder_1_out8), .out9(decoder_1_out9), .out10(decoder_1_out10), .out11(decoder_1_out11),
    .out12(decoder_1_out12), .out13(decoder_1_out13), .out14(decoder_1_out14), .out15(decoder_1_out15),
    .out16(decoder_1_out16), .out17(decoder_1_out17), .out18(decoder_1_out18), .out19(decoder_1_out19),
    .out20(decoder_1_out20), .out21(decoder_1_out21), .out22(decoder_1_out22), .out23(decoder_1_out23),
    .out24(decoder_1_out24), .out25(decoder_1_out25), .out26(decoder_1_out26), .out27(decoder_1_out27),
    .out28(decoder_1_out28), .out29(decoder_1_out29), .out30(decoder_1_out30), .out31(decoder_1_out31),
    .sel(WRITE_ADDR), .en(WRITE_ENABLE));
  Decoder #(.enable("false"), .select(5)) decoder_2 (
    .out0(decoder_2_out0), .out1(decoder_2_out1), .out2(decoder_2_out2), .out3(decoder_2_out3),
    .out4(decoder_2_out4), .out5(decoder_2_out5), .out6(decoder_2_out6), .out7(decoder_2_out7),
    .out8(decoder_2_out8), .out9(decoder_2_out9), .out10(decoder_2_out10), .out11(decoder_2_out11),
    .out12(decoder_2_out12), .out13(decoder_2_out13), .out14(decoder_2_out14), .out15(decoder_2_out15),
    .out16(decoder_2_out16), .out17(decoder_2_out17), .out18(decoder_2_out18), .out19(decoder_2_out19),
    .out20(decoder_2_out20), .out21(decoder_2_out21), .out22(decoder_2_out22), .out23(decoder_2_out23),
    .out24(decoder_2_out24), .out25(decoder_2_out25), .out26(decoder_2_out26), .out27(decoder_2_out27),
    .out28(decoder_2_out28), .out29(decoder_2_out29), .out30(decoder_2_out30), .out31(decoder_2_out31),
    .sel(READ_ADDR1));
  Decoder #(.enable("false"), .select(5)) decoder_3 (
    .out0(decoder_3_out0), .out1(decoder_3_out1), .out2(decoder_3_out2), .out3(decoder_3_out3),
    .out4(decoder_3_out4), .out5(decoder_3_out5), .out6(decoder_3_out6), .out7(decoder_3_out7),
    .out8(decoder_3_out8), .out9(decoder_3_out9), .out10(decoder_3_out10), .out11(decoder_3_out11),
    .out12(decoder_3_out12), .out13(decoder_3_out13), .out14(decoder_3_out14), .out15(decoder_3_out15),
    .out16(decoder_3_out16), .out17(decoder_3_out17), .out18(decoder_3_out18), .out19(decoder_3_out19),
    .out20(decoder_3_out20), .out21(decoder_3_out21), .out22(decoder_3_out22), .out23(decoder_3_out23),
    .out24(decoder_3_out24), .out25(decoder_3_out25), .out26(decoder_3_out26), .out27(decoder_3_out27),
    .out28(decoder_3_out28), .out29(decoder_3_out29), .out30(decoder_3_out30), .out31(decoder_3_out31),
    .sel(READ_ADDR2));
  Register #(.width(64)) X0 (.D(WRITE_DATA), .en(decoder_1_out0), .clk(CLOCK), .Q(X0_q));  // open: clr
  Register #(.width(64)) X1 (.D(WRITE_DATA), .en(decoder_1_out1), .clk(CLOCK), .Q(X1_q));  // open: clr
  Register #(.width(64)) X2 (.D(WRITE_DATA), .en(decoder_1_out2), .clk(CLOCK), .Q(X2_q));  // open: clr
  Register #(.width(64)) X3 (.D(WRITE_DATA), .en(decoder_1_out3), .clk(CLOCK), .Q(X3_q));  // open: clr
  Register #(.width(64)) X4 (.D(WRITE_DATA), .en(decoder_1_out4), .clk(CLOCK), .Q(X4_q));  // open: clr
  Register #(.width(64)) X5 (.D(WRITE_DATA), .en(decoder_1_out5), .clk(CLOCK), .Q(X5_q));  // open: clr
  Register #(.width(64)) X6 (.D(WRITE_DATA), .en(decoder_1_out6), .clk(CLOCK), .Q(X6_q));  // open: clr
  Register #(.width(64)) X7 (.D(WRITE_DATA), .en(decoder_1_out7), .clk(CLOCK), .Q(X7_q));  // open: clr
  Register #(.width(64)) X8 (.D(WRITE_DATA), .en(decoder_1_out8), .clk(CLOCK), .Q(X8_q));  // open: clr
  Register #(.width(64)) X9 (.D(WRITE_DATA), .en(decoder_1_out9), .clk(CLOCK), .Q(X9_q));  // open: clr
  Register #(.width(64)) X10 (.D(WRITE_DATA), .en(decoder_1_out10), .clk(CLOCK), .Q(X10_q));  // open: clr
  Register #(.width(64)) X11 (.D(WRITE_DATA), .en(decoder_1_out11), .clk(CLOCK), .Q(X11_q));  // open: clr
  Register #(.width(64)) X12 (.D(WRITE_DATA), .en(decoder_1_out12), .clk(CLOCK), .Q(X12_q));  // open: clr
  Register #(.width(64)) X13 (.D(WRITE_DATA), .en(decoder_1_out13), .clk(CLOCK), .Q(X13_q));  // open: clr
  Register #(.width(64)) X14 (.D(WRITE_DATA), .en(decoder_1_out14), .clk(CLOCK), .Q(X14_q));  // open: clr
  Register #(.width(64)) X15 (.D(WRITE_DATA), .en(decoder_1_out15), .clk(CLOCK), .Q(X15_q));  // open: clr
  Register #(.width(64)) X16 (.D(WRITE_DATA), .en(decoder_1_out16), .clk(CLOCK), .Q(X16_q));  // open: clr
  Register #(.width(64)) X17 (.D(WRITE_DATA), .en(decoder_1_out17), .clk(CLOCK), .Q(X17_q));  // open: clr
  Register #(.width(64)) X18 (.D(WRITE_DATA), .en(decoder_1_out18), .clk(CLOCK), .Q(X18_q));  // open: clr
  Register #(.width(64)) X19 (.D(WRITE_DATA), .en(decoder_1_out19), .clk(CLOCK), .Q(X19_q));  // open: clr
  Register #(.width(64)) X20 (.D(WRITE_DATA), .en(decoder_1_out20), .clk(CLOCK), .Q(X20_q));  // open: clr
  Register #(.width(64)) X21 (.D(WRITE_DATA), .en(decoder_1_out21), .clk(CLOCK), .Q(X21_q));  // open: clr
  Register #(.width(64)) X22 (.D(WRITE_DATA), .en(decoder_1_out22), .clk(CLOCK), .Q(X22_q));  // open: clr
  Register #(.width(64)) X23 (.D(WRITE_DATA), .en(decoder_1_out23), .clk(CLOCK), .Q(X23_q));  // open: clr
  Register #(.width(64)) X24 (.D(WRITE_DATA), .en(decoder_1_out24), .clk(CLOCK), .Q(X24_q));  // open: clr
  Register #(.width(64)) X25 (.D(WRITE_DATA), .en(decoder_1_out25), .clk(CLOCK), .Q(X25_q));  // open: clr
  Register #(.width(64)) X26 (.D(WRITE_DATA), .en(decoder_1_out26), .clk(CLOCK), .Q(X26_q));  // open: clr
  Register #(.width(64)) X27 (.D(WRITE_DATA), .en(decoder_1_out27), .clk(CLOCK), .Q(X27_q));  // open: clr
  Register #(.width(64)) X28 (.D(WRITE_DATA), .en(decoder_1_out28), .clk(CLOCK), .Q(X28_q));  // open: clr
  Register #(.width(64)) X29 (.D(WRITE_DATA), .en(decoder_1_out29), .clk(CLOCK), .Q(X29_q));  // open: clr
  Register #(.width(64)) X30 (.D(WRITE_DATA), .en(decoder_1_out30), .clk(CLOCK), .Q(X30_q));  // open: clr
  Register #(.width(64)) SP (.D(WRITE_DATA), .en(and_1_out), .clk(CLOCK), .Q(SP_q));  // open: clr
  and and_1 (and_1_out, WRITE_USE_SP, decoder_1_out31);
  and and_2 (and_2_out, READ1_USE_SP, decoder_2_out31);
  assign RD11 = decoder_2_out0 ? X0_q : 64'bz;  // Controlled_Buffer controlled_buffer_1
  assign RD11 = decoder_2_out1 ? X1_q : 64'bz;  // Controlled_Buffer controlled_buffer_2
  assign RD11 = decoder_2_out2 ? X2_q : 64'bz;  // Controlled_Buffer controlled_buffer_3
  assign RD11 = decoder_2_out3 ? X3_q : 64'bz;  // Controlled_Buffer controlled_buffer_4
  assign RD11 = decoder_2_out4 ? X4_q : 64'bz;  // Controlled_Buffer controlled_buffer_5
  assign RD11 = decoder_2_out5 ? X5_q : 64'bz;  // Controlled_Buffer controlled_buffer_6
  assign RD11 = decoder_2_out6 ? X6_q : 64'bz;  // Controlled_Buffer controlled_buffer_7
  assign RD11 = decoder_2_out7 ? X7_q : 64'bz;  // Controlled_Buffer controlled_buffer_8
  assign RD11 = decoder_2_out8 ? X8_q : 64'bz;  // Controlled_Buffer controlled_buffer_9
  assign RD11 = decoder_2_out9 ? X9_q : 64'bz;  // Controlled_Buffer controlled_buffer_10
  assign RD11 = decoder_2_out10 ? X10_q : 64'bz;  // Controlled_Buffer controlled_buffer_11
  assign RD11 = decoder_2_out11 ? X11_q : 64'bz;  // Controlled_Buffer controlled_buffer_12
  assign RD11 = decoder_2_out12 ? X12_q : 64'bz;  // Controlled_Buffer controlled_buffer_13
  assign RD11 = decoder_2_out13 ? X13_q : 64'bz;  // Controlled_Buffer controlled_buffer_14
  assign RD11 = decoder_2_out14 ? X14_q : 64'bz;  // Controlled_Buffer controlled_buffer_15
  assign RD11 = decoder_2_out15 ? X15_q : 64'bz;  // Controlled_Buffer controlled_buffer_16
  assign RD11 = decoder_2_out16 ? X16_q : 64'bz;  // Controlled_Buffer controlled_buffer_17
  assign RD11 = decoder_2_out17 ? X17_q : 64'bz;  // Controlled_Buffer controlled_buffer_18
  assign RD11 = decoder_2_out18 ? X18_q : 64'bz;  // Controlled_Buffer controlled_buffer_19
  assign RD11 = decoder_2_out19 ? X19_q : 64'bz;  // Controlled_Buffer controlled_buffer_20
  assign RD11 = decoder_2_out20 ? X20_q : 64'bz;  // Controlled_Buffer controlled_buffer_21
  assign RD11 = decoder_2_out21 ? X21_q : 64'bz;  // Controlled_Buffer controlled_buffer_22
  assign RD11 = decoder_2_out22 ? X22_q : 64'bz;  // Controlled_Buffer controlled_buffer_23
  assign RD11 = decoder_2_out23 ? X23_q : 64'bz;  // Controlled_Buffer controlled_buffer_24
  assign RD11 = decoder_2_out24 ? X24_q : 64'bz;  // Controlled_Buffer controlled_buffer_25
  assign RD11 = decoder_2_out25 ? X25_q : 64'bz;  // Controlled_Buffer controlled_buffer_26
  assign RD11 = decoder_2_out26 ? X26_q : 64'bz;  // Controlled_Buffer controlled_buffer_27
  assign RD11 = decoder_2_out27 ? X27_q : 64'bz;  // Controlled_Buffer controlled_buffer_28
  assign RD11 = decoder_2_out28 ? X28_q : 64'bz;  // Controlled_Buffer controlled_buffer_29
  assign RD11 = decoder_2_out29 ? X29_q : 64'bz;  // Controlled_Buffer controlled_buffer_30
  assign RD11 = decoder_2_out30 ? X30_q : 64'bz;  // Controlled_Buffer controlled_buffer_31
  assign RD11 = and_2_out ? SP_q : 64'bz;  // Controlled_Buffer controlled_buffer_32
  assign RD11 = and_3_out ? {64{1'b0}} : 64'bz;  // Controlled_Buffer controlled_buffer_33
  and and_3 (and_3_out, ~READ1_USE_SP, decoder_2_out31);  // AND_Gate
  assign RD21 = decoder_3_out0 ? X0_q : 64'bz;  // Controlled_Buffer controlled_buffer_34
  assign RD21 = decoder_3_out1 ? X1_q : 64'bz;  // Controlled_Buffer controlled_buffer_35
  assign RD21 = decoder_3_out2 ? X2_q : 64'bz;  // Controlled_Buffer controlled_buffer_36
  assign RD21 = decoder_3_out3 ? X3_q : 64'bz;  // Controlled_Buffer controlled_buffer_37
  assign RD21 = decoder_3_out4 ? X4_q : 64'bz;  // Controlled_Buffer controlled_buffer_38
  assign RD21 = decoder_3_out5 ? X5_q : 64'bz;  // Controlled_Buffer controlled_buffer_39
  assign RD21 = decoder_3_out6 ? X6_q : 64'bz;  // Controlled_Buffer controlled_buffer_40
  assign RD21 = decoder_3_out7 ? X7_q : 64'bz;  // Controlled_Buffer controlled_buffer_41
  assign RD21 = decoder_3_out8 ? X8_q : 64'bz;  // Controlled_Buffer controlled_buffer_42
  assign RD21 = decoder_3_out9 ? X9_q : 64'bz;  // Controlled_Buffer controlled_buffer_43
  assign RD21 = decoder_3_out10 ? X10_q : 64'bz;  // Controlled_Buffer controlled_buffer_44
  assign RD21 = decoder_3_out11 ? X11_q : 64'bz;  // Controlled_Buffer controlled_buffer_45
  assign RD21 = decoder_3_out12 ? X12_q : 64'bz;  // Controlled_Buffer controlled_buffer_46
  assign RD21 = decoder_3_out13 ? X13_q : 64'bz;  // Controlled_Buffer controlled_buffer_47
  assign RD21 = decoder_3_out14 ? X14_q : 64'bz;  // Controlled_Buffer controlled_buffer_48
  assign RD21 = decoder_3_out15 ? X15_q : 64'bz;  // Controlled_Buffer controlled_buffer_49
  assign RD21 = decoder_3_out16 ? X16_q : 64'bz;  // Controlled_Buffer controlled_buffer_50
  assign RD21 = decoder_3_out17 ? X17_q : 64'bz;  // Controlled_Buffer controlled_buffer_51
  assign RD21 = decoder_3_out18 ? X18_q : 64'bz;  // Controlled_Buffer controlled_buffer_52
  assign RD21 = decoder_3_out19 ? X19_q : 64'bz;  // Controlled_Buffer controlled_buffer_53
  assign RD21 = decoder_3_out20 ? X20_q : 64'bz;  // Controlled_Buffer controlled_buffer_54
  assign RD21 = decoder_3_out21 ? X21_q : 64'bz;  // Controlled_Buffer controlled_buffer_55
  assign RD21 = decoder_3_out22 ? X22_q : 64'bz;  // Controlled_Buffer controlled_buffer_56
  assign RD21 = decoder_3_out23 ? X23_q : 64'bz;  // Controlled_Buffer controlled_buffer_57
  assign RD21 = decoder_3_out24 ? X24_q : 64'bz;  // Controlled_Buffer controlled_buffer_58
  assign RD21 = decoder_3_out25 ? X25_q : 64'bz;  // Controlled_Buffer controlled_buffer_59
  assign RD21 = decoder_3_out26 ? X26_q : 64'bz;  // Controlled_Buffer controlled_buffer_60
  assign RD21 = decoder_3_out27 ? X27_q : 64'bz;  // Controlled_Buffer controlled_buffer_61
  assign RD21 = decoder_3_out28 ? X28_q : 64'bz;  // Controlled_Buffer controlled_buffer_62
  assign RD21 = decoder_3_out29 ? X29_q : 64'bz;  // Controlled_Buffer controlled_buffer_63
  assign RD21 = decoder_3_out30 ? X30_q : 64'bz;  // Controlled_Buffer controlled_buffer_64
  assign RD21 = decoder_3_out31 ? {64{1'b0}} : 64'bz;  // Controlled_Buffer controlled_buffer_65

  assign RA1 = READ_ADDR1;
  assign RA2 = READ_ADDR2;
  assign RD12 = RD11;
  assign RD13 = RD11;
  assign RD22 = RD21;
  assign RD23 = RD21;
  assign READ_DATA1 = RD11;
  assign READ_DATA2 = RD21;
  assign WA = WRITE_ADDR;
  assign WD1 = WRITE_DATA;
  assign WD2 = WRITE_DATA;
  assign WD3 = WRITE_DATA;
  assign WE = WRITE_ENABLE;
endmodule

module ArithmeticLogicUnit (
  input  [5:0] SHIFT_AMOUNT,
  input  [63:0] OPERAND1,
  input  [63:0] OPERAND2,
  input  [3:0] ALU_OP,
  output [5:0] SHAMT,
  output [63:0] O11,
  output [63:0] O12,
  output [63:0] O13,
  output [63:0] O21,
  output [63:0] O22,
  output [63:0] O23,
  output pAND,
  output pOR,
  output pEOR,
  output pADD,
  output pSUB,
  output pLSL,
  output pLSR,
  output pLSLV,
  output pLSRV,
  output pMUL,
  output pUMULH,
  output pSMULH,
  output UDIV,
  output SDIV,
  output pPASS_B,
  output [63:0] R1,
  output [63:0] R2,
  output [63:0] R3,
  output [63:0] RESULT,
  output ZERO,
  output Z,
  output N,
  output [3:0] FLAGS,
  output C,
  output V
);

  wire adder_1_cout, adder_2_cout, adder_3_cout, adder_4_cout, and_2_out, and_3_out, and_4_out, and_5_out,
       xor_2_out, xor_3_out;
  wire [63:0] adder_1_out, adder_2_out, and_1_out, bit_extender_1_out, divider_1_out, divider_2_out,
       multiplier_1_cout, multiplier_1_out, multiplier_2_cout, not_1_out, not_2_out, or_1_out, shifter_1_out,
       shifter_2_out, shifter_3_out, shifter_4_out, xor_1_out;

  assign not_1_out = ~OPERAND2;  // NOT_Gate not_1, 64 bits wide
  assign not_2_out = ~OPERAND2;  // NOT_Gate not_2, 64 bits wide
  Adder #(.width(64)) adder_1 (.a(OPERAND1), .b(OPERAND2), .out(adder_1_out), .cin(1'b0), .cout(adder_1_cout));
  Adder #(.width(64)) adder_2 (.a(OPERAND1), .b(not_1_out), .out(adder_2_out), .cin(1'b1), .cout(adder_2_cout));
  Shifter #(.width(64)) shifter_1 (.in(OPERAND1), .\dist (SHIFT_AMOUNT), .out(shifter_1_out));
  Shifter #(.shift("lr"), .width(64)) shifter_2 (.in(OPERAND1), .\dist (SHIFT_AMOUNT), .out(shifter_2_out));
  Shifter #(.width(64)) shifter_3 (.in(OPERAND1), .\dist (OPERAND2[5:0]), .out(shifter_3_out));
  Shifter #(.shift("lr"), .width(64)) shifter_4 (.in(OPERAND1), .\dist (OPERAND2[5:0]), .out(shifter_4_out));
  Multiplier #(.width(64)) multiplier_1 (
    .a(OPERAND1), .b(OPERAND2), .out(multiplier_1_out), .cin({64{1'b0}}), .cout(multiplier_1_cout));
  Multiplier #(.mode("twosComplement"), .width(64)) multiplier_2 (
    .a(OPERAND1), .b(OPERAND2), .cin({64{1'b0}}), .cout(multiplier_2_cout));  // open: out
  Divider #(.width(64)) divider_1 (.a(OPERAND1), .b(OPERAND2), .out(divider_1_out), .upper({64{1'b0}}));  // open: rem
  assign bit_extender_1_out = {{63{OPERAND1[63]}}, OPERAND1[63]};  // Bit_Extender bit_extender_1
  Divider #(.mode("twosComplement"), .width(64)) divider_2 (
    .a(OPERAND1), .b(OPERAND2), .out(divider_2_out), .upper(bit_extender_1_out));  // open: rem
  Adder #(.width(63)) adder_3 (.a(OPERAND1[62:0]), .b(OPERAND2[62:0]), .cin(1'b0), .cout(adder_3_cout));  // open: out
  Adder #(.width(63)) adder_4 (.a(OPERAND1[62:0]), .b(not_2_out[62:0]), .cin(1'b1), .cout(adder_4_cout));  // open: out
  assign and_1_out = OPERAND1 & OPERAND2;  // AND_Gate and_1, 64 bits wide
  assign or_1_out = OPERAND1 | OPERAND2;  // OR_Gate or_1, 64 bits wide
  assign xor_1_out = OPERAND1 ^ OPERAND2;  // XOR_Gate xor_1, 64 bits wide
  Multiplexer #(.enable("false"), .select(4), .width(64)) multiplexer_1 (
    .in0(and_1_out), .in1(or_1_out), .in2(xor_1_out), .in3(adder_1_out), .in4(adder_2_out),
    .in5(shifter_1_out), .in6(shifter_2_out), .in7(shifter_3_out), .in8(shifter_4_out),
    .in9(multiplier_1_out), .in10(multiplier_1_cout), .in11(multiplier_2_cout), .in12(divider_1_out),
    .in13(divider_2_out), .in14(OPERAND2), .out(R1), .sel(ALU_OP));  // open: in15
  Decoder #(.enable("false"), .select(4)) decoder_1 (
    .out0(pAND), .out1(pOR), .out2(pEOR), .out3(pADD), .out4(pSUB), .out5(pLSL), .out6(pLSR), .out7(pLSLV),
    .out8(pLSRV), .out9(pMUL), .out10(pUMULH), .out11(pSMULH), .out12(UDIV), .out13(SDIV), .out14(pPASS_B),
    .sel(ALU_OP));  // open: out15
  xor xor_2 (xor_2_out, adder_1_cout, adder_3_cout);
  xor xor_3 (xor_3_out, adder_2_cout, adder_4_cout);
  and and_2 (and_2_out, pADD, adder_1_cout);
  and and_3 (and_3_out, pSUB, adder_2_cout);
  and and_4 (and_4_out, pADD, xor_2_out);
  and and_5 (and_5_out, pSUB, xor_3_out);
  or or_2 (C, and_2_out, and_3_out);
  or or_3 (FLAGS[3], and_4_out, and_5_out);
  Comparator #(.width(64)) comparator_1 (.a(R1), .b({64{1'b0}}), .eq(FLAGS[0]), .lt(FLAGS[1]));  // open: gt

  assign FLAGS[2] = C;
  assign N = FLAGS[1];
  assign O11 = OPERAND1;
  assign O12 = OPERAND1;
  assign O13 = OPERAND1;
  assign O21 = OPERAND2;
  assign O22 = OPERAND2;
  assign O23 = OPERAND2;
  assign R2 = R1;
  assign R3 = R1;
  assign RESULT = R1;
  assign SHAMT = SHIFT_AMOUNT;
  assign V = FLAGS[3];
  assign Z = FLAGS[0];
  assign ZERO = FLAGS[0];
endmodule

module MemoryController (
  input  [63:0] DATA_IN,
  input  [63:0] ADDRESS,
  input  MEM_READ,
  input  MEM_WRITE,
  input  [1:0] ACCESS_SIZE,
  output [63:0] DATA_OUT,
  output DATA_MEMORY_ACCESS,
  output PERIPHERAL_ACCESS,
  output ADDRESS_OUT_OF_RANGE,
  output [23:0] DATA_MEMORY_ADDRESS,
  output DATA_MEMORY_READ,
  output R,
  output DATA_MEMORY_WRITE,
  output W,
  output [63:0] ACCESS_MASK,
  output A0,
  output A1,
  output [7:0] DATA_MEMORY_BYTE_ENABLE,
  output A3,
  output A2,
  output GPIO_ACCESS,
  output [7:0] GPIO_ADDRESS,
  output GPIO_ADDRESS_NOT_ALIGNED,
  output GPIO_ACCESS_SIZE_INVALID,
  output GPIO_READ,
  output GPIO_WRITE,
  output PERIPHERAL_NOT_IMPLEMENTED
);

  wire and_4_out, comparator_1_eq, comparator_2_eq, comparator_3_eq, comparator_3_gt, comparator_4_gt,
       comparator_6_eq, comparator_6_gt, comparator_7_lt, comparator_8_eq, comparator_9_eq, or_1_out,
       or_2_out;
  wire [63:0] multiplexer_1_out;

  or or_1 (or_1_out, MEM_READ, MEM_WRITE);
  Comparator #(.mode("unsigned"), .width(40)) comparator_1 (
    .a({40{1'b0}}), .b(ADDRESS[63:24]), .eq(comparator_1_eq));  // open: gt, lt
  Comparator #(.mode("unsigned"), .width(40)) comparator_2 (
    .a(40'h3f), .b(ADDRESS[63:24]), .eq(comparator_2_eq));  // open: gt, lt
  Comparator #(.mode("unsigned"), .width(2)) comparator_3 (
    .a(ACCESS_SIZE), .b(2'b00), .gt(comparator_3_gt), .eq(comparator_3_eq));  // open: lt
  Comparator #(.mode("unsigned"), .width(2)) comparator_4 (
    .a(ACCESS_SIZE), .b(2'b01), .gt(comparator_4_gt), .eq(A1));  // open: lt
  Comparator #(.mode("unsigned"), .width(2)) comparator_5 (.a(ACCESS_SIZE), .b(2'b10), .gt(A3), .eq(A2));  // open: lt
  or or_2 (or_2_out, comparator_6_gt, comparator_6_eq);
  Comparator #(.mode("unsigned"), .width(24)) comparator_6 (
    .a(ADDRESS[23:0]), .b(24'h200000), .gt(comparator_6_gt), .eq(comparator_6_eq));  // open: lt
  Comparator #(.mode("unsigned"), .width(24)) comparator_7 (
    .a(ADDRESS[23:0]), .b(24'h2000b4), .lt(comparator_7_lt));  // open: gt, eq
  Comparator #(.mode("unsigned"), .width(2)) comparator_8 (
    .a(ADDRESS[1:0]), .b(2'b00), .eq(comparator_8_eq));  // open: gt, lt
  Comparator #(.mode("unsigned"), .width(2)) comparator_9 (
    .a(ACCESS_SIZE), .b(2'b10), .eq(comparator_9_eq));  // open: gt, lt
  and and_1 (DATA_MEMORY_ACCESS, or_1_out, comparator_1_eq);
  and and_2 (PERIPHERAL_ACCESS, or_1_out, comparator_2_eq);
  and and_3 (ADDRESS_OUT_OF_RANGE, or_1_out, ~comparator_1_eq, ~comparator_2_eq);  // AND_Gate
  and and_4 (and_4_out, comparator_8_eq, comparator_9_eq);
  assign DATA_MEMORY_ADDRESS = DATA_MEMORY_ACCESS ? ADDRESS[23:0] : 24'bz;  // Controlled_Buffer controlled_buffer_1
  and and_5 (DATA_MEMORY_READ, DATA_MEMORY_ACCESS, MEM_READ);
  and and_6 (DATA_MEMORY_WRITE, DATA_MEMORY_ACCESS, MEM_WRITE);
  and and_7 (DATA_MEMORY_BYTE_ENABLE[1], comparator_3_gt, DATA_MEMORY_ACCESS);
  and and_8 (DATA_MEMORY_BYTE_ENABLE[3], comparator_4_gt, DATA_MEMORY_ACCESS);
  and and_9 (DATA_MEMORY_BYTE_ENABLE[7], A3, DATA_MEMORY_ACCESS);
  and and_10 (GPIO_ACCESS, PERIPHERAL_ACCESS, or_2_out, comparator_7_lt);
  Multiplexer #(.enable("false"), .select(2), .width(64)) multiplexer_1 (
    .in0(64'hff), .in1(64'hffff), .in2(64'hffffffff), .in3({64{1'b1}}), .out(multiplexer_1_out),
    .sel(ACCESS_SIZE));
  and and_11 (A0, comparator_3_eq, DATA_MEMORY_ACCESS);
  assign GPIO_ADDRESS = GPIO_ACCESS ? ADDRESS[7:0] : 8'bz;  // Controlled_Buffer controlled_buffer_2
  and and_12 (GPIO_ADDRESS_NOT_ALIGNED, GPIO_ACCESS, ~comparator_8_eq);  // AND_Gate
  and and_13 (GPIO_ACCESS_SIZE_INVALID, GPIO_ACCESS, ~comparator_9_eq);  // AND_Gate
  and and_14 (GPIO_READ, GPIO_ACCESS, and_4_out, MEM_READ);
  and and_15 (GPIO_WRITE, GPIO_ACCESS, and_4_out, MEM_WRITE);
  and and_16 (PERIPHERAL_NOT_IMPLEMENTED, PERIPHERAL_ACCESS, ~GPIO_ACCESS);  // AND_Gate
  Multiplexer #(.enable("false"), .width(64)) multiplexer_2 (
    .in0({64{1'b0}}), .in1(multiplexer_1_out), .out(ACCESS_MASK), .sel(or_1_out));

  assign {DATA_MEMORY_BYTE_ENABLE[6:4], DATA_MEMORY_BYTE_ENABLE[2], DATA_MEMORY_BYTE_ENABLE[0]} = {{3{DATA_MEMORY_BYTE_ENABLE[7]}}, DATA_MEMORY_BYTE_ENABLE[3], DATA_MEMORY_ACCESS};
  assign DATA_OUT = DATA_IN;
  assign R = MEM_READ;
  assign W = MEM_WRITE;
endmodule

module BitmaskImmediate (
  input  [12:0] in_1,
  output [63:0] out_2
);

  wire g2_out, g4_out, g8_out, g16_out, g32_out;
  wire [1:0] shifter_1_out, subtractor_1_out;
  wire [3:0] shifter_2_out, subtractor_2_out;
  wire [7:0] shifter_3_out, subtractor_3_out;
  wire [15:0] shifter_4_out, subtractor_4_out;
  wire [31:0] shifter_5_out, subtractor_5_out;
  wire [63:0] shifter_6_out, shifter_12_out, subtractor_6_out;
  wire [63:32] shifter_11_out;
  wire [63:48] shifter_10_out;
  wire [63:56] shifter_9_out;
  wire [63:60] shifter_8_out;
  wire [63:62] shifter_7_out;

  and g2 (g2_out, ~in_1[12], in_1[5], in_1[4], in_1[3], in_1[2], in_1[1]);  // AND_Gate
  and g4 (g4_out, ~in_1[12], in_1[5], in_1[4], in_1[3], in_1[2]);  // AND_Gate
  and g8 (g8_out, ~in_1[12], in_1[5], in_1[4], in_1[3]);  // AND_Gate
  and g16 (g16_out, ~in_1[12], in_1[5], in_1[4]);  // AND_Gate
  and g32 (g32_out, ~in_1[12], in_1[5]);  // AND_Gate
  Shifter #(.width(2)) shifter_1 (.in(2'b10), .\dist (in_1[0]), .out(shifter_1_out));
  Shifter #(.width(4)) shifter_2 (.in(4'b0010), .\dist (in_1[1:0]), .out(shifter_2_out));
  Shifter shifter_3 (.in(8'h2), .\dist (in_1[2:0]), .out(shifter_3_out));
  Shifter #(.width(16)) shifter_4 (.in(16'h2), .\dist (in_1[3:0]), .out(shifter_4_out));
  Shifter #(.width(32)) shifter_5 (.in(32'h2), .\dist (in_1[4:0]), .out(shifter_5_out));
  Shifter #(.width(64)) shifter_6 (.in(64'h2), .\dist (in_1[5:0]), .out(shifter_6_out));
  Subtractor #(.width(2)) subtractor_1 (.a(shifter_1_out), .b(2'b01), .out(subtractor_1_out));  // open: bin, bout
  Subtractor #(.width(4)) subtractor_2 (.a(shifter_2_out), .b(4'b0001), .out(subtractor_2_out));  // open: bin, bout
  Subtractor subtractor_3 (.a(shifter_3_out), .b(8'h1), .out(subtractor_3_out));  // open: bin, bout
  Subtractor #(.width(16)) subtractor_4 (.a(shifter_4_out), .b(16'h1), .out(subtractor_4_out));  // open: bin, bout
  Subtractor #(.width(32)) subtractor_5 (.a(shifter_5_out), .b(32'h1), .out(subtractor_5_out));  // open: bin, bout
  Subtractor #(.width(64)) subtractor_6 (.a(shifter_6_out), .b(64'h1), .out(subtractor_6_out));  // open: bin, bout
  Shifter #(.shift("rr"), .width(2)) shifter_7 (.in(subtractor_1_out), .\dist (in_1[6]), .out(shifter_7_out));
  Shifter #(.shift("rr"), .width(4)) shifter_8 (.in(subtractor_2_out), .\dist (in_1[7:6]), .out(shifter_8_out));
  Shifter #(.shift("rr")) shifter_9 (.in(subtractor_3_out), .\dist (in_1[8:6]), .out(shifter_9_out));
  Shifter #(.shift("rr"), .width(16)) shifter_10 (.in(subtractor_4_out), .\dist (in_1[9:6]), .out(shifter_10_out));
  Shifter #(.shift("rr"), .width(32)) shifter_11 (.in(subtractor_5_out), .\dist (in_1[10:6]), .out(shifter_11_out));
  Shifter #(.shift("rr"), .width(64)) shifter_12 (.in(subtractor_6_out), .\dist (in_1[11:6]), .out(shifter_12_out));
  assign out_2 = g32_out ? {shifter_11_out, shifter_11_out} : 64'bz;  // Controlled_Buffer controlled_buffer_1
  assign out_2 = in_1[12] ? shifter_12_out : 64'bz;  // Controlled_Buffer controlled_buffer_2
  assign out_2 = g2_out ? {shifter_7_out, shifter_7_out, shifter_7_out, shifter_7_out, shifter_7_out, shifter_7_out, shifter_7_out, shifter_7_out, shifter_7_out, shifter_7_out, shifter_7_out, shifter_7_out, shifter_7_out, shifter_7_out, shifter_7_out, shifter_7_out, shifter_7_out, shifter_7_out, shifter_7_out, shifter_7_out, shifter_7_out, shifter_7_out, shifter_7_out, shifter_7_out, shifter_7_out, shifter_7_out, shifter_7_out, shifter_7_out, shifter_7_out, shifter_7_out, shifter_7_out, shifter_7_out} : 64'bz;  // Controlled_Buffer controlled_buffer_3
  assign out_2 = g4_out ? {shifter_8_out, shifter_8_out, shifter_8_out, shifter_8_out, shifter_8_out, shifter_8_out, shifter_8_out, shifter_8_out, shifter_8_out, shifter_8_out, shifter_8_out, shifter_8_out, shifter_8_out, shifter_8_out, shifter_8_out, shifter_8_out} : 64'bz;  // Controlled_Buffer controlled_buffer_4
  assign out_2 = g8_out ? {shifter_9_out, shifter_9_out, shifter_9_out, shifter_9_out, shifter_9_out, shifter_9_out, shifter_9_out, shifter_9_out} : 64'bz;  // Controlled_Buffer controlled_buffer_5
  assign out_2 = g16_out ? {shifter_10_out, shifter_10_out, shifter_10_out, shifter_10_out} : 64'bz;  // Controlled_Buffer controlled_buffer_6
endmodule

module WideImmediate (
  input  MOVK,
  input  MOVZ,
  input  MOVN,
  input  [63:0] REG_DATA,
  input  [5:0] SHAMT,
  input  [63:0] IMM_IN,
  output [63:0] IMM_OUT
);

  wire and_2_out;
  wire [63:0] and_1_out, or_1_out, shifter_1_out, shifter_2_out;

  Shifter #(.shift("rl"), .width(64)) shifter_1 (.in(64'hffffffffffff0000), .\dist (SHAMT), .out(shifter_1_out));
  Shifter #(.width(64)) shifter_2 (.in(IMM_IN), .\dist (SHAMT), .out(shifter_2_out));
  assign and_1_out = REG_DATA & shifter_1_out;  // AND_Gate and_1, 64 bits wide
  and and_2 (and_2_out, ~MOVK, ~MOVZ, ~MOVN);  // AND_Gate
  assign or_1_out = and_1_out | shifter_2_out;  // OR_Gate or_1, 64 bits wide
  assign IMM_OUT = MOVK ? or_1_out : 64'bz;  // Controlled_Buffer controlled_buffer_1
  assign IMM_OUT = MOVZ ? shifter_2_out : 64'bz;  // Controlled_Buffer controlled_buffer_2
  assign IMM_OUT = MOVN ? ~shifter_2_out : 64'bz;  // Controlled_Inverter controlled_inverter_1
  assign IMM_OUT = and_2_out ? IMM_IN : 64'bz;  // Controlled_Buffer controlled_buffer_3
endmodule
