// Logisim project added_lcd_display.circ as structural Verilog: 14 circuits, main circuit main
module main (
);

  wire and_1_out, and_2_out, arithmeticlogicunit_1_c, arithmeticlogicunit_1_n, arithmeticlogicunit_1_padd,
       arithmeticlogicunit_1_pand, arithmeticlogicunit_1_peor, arithmeticlogicunit_1_plsl,
       arithmeticlogicunit_1_plslv, arithmeticlogicunit_1_plsr, arithmeticlogicunit_1_plsrv,
       arithmeticlogicunit_1_pmul, arithmeticlogicunit_1_por, arithmeticlogicunit_1_ppass_b,
       arithmeticlogicunit_1_psmulh, arithmeticlogicunit_1_psub, arithmeticlogicunit_1_pumulh,
       arithmeticlogicunit_1_sdiv, arithmeticlogicunit_1_udiv, arithmeticlogicunit_1_v,
       arithmeticlogicunit_1_z, arithmeticlogicunit_1_zero, BSC1_scl_out, BSC1_scl_pulldown, BSC1_sda_out,
       BSC1_sda_pulldown, buffer_1_out, buffer_2_out, buffer_3_out, CLK_out, controlunit_1_adr,
       controlunit_1_alusrc, controlunit_1_b, controlunit_1_bcond_true, controlunit_1_bl, controlunit_1_br,
       controlunit_1_cbnz, controlunit_1_cbz, controlunit_1_insadd, controlunit_1_insaddi,
       controlunit_1_insaddis, controlunit_1_insadds, controlunit_1_insadr, controlunit_1_insand,
       controlunit_1_insandi, controlunit_1_insandis, controlunit_1_insands, controlunit_1_insb,
       controlunit_1_insbcond, controlunit_1_insbl, controlunit_1_insbr, controlunit_1_inscbnz,
       controlunit_1_inscbz, controlunit_1_inseor, controlunit_1_inseori, controlunit_1_insldur,
       controlunit_1_inslsl, controlunit_1_inslslv, controlunit_1_inslsr, controlunit_1_inslsrv,
       controlunit_1_insmovk, controlunit_1_insmovn, controlunit_1_insmovz, controlunit_1_insmul,
       controlunit_1_insnot_implemented, controlunit_1_insorr, controlunit_1_insorri, controlunit_1_inssdiv,
       controlunit_1_inssmulh, controlunit_1_insstur, controlunit_1_inssub, controlunit_1_inssubi,
       controlunit_1_inssubis, controlunit_1_inssubs, controlunit_1_insudiv, controlunit_1_insumulh,
       controlunit_1_memread, controlunit_1_memtoreg, controlunit_1_memwrite, controlunit_1_movk,
       controlunit_1_movn, controlunit_1_movz, controlunit_1_rdsp, controlunit_1_reg2loc,
       controlunit_1_regwrite, controlunit_1_rnsp, controlunit_1_setflags, gpio_1_gpio_scl, gpio_1_gpio_sda,
       immediateextend_1_imm9, immediateextend_1_imm12, immediateextend_1_imm13, immediateextend_1_imm16,
       immediateextend_1_imm19, immediateextend_1_imm26, immediateextend_1_sign_extend,
       immediateextend_1_zero_extend, insaddralignment_1_aligned, insaddralignment_1_not_aligned,
       insaddrrange_1_in_range, insaddrrange_1_out_of_range, memorycontroller_1_a0, memorycontroller_1_a1,
       memorycontroller_1_a2, memorycontroller_1_a3, memorycontroller_1_address_out_of_range,
       memorycontroller_1_bsc1_access, memorycontroller_1_bsc1_read, memorycontroller_1_bsc1_write,
       memorycontroller_1_data_memory_access, memorycontroller_1_data_memory_read,
       memorycontroller_1_data_memory_write, memorycontroller_1_gpio_access, memorycontroller_1_gpio_read,
       memorycontroller_1_gpio_write, memorycontroller_1_peripheral_access,
       memorycontroller_1_peripheral_access_size_invalid, memorycontroller_1_peripheral_address_not_aligned,
       memorycontroller_1_peripheral_not_implemented, memorycontroller_1_r, memorycontroller_1_w, or_1_out,
       or_2_out, pcf8574_1_sda_out, pcf8574_1_sda_pulldown, registerfile_1_we, Reset_out, xor_1_out;
  wire [1:0] controlunit_1_accesssize;
  wire [2:0] controlunit_1_immsel;
  wire [3:0] arithmeticlogicunit_1_flags, controlunit_1_aluop, FLAGS_q;
  wire [4:0] multiplexer_2_out, multiplexer_3_out, registerfile_1_ra1, registerfile_1_ra2, registerfile_1_wa;
  wire [5:0] arithmeticlogicunit_1_shamt, controlunit_1_shamt;
  wire [7:0] hd44780_1_out_13, hd44780_1_out_14, hd44780_1_out_15, hd44780_1_out_16, hd44780_1_out_17,
       hd44780_1_out_18, hd44780_1_out_19, hd44780_1_out_20, hd44780_1_out_21, hd44780_1_out_22,
       hd44780_1_out_23, hd44780_1_out_24, hd44780_1_out_25, hd44780_1_out_26, hd44780_1_out_27,
       hd44780_1_out_28, hd44780_1_out_29, hd44780_1_out_30, hd44780_1_out_31, hd44780_1_out_32,
       hd44780_1_out_33, hd44780_1_out_34, hd44780_1_out_35, hd44780_1_out_36, hd44780_1_out_37,
       hd44780_1_out_38, hd44780_1_out_39, hd44780_1_out_40, hd44780_1_out_41, hd44780_1_out_42,
       hd44780_1_out_43, hd44780_1_out_44, hd44780_1_out_45, hd44780_1_out_46, hd44780_1_out_47,
       hd44780_1_out_48, hd44780_1_out_49, hd44780_1_out_50, hd44780_1_out_51, hd44780_1_out_52,
       hd44780_1_out_53, hd44780_1_out_54, hd44780_1_out_55, hd44780_1_out_56, hd44780_1_out_57,
       hd44780_1_out_58, hd44780_1_out_59, hd44780_1_out_60, hd44780_1_out_61, hd44780_1_out_62,
       hd44780_1_out_63, hd44780_1_out_64, hd44780_1_out_65, hd44780_1_out_66, hd44780_1_out_67,
       hd44780_1_out_68, hd44780_1_out_69, hd44780_1_out_70, hd44780_1_out_71, hd44780_1_out_72,
       hd44780_1_out_73, hd44780_1_out_74, hd44780_1_out_75, hd44780_1_out_76, hd44780_1_out_77,
       hd44780_1_out_78, hd44780_1_out_79, hd44780_1_out_80, hd44780_1_out_81, hd44780_1_out_82,
       hd44780_1_out_83, hd44780_1_out_84, hd44780_1_out_85, hd44780_1_out_86, hd44780_1_out_87,
       hd44780_1_out_88, hd44780_1_out_89, hd44780_1_out_90, hd44780_1_out_91, hd44780_1_out_92,
       hd44780_1_out_93, hd44780_1_out_94, hd44780_1_out_95, hd44780_1_out_96, hd44780_1_out_97,
       hd44780_1_out_98, hd44780_1_out_99, hd44780_1_out_100, hd44780_1_out_101, hd44780_1_out_102,
       hd44780_1_out_103, hd44780_1_out_104, hd44780_1_out_105, hd44780_1_out_106, hd44780_1_out_107,
       hd44780_1_out_108, hd44780_1_out_109, hd44780_1_out_110, hd44780_1_out_111, hd44780_1_out_112,
       hd44780_1_out_113, hd44780_1_out_114, hd44780_1_out_115, hd44780_1_out_116, hd44780_1_out_117,
       hd44780_1_out_118, hd44780_1_out_119, hd44780_1_out_120, hd44780_1_out_121, hd44780_1_out_122,
       hd44780_1_out_123, hd44780_1_out_124, hd44780_1_out_125, hd44780_1_out_126, hd44780_1_out_127,
       hd44780_1_out_128, hd44780_1_out_129, hd44780_1_out_130, hd44780_1_out_131, hd44780_1_out_132,
       hd44780_1_out_133, hd44780_1_out_134, hd44780_1_out_135, hd44780_1_out_136, hd44780_1_out_137,
       hd44780_1_out_138, hd44780_1_out_139, hd44780_1_out_140, hd44780_1_out_141, hd44780_1_out_142,
       hd44780_1_out_143, hd44780_1_out_144, hd44780_1_out_145, hd44780_1_out_146, hd44780_1_out_147,
       hd44780_1_out_148, hd44780_1_out_149, hd44780_1_out_150, hd44780_1_out_151, hd44780_1_out_152,
       hd44780_1_out_153, hd44780_1_out_154, hd44780_1_out_155, hd44780_1_out_156, hd44780_1_out_157,
       hd44780_1_out_158, hd44780_1_out_159, hd44780_1_out_160, hd44780_1_out_161, hd44780_1_out_162,
       hd44780_1_out_163, hd44780_1_out_164, hd44780_1_out_165, hd44780_1_out_166, hd44780_1_out_167,
       hd44780_1_out_168, hd44780_1_out_169, hd44780_1_out_170, hd44780_1_out_171, hd44780_1_out_172,
       hd44780_1_out_173, hd44780_1_out_174, hd44780_1_out_175, hd44780_1_out_176, hd44780_1_out_177,
       hd44780_1_out_178, hd44780_1_out_179, hd44780_1_out_180, hd44780_1_out_181, hd44780_1_out_182,
       hd44780_1_out_183, hd44780_1_out_184, hd44780_1_out_185, hd44780_1_out_186, hd44780_1_out_187,
       hd44780_1_out_188, hd44780_1_out_189, hd44780_1_out_190, hd44780_1_out_191, hd44780_1_out_192,
       hd44780_1_out_193, hd44780_1_out_194, hd44780_1_out_195, hd44780_1_out_196, hd44780_1_out_197,
       hd44780_1_out_198, hd44780_1_out_199, hd44780_1_out_200, hd44780_1_out_201, hd44780_1_out_202,
       hd44780_1_out_203, hd44780_1_out_204, hd44780_1_out_205, hd44780_1_out_206, hd44780_1_out_207,
       hd44780_1_out_208, hd44780_1_out_209, hd44780_1_out_210, hd44780_1_out_211, hd44780_1_out_212,
       hd44780_1_out_213, hd44780_1_out_214, hd44780_1_out_215, hd44780_1_out_216, hd44780_1_out_217,
       hd44780_1_out_218, hd44780_1_out_219, hd44780_1_out_220, hd44780_1_out_221, hd44780_1_out_222,
       hd44780_1_out_223, hd44780_1_out_224, hd44780_1_out_225, hd44780_1_out_226, hd44780_1_out_227,
       hd44780_1_out_228, hd44780_1_out_229, hd44780_1_out_230, hd44780_1_out_231, hd44780_1_out_232,
       hd44780_1_out_233, hd44780_1_out_234, hd44780_1_out_235, hd44780_1_out_236, hd44780_1_out_237,
       hd44780_1_out_238, hd44780_1_out_239, hd44780_1_out_240, hd44780_1_out_241, hd44780_1_out_242,
       hd44780_1_out_243, hd44780_1_out_244, hd44780_1_out_245, hd44780_1_out_246, hd44780_1_out_247,
       hd44780_1_out_248, hd44780_1_out_249, hd44780_1_out_250, hd44780_1_out_251, hd44780_1_out_252,
       hd44780_1_out_253, hd44780_1_out_254, hd44780_1_out_255, hd44780_1_out_256, hd44780_1_out_257,
       hd44780_1_out_258, hd44780_1_out_259, hd44780_1_out_260, hd44780_1_out_261, hd44780_1_out_262,
       hd44780_1_out_263, hd44780_1_out_264, hd44780_1_out_265, hd44780_1_out_266, hd44780_1_out_267,
       hd44780_1_out_268, hd44780_1_out_269, hd44780_1_out_270, hd44780_1_out_271, hd44780_1_out_272,
       hd44780_1_out_273, hd44780_1_out_274, hd44780_1_out_275, hd44780_1_out_276, hd44780_1_out_277,
       hd44780_1_out_278, hd44780_1_out_279, hd44780_1_out_280, hd44780_1_out_281, hd44780_1_out_282,
       hd44780_1_out_283, hd44780_1_out_284, hd44780_1_out_285, hd44780_1_out_286, hd44780_1_out_287,
       hd44780_1_out_288, hd44780_1_out_289, hd44780_1_out_290, hd44780_1_out_291, hd44780_1_out_292,
       hd44780_1_out_293, hd44780_1_out_294, hd44780_1_out_295, hd44780_1_out_296, hd44780_1_out_297,
       hd44780_1_out_298, hd44780_1_out_299, hd44780_1_out_300, hd44780_1_out_301, hd44780_1_out_302,
       hd44780_1_out_303, hd44780_1_out_304, hd44780_1_out_305, hd44780_1_out_306, hd44780_1_out_307,
       hd44780_1_out_308, hd44780_1_out_309, hd44780_1_out_310, hd44780_1_out_311, hd44780_1_out_312,
       hd44780_1_out_313, hd44780_1_out_314, hd44780_1_out_315, hd44780_1_out_316, hd44780_1_out_317,
       hd44780_1_out_318, hd44780_1_out_319, hd44780_1_out_320, hd44780_1_out_321, hd44780_1_out_322,
       hd44780_1_out_323, hd44780_1_out_324, hd44780_1_out_325, hd44780_1_out_326, hd44780_1_out_327,
       hd44780_1_out_328, hd44780_1_out_329, hd44780_1_out_330, hd44780_1_out_331, hd44780_1_out_332,
       hd44780_1_out_333, hd44780_1_out_334, hd44780_1_out_335, hd44780_1_out_336, hd44780_1_out_337,
       hd44780_1_out_338, hd44780_1_out_339, hd44780_1_out_340, hd44780_1_out_341, hd44780_1_out_342,
       hd44780_1_out_343, hd44780_1_out_344, hd44780_1_out_345, hd44780_1_out_346, hd44780_1_out_347,
       hd44780_1_out_348, hd44780_1_out_349, hd44780_1_out_350, hd44780_1_out_351, hd44780_1_out_352,
       hd44780_1_out_353, hd44780_1_out_354, hd44780_1_out_355, hd44780_1_out_356, hd44780_1_out_357,
       hd44780_1_out_358, hd44780_1_out_359, hd44780_1_out_360, hd44780_1_out_361, hd44780_1_out_362,
       hd44780_1_out_363, hd44780_1_out_364, hd44780_1_out_365, hd44780_1_out_366, hd44780_1_out_367,
       hd44780_1_out_368, hd44780_1_out_369, hd44780_1_out_370, hd44780_1_out_371, hd44780_1_out_372,
       hd44780_1_out_373, hd44780_1_out_374, hd44780_1_out_375, hd44780_1_out_376, hd44780_1_out_377,
       hd44780_1_out_378, hd44780_1_out_379, hd44780_1_out_380, hd44780_1_out_381, hd44780_1_out_382,
       hd44780_1_out_383, hd44780_1_out_384, hd44780_1_out_385, hd44780_1_out_386, hd44780_1_out_387,
       hd44780_1_out_388, hd44780_1_out_389, hd44780_1_out_390, hd44780_1_out_391, hd44780_1_out_392,
       hd44780_1_out_393, hd44780_1_out_394, hd44780_1_out_395, hd44780_1_out_396, hd44780_1_out_397,
       hd44780_1_out_398, hd44780_1_out_399, hd44780_1_out_400, hd44780_1_out_401, hd44780_1_out_402,
       hd44780_1_out_403, hd44780_1_out_404, hd44780_1_out_405, hd44780_1_out_406, hd44780_1_out_407,
       hd44780_1_out_408, hd44780_1_out_409, hd44780_1_out_410, hd44780_1_out_411, hd44780_1_out_412,
       INSTRUCTION_MEMORY_p2, INSTRUCTION_MEMORY_p3, INSTRUCTION_MEMORY_p4, INSTRUCTION_MEMORY_p5,
       memorycontroller_1_bsc1_address, memorycontroller_1_data_memory_byte_enable,
       memorycontroller_1_gpio_address, pcf8574_1_data_out, ram_1_p12, ram_1_p13, ram_1_p14, ram_1_p15,
       ram_1_p16, ram_1_p17, ram_1_p18, ram_1_p19;
  wire [23:0] memorycontroller_1_data_memory_address;
  wire [53:0] gpio_1_gpio_drive, gpio_1_gpio_out, undriven;
  wire [63:0] adder_1_out, adder_2_out, and_3_out, arithmeticlogicunit_1_o11, arithmeticlogicunit_1_o12,
       arithmeticlogicunit_1_o13, arithmeticlogicunit_1_o21, arithmeticlogicunit_1_o22,
       arithmeticlogicunit_1_o23, arithmeticlogicunit_1_r1, arithmeticlogicunit_1_r2,
       arithmeticlogicunit_1_r3, arithmeticlogicunit_1_result, BSC1_data_out, controlled_buffer_1_out,
       gpio_1_data_out, immediateextend_1_extended1, immediateextend_1_extended2,
       immediateextend_1_extended3, immediateextend_1_immediate, memorycontroller_1_access_mask,
       memorycontroller_1_data_out, multiplexer_1_out, multiplexer_4_out, multiplexer_5_out,
       multiplexer_6_out, multiplexer_7_out, multiplexer_8_out, multiplexer_9_out, PC_q, registerfile_1_rd11,
       registerfile_1_rd12, registerfile_1_rd13, registerfile_1_rd21, registerfile_1_rd22,
       registerfile_1_rd23, registerfile_1_read_data1, registerfile_1_read_data2, registerfile_1_wd1,
       registerfile_1_wd2, registerfile_1_wd3, shifter_1_out, wideimmediate_1_imm_out;

  Button Reset (.out(Reset_out));
  buf buffer_1 (buffer_1_out, Reset_out);
  Clock CLK (.out(CLK_out));
  buf buffer_2 (buffer_2_out, buffer_1_out);
  buf buffer_3 (buffer_3_out, buffer_2_out);
  Register #(.width(64)) PC (.D(multiplexer_1_out), .en(1'b1), .clk(xor_1_out), .Q(PC_q));  // open: clr
  Multiplexer #(.enable("false"), .width(64)) multiplexer_1 (
    .in0(multiplexer_6_out), .in1(64'h80000), .out(multiplexer_1_out), .sel(or_1_out));
  or or_1 (or_1_out, Reset_out, buffer_3_out);
  xor xor_1 (xor_1_out, buffer_3_out, CLK_out);
  // ROM #(.addrWidth(24), .line("quad")) INSTRUCTION_MEMORY: pin names not known; wires that end beside it: PC_q[23:0], INSTRUCTION_MEMORY_p2, INSTRUCTION_MEMORY_p3, INSTRUCTION_MEMORY_p4, INSTRUCTION_MEMORY_p5
  Adder #(.width(64)) adder_1 (.a(64'h4), .b(PC_q), .out(adder_1_out), .cin(1'b0));  // open: cout
  LED led_1 (.in(insaddralignment_1_aligned));
  LED led_2 (.in(insaddralignment_1_not_aligned));
  LED led_3 (.in(insaddrrange_1_in_range));
  LED led_4 (.in(insaddrrange_1_out_of_range));
  InsAddrAlignment insaddralignment_1 (
    .ALIGNED(insaddralignment_1_aligned), .NOT_ALIGNED(insaddralignment_1_not_aligned), .ADDR(PC_q));
  InsAddrRange insaddrrange_1 (
    .IN_RANGE(insaddrrange_1_in_range), .OUT_OF_RANGE(insaddrrange_1_out_of_range), .ADDR(PC_q));
  LED led_5 (.in(controlunit_1_insnot_implemented));
  LED led_6 (.in(controlunit_1_insb));
  LED led_7 (.in(controlunit_1_insbl));
  LED led_8 (.in(controlunit_1_insbr));
  LED led_9 (.in(controlunit_1_insldur));
  LED led_10 (.in(controlunit_1_insand));
  LED led_11 (.in(controlunit_1_insorr));
  LED led_12 (.in(controlunit_1_inseor));
  LED led_13 (.in(controlunit_1_insadd));
  LED led_14 (.in(controlunit_1_inssub));
  LED led_15 (.in(controlunit_1_insands));
  LED led_16 (.in(controlunit_1_insadds));
  LED led_17 (.in(controlunit_1_inssubs));
  LED led_18 (.in(controlunit_1_inslsl));
  LED led_19 (.in(controlunit_1_inslsr));
  LED led_20 (.in(controlunit_1_insmovk));
  LED led_21 (.in(controlunit_1_insmovn));
  LED led_22 (.in(controlunit_1_insumulh));
  LED led_23 (.in(controlunit_1_insudiv));
  LED led_24 (.in(controlunit_1_insadr));
  LED led_25 (.in(controlunit_1_insbcond));
  LED led_26 (.in(controlunit_1_inscbz));
  LED led_27 (.in(controlunit_1_inscbnz));
  LED led_28 (.in(controlunit_1_insstur));
  LED led_29 (.in(controlunit_1_insandi));
  LED led_30 (.in(controlunit_1_insorri));
  LED led_31 (.in(controlunit_1_inseori));
  LED led_32 (.in(controlunit_1_insaddi));
  LED led_33 (.in(controlunit_1_inssubi));
  LED led_34 (.in(controlunit_1_insandis));
  LED led_35 (.in(controlunit_1_insaddis));
  LED led_36 (.in(controlunit_1_inssubis));
  LED led_37 (.in(controlunit_1_inslslv));
  LED led_38 (.in(controlunit_1_inslsrv));
  LED led_39 (.in(controlunit_1_insmovz));
  LED led_40 (.in(controlunit_1_insmul));
  LED led_41 (.in(controlunit_1_inssmulh));
  LED led_42 (.in(controlunit_1_inssdiv));
  ControlUnit controlunit_1 (
    .insB(controlunit_1_insb), .insBL(controlunit_1_insbl), .insBR(controlunit_1_insbr),
    .insCBZ(controlunit_1_inscbz), .insCBNZ(controlunit_1_inscbnz), .insBCOND(controlunit_1_insbcond),
    .insSTUR(controlunit_1_insstur), .insLDUR(controlunit_1_insldur), .insAND(controlunit_1_insand),
    .insORR(controlunit_1_insorr), .insEOR(controlunit_1_inseor), .insADD(controlunit_1_insadd),
    .insSUB(controlunit_1_inssub), .insANDI(controlunit_1_insandi), .insORRI(controlunit_1_insorri),
    .insEORI(controlunit_1_inseori), .insADDI(controlunit_1_insaddi), .insSUBI(controlunit_1_inssubi),
    .insANDS(controlunit_1_insands), .insADDS(controlunit_1_insadds), .insSUBS(controlunit_1_inssubs),
    .insANDIS(controlunit_1_insandis), .insADDIS(controlunit_1_insaddis), .insSUBIS(controlunit_1_inssubis),
    .insLSL(controlunit_1_inslsl), .insLSR(controlunit_1_inslsr), .insMOVK(controlunit_1_insmovk),
    .insMOVZ(controlunit_1_insmovz), .insMOVN(controlunit_1_insmovn), .insLSLV(controlunit_1_inslslv),
    .insLSRV(controlunit_1_inslsrv), .insMUL(controlunit_1_insmul), .insUMULH(controlunit_1_insumulh),
    .insSMULH(controlunit_1_inssmulh), .insUDIV(controlunit_1_insudiv), .insSDIV(controlunit_1_inssdiv),
    .insADR(controlunit_1_insadr), .insNOT_IMPLEMENTED(controlunit_1_insnot_implemented),
    .AccessSize(controlunit_1_accesssize), .B(controlunit_1_b), .BL(controlunit_1_bl), .BR(controlunit_1_br),
    .CBZ(controlunit_1_cbz), .CBNZ(controlunit_1_cbnz), .MOVK(controlunit_1_movk), .MOVZ(controlunit_1_movz),
    .MOVN(controlunit_1_movn), .ADR(controlunit_1_adr), .Reg2Loc(controlunit_1_reg2loc),
    .RegWrite(controlunit_1_regwrite), .MemRead(controlunit_1_memread), .MemWrite(controlunit_1_memwrite),
    .ALUSrc(controlunit_1_alusrc), .MemtoReg(controlunit_1_memtoreg), .ALUop(controlunit_1_aluop),
    .ImmSel(controlunit_1_immsel), .SetFlags(controlunit_1_setflags), .RdSP(controlunit_1_rdsp),
    .RnSP(controlunit_1_rnsp), .Shamt(controlunit_1_shamt), .BCOND_TRUE(controlunit_1_bcond_true),
    .INS({INSTRUCTION_MEMORY_p5, INSTRUCTION_MEMORY_p4, INSTRUCTION_MEMORY_p3, INSTRUCTION_MEMORY_p2}),
    .FLAGS(FLAGS_q));
  Multiplexer #(.enable("false"), .width(5)) multiplexer_2 (
    .in0(INSTRUCTION_MEMORY_p4[4:0]), .in1(INSTRUCTION_MEMORY_p2[4:0]), .out(multiplexer_2_out),
    .sel(controlunit_1_reg2loc));
  Multiplexer #(.enable("false"), .width(5)) multiplexer_3 (
    .in0(INSTRUCTION_MEMORY_p2[4:0]), .in1(5'b11110), .out(multiplexer_3_out), .sel(controlunit_1_bl));
  // Probe on registerfile_1_ra1
  // Probe on registerfile_1_ra2
  // Probe on registerfile_1_wa
  LED led_43 (.in(registerfile_1_we));
  LED led_44 (.in(immediateextend_1_zero_extend));
  LED led_45 (.in(immediateextend_1_imm9));
  LED led_46 (.in(immediateextend_1_imm12));
  LED led_47 (.in(immediateextend_1_imm13));
  // Probe on immediateextend_1_extended2
  // Probe on immediateextend_1_extended3
  // Probe on registerfile_1_rd11
  // Probe on registerfile_1_rd12
  // Probe on registerfile_1_rd13
  // Probe on registerfile_1_rd23
  // Probe on registerfile_1_rd22
  // Probe on registerfile_1_rd21
  // Probe on registerfile_1_wd1
  // Probe on registerfile_1_wd3
  // Probe on registerfile_1_wd2
  LED led_48 (.in(immediateextend_1_sign_extend));
  LED led_49 (.in(immediateextend_1_imm16));
  LED led_50 (.in(immediateextend_1_imm19));
  LED led_51 (.in(immediateextend_1_imm26));
  // Probe on immediateextend_1_extended1
  RegisterFile registerfile_1 (
    .RD11(registerfile_1_rd11), .RD12(registerfile_1_rd12), .RD13(registerfile_1_rd13),
    .RD21(registerfile_1_rd21), .RD22(registerfile_1_rd22), .RD23(registerfile_1_rd23),
    .READ_DATA1(registerfile_1_read_data1), .READ_DATA2(registerfile_1_read_data2), .WE(registerfile_1_we),
    .RA1(registerfile_1_ra1), .RA2(registerfile_1_ra2), .WA(registerfile_1_wa), .WD1(registerfile_1_wd1),
    .WD2(registerfile_1_wd2), .WD3(registerfile_1_wd3), .WRITE_USE_SP(controlunit_1_rdsp),
    .READ1_USE_SP(controlunit_1_rnsp), .WRITE_ENABLE(controlunit_1_regwrite), .CLOCK(CLK_out),
    .READ_ADDR1({INSTRUCTION_MEMORY_p3[1:0], INSTRUCTION_MEMORY_p2[7:5]}), .READ_ADDR2(multiplexer_2_out),
    .WRITE_ADDR(multiplexer_3_out), .WRITE_DATA(multiplexer_9_out));
  ImmediateExtend immediateextend_1 (
    .SIGN_EXTEND(immediateextend_1_sign_extend), .IMM12(immediateextend_1_imm12),
    .IMM9(immediateextend_1_imm9), .IMM26(immediateextend_1_imm26), .IMM19(immediateextend_1_imm19),
    .IMM16(immediateextend_1_imm16), .IMM13(immediateextend_1_imm13),
    .IMMEDIATE(immediateextend_1_immediate), .ZERO_EXTEND(immediateextend_1_zero_extend),
    .EXTENDED1(immediateextend_1_extended1), .EXTENDED2(immediateextend_1_extended2),
    .EXTENDED3(immediateextend_1_extended3), .CTRL(controlunit_1_immsel),
    .INS({INSTRUCTION_MEMORY_p5, INSTRUCTION_MEMORY_p4, INSTRUCTION_MEMORY_p3, INSTRUCTION_MEMORY_p2}));
  Shifter #(.width(64)) shifter_1 (.in(immediateextend_1_immediate), .\dist (6'b000010), .out(shifter_1_out));
  WideImmediate wideimmediate_1 (
    .IMM_OUT(wideimmediate_1_imm_out), .MOVK(controlunit_1_movk), .MOVZ(controlunit_1_movz),
    .MOVN(controlunit_1_movn), .REG_DATA(registerfile_1_read_data2), .SHAMT(controlunit_1_shamt),
    .IMM_IN(immediateextend_1_immediate));
  Adder #(.width(64)) adder_2 (.a(PC_q), .b(shifter_1_out), .out(adder_2_out), .cin(1'b0));  // open: cout
  Multiplexer #(.enable("false"), .width(64)) multiplexer_4 (
    .in0(registerfile_1_read_data2), .in1(wideimmediate_1_imm_out), .out(multiplexer_4_out),
    .sel(controlunit_1_alusrc));
  Multiplexer #(.enable("false"), .width(64)) multiplexer_5 (
    .in0(adder_2_out), .in1(registerfile_1_read_data1), .out(multiplexer_5_out), .sel(controlunit_1_br));
  LED led_52 (.in(arithmeticlogicunit_1_pand));
  LED led_53 (.in(arithmeticlogicunit_1_por));
  LED led_54 (.in(arithmeticlogicunit_1_peor));
  LED led_55 (.in(arithmeticlogicunit_1_padd));
  LED led_56 (.in(arithmeticlogicunit_1_psub));
  LED led_57 (.in(arithmeticlogicunit_1_plsl));
  LED led_58 (.in(arithmeticlogicunit_1_plsr));
  LED led_59 (.in(arithmeticlogicunit_1_plslv));
  LED led_60 (.in(arithmeticlogicunit_1_plsrv));
  LED led_61 (.in(arithmeticlogicunit_1_pmul));
  LED led_62 (.in(arithmeticlogicunit_1_pumulh));
  LED led_63 (.in(arithmeticlogicunit_1_psmulh));
  LED led_64 (.in(arithmeticlogicunit_1_udiv));
  LED led_65 (.in(arithmeticlogicunit_1_sdiv));
  LED led_66 (.in(arithmeticlogicunit_1_ppass_b));
  // Probe on arithmeticlogicunit_1_o12
  // Probe on arithmeticlogicunit_1_o13
  // Probe on arithmeticlogicunit_1_o22
  // Probe on arithmeticlogicunit_1_o23
  // Probe on arithmeticlogicunit_1_r2
  // Probe on arithmeticlogicunit_1_r3
  // Probe on arithmeticlogicunit_1_shamt
  // Probe on arithmeticlogicunit_1_o11
  // Probe on arithmeticlogicunit_1_o21
  // Probe on arithmeticlogicunit_1_r1
  LED led_67 (.in(arithmeticlogicunit_1_z));
  LED led_68 (.in(arithmeticlogicunit_1_n));
  LED led_69 (.in(arithmeticlogicunit_1_c));
  LED led_70 (.in(arithmeticlogicunit_1_v));
  ArithmeticLogicUnit arithmeticlogicunit_1 (
    .pAND(arithmeticlogicunit_1_pand), .pOR(arithmeticlogicunit_1_por), .pEOR(arithmeticlogicunit_1_peor),
    .pADD(arithmeticlogicunit_1_padd), .pSUB(arithmeticlogicunit_1_psub), .pLSL(arithmeticlogicunit_1_plsl),
    .pLSR(arithmeticlogicunit_1_plsr), .pLSLV(arithmeticlogicunit_1_plslv),
    .pLSRV(arithmeticlogicunit_1_plsrv), .pMUL(arithmeticlogicunit_1_pmul),
    .pUMULH(arithmeticlogicunit_1_pumulh), .pSMULH(arithmeticlogicunit_1_psmulh),
    .UDIV(arithmeticlogicunit_1_udiv), .SDIV(arithmeticlogicunit_1_sdiv),
    .pPASS_B(arithmeticlogicunit_1_ppass_b), .R1(arithmeticlogicunit_1_r1), .R2(arithmeticlogicunit_1_r2),
    .R3(arithmeticlogicunit_1_r3), .RESULT(arithmeticlogicunit_1_result), .ZERO(arithmeticlogicunit_1_zero),
    .Z(arithmeticlogicunit_1_z), .N(arithmeticlogicunit_1_n), .FLAGS(arithmeticlogicunit_1_flags),
    .C(arithmeticlogicunit_1_c), .V(arithmeticlogicunit_1_v), .SHAMT(arithmeticlogicunit_1_shamt),
    .O11(arithmeticlogicunit_1_o11), .O12(arithmeticlogicunit_1_o12), .O13(arithmeticlogicunit_1_o13),
    .O21(arithmeticlogicunit_1_o21), .O22(arithmeticlogicunit_1_o22), .O23(arithmeticlogicunit_1_o23),
    .SHIFT_AMOUNT(controlunit_1_shamt), .OPERAND1(registerfile_1_read_data1), .OPERAND2(multiplexer_4_out),
    .ALU_OP(controlunit_1_aluop));
  and and_1 (and_1_out, controlunit_1_cbz, arithmeticlogicunit_1_zero);
  and and_2 (and_2_out, controlunit_1_cbnz, ~arithmeticlogicunit_1_zero);  // AND_Gate
  Register #(.width(4)) FLAGS (
    .D(arithmeticlogicunit_1_flags), .en(controlunit_1_setflags), .clk(CLK_out), .Q(FLAGS_q));  // open: clr
  Multiplexer #(.enable("false"), .width(64)) multiplexer_6 (
    .in0(adder_1_out), .in1(multiplexer_5_out), .out(multiplexer_6_out), .sel(or_2_out));
  or or_2 (or_2_out, controlunit_1_b, controlunit_1_bl, controlunit_1_br, controlunit_1_bcond_true, and_1_out, and_2_out);
  LED led_71 (.in(memorycontroller_1_r));
  LED led_72 (.in(memorycontroller_1_a0));
  LED led_73 (.in(memorycontroller_1_a2));
  LED led_74 (.in(memorycontroller_1_gpio_access));
  LED led_75 (.in(memorycontroller_1_peripheral_not_implemented));
  LED led_76 (.in(memorycontroller_1_peripheral_access_size_invalid));
  LED led_77 (.in(memorycontroller_1_w));
  LED led_78 (.in(memorycontroller_1_a1));
  LED led_79 (.in(memorycontroller_1_a3));
  LED led_80 (.in(memorycontroller_1_data_memory_access));
  LED led_81 (.in(memorycontroller_1_peripheral_access));
  LED led_82 (.in(memorycontroller_1_bsc1_access));
  LED led_83 (.in(memorycontroller_1_peripheral_address_not_aligned));
  LED led_84 (.in(memorycontroller_1_address_out_of_range));
  MemoryController memorycontroller_1 (
    .A1(memorycontroller_1_a1), .A2(memorycontroller_1_a2), .R(memorycontroller_1_r),
    .W(memorycontroller_1_w), .A3(memorycontroller_1_a3), .GPIO_ADDRESS(memorycontroller_1_gpio_address),
    .BSC1_ACCESS(memorycontroller_1_bsc1_access), .BSC1_ADDRESS(memorycontroller_1_bsc1_address),
    .PERIPHERAL_ACCESS(memorycontroller_1_peripheral_access),
    .ADDRESS_OUT_OF_RANGE(memorycontroller_1_address_out_of_range),
    .DATA_MEMORY_ADDRESS(memorycontroller_1_data_memory_address),
    .DATA_MEMORY_READ(memorycontroller_1_data_memory_read), .DATA_OUT(memorycontroller_1_data_out),
    .DATA_MEMORY_WRITE(memorycontroller_1_data_memory_write), .A0(memorycontroller_1_a0),
    .DATA_MEMORY_BYTE_ENABLE(memorycontroller_1_data_memory_byte_enable),
    .DATA_MEMORY_ACCESS(memorycontroller_1_data_memory_access), .GPIO_ACCESS(memorycontroller_1_gpio_access),
    .PERIPHERAL_ADDRESS_NOT_ALIGNED(memorycontroller_1_peripheral_address_not_aligned),
    .PERIPHERAL_ACCESS_SIZE_INVALID(memorycontroller_1_peripheral_access_size_invalid),
    .GPIO_READ(memorycontroller_1_gpio_read), .GPIO_WRITE(memorycontroller_1_gpio_write),
    .BSC1_READ(memorycontroller_1_bsc1_read), .BSC1_WRITE(memorycontroller_1_bsc1_write),
    .PERIPHERAL_NOT_IMPLEMENTED(memorycontroller_1_peripheral_not_implemented),
    .ACCESS_MASK(memorycontroller_1_access_mask), .ADDRESS(arithmeticlogicunit_1_result),
    .DATA_IN(registerfile_1_read_data2), .ACCESS_SIZE(controlunit_1_accesssize),
    .MEM_READ(controlunit_1_memread), .MEM_WRITE(controlunit_1_memwrite));
  // RAM #(.addrWidth(24), .enables("line"), .line("octo"), .misaligned("true")) ram_1: pin names not known; wires that end beside it: memorycontroller_1_data_memory_address, memorycontroller_1_data_memory_write, CLK_out, memorycontroller_1_data_out[7:0], memorycontroller_1_data_out[15:8], memorycontroller_1_data_out[23:16], memorycontroller_1_data_out[31:24], memorycontroller_1_data_out[39:32], memorycontroller_1_data_out[47:40], memorycontroller_1_data_out[55:48], memorycontroller_1_data_out[63:56], ram_1_p12, ram_1_p13, ram_1_p14, ram_1_p15, ram_1_p16, ram_1_p17, ram_1_p18, ram_1_p19
  GPIO gpio_1 (
    .GPIO_SDA(gpio_1_gpio_sda), .GPIO_SCL(gpio_1_gpio_scl), .GPIO_OUT(gpio_1_gpio_out),
    .GPIO_DRIVE(gpio_1_gpio_drive), .DATA_OUT(gpio_1_data_out), .SDA_GPIO(BSC1_sda_out),
    .SCL_GPIO(BSC1_scl_out), .SDA_DRIVE(BSC1_sda_pulldown), .SCL_DRIVE(BSC1_scl_pulldown),
    .GPIO_IN(undriven), .CLK(CLK_out), .WRITE(memorycontroller_1_gpio_write),
    .ADDR(memorycontroller_1_gpio_address), .DATA_IN(memorycontroller_1_data_out));
  I2C_master BSC1 (
    .DATA_IN(memorycontroller_1_data_out), .WRITE(memorycontroller_1_bsc1_write),
    .ADDR(memorycontroller_1_bsc1_address), .CLK(CLK_out), .SCL_IN(gpio_1_gpio_scl),
    .SDA_IN(gpio_1_gpio_sda), .DATA_OUT(BSC1_data_out), .SDA_OUT(BSC1_sda_out),
    .SDA_PULLDOWN(BSC1_sda_pulldown), .SCL_OUT(BSC1_scl_out), .SCL_PULLDOWN(BSC1_scl_pulldown));
  assign controlled_buffer_1_out = memorycontroller_1_data_memory_read ? {ram_1_p19, ram_1_p18, ram_1_p17, ram_1_p16, ram_1_p15, ram_1_p14, ram_1_p13, ram_1_p12} : 64'bz;  // Controlled_Buffer controlled_buffer_1
  assign controlled_buffer_1_out = memorycontroller_1_gpio_read ? gpio_1_data_out : 64'bz;  // Controlled_Buffer controlled_buffer_2
  assign controlled_buffer_1_out = memorycontroller_1_bsc1_read ? BSC1_data_out : 64'bz;  // Controlled_Buffer controlled_buffer_3
  assign and_3_out = controlled_buffer_1_out & memorycontroller_1_access_mask;  // AND_Gate and_3, 64 bits wide
  LED RED_LED (.in(gpio_1_gpio_out[5]));
  LED GREEN_LED (.in(gpio_1_gpio_out[6]));
  assign undriven[2] = gpio_1_gpio_drive[2] ? gpio_1_gpio_out[2] : 1'bz;  // Controlled_Buffer controlled_buffer_4
  assign undriven[3] = gpio_1_gpio_drive[3] ? gpio_1_gpio_out[3] : 1'bz;  // Controlled_Buffer controlled_buffer_5
  Multiplexer #(.enable("false"), .width(64)) multiplexer_7 (
    .in0(arithmeticlogicunit_1_result), .in1(and_3_out), .out(multiplexer_7_out), .sel(controlunit_1_memtoreg));
  Multiplexer #(.enable("false"), .width(64)) multiplexer_8 (
    .in0(multiplexer_7_out), .in1(adder_1_out), .out(multiplexer_8_out), .sel(controlunit_1_bl));
  Multiplexer #(.enable("false"), .width(64)) multiplexer_9 (
    .in0(multiplexer_8_out), .in1(multiplexer_5_out), .out(multiplexer_9_out), .sel(controlunit_1_adr));
  Pull_Resistor #(.pull(1)) pull_resistor_1 (.node(undriven[2]));
  Pull_Resistor #(.pull(1)) pull_resistor_2 (.node(undriven[3]));
  assign undriven[2] = pcf8574_1_sda_pulldown ? pcf8574_1_sda_out : 1'bz;  // Controlled_Buffer controlled_buffer_6
  PCF8574 pcf8574_1 (
    .SDA_IN(undriven[2]), .SCL(undriven[3]), .SDA_OUT(pcf8574_1_sda_out),
    .SDA_PULLDOWN(pcf8574_1_sda_pulldown), .DATA_OUT(pcf8574_1_data_out));
  DotMatrix #(.matrixrows(8)) dotmatrix_1 (
    .col0(hd44780_1_out_13), .col1(hd44780_1_out_33), .col2(hd44780_1_out_53), .col3(hd44780_1_out_73),
    .col4(hd44780_1_out_93));
  DotMatrix #(.matrixrows(8)) dotmatrix_2 (
    .col0(hd44780_1_out_113), .col1(hd44780_1_out_133), .col2(hd44780_1_out_153), .col3(hd44780_1_out_173),
    .col4(hd44780_1_out_193));
  DotMatrix #(.matrixrows(8)) dotmatrix_3 (
    .col0(hd44780_1_out_213), .col1(hd44780_1_out_233), .col2(hd44780_1_out_253), .col3(hd44780_1_out_273),
    .col4(hd44780_1_out_293));
  DotMatrix #(.matrixrows(8)) dotmatrix_4 (
    .col0(hd44780_1_out_313), .col1(hd44780_1_out_333), .col2(hd44780_1_out_353), .col3(hd44780_1_out_373),
    .col4(hd44780_1_out_393));
  DotMatrix #(.matrixrows(8)) dotmatrix_5 (
    .col0(hd44780_1_out_14), .col1(hd44780_1_out_34), .col2(hd44780_1_out_54), .col3(hd44780_1_out_74),
    .col4(hd44780_1_out_94));
  DotMatrix #(.matrixrows(8)) dotmatrix_6 (
    .col0(hd44780_1_out_15), .col1(hd44780_1_out_35), .col2(hd44780_1_out_55), .col3(hd44780_1_out_75),
    .col4(hd44780_1_out_95));
  DotMatrix #(.matrixrows(8)) dotmatrix_7 (
    .col0(hd44780_1_out_114), .col1(hd44780_1_out_134), .col2(hd44780_1_out_154), .col3(hd44780_1_out_174),
    .col4(hd44780_1_out_194));
  DotMatrix #(.matrixrows(8)) dotmatrix_8 (
    .col0(hd44780_1_out_115), .col1(hd44780_1_out_135), .col2(hd44780_1_out_155), .col3(hd44780_1_out_175),
    .col4(hd44780_1_out_195));
  DotMatrix #(.matrixrows(8)) dotmatrix_9 (
    .col0(hd44780_1_out_214), .col1(hd44780_1_out_234), .col2(hd44780_1_out_254), .col3(hd44780_1_out_274),
    .col4(hd44780_1_out_294));
  DotMatrix #(.matrixrows(8)) dotmatrix_10 (
    .col0(hd44780_1_out_215), .col1(hd44780_1_out_235), .col2(hd44780_1_out_255), .col3(hd44780_1_out_275),
    .col4(hd44780_1_out_295));
  DotMatrix #(.matrixrows(8)) dotmatrix_11 (
    .col0(hd44780_1_out_314), .col1(hd44780_1_out_334), .col2(hd44780_1_out_354), .col3(hd44780_1_out_374),
    .col4(hd44780_1_out_394));
  DotMatrix #(.matrixrows(8)) dotmatrix_12 (
    .col0(hd44780_1_out_315), .col1(hd44780_1_out_335), .col2(hd44780_1_out_355), .col3(hd44780_1_out_375),
    .col4(hd44780_1_out_395));
  DotMatrix #(.matrixrows(8)) dotmatrix_13 (
    .col0(hd44780_1_out_16), .col1(hd44780_1_out_36), .col2(hd44780_1_out_56), .col3(hd44780_1_out_76),
    .col4(hd44780_1_out_96));
  DotMatrix #(.matrixrows(8)) dotmatrix_14 (
    .col0(hd44780_1_out_116), .col1(hd44780_1_out_136), .col2(hd44780_1_out_156), .col3(hd44780_1_out_176),
    .col4(hd44780_1_out_196));
  DotMatrix #(.matrixrows(8)) dotmatrix_15 (
    .col0(hd44780_1_out_216), .col1(hd44780_1_out_236), .col2(hd44780_1_out_256), .col3(hd44780_1_out_276),
    .col4(hd44780_1_out_296));
  DotMatrix #(.matrixrows(8)) dotmatrix_16 (
    .col0(hd44780_1_out_316), .col1(hd44780_1_out_336), .col2(hd44780_1_out_356), .col3(hd44780_1_out_376),
    .col4(hd44780_1_out_396));
  DotMatrix #(.matrixrows(8)) dotmatrix_17 (
    .col0(hd44780_1_out_17), .col1(hd44780_1_out_37), .col2(hd44780_1_out_57), .col3(hd44780_1_out_77),
    .col4(hd44780_1_out_97));
  DotMatrix #(.matrixrows(8)) dotmatrix_18 (
    .col0(hd44780_1_out_117), .col1(hd44780_1_out_137), .col2(hd44780_1_out_157), .col3(hd44780_1_out_177),
    .col4(hd44780_1_out_197));
  DotMatrix #(.matrixrows(8)) dotmatrix_19 (
    .col0(hd44780_1_out_217), .col1(hd44780_1_out_237), .col2(hd44780_1_out_257), .col3(hd44780_1_out_277),
    .col4(hd44780_1_out_297));
  DotMatrix #(.matrixrows(8)) dotmatrix_20 (
    .col0(hd44780_1_out_317), .col1(hd44780_1_out_337), .col2(hd44780_1_out_357), .col3(hd44780_1_out_377),
    .col4(hd44780_1_out_397));
  DotMatrix #(.matrixrows(8)) dotmatrix_21 (
    .col0(hd44780_1_out_18), .col1(hd44780_1_out_38), .col2(hd44780_1_out_58), .col3(hd44780_1_out_78),
    .col4(hd44780_1_out_98));
  DotMatrix #(.matrixrows(8)) dotmatrix_22 (
    .col0(hd44780_1_out_19), .col1(hd44780_1_out_39), .col2(hd44780_1_out_59), .col3(hd44780_1_out_79),
    .col4(hd44780_1_out_99));
  DotMatrix #(.matrixrows(8)) dotmatrix_23 (
    .col0(hd44780_1_out_118), .col1(hd44780_1_out_138), .col2(hd44780_1_out_158), .col3(hd44780_1_out_178),
    .col4(hd44780_1_out_198));
  DotMatrix #(.matrixrows(8)) dotmatrix_24 (
    .col0(hd44780_1_out_119), .col1(hd44780_1_out_139), .col2(hd44780_1_out_159), .col3(hd44780_1_out_179),
    .col4(hd44780_1_out_199));
  DotMatrix #(.matrixrows(8)) dotmatrix_25 (
    .col0(hd44780_1_out_218), .col1(hd44780_1_out_238), .col2(hd44780_1_out_258), .col3(hd44780_1_out_278),
    .col4(hd44780_1_out_298));
  DotMatrix #(.matrixrows(8)) dotmatrix_26 (
    .col0(hd44780_1_out_219), .col1(hd44780_1_out_239), .col2(hd44780_1_out_259), .col3(hd44780_1_out_279),
    .col4(hd44780_1_out_299));
  DotMatrix #(.matrixrows(8)) dotmatrix_27 (
    .col0(hd44780_1_out_318), .col1(hd44780_1_out_338), .col2(hd44780_1_out_358), .col3(hd44780_1_out_378),
    .col4(hd44780_1_out_398));
  DotMatrix #(.matrixrows(8)) dotmatrix_28 (
    .col0(hd44780_1_out_319), .col1(hd44780_1_out_339), .col2(hd44780_1_out_359), .col3(hd44780_1_out_379),
    .col4(hd44780_1_out_399));
  DotMatrix #(.matrixrows(8)) dotmatrix_29 (
    .col0(hd44780_1_out_20), .col1(hd44780_1_out_40), .col2(hd44780_1_out_60), .col3(hd44780_1_out_80),
    .col4(hd44780_1_out_100));
  DotMatrix #(.matrixrows(8)) dotmatrix_30 (
    .col0(hd44780_1_out_120), .col1(hd44780_1_out_140), .col2(hd44780_1_out_160), .col3(hd44780_1_out_180),
    .col4(hd44780_1_out_200));
  DotMatrix #(.matrixrows(8)) dotmatrix_31 (
    .col0(hd44780_1_out_220), .col1(hd44780_1_out_240), .col2(hd44780_1_out_260), .col3(hd44780_1_out_280),
    .col4(hd44780_1_out_300));
  DotMatrix #(.matrixrows(8)) dotmatrix_32 (
    .col0(hd44780_1_out_320), .col1(hd44780_1_out_340), .col2(hd44780_1_out_360), .col3(hd44780_1_out_380),
    .col4(hd44780_1_out_400));
  DotMatrix #(.matrixrows(8)) dotmatrix_33 (
    .col0(hd44780_1_out_21), .col1(hd44780_1_out_41), .col2(hd44780_1_out_61), .col3(hd44780_1_out_81),
    .col4(hd44780_1_out_101));
  DotMatrix #(.matrixrows(8)) dotmatrix_34 (
    .col0(hd44780_1_out_121), .col1(hd44780_1_out_141), .col2(hd44780_1_out_161), .col3(hd44780_1_out_181),
    .col4(hd44780_1_out_201));
  DotMatrix #(.matrixrows(8)) dotmatrix_35 (
    .col0(hd44780_1_out_221), .col1(hd44780_1_out_241), .col2(hd44780_1_out_261), .col3(hd44780_1_out_281),
    .col4(hd44780_1_out_301));
  DotMatrix #(.matrixrows(8)) dotmatrix_36 (
    .col0(hd44780_1_out_321), .col1(hd44780_1_out_341), .col2(hd44780_1_out_361), .col3(hd44780_1_out_381),
    .col4(hd44780_1_out_401));
  DotMatrix #(.matrixrows(8)) dotmatrix_37 (
    .col0(hd44780_1_out_22), .col1(hd44780_1_out_42), .col2(hd44780_1_out_62), .col3(hd44780_1_out_82),
    .col4(hd44780_1_out_102));
  DotMatrix #(.matrixrows(8)) dotmatrix_38 (
    .col0(hd44780_1_out_23), .col1(hd44780_1_out_43), .col2(hd44780_1_out_63), .col3(hd44780_1_out_83),
    .col4(hd44780_1_out_103));
  DotMatrix #(.matrixrows(8)) dotmatrix_39 (
    .col0(hd44780_1_out_122), .col1(hd44780_1_out_142), .col2(hd44780_1_out_162), .col3(hd44780_1_out_182),
    .col4(hd44780_1_out_202));
  DotMatrix #(.matrixrows(8)) dotmatrix_40 (
    .col0(hd44780_1_out_123), .col1(hd44780_1_out_143), .col2(hd44780_1_out_163), .col3(hd44780_1_out_183),
    .col4(hd44780_1_out_203));
  DotMatrix #(.matrixrows(8)) dotmatrix_41 (
    .col0(hd44780_1_out_222), .col1(hd44780_1_out_242), .col2(hd44780_1_out_262), .col3(hd44780_1_out_282),
    .col4(hd44780_1_out_302));
  DotMatrix #(.matrixrows(8)) dotmatrix_42 (
    .col0(hd44780_1_out_223), .col1(hd44780_1_out_243), .col2(hd44780_1_out_263), .col3(hd44780_1_out_283),
    .col4(hd44780_1_out_303));
  DotMatrix #(.matrixrows(8)) dotmatrix_43 (
    .col0(hd44780_1_out_322), .col1(hd44780_1_out_342), .col2(hd44780_1_out_362), .col3(hd44780_1_out_382),
    .col4(hd44780_1_out_402));
  DotMatrix #(.matrixrows(8)) dotmatrix_44 (
    .col0(hd44780_1_out_323), .col1(hd44780_1_out_343), .col2(hd44780_1_out_363), .col3(hd44780_1_out_383),
    .col4(hd44780_1_out_403));
  DotMatrix #(.matrixrows(8)) dotmatrix_45 (
    .col0(hd44780_1_out_24), .col1(hd44780_1_out_44), .col2(hd44780_1_out_64), .col3(hd44780_1_out_84),
    .col4(hd44780_1_out_104));
  DotMatrix #(.matrixrows(8)) dotmatrix_46 (
    .col0(hd44780_1_out_124), .col1(hd44780_1_out_144), .col2(hd44780_1_out_164), .col3(hd44780_1_out_184),
    .col4(hd44780_1_out_204));
  DotMatrix #(.matrixrows(8)) dotmatrix_47 (
    .col0(hd44780_1_out_224), .col1(hd44780_1_out_244), .col2(hd44780_1_out_264), .col3(hd44780_1_out_284),
    .col4(hd44780_1_out_304));
  DotMatrix #(.matrixrows(8)) dotmatrix_48 (
    .col0(hd44780_1_out_324), .col1(hd44780_1_out_344), .col2(hd44780_1_out_364), .col3(hd44780_1_out_384),
    .col4(hd44780_1_out_404));
  DotMatrix #(.matrixrows(8)) dotmatrix_49 (
    .col0(hd44780_1_out_25), .col1(hd44780_1_out_45), .col2(hd44780_1_out_65), .col3(hd44780_1_out_85),
    .col4(hd44780_1_out_105));
  DotMatrix #(.matrixrows(8)) dotmatrix_50 (
    .col0(hd44780_1_out_125), .col1(hd44780_1_out_145), .col2(hd44780_1_out_165), .col3(hd44780_1_out_185),
    .col4(hd44780_1_out_205));
  DotMatrix #(.matrixrows(8)) dotmatrix_51 (
    .col0(hd44780_1_out_225), .col1(hd44780_1_out_245), .col2(hd44780_1_out_265), .col3(hd44780_1_out_285),
    .col4(hd44780_1_out_305));
  DotMatrix #(.matrixrows(8)) dotmatrix_52 (
    .col0(hd44780_1_out_325), .col1(hd44780_1_out_345), .col2(hd44780_1_out_365), .col3(hd44780_1_out_385),
    .col4(hd44780_1_out_405));
  DotMatrix #(.matrixrows(8)) dotmatrix_53 (
    .col0(hd44780_1_out_26), .col1(hd44780_1_out_46), .col2(hd44780_1_out_66), .col3(hd44780_1_out_86),
    .col4(hd44780_1_out_106));
  DotMatrix #(.matrixrows(8)) dotmatrix_54 (
    .col0(hd44780_1_out_27), .col1(hd44780_1_out_47), .col2(hd44780_1_out_67), .col3(hd44780_1_out_87),
    .col4(hd44780_1_out_107));
  DotMatrix #(.matrixrows(8)) dotmatrix_55 (
    .col0(hd44780_1_out_126), .col1(hd44780_1_out_146), .col2(hd44780_1_out_166), .col3(hd44780_1_out_186),
    .col4(hd44780_1_out_206));
  DotMatrix #(.matrixrows(8)) dotmatrix_56 (
    .col0(hd44780_1_out_127), .col1(hd44780_1_out_147), .col2(hd44780_1_out_167), .col3(hd44780_1_out_187),
    .col4(hd44780_1_out_207));
  DotMatrix #(.matrixrows(8)) dotmatrix_57 (
    .col0(hd44780_1_out_226), .col1(hd44780_1_out_246), .col2(hd44780_1_out_266), .col3(hd44780_1_out_286),
    .col4(hd44780_1_out_306));
  DotMatrix #(.matrixrows(8)) dotmatrix_58 (
    .col0(hd44780_1_out_227), .col1(hd44780_1_out_247), .col2(hd44780_1_out_267), .col3(hd44780_1_out_287),
    .col4(hd44780_1_out_307));
  DotMatrix #(.matrixrows(8)) dotmatrix_59 (
    .col0(hd44780_1_out_326), .col1(hd44780_1_out_346), .col2(hd44780_1_out_366), .col3(hd44780_1_out_386),
    .col4(hd44780_1_out_406));
  DotMatrix #(.matrixrows(8)) dotmatrix_60 (
    .col0(hd44780_1_out_327), .col1(hd44780_1_out_347), .col2(hd44780_1_out_367), .col3(hd44780_1_out_387),
    .col4(hd44780_1_out_407));
  DotMatrix #(.matrixrows(8)) dotmatrix_61 (
    .col0(hd44780_1_out_28), .col1(hd44780_1_out_48), .col2(hd44780_1_out_68), .col3(hd44780_1_out_88),
    .col4(hd44780_1_out_108));
  DotMatrix #(.matrixrows(8)) dotmatrix_62 (
    .col0(hd44780_1_out_128), .col1(hd44780_1_out_148), .col2(hd44780_1_out_168), .col3(hd44780_1_out_188),
    .col4(hd44780_1_out_208));
  DotMatrix #(.matrixrows(8)) dotmatrix_63 (
    .col0(hd44780_1_out_228), .col1(hd44780_1_out_248), .col2(hd44780_1_out_268), .col3(hd44780_1_out_288),
    .col4(hd44780_1_out_308));
  DotMatrix #(.matrixrows(8)) dotmatrix_64 (
    .col0(hd44780_1_out_328), .col1(hd44780_1_out_348), .col2(hd44780_1_out_368), .col3(hd44780_1_out_388),
    .col4(hd44780_1_out_408));
  DotMatrix #(.matrixrows(8)) dotmatrix_65 (
    .col0(hd44780_1_out_29), .col1(hd44780_1_out_49), .col2(hd44780_1_out_69), .col3(hd44780_1_out_89),
    .col4(hd44780_1_out_109));
  DotMatrix #(.matrixrows(8)) dotmatrix_66 (
    .col0(hd44780_1_out_129), .col1(hd44780_1_out_149), .col2(hd44780_1_out_169), .col3(hd44780_1_out_189),
    .col4(hd44780_1_out_209));
  DotMatrix #(.matrixrows(8)) dotmatrix_67 (
    .col0(hd44780_1_out_229), .col1(hd44780_1_out_249), .col2(hd44780_1_out_269), .col3(hd44780_1_out_289),
    .col4(hd44780_1_out_309));
  DotMatrix #(.matrixrows(8)) dotmatrix_68 (
    .col0(hd44780_1_out_329), .col1(hd44780_1_out_349), .col2(hd44780_1_out_369), .col3(hd44780_1_out_389),
    .col4(hd44780_1_out_409));
  DotMatrix #(.matrixrows(8)) dotmatrix_69 (
    .col0(hd44780_1_out_30), .col1(hd44780_1_out_50), .col2(hd44780_1_out_70), .col3(hd44780_1_out_90),
    .col4(hd44780_1_out_110));
  DotMatrix #(.matrixrows(8)) dotmatrix_70 (
    .col0(hd44780_1_out_31), .col1(hd44780_1_out_51), .col2(hd44780_1_out_71), .col3(hd44780_1_out_91),
    .col4(hd44780_1_out_111));
  DotMatrix #(.matrixrows(8)) dotmatrix_71 (
    .col0(hd44780_1_out_130), .col1(hd44780_1_out_150), .col2(hd44780_1_out_170), .col3(hd44780_1_out_190),
    .col4(hd44780_1_out_210));
  DotMatrix #(.matrixrows(8)) dotmatrix_72 (
    .col0(hd44780_1_out_131), .col1(hd44780_1_out_151), .col2(hd44780_1_out_171), .col3(hd44780_1_out_191),
    .col4(hd44780_1_out_211));
  DotMatrix #(.matrixrows(8)) dotmatrix_73 (
    .col0(hd44780_1_out_230), .col1(hd44780_1_out_250), .col2(hd44780_1_out_270), .col3(hd44780_1_out_290),
    .col4(hd44780_1_out_310));
  DotMatrix #(.matrixrows(8)) dotmatrix_74 (
    .col0(hd44780_1_out_231), .col1(hd44780_1_out_251), .col2(hd44780_1_out_271), .col3(hd44780_1_out_291),
    .col4(hd44780_1_out_311));
  DotMatrix #(.matrixrows(8)) dotmatrix_75 (
    .col0(hd44780_1_out_330), .col1(hd44780_1_out_350), .col2(hd44780_1_out_370), .col3(hd44780_1_out_390),
    .col4(hd44780_1_out_410));
  DotMatrix #(.matrixrows(8)) dotmatrix_76 (
    .col0(hd44780_1_out_331), .col1(hd44780_1_out_351), .col2(hd44780_1_out_371), .col3(hd44780_1_out_391),
    .col4(hd44780_1_out_411));
  DotMatrix #(.matrixrows(8)) dotmatrix_77 (
    .col0(hd44780_1_out_32), .col1(hd44780_1_out_52), .col2(hd44780_1_out_72), .col3(hd44780_1_out_92),
    .col4(hd44780_1_out_112));
  DotMatrix #(.matrixrows(8)) dotmatrix_78 (
    .col0(hd44780_1_out_132), .col1(hd44780_1_out_152), .col2(hd44780_1_out_172), .col3(hd44780_1_out_192),
    .col4(hd44780_1_out_212));
  DotMatrix #(.matrixrows(8)) dotmatrix_79 (
    .col0(hd44780_1_out_232), .col1(hd44780_1_out_252), .col2(hd44780_1_out_272), .col3(hd44780_1_out_292),
    .col4(hd44780_1_out_312));
  DotMatrix #(.matrixrows(8)) dotmatrix_80 (
    .col0(hd44780_1_out_332), .col1(hd44780_1_out_352), .col2(hd44780_1_out_372), .col3(hd44780_1_out_392),
    .col4(hd44780_1_out_412));
  HD44780 hd44780_1 (
    .out_313(hd44780_1_out_313), .out_333(hd44780_1_out_333), .out_353(hd44780_1_out_353),
    .out_373(hd44780_1_out_373), .out_393(hd44780_1_out_393), .out_13(hd44780_1_out_13),
    .out_33(hd44780_1_out_33), .out_53(hd44780_1_out_53), .out_73(hd44780_1_out_73),
    .out_93(hd44780_1_out_93), .out_113(hd44780_1_out_113), .out_133(hd44780_1_out_133),
    .out_153(hd44780_1_out_153), .out_173(hd44780_1_out_173), .out_193(hd44780_1_out_193),
    .out_213(hd44780_1_out_213), .out_233(hd44780_1_out_233), .out_253(hd44780_1_out_253),
    .out_273(hd44780_1_out_273), .out_293(hd44780_1_out_293), .out_314(hd44780_1_out_314),
    .out_334(hd44780_1_out_334), .out_354(hd44780_1_out_354), .out_374(hd44780_1_out_374),
    .out_394(hd44780_1_out_394), .out_14(hd44780_1_out_14), .out_34(hd44780_1_out_34),
    .out_54(hd44780_1_out_54), .out_74(hd44780_1_out_74), .out_94(hd44780_1_out_94),
    .out_114(hd44780_1_out_114), .out_134(hd44780_1_out_134), .out_154(hd44780_1_out_154),
    .out_174(hd44780_1_out_174), .out_194(hd44780_1_out_194), .out_214(hd44780_1_out_214),
    .out_234(hd44780_1_out_234), .out_254(hd44780_1_out_254), .out_274(hd44780_1_out_274),
    .out_294(hd44780_1_out_294), .out_315(hd44780_1_out_315), .out_335(hd44780_1_out_335),
    .out_355(hd44780_1_out_355), .out_375(hd44780_1_out_375), .out_395(hd44780_1_out_395),
    .out_15(hd44780_1_out_15), .out_35(hd44780_1_out_35), .out_55(hd44780_1_out_55),
    .out_75(hd44780_1_out_75), .out_95(hd44780_1_out_95), .out_115(hd44780_1_out_115),
    .out_135(hd44780_1_out_135), .out_155(hd44780_1_out_155), .out_175(hd44780_1_out_175),
    .out_195(hd44780_1_out_195), .out_215(hd44780_1_out_215), .out_235(hd44780_1_out_235),
    .out_255(hd44780_1_out_255), .out_275(hd44780_1_out_275), .out_295(hd44780_1_out_295),
    .out_316(hd44780_1_out_316), .out_336(hd44780_1_out_336), .out_356(hd44780_1_out_356),
    .out_376(hd44780_1_out_376), .out_396(hd44780_1_out_396), .out_16(hd44780_1_out_16),
    .out_36(hd44780_1_out_36), .out_56(hd44780_1_out_56), .out_76(hd44780_1_out_76),
    .out_96(hd44780_1_out_96), .out_116(hd44780_1_out_116), .out_136(hd44780_1_out_136),
    .out_156(hd44780_1_out_156), .out_176(hd44780_1_out_176), .out_196(hd44780_1_out_196),
    .out_216(hd44780_1_out_216), .out_236(hd44780_1_out_236), .out_256(hd44780_1_out_256),
    .out_276(hd44780_1_out_276), .out_296(hd44780_1_out_296), .out_317(hd44780_1_out_317),
    .out_337(hd44780_1_out_337), .out_357(hd44780_1_out_357), .out_377(hd44780_1_out_377),
    .out_397(hd44780_1_out_397), .out_17(hd44780_1_out_17), .out_37(hd44780_1_out_37),
    .out_57(hd44780_1_out_57), .out_77(hd44780_1_out_77), .out_97(hd44780_1_out_97),
    .out_117(hd44780_1_out_117), .out_137(hd44780_1_out_137), .out_157(hd44780_1_out_157),
    .out_177(hd44780_1_out_177), .out_197(hd44780_1_out_197), .out_217(hd44780_1_out_217),
    .out_237(hd44780_1_out_237), .out_257(hd44780_1_out_257), .out_277(hd44780_1_out_277),
    .out_297(hd44780_1_out_297), .out_318(hd44780_1_out_318), .out_338(hd44780_1_out_338),
    .out_358(hd44780_1_out_358), .out_378(hd44780_1_out_378), .out_398(hd44780_1_out_398),
    .out_18(hd44780_1_out_18), .out_38(hd44780_1_out_38), .out_58(hd44780_1_out_58),
    .out_78(hd44780_1_out_78), .out_98(hd44780_1_out_98), .out_118(hd44780_1_out_118),
    .out_138(hd44780_1_out_138), .out_158(hd44780_1_out_158), .out_178(hd44780_1_out_178),
    .out_198(hd44780_1_out_198), .out_218(hd44780_1_out_218), .out_238(hd44780_1_out_238),
    .out_258(hd44780_1_out_258), .out_278(hd44780_1_out_278), .out_298(hd44780_1_out_298),
    .out_319(hd44780_1_out_319), .out_339(hd44780_1_out_339), .out_359(hd44780_1_out_359),
    .out_379(hd44780_1_out_379), .out_399(hd44780_1_out_399), .out_19(hd44780_1_out_19),
    .out_39(hd44780_1_out_39), .out_59(hd44780_1_out_59), .out_79(hd44780_1_out_79),
    .out_99(hd44780_1_out_99), .out_119(hd44780_1_out_119), .out_139(hd44780_1_out_139),
    .out_159(hd44780_1_out_159), .out_179(hd44780_1_out_179), .out_199(hd44780_1_out_199),
    .out_219(hd44780_1_out_219), .out_239(hd44780_1_out_239), .out_259(hd44780_1_out_259),
    .out_279(hd44780_1_out_279), .out_299(hd44780_1_out_299), .out_320(hd44780_1_out_320),
    .out_340(hd44780_1_out_340), .out_360(hd44780_1_out_360), .out_380(hd44780_1_out_380),
    .out_400(hd44780_1_out_400), .out_20(hd44780_1_out_20), .out_40(hd44780_1_out_40),
    .out_60(hd44780_1_out_60), .out_80(hd44780_1_out_80), .out_100(hd44780_1_out_100),
    .out_120(hd44780_1_out_120), .out_140(hd44780_1_out_140), .out_160(hd44780_1_out_160),
    .out_180(hd44780_1_out_180), .out_200(hd44780_1_out_200), .out_220(hd44780_1_out_220),
    .out_240(hd44780_1_out_240), .out_260(hd44780_1_out_260), .out_280(hd44780_1_out_280),
    .out_300(hd44780_1_out_300), .out_321(hd44780_1_out_321), .out_341(hd44780_1_out_341),
    .out_361(hd44780_1_out_361), .out_381(hd44780_1_out_381), .out_401(hd44780_1_out_401),
    .out_21(hd44780_1_out_21), .out_41(hd44780_1_out_41), .out_61(hd44780_1_out_61),
    .out_81(hd44780_1_out_81), .out_101(hd44780_1_out_101), .out_121(hd44780_1_out_121),
    .out_141(hd44780_1_out_141), .out_161(hd44780_1_out_161), .out_181(hd44780_1_out_181),
    .out_201(hd44780_1_out_201), .out_221(hd44780_1_out_221), .out_241(hd44780_1_out_241),
    .out_261(hd44780_1_out_261), .out_281(hd44780_1_out_281), .out_301(hd44780_1_out_301),
    .out_322(hd44780_1_out_322), .out_342(hd44780_1_out_342), .out_362(hd44780_1_out_362),
    .out_382(hd44780_1_out_382), .out_402(hd44780_1_out_402), .out_22(hd44780_1_out_22),
    .out_42(hd44780_1_out_42), .out_62(hd44780_1_out_62), .out_82(hd44780_1_out_82),
    .out_102(hd44780_1_out_102), .out_122(hd44780_1_out_122), .out_142(hd44780_1_out_142),
    .out_162(hd44780_1_out_162), .out_182(hd44780_1_out_182), .out_202(hd44780_1_out_202),
    .out_222(hd44780_1_out_222), .out_242(hd44780_1_out_242), .out_262(hd44780_1_out_262),
    .out_282(hd44780_1_out_282), .out_302(hd44780_1_out_302), .out_323(hd44780_1_out_323),
    .out_343(hd44780_1_out_343), .out_363(hd44780_1_out_363), .out_383(hd44780_1_out_383),
    .out_403(hd44780_1_out_403), .out_23(hd44780_1_out_23), .out_43(hd44780_1_out_43),
    .out_63(hd44780_1_out_63), .out_83(hd44780_1_out_83), .out_103(hd44780_1_out_103),
    .out_123(hd44780_1_out_123), .out_143(hd44780_1_out_143), .out_163(hd44780_1_out_163),
    .out_183(hd44780_1_out_183), .out_203(hd44780_1_out_203), .out_223(hd44780_1_out_223),
    .out_243(hd44780_1_out_243), .out_263(hd44780_1_out_263), .out_283(hd44780_1_out_283),
    .out_303(hd44780_1_out_303), .out_324(hd44780_1_out_324), .out_344(hd44780_1_out_344),
    .out_364(hd44780_1_out_364), .out_384(hd44780_1_out_384), .out_404(hd44780_1_out_404),
    .out_24(hd44780_1_out_24), .out_44(hd44780_1_out_44), .out_64(hd44780_1_out_64),
    .out_84(hd44780_1_out_84), .out_104(hd44780_1_out_104), .out_124(hd44780_1_out_124),
    .out_144(hd44780_1_out_144), .out_164(hd44780_1_out_164), .out_184(hd44780_1_out_184),
    .out_204(hd44780_1_out_204), .out_224(hd44780_1_out_224), .out_244(hd44780_1_out_244),
    .out_264(hd44780_1_out_264), .out_284(hd44780_1_out_284), .out_304(hd44780_1_out_304),
    .out_325(hd44780_1_out_325), .out_345(hd44780_1_out_345), .out_365(hd44780_1_out_365),
    .out_385(hd44780_1_out_385), .out_405(hd44780_1_out_405), .out_25(hd44780_1_out_25),
    .out_45(hd44780_1_out_45), .out_65(hd44780_1_out_65), .out_85(hd44780_1_out_85),
    .out_105(hd44780_1_out_105), .out_125(hd44780_1_out_125), .out_145(hd44780_1_out_145),
    .out_165(hd44780_1_out_165), .out_185(hd44780_1_out_185), .out_205(hd44780_1_out_205),
    .out_225(hd44780_1_out_225), .out_245(hd44780_1_out_245), .out_265(hd44780_1_out_265),
    .out_285(hd44780_1_out_285), .out_305(hd44780_1_out_305), .out_326(hd44780_1_out_326),
    .out_346(hd44780_1_out_346), .out_366(hd44780_1_out_366), .out_386(hd44780_1_out_386),
    .out_406(hd44780_1_out_406), .out_26(hd44780_1_out_26), .out_46(hd44780_1_out_46),
    .out_66(hd44780_1_out_66), .out_86(hd44780_1_out_86), .out_106(hd44780_1_out_106),
    .out_126(hd44780_1_out_126), .out_146(hd44780_1_out_146), .out_166(hd44780_1_out_166),
    .out_186(hd44780_1_out_186), .out_206(hd44780_1_out_206), .out_226(hd44780_1_out_226),
    .out_246(hd44780_1_out_246), .out_266(hd44780_1_out_266), .out_286(hd44780_1_out_286),
    .out_306(hd44780_1_out_306), .out_327(hd44780_1_out_327), .out_347(hd44780_1_out_347),
    .out_367(hd44780_1_out_367), .out_387(hd44780_1_out_387), .out_407(hd44780_1_out_407),
    .out_27(hd44780_1_out_27), .out_47(hd44780_1_out_47), .out_67(hd44780_1_out_67),
    .out_87(hd44780_1_out_87), .out_107(hd44780_1_out_107), .out_127(hd44780_1_out_127),
    .out_147(hd44780_1_out_147), .out_167(hd44780_1_out_167), .out_187(hd44780_1_out_187),
    .out_207(hd44780_1_out_207), .out_227(hd44780_1_out_227), .out_247(hd44780_1_out_247),
    .out_267(hd44780_1_out_267), .out_287(hd44780_1_out_287), .out_307(hd44780_1_out_307),
    .out_328(hd44780_1_out_328), .out_348(hd44780_1_out_348), .out_368(hd44780_1_out_368),
    .out_388(hd44780_1_out_388), .out_408(hd44780_1_out_408), .out_28(hd44780_1_out_28),
    .out_48(hd44780_1_out_48), .out_68(hd44780_1_out_68), .out_88(hd44780_1_out_88),
    .out_108(hd44780_1_out_108), .out_128(hd44780_1_out_128), .out_148(hd44780_1_out_148),
    .out_168(hd44780_1_out_168), .out_188(hd44780_1_out_188), .out_208(hd44780_1_out_208),
    .out_228(hd44780_1_out_228), .out_248(hd44780_1_out_248), .out_268(hd44780_1_out_268),
    .out_288(hd44780_1_out_288), .out_308(hd44780_1_out_308), .out_329(hd44780_1_out_329),
    .out_349(hd44780_1_out_349), .out_369(hd44780_1_out_369), .out_389(hd44780_1_out_389),
    .out_409(hd44780_1_out_409), .out_29(hd44780_1_out_29), .out_49(hd44780_1_out_49),
    .out_69(hd44780_1_out_69), .out_89(hd44780_1_out_89), .out_109(hd44780_1_out_109),
    .out_129(hd44780_1_out_129), .out_149(hd44780_1_out_149), .out_169(hd44780_1_out_169),
    .out_189(hd44780_1_out_189), .out_209(hd44780_1_out_209), .out_229(hd44780_1_out_229),
    .out_249(hd44780_1_out_249), .out_269(hd44780_1_out_269), .out_289(hd44780_1_out_289),
    .out_309(hd44780_1_out_309), .out_330(hd44780_1_out_330), .out_350(hd44780_1_out_350),
    .out_370(hd44780_1_out_370), .out_390(hd44780_1_out_390), .out_410(hd44780_1_out_410),
    .out_30(hd44780_1_out_30), .out_50(hd44780_1_out_50), .out_70(hd44780_1_out_70),
    .out_90(hd44780_1_out_90), .out_110(hd44780_1_out_110), .out_130(hd44780_1_out_130),
    .out_150(hd44780_1_out_150), .out_170(hd44780_1_out_170), .out_190(hd44780_1_out_190),
    .out_210(hd44780_1_out_210), .out_230(hd44780_1_out_230), .out_250(hd44780_1_out_250),
    .out_270(hd44780_1_out_270), .out_290(hd44780_1_out_290), .out_310(hd44780_1_out_310),
    .out_331(hd44780_1_out_331), .out_351(hd44780_1_out_351), .out_371(hd44780_1_out_371),
    .out_391(hd44780_1_out_391), .out_411(hd44780_1_out_411), .out_31(hd44780_1_out_31),
    .out_51(hd44780_1_out_51), .out_71(hd44780_1_out_71), .out_91(hd44780_1_out_91),
    .out_111(hd44780_1_out_111), .out_131(hd44780_1_out_131), .out_151(hd44780_1_out_151),
    .out_171(hd44780_1_out_171), .out_191(hd44780_1_out_191), .out_211(hd44780_1_out_211),
    .out_231(hd44780_1_out_231), .out_251(hd44780_1_out_251), .out_271(hd44780_1_out_271),
    .out_291(hd44780_1_out_291), .out_311(hd44780_1_out_311), .out_332(hd44780_1_out_332),
    .out_352(hd44780_1_out_352), .out_372(hd44780_1_out_372), .out_392(hd44780_1_out_392),
    .out_412(hd44780_1_out_412), .out_32(hd44780_1_out_32), .out_52(hd44780_1_out_52),
    .out_72(hd44780_1_out_72), .out_92(hd44780_1_out_92), .out_112(hd44780_1_out_112),
    .out_132(hd44780_1_out_132), .out_152(hd44780_1_out_152), .out_172(hd44780_1_out_172),
    .out_192(hd44780_1_out_192), .out_212(hd44780_1_out_212), .out_232(hd44780_1_out_232),
    .out_252(hd44780_1_out_252), .out_272(hd44780_1_out_272), .out_292(hd44780_1_out_292),
    .out_312(hd44780_1_out_312), .BL(pcf8574_1_data_out[3]), .D7(pcf8574_1_data_out[7]),
    .D6(pcf8574_1_data_out[6]), .D5(pcf8574_1_data_out[5]), .D4(pcf8574_1_data_out[4]),
    .E(pcf8574_1_data_out[2]), .RW(pcf8574_1_data_out[1]), .RS(pcf8574_1_data_out[0]));  // open: D3, D2, D1, D0
endmodule

module GPIO (
  input  [63:0] DATA_IN,
  input  [53:0] GPIO_IN,
  input  CLK,
  input  WRITE,
  input  [7:0] ADDR,
  input  SDA_GPIO,
  input  SCL_GPIO,
  input  SDA_DRIVE,
  input  SCL_DRIVE,
  output [63:0] DATA_OUT,
  output [53:0] GPIO_OUT,
  output [53:0] GPIO_DRIVE,
  output GPIO_SDA,
  output GPIO_SCL
);

  wire and_1_out, and_2_out, and_3_out, and_4_out, and_5_out, and_6_out, and_7_out, and_8_out, and_9_out,
       and_10_out, comparator_1_eq, comparator_2_eq, comparator_3_eq, comparator_4_eq, comparator_5_eq,
       comparator_6_eq, comparator_7_eq, comparator_8_eq, comparator_9_eq, comparator_10_eq,
       comparator_11_eq, comparator_12_eq, comparator_13_eq, comparator_14_eq, comparator_15_eq,
       comparator_16_eq, d_ff_1_q, d_ff_2_q, d_ff_3_q, d_ff_4_q, or_1_out, s_r_ff_1_q, s_r_ff_2_q,
       s_r_ff_3_q, s_r_ff_4_q, s_r_ff_5_q, s_r_ff_6_q, s_r_ff_7_q, s_r_ff_8_q, s_r_ff_9_q, s_r_ff_10_q,
       s_r_ff_11_q, s_r_ff_12_q, s_r_ff_13_q, s_r_ff_14_q, s_r_ff_15_q, s_r_ff_16_q, s_r_ff_17_q,
       s_r_ff_18_q, s_r_ff_19_q, s_r_ff_20_q, s_r_ff_21_q, s_r_ff_22_q, s_r_ff_23_q, s_r_ff_24_q,
       s_r_ff_25_q, s_r_ff_26_q, s_r_ff_27_q, s_r_ff_28_q, s_r_ff_29_q, s_r_ff_30_q, s_r_ff_31_q,
       s_r_ff_32_q, s_r_ff_33_q, s_r_ff_34_q, s_r_ff_35_q, s_r_ff_36_q, s_r_ff_37_q, s_r_ff_38_q,
       s_r_ff_39_q, s_r_ff_40_q, s_r_ff_41_q, s_r_ff_42_q, s_r_ff_43_q, s_r_ff_44_q, s_r_ff_45_q,
       s_r_ff_46_q, s_r_ff_47_q, s_r_ff_48_q, s_r_ff_49_q, s_r_ff_50_q, s_r_ff_51_q, s_r_ff_52_q,
       s_r_ff_53_q, s_r_ff_54_q;
  wire [3:2] and_119_out;
  wire [21:0] GPCLR1_q, GPSET1_q, register_33_q;
  wire [31:0] controlled_buffer_1_out, GPCLR0_q, GPFSEL0_q, GPFSEL1_q, GPFSEL2_q, GPFSEL3_q, GPFSEL4_q,
       GPFSEL5_q, GPSET0_q, register_1_q;
  wire [53:0] and_11_out, and_65_out;

  Comparator comparator_1 (.a(ADDR), .b({8{1'b0}}), .eq(comparator_1_eq));  // open: gt, lt
  Comparator comparator_2 (.a(ADDR), .b(8'h4), .eq(comparator_2_eq));  // open: gt, lt
  Comparator comparator_3 (.a(ADDR), .b(8'h8), .eq(comparator_3_eq));  // open: gt, lt
  Comparator comparator_4 (.a(ADDR), .b(8'hc), .eq(comparator_4_eq));  // open: gt, lt
  Comparator comparator_5 (.a(ADDR), .b(8'h10), .eq(comparator_5_eq));  // open: gt, lt
  Comparator comparator_6 (.a(ADDR), .b(8'h14), .eq(comparator_6_eq));  // open: gt, lt
  Comparator comparator_7 (.a(ADDR), .b(8'h1c), .eq(comparator_7_eq));  // open: gt, lt
  Comparator comparator_8 (.a(ADDR), .b(8'h20), .eq(comparator_8_eq));  // open: gt, lt
  Comparator comparator_9 (.a(ADDR), .b(8'h28), .eq(comparator_9_eq));  // open: gt, lt
  Comparator comparator_10 (.a(ADDR), .b(8'h2c), .eq(comparator_10_eq));  // open: gt, lt
  Comparator comparator_11 (.a(ADDR), .b(8'h34), .eq(comparator_11_eq));  // open: gt, lt
  Comparator comparator_12 (.a(ADDR), .b(8'h38), .eq(comparator_12_eq));  // open: gt, lt
  Comparator comparator_13 (.a(ADDR), .b(8'h1c), .eq(comparator_13_eq));  // open: gt, lt
  Comparator comparator_14 (.a(ADDR), .b(8'h20), .eq(comparator_14_eq));  // open: gt, lt
  Comparator comparator_15 (.a(ADDR), .b(8'h28), .eq(comparator_15_eq));  // open: gt, lt
  Comparator comparator_16 (.a(ADDR), .b(8'h2c), .eq(comparator_16_eq));  // open: gt, lt
  and and_1 (and_1_out, comparator_1_eq, WRITE);
  and and_2 (and_2_out, comparator_2_eq, WRITE);
  and and_3 (and_3_out, comparator_3_eq, WRITE);
  and and_4 (and_4_out, comparator_4_eq, WRITE);
  and and_5 (and_5_out, comparator_5_eq, WRITE);
  and and_6 (and_6_out, comparator_6_eq, WRITE);
  and and_7 (and_7_out, comparator_7_eq, WRITE);
  and and_8 (and_8_out, comparator_8_eq, WRITE);
  and and_9 (and_9_out, comparator_9_eq, WRITE);
  and and_10 (and_10_out, comparator_10_eq, WRITE);
  Register #(.width(32)) GPFSEL0 (.D(DATA_IN[31:0]), .en(and_1_out), .clk(CLK), .Q(GPFSEL0_q));  // open: clr
  Register #(.width(32)) GPFSEL1 (.D(DATA_IN[31:0]), .en(and_2_out), .clk(CLK), .Q(GPFSEL1_q));  // open: clr
  Register #(.width(32)) GPFSEL2 (.D(DATA_IN[31:0]), .en(and_3_out), .clk(CLK), .Q(GPFSEL2_q));  // open: clr
  Register #(.width(32)) GPFSEL3 (.D(DATA_IN[31:0]), .en(and_4_out), .clk(CLK), .Q(GPFSEL3_q));  // open: clr
  Register #(.width(32)) GPFSEL4 (.D(DATA_IN[31:0]), .en(and_5_out), .clk(CLK), .Q(GPFSEL4_q));  // open: clr
  Register #(.width(32)) GPFSEL5 (.D(DATA_IN[31:0]), .en(and_6_out), .clk(CLK), .Q(GPFSEL5_q));  // open: clr
  Register #(.trigger("high"), .width(32)) GPSET0 (
    .D(DATA_IN[31:0]), .en(and_7_out), .clk(CLK), .Q(GPSET0_q), .clr(d_ff_1_q));
  D_Flip_Flop d_ff_1 (.D(and_7_out), .clk(CLK), .Q(d_ff_1_q));  // open: Qn, preset, reset
  Register #(.trigger("high"), .width(22)) GPSET1 (
    .D(DATA_IN[21:0]), .en(and_8_out), .clk(CLK), .Q(GPSET1_q), .clr(d_ff_2_q));
  D_Flip_Flop d_ff_2 (.D(and_8_out), .clk(CLK), .Q(d_ff_2_q));  // open: Qn, preset, reset
  Register #(.trigger("high"), .width(32)) GPCLR0 (
    .D(DATA_IN[31:0]), .en(and_9_out), .clk(CLK), .Q(GPCLR0_q), .clr(d_ff_3_q));
  D_Flip_Flop d_ff_3 (.D(and_9_out), .clk(CLK), .Q(d_ff_3_q));  // open: Qn, preset, reset
  Register #(.trigger("high"), .width(22)) GPCLR1 (
    .D(DATA_IN[21:0]), .en(and_10_out), .clk(CLK), .Q(GPCLR1_q), .clr(d_ff_4_q));
  D_Flip_Flop d_ff_4 (.D(and_10_out), .clk(CLK), .Q(d_ff_4_q));  // open: Qn, preset, reset
  or or_1 (or_1_out, comparator_13_eq, comparator_14_eq, comparator_15_eq, comparator_16_eq);
  assign controlled_buffer_1_out = comparator_1_eq ? GPFSEL0_q : 32'bz;  // Controlled_Buffer controlled_buffer_1
  assign controlled_buffer_1_out = comparator_2_eq ? GPFSEL1_q : 32'bz;  // Controlled_Buffer controlled_buffer_2
  assign controlled_buffer_1_out = comparator_3_eq ? GPFSEL2_q : 32'bz;  // Controlled_Buffer controlled_buffer_3
  assign controlled_buffer_1_out = comparator_4_eq ? GPFSEL3_q : 32'bz;  // Controlled_Buffer controlled_buffer_4
  assign controlled_buffer_1_out = comparator_5_eq ? GPFSEL4_q : 32'bz;  // Controlled_Buffer controlled_buffer_5
  assign controlled_buffer_1_out = comparator_6_eq ? GPFSEL5_q : 32'bz;  // Controlled_Buffer controlled_buffer_6
  assign controlled_buffer_1_out = or_1_out ? 32'h6770696f : 32'bz;  // Controlled_Buffer controlled_buffer_7
  and and_11 (and_11_out[0], GPFSEL0_q[0], ~GPFSEL0_q[1], ~GPFSEL0_q[2]);  // AND_Gate
  and and_12 (and_11_out[1], GPFSEL0_q[3], ~GPFSEL0_q[4], ~GPFSEL0_q[5]);  // AND_Gate
  and and_13 (and_11_out[2], GPFSEL0_q[6], ~GPFSEL0_q[7], ~GPFSEL0_q[8]);  // AND_Gate
  and and_14 (and_11_out[3], GPFSEL0_q[9], ~GPFSEL0_q[10], ~GPFSEL0_q[11]);  // AND_Gate
  and and_15 (and_11_out[4], GPFSEL0_q[12], ~GPFSEL0_q[13], ~GPFSEL0_q[14]);  // AND_Gate
  and and_16 (and_11_out[5], GPFSEL0_q[15], ~GPFSEL0_q[16], ~GPFSEL0_q[17]);  // AND_Gate
  and and_17 (and_11_out[6], GPFSEL0_q[18], ~GPFSEL0_q[19], ~GPFSEL0_q[20]);  // AND_Gate
  and and_18 (and_11_out[7], GPFSEL0_q[21], ~GPFSEL0_q[22], ~GPFSEL0_q[23]);  // AND_Gate
  and and_19 (and_11_out[8], GPFSEL0_q[24], ~GPFSEL0_q[25], ~GPFSEL0_q[26]);  // AND_Gate
  and and_20 (and_11_out[9], GPFSEL0_q[27], ~GPFSEL0_q[28], ~GPFSEL0_q[29]);  // AND_Gate
  and and_21 (and_11_out[10], GPFSEL1_q[0], ~GPFSEL1_q[1], ~GPFSEL1_q[2]);  // AND_Gate
  and and_22 (and_11_out[11], GPFSEL1_q[3], ~GPFSEL1_q[4], ~GPFSEL1_q[5]);  // AND_Gate
  and and_23 (and_11_out[12], GPFSEL1_q[6], ~GPFSEL1_q[7], ~GPFSEL1_q[8]);  // AND_Gate
  and and_24 (and_11_out[13], GPFSEL1_q[9], ~GPFSEL1_q[10], ~GPFSEL1_q[11]);  // AND_Gate
  and and_25 (and_11_out[14], GPFSEL1_q[12], ~GPFSEL1_q[13], ~GPFSEL1_q[14]);  // AND_Gate
  and and_26 (and_11_out[15], GPFSEL1_q[15], ~GPFSEL1_q[16], ~GPFSEL1_q[17]);  // AND_Gate
  and and_27 (and_11_out[16], GPFSEL1_q[18], ~GPFSEL1_q[19], ~GPFSEL1_q[20]);  // AND_Gate
  and and_28 (and_11_out[17], GPFSEL1_q[21], ~GPFSEL1_q[22], ~GPFSEL1_q[23]);  // AND_Gate
  and and_29 (and_11_out[18], GPFSEL1_q[24], ~GPFSEL1_q[25], ~GPFSEL1_q[26]);  // AND_Gate
  and and_30 (and_11_out[19], GPFSEL1_q[27], ~GPFSEL1_q[28], ~GPFSEL1_q[29]);  // AND_Gate
  and and_31 (and_11_out[20], GPFSEL2_q[0], ~GPFSEL2_q[1], ~GPFSEL2_q[2]);  // AND_Gate
  and and_32 (and_11_out[21], GPFSEL2_q[3], ~GPFSEL2_q[4], ~GPFSEL2_q[5]);  // AND_Gate
  and and_33 (and_11_out[22], GPFSEL2_q[6], ~GPFSEL2_q[7], ~GPFSEL2_q[8]);  // AND_Gate
  and and_34 (and_11_out[23], GPFSEL2_q[9], ~GPFSEL2_q[10], ~GPFSEL2_q[11]);  // AND_Gate
  and and_35 (and_11_out[24], GPFSEL2_q[12], ~GPFSEL2_q[13], ~GPFSEL2_q[14]);  // AND_Gate
  and and_36 (and_11_out[25], GPFSEL2_q[15], ~GPFSEL2_q[16], ~GPFSEL2_q[17]);  // AND_Gate
  and and_37 (and_11_out[26], GPFSEL2_q[18], ~GPFSEL2_q[19], ~GPFSEL2_q[20]);  // AND_Gate
  and and_38 (and_11_out[27], GPFSEL2_q[21], ~GPFSEL2_q[22], ~GPFSEL2_q[23]);  // AND_Gate
  and and_39 (and_11_out[28], GPFSEL2_q[24], ~GPFSEL2_q[25], ~GPFSEL2_q[26]);  // AND_Gate
  and and_40 (and_11_out[29], GPFSEL2_q[27], ~GPFSEL2_q[28], ~GPFSEL2_q[29]);  // AND_Gate
  and and_41 (and_11_out[30], GPFSEL3_q[0], ~GPFSEL3_q[1], ~GPFSEL3_q[2]);  // AND_Gate
  and and_42 (and_11_out[31], GPFSEL3_q[3], ~GPFSEL3_q[4], ~GPFSEL3_q[5]);  // AND_Gate
  and and_43 (and_11_out[32], GPFSEL3_q[6], ~GPFSEL3_q[7], ~GPFSEL3_q[8]);  // AND_Gate
  and and_44 (and_11_out[33], GPFSEL3_q[9], ~GPFSEL3_q[10], ~GPFSEL3_q[11]);  // AND_Gate
  and and_45 (and_11_out[34], GPFSEL3_q[12], ~GPFSEL3_q[13], ~GPFSEL3_q[14]);  // AND_Gate
  and and_46 (and_11_out[35], GPFSEL3_q[15], ~GPFSEL3_q[16], ~GPFSEL3_q[17]);  // AND_Gate
  and and_47 (and_11_out[36], GPFSEL3_q[18], ~GPFSEL3_q[19], ~GPFSEL3_q[20]);  // AND_Gate
  and and_48 (and_11_out[37], GPFSEL3_q[21], ~GPFSEL3_q[22], ~GPFSEL3_q[23]);  // AND_Gate
  and and_49 (and_11_out[38], GPFSEL3_q[24], ~GPFSEL3_q[25], ~GPFSEL3_q[26]);  // AND_Gate
  and and_50 (and_11_out[39], GPFSEL3_q[27], ~GPFSEL3_q[28], ~GPFSEL3_q[29]);  // AND_Gate
  and and_51 (and_11_out[40], GPFSEL4_q[0], ~GPFSEL4_q[1], ~GPFSEL4_q[2]);  // AND_Gate
  and and_52 (and_11_out[41], GPFSEL4_q[3], ~GPFSEL4_q[4], ~GPFSEL4_q[5]);  // AND_Gate
  and and_53 (and_11_out[42], GPFSEL4_q[6], ~GPFSEL4_q[7], ~GPFSEL4_q[8]);  // AND_Gate
  and and_54 (and_11_out[43], GPFSEL4_q[9], ~GPFSEL4_q[10], ~GPFSEL4_q[11]);  // AND_Gate
  and and_55 (and_11_out[44], GPFSEL4_q[12], ~GPFSEL4_q[13], ~GPFSEL4_q[14]);  // AND_Gate
  and and_56 (and_11_out[45], GPFSEL4_q[15], ~GPFSEL4_q[16], ~GPFSEL4_q[17]);  // AND_Gate
  and and_57 (and_11_out[46], GPFSEL4_q[18], ~GPFSEL4_q[19], ~GPFSEL4_q[20]);  // AND_Gate
  and and_58 (and_11_out[47], GPFSEL4_q[21], ~GPFSEL4_q[22], ~GPFSEL4_q[23]);  // AND_Gate
  and and_59 (and_11_out[48], GPFSEL4_q[24], ~GPFSEL4_q[25], ~GPFSEL4_q[26]);  // AND_Gate
  and and_60 (and_11_out[49], GPFSEL4_q[27], ~GPFSEL4_q[28], ~GPFSEL4_q[29]);  // AND_Gate
  and and_61 (and_11_out[50], GPFSEL5_q[0], ~GPFSEL5_q[1], ~GPFSEL5_q[2]);  // AND_Gate
  and and_62 (and_11_out[51], GPFSEL5_q[3], ~GPFSEL5_q[4], ~GPFSEL5_q[5]);  // AND_Gate
  and and_63 (and_11_out[52], GPFSEL5_q[6], ~GPFSEL5_q[7], ~GPFSEL5_q[8]);  // AND_Gate
  and and_64 (and_11_out[53], GPFSEL5_q[9], ~GPFSEL5_q[10], ~GPFSEL5_q[11]);  // AND_Gate
  and and_65 (and_65_out[0], ~GPFSEL0_q[0], ~GPFSEL0_q[1], ~GPFSEL0_q[2]);  // AND_Gate
  and and_66 (and_65_out[1], ~GPFSEL0_q[3], ~GPFSEL0_q[4], ~GPFSEL0_q[5]);  // AND_Gate
  and and_67 (and_65_out[2], ~GPFSEL0_q[6], ~GPFSEL0_q[7], ~GPFSEL0_q[8]);  // AND_Gate
  and and_68 (and_65_out[3], ~GPFSEL0_q[9], ~GPFSEL0_q[10], ~GPFSEL0_q[11]);  // AND_Gate
  and and_69 (and_65_out[4], ~GPFSEL0_q[12], ~GPFSEL0_q[13], ~GPFSEL0_q[14]);  // AND_Gate
  and and_70 (and_65_out[5], ~GPFSEL0_q[15], ~GPFSEL0_q[16], ~GPFSEL0_q[17]);  // AND_Gate
  and and_71 (and_65_out[6], ~GPFSEL0_q[18], ~GPFSEL0_q[19], ~GPFSEL0_q[20]);  // AND_Gate
  and and_72 (and_65_out[7], ~GPFSEL0_q[21], ~GPFSEL0_q[22], ~GPFSEL0_q[23]);  // AND_Gate
  and and_73 (and_65_out[8], ~GPFSEL0_q[24], ~GPFSEL0_q[25], ~GPFSEL0_q[26]);  // AND_Gate
  and and_74 (and_65_out[9], ~GPFSEL0_q[27], ~GPFSEL0_q[28], ~GPFSEL0_q[29]);  // AND_Gate
  and and_75 (and_65_out[10], ~GPFSEL1_q[0], ~GPFSEL1_q[1], ~GPFSEL1_q[2]);  // AND_Gate
  and and_76 (and_65_out[11], ~GPFSEL1_q[3], ~GPFSEL1_q[4], ~GPFSEL1_q[5]);  // AND_Gate
  and and_77 (and_65_out[12], ~GPFSEL1_q[6], ~GPFSEL1_q[7], ~GPFSEL1_q[8]);  // AND_Gate
  and and_78 (and_65_out[13], ~GPFSEL1_q[9], ~GPFSEL1_q[10], ~GPFSEL1_q[11]);  // AND_Gate
  and and_79 (and_65_out[14], ~GPFSEL1_q[12], ~GPFSEL1_q[13], ~GPFSEL1_q[14]);  // AND_Gate
  and and_80 (and_65_out[15], ~GPFSEL1_q[15], ~GPFSEL1_q[16], ~GPFSEL1_q[17]);  // AND_Gate
  and and_81 (and_65_out[16], ~GPFSEL1_q[18], ~GPFSEL1_q[19], ~GPFSEL1_q[20]);  // AND_Gate
  and and_82 (and_65_out[17], ~GPFSEL1_q[21], ~GPFSEL1_q[22], ~GPFSEL1_q[23]);  // AND_Gate
  and and_83 (and_65_out[18], ~GPFSEL1_q[24], ~GPFSEL1_q[25], ~GPFSEL1_q[26]);  // AND_Gate
  and and_84 (and_65_out[19], ~GPFSEL1_q[27], ~GPFSEL1_q[28], ~GPFSEL1_q[29]);  // AND_Gate
  and and_85 (and_65_out[20], ~GPFSEL2_q[0], ~GPFSEL2_q[1], ~GPFSEL2_q[2]);  // AND_Gate
  and and_86 (and_65_out[21], ~GPFSEL2_q[3], ~GPFSEL2_q[4], ~GPFSEL2_q[5]);  // AND_Gate
  and and_87 (and_65_out[22], ~GPFSEL2_q[6], ~GPFSEL2_q[7], ~GPFSEL2_q[8]);  // AND_Gate
  and and_88 (and_65_out[23], ~GPFSEL2_q[9], ~GPFSEL2_q[10], ~GPFSEL2_q[11]);  // AND_Gate
  and and_89 (and_65_out[24], ~GPFSEL2_q[12], ~GPFSEL2_q[13], ~GPFSEL2_q[14]);  // AND_Gate
  and and_90 (and_65_out[25], ~GPFSEL2_q[15], ~GPFSEL2_q[16], ~GPFSEL2_q[17]);  // AND_Gate
  and and_91 (and_65_out[26], ~GPFSEL2_q[18], ~GPFSEL2_q[19], ~GPFSEL2_q[20]);  // AND_Gate
  and and_92 (and_65_out[27], ~GPFSEL2_q[21], ~GPFSEL2_q[22], ~GPFSEL2_q[23]);  // AND_Gate
  and and_93 (and_65_out[28], ~GPFSEL2_q[24], ~GPFSEL2_q[25], ~GPFSEL2_q[26]);  // AND_Gate
  and and_94 (and_65_out[29], ~GPFSEL2_q[27], ~GPFSEL2_q[28], ~GPFSEL2_q[29]);  // AND_Gate
  and and_95 (and_65_out[30], ~GPFSEL3_q[0], ~GPFSEL3_q[1], ~GPFSEL3_q[2]);  // AND_Gate
  and and_96 (and_65_out[31], ~GPFSEL3_q[3], ~GPFSEL3_q[4], ~GPFSEL3_q[5]);  // AND_Gate
  and and_97 (and_65_out[32], ~GPFSEL3_q[6], ~GPFSEL3_q[7], ~GPFSEL3_q[8]);  // AND_Gate
  and and_98 (and_65_out[33], ~GPFSEL3_q[9], ~GPFSEL3_q[10], ~GPFSEL3_q[11]);  // AND_Gate
  and and_99 (and_65_out[34], ~GPFSEL3_q[12], ~GPFSEL3_q[13], ~GPFSEL3_q[14]);  // AND_Gate
  and and_100 (and_65_out[35], ~GPFSEL3_q[15], ~GPFSEL3_q[16], ~GPFSEL3_q[17]);  // AND_Gate
  and and_101 (and_65_out[36], ~GPFSEL3_q[18], ~GPFSEL3_q[19], ~GPFSEL3_q[20]);  // AND_Gate
  and and_102 (and_65_out[37], ~GPFSEL3_q[21], ~GPFSEL3_q[22], ~GPFSEL3_q[23]);  // AND_Gate
  and and_103 (and_65_out[38], ~GPFSEL3_q[24], ~GPFSEL3_q[25], ~GPFSEL3_q[26]);  // AND_Gate
  and and_104 (and_65_out[39], ~GPFSEL3_q[27], ~GPFSEL3_q[28], ~GPFSEL3_q[29]);  // AND_Gate
  and and_105 (and_65_out[40], ~GPFSEL4_q[0], ~GPFSEL4_q[1], ~GPFSEL4_q[2]);  // AND_Gate
  and and_106 (and_65_out[41], ~GPFSEL4_q[3], ~GPFSEL4_q[4], ~GPFSEL4_q[5]);  // AND_Gate
  and and_107 (and_65_out[42], ~GPFSEL4_q[6], ~GPFSEL4_q[7], ~GPFSEL4_q[8]);  // AND_Gate
  and and_108 (and_65_out[43], ~GPFSEL4_q[9], ~GPFSEL4_q[10], ~GPFSEL4_q[11]);  // AND_Gate
  and and_109 (and_65_out[44], ~GPFSEL4_q[12], ~GPFSEL4_q[13], ~GPFSEL4_q[14]);  // AND_Gate
  and and_110 (and_65_out[45], ~GPFSEL4_q[15], ~GPFSEL4_q[16], ~GPFSEL4_q[17]);  // AND_Gate
  and and_111 (and_65_out[46], ~GPFSEL4_q[18], ~GPFSEL4_q[19], ~GPFSEL4_q[20]);  // AND_Gate
  and and_112 (and_65_out[47], ~GPFSEL4_q[21], ~GPFSEL4_q[22], ~GPFSEL4_q[23]);  // AND_Gate
  and and_113 (and_65_out[48], ~GPFSEL4_q[24], ~GPFSEL4_q[25], ~GPFSEL4_q[26]);  // AND_Gate
  and and_114 (and_65_out[49], ~GPFSEL4_q[27], ~GPFSEL4_q[28], ~GPFSEL4_q[29]);  // AND_Gate
  and and_115 (and_65_out[50], ~GPFSEL5_q[0], ~GPFSEL5_q[1], ~GPFSEL5_q[2]);  // AND_Gate
  and and_116 (and_65_out[51], ~GPFSEL5_q[3], ~GPFSEL5_q[4], ~GPFSEL5_q[5]);  // AND_Gate
  and and_117 (and_65_out[52], ~GPFSEL5_q[6], ~GPFSEL5_q[7], ~GPFSEL5_q[8]);  // AND_Gate
  and and_118 (and_65_out[53], ~GPFSEL5_q[9], ~GPFSEL5_q[10], ~GPFSEL5_q[11]);  // AND_Gate
  and and_119 (and_119_out[2], ~GPFSEL0_q[6], ~GPFSEL0_q[7], GPFSEL0_q[8]);  // AND_Gate
  and and_120 (and_119_out[3], ~GPFSEL0_q[9], ~GPFSEL0_q[10], GPFSEL0_q[11]);  // AND_Gate
  S_R_Flip_Flop s_r_ff_1 (.S(GPSET0_q[0]), .R(GPCLR0_q[0]), .clk(CLK), .Q(s_r_ff_1_q));  // open: reset, Qn, preset
  S_R_Flip_Flop s_r_ff_2 (.S(GPSET0_q[1]), .R(GPCLR0_q[1]), .clk(CLK), .Q(s_r_ff_2_q));  // open: reset, Qn, preset
  S_R_Flip_Flop s_r_ff_3 (.S(GPSET0_q[2]), .R(GPCLR0_q[2]), .clk(CLK), .Q(s_r_ff_3_q));  // open: reset, Qn, preset
  S_R_Flip_Flop s_r_ff_4 (.S(GPSET0_q[3]), .R(GPCLR0_q[3]), .clk(CLK), .Q(s_r_ff_4_q));  // open: reset, Qn, preset
  S_R_Flip_Flop s_r_ff_5 (.S(GPSET0_q[4]), .R(GPCLR0_q[4]), .clk(CLK), .Q(s_r_ff_5_q));  // open: reset, Qn, preset
  S_R_Flip_Flop s_r_ff_6 (.S(GPSET0_q[5]), .R(GPCLR0_q[5]), .clk(CLK), .Q(s_r_ff_6_q));  // open: reset, Qn, preset
  S_R_Flip_Flop s_r_ff_7 (.S(GPSET0_q[6]), .R(GPCLR0_q[6]), .clk(CLK), .Q(s_r_ff_7_q));  // open: reset, Qn, preset
  S_R_Flip_Flop s_r_ff_8 (.S(GPSET0_q[7]), .R(GPCLR0_q[7]), .clk(CLK), .Q(s_r_ff_8_q));  // open: reset, Qn, preset
  S_R_Flip_Flop s_r_ff_9 (.S(GPSET0_q[8]), .R(GPCLR0_q[8]), .clk(CLK), .Q(s_r_ff_9_q));  // open: reset, Qn, preset
  S_R_Flip_Flop s_r_ff_10 (.S(GPSET0_q[9]), .R(GPCLR0_q[9]), .clk(CLK), .Q(s_r_ff_10_q));  // open: reset, Qn, preset
  S_R_Flip_Flop s_r_ff_11 (.S(GPSET0_q[10]), .R(GPCLR0_q[10]), .clk(CLK), .Q(s_r_ff_11_q));  // open: reset, Qn, preset
  S_R_Flip_Flop s_r_ff_12 (.S(GPSET0_q[11]), .R(GPCLR0_q[11]), .clk(CLK), .Q(s_r_ff_12_q));  // open: reset, Qn, preset
  S_R_Flip_Flop s_r_ff_13 (.S(GPSET0_q[12]), .R(GPCLR0_q[12]), .clk(CLK), .Q(s_r_ff_13_q));  // open: reset, Qn, preset
  S_R_Flip_Flop s_r_ff_14 (.S(GPSET0_q[13]), .R(GPCLR0_q[13]), .clk(CLK), .Q(s_r_ff_14_q));  // open: reset, Qn, preset
  S_R_Flip_Flop s_r_ff_15 (.S(GPSET0_q[14]), .R(GPCLR0_q[14]), .clk(CLK), .Q(s_r_ff_15_q));  // open: reset, Qn, preset
  S_R_Flip_Flop s_r_ff_16 (.S(GPSET0_q[15]), .R(GPCLR0_q[15]), .clk(CLK), .Q(s_r_ff_16_q));  // open: reset, Qn, preset
  S_R_Flip_Flop s_r_ff_17 (.S(GPSET0_q[16]), .R(GPCLR0_q[16]), .clk(CLK), .Q(s_r_ff_17_q));  // open: reset, Qn, preset
  S_R_Flip_Flop s_r_ff_18 (.S(GPSET0_q[17]), .R(GPCLR0_q[17]), .clk(CLK), .Q(s_r_ff_18_q));  // open: reset, Qn, preset
  S_R_Flip_Flop s_r_ff_19 (.S(GPSET0_q[18]), .R(GPCLR0_q[18]), .clk(CLK), .Q(s_r_ff_19_q));  // open: reset, Qn, preset
  S_R_Flip_Flop s_r_ff_20 (.S(GPSET0_q[19]), .R(GPCLR0_q[19]), .clk(CLK), .Q(s_r_ff_20_q));  // open: reset, Qn, preset
  S_R_Flip_Flop s_r_ff_21 (.S(GPSET0_q[20]), .R(GPCLR0_q[20]), .clk(CLK), .Q(s_r_ff_21_q));  // open: reset, Qn, preset
  S_R_Flip_Flop s_r_ff_22 (.S(GPSET0_q[21]), .R(GPCLR0_q[21]), .clk(CLK), .Q(s_r_ff_22_q));  // open: reset, Qn, preset
  S_R_Flip_Flop s_r_ff_23 (.S(GPSET0_q[22]), .R(GPCLR0_q[22]), .clk(CLK), .Q(s_r_ff_23_q));  // open: reset, Qn, preset
  S_R_Flip_Flop s_r_ff_24 (.S(GPSET0_q[23]), .R(GPCLR0_q[23]), .clk(CLK), .Q(s_r_ff_24_q));  // open: reset, Qn, preset
  S_R_Flip_Flop s_r_ff_25 (.S(GPSET0_q[24]), .R(GPCLR0_q[24]), .clk(CLK), .Q(s_r_ff_25_q));  // open: reset, Qn, preset
  S_R_Flip_Flop s_r_ff_26 (.S(GPSET0_q[25]), .R(GPCLR0_q[25]), .clk(CLK), .Q(s_r_ff_26_q));  // open: reset, Qn, preset
  S_R_Flip_Flop s_r_ff_27 (.S(GPSET0_q[26]), .R(GPCLR0_q[26]), .clk(CLK), .Q(s_r_ff_27_q));  // open: reset, Qn, preset
  S_R_Flip_Flop s_r_ff_28 (.S(GPSET0_q[27]), .R(GPCLR0_q[27]), .clk(CLK), .Q(s_r_ff_28_q));  // open: reset, Qn, preset
  S_R_Flip_Flop s_r_ff_29 (.S(GPSET0_q[28]), .R(GPCLR0_q[28]), .clk(CLK), .Q(s_r_ff_29_q));  // open: reset, Qn, preset
  S_R_Flip_Flop s_r_ff_30 (.S(GPSET0_q[29]), .R(GPCLR0_q[29]), .clk(CLK), .Q(s_r_ff_30_q));  // open: reset, Qn, preset
  S_R_Flip_Flop s_r_ff_31 (.S(GPSET0_q[30]), .R(GPCLR0_q[30]), .clk(CLK), .Q(s_r_ff_31_q));  // open: reset, Qn, preset
  S_R_Flip_Flop s_r_ff_32 (.S(GPSET0_q[31]), .R(GPCLR0_q[31]), .clk(CLK), .Q(s_r_ff_32_q));  // open: reset, Qn, preset
  S_R_Flip_Flop s_r_ff_33 (.S(GPSET1_q[0]), .R(GPCLR1_q[0]), .clk(CLK), .Q(s_r_ff_33_q));  // open: reset, Qn, preset
  S_R_Flip_Flop s_r_ff_34 (.S(GPSET1_q[1]), .R(GPCLR1_q[1]), .clk(CLK), .Q(s_r_ff_34_q));  // open: reset, Qn, preset
  S_R_Flip_Flop s_r_ff_35 (.S(GPSET1_q[2]), .R(GPCLR1_q[2]), .clk(CLK), .Q(s_r_ff_35_q));  // open: reset, Qn, preset
  S_R_Flip_Flop s_r_ff_36 (.S(GPSET1_q[3]), .R(GPCLR1_q[3]), .clk(CLK), .Q(s_r_ff_36_q));  // open: reset, Qn, preset
  S_R_Flip_Flop s_r_ff_37 (.S(GPSET1_q[4]), .R(GPCLR1_q[4]), .clk(CLK), .Q(s_r_ff_37_q));  // open: reset, Qn, preset
  S_R_Flip_Flop s_r_ff_38 (.S(GPSET1_q[5]), .R(GPCLR1_q[5]), .clk(CLK), .Q(s_r_ff_38_q));  // open: reset, Qn, preset
  S_R_Flip_Flop s_r_ff_39 (.S(GPSET1_q[6]), .R(GPCLR1_q[6]), .clk(CLK), .Q(s_r_ff_39_q));  // open: reset, Qn, preset
  S_R_Flip_Flop s_r_ff_40 (.S(GPSET1_q[7]), .R(GPCLR1_q[7]), .clk(CLK), .Q(s_r_ff_40_q));  // open: reset, Qn, preset
  S_R_Flip_Flop s_r_ff_41 (.S(GPSET1_q[8]), .R(GPCLR1_q[8]), .clk(CLK), .Q(s_r_ff_41_q));  // open: reset, Qn, preset
  S_R_Flip_Flop s_r_ff_42 (.S(GPSET1_q[9]), .R(GPCLR1_q[9]), .clk(CLK), .Q(s_r_ff_42_q));  // open: reset, Qn, preset
  S_R_Flip_Flop s_r_ff_43 (.S(GPSET1_q[10]), .R(GPCLR1_q[10]), .clk(CLK), .Q(s_r_ff_43_q));  // open: reset, Qn, preset
  S_R_Flip_Flop s_r_ff_44 (.S(GPSET1_q[11]), .R(GPCLR1_q[11]), .clk(CLK), .Q(s_r_ff_44_q));  // open: reset, Qn, preset
  S_R_Flip_Flop s_r_ff_45 (.S(GPSET1_q[12]), .R(GPCLR1_q[12]), .clk(CLK), .Q(s_r_ff_45_q));  // open: reset, Qn, preset
  S_R_Flip_Flop s_r_ff_46 (.S(GPSET1_q[13]), .R(GPCLR1_q[13]), .clk(CLK), .Q(s_r_ff_46_q));  // open: reset, Qn, preset
  S_R_Flip_Flop s_r_ff_47 (.S(GPSET1_q[14]), .R(GPCLR1_q[14]), .clk(CLK), .Q(s_r_ff_47_q));  // open: reset, Qn, preset
  S_R_Flip_Flop s_r_ff_48 (.S(GPSET1_q[15]), .R(GPCLR1_q[15]), .clk(CLK), .Q(s_r_ff_48_q));  // open: reset, Qn, preset
  S_R_Flip_Flop s_r_ff_49 (.S(GPSET1_q[16]), .R(GPCLR1_q[16]), .clk(CLK), .Q(s_r_ff_49_q));  // open: reset, Qn, preset
  S_R_Flip_Flop s_r_ff_50 (.S(GPSET1_q[17]), .R(GPCLR1_q[17]), .clk(CLK), .Q(s_r_ff_50_q));  // open: reset, Qn, preset
  S_R_Flip_Flop s_r_ff_51 (.S(GPSET1_q[18]), .R(GPCLR1_q[18]), .clk(CLK), .Q(s_r_ff_51_q));  // open: reset, Qn, preset
  S_R_Flip_Flop s_r_ff_52 (.S(GPSET1_q[19]), .R(GPCLR1_q[19]), .clk(CLK), .Q(s_r_ff_52_q));  // open: reset, Qn, preset
  S_R_Flip_Flop s_r_ff_53 (.S(GPSET1_q[20]), .R(GPCLR1_q[20]), .clk(CLK), .Q(s_r_ff_53_q));  // open: reset, Qn, preset
  S_R_Flip_Flop s_r_ff_54 (.S(GPSET1_q[21]), .R(GPCLR1_q[21]), .clk(CLK), .Q(s_r_ff_54_q));  // open: reset, Qn, preset
  assign GPIO_OUT[0] = and_11_out[0] ? s_r_ff_1_q : 1'bz;  // Controlled_Buffer controlled_buffer_8
  assign GPIO_OUT[1] = and_11_out[1] ? s_r_ff_2_q : 1'bz;  // Controlled_Buffer controlled_buffer_9
  assign GPIO_OUT[2] = and_11_out[2] ? s_r_ff_3_q : 1'bz;  // Controlled_Buffer controlled_buffer_10
  assign GPIO_OUT[3] = and_11_out[3] ? s_r_ff_4_q : 1'bz;  // Controlled_Buffer controlled_buffer_11
  assign GPIO_OUT[4] = and_11_out[4] ? s_r_ff_5_q : 1'bz;  // Controlled_Buffer controlled_buffer_12
  assign GPIO_OUT[5] = and_11_out[5] ? s_r_ff_6_q : 1'bz;  // Controlled_Buffer controlled_buffer_13
  assign GPIO_OUT[6] = and_11_out[6] ? s_r_ff_7_q : 1'bz;  // Controlled_Buffer controlled_buffer_14
  assign GPIO_OUT[7] = and_11_out[7] ? s_r_ff_8_q : 1'bz;  // Controlled_Buffer controlled_buffer_15
  assign GPIO_OUT[8] = and_11_out[8] ? s_r_ff_9_q : 1'bz;  // Controlled_Buffer controlled_buffer_16
  assign GPIO_OUT[9] = and_11_out[9] ? s_r_ff_10_q : 1'bz;  // Controlled_Buffer controlled_buffer_17
  assign GPIO_OUT[10] = and_11_out[10] ? s_r_ff_11_q : 1'bz;  // Controlled_Buffer controlled_buffer_18
  assign GPIO_OUT[11] = and_11_out[11] ? s_r_ff_12_q : 1'bz;  // Controlled_Buffer controlled_buffer_19
  assign GPIO_OUT[12] = and_11_out[12] ? s_r_ff_13_q : 1'bz;  // Controlled_Buffer controlled_buffer_20
  assign GPIO_OUT[13] = and_11_out[13] ? s_r_ff_14_q : 1'bz;  // Controlled_Buffer controlled_buffer_21
  assign GPIO_OUT[14] = and_11_out[14] ? s_r_ff_15_q : 1'bz;  // Controlled_Buffer controlled_buffer_22
  assign GPIO_OUT[15] = and_11_out[15] ? s_r_ff_16_q : 1'bz;  // Controlled_Buffer controlled_buffer_23
  assign GPIO_OUT[16] = and_11_out[16] ? s_r_ff_17_q : 1'bz;  // Controlled_Buffer controlled_buffer_24
  assign GPIO_OUT[17] = and_11_out[17] ? s_r_ff_18_q : 1'bz;  // Controlled_Buffer controlled_buffer_25
  assign GPIO_OUT[18] = and_11_out[18] ? s_r_ff_19_q : 1'bz;  // Controlled_Buffer controlled_buffer_26
  assign GPIO_OUT[19] = and_11_out[19] ? s_r_ff_20_q : 1'bz;  // Controlled_Buffer controlled_buffer_27
  assign GPIO_OUT[20] = and_11_out[20] ? s_r_ff_21_q : 1'bz;  // Controlled_Buffer controlled_buffer_28
  assign GPIO_OUT[21] = and_11_out[21] ? s_r_ff_22_q : 1'bz;  // Controlled_Buffer controlled_buffer_29
  assign GPIO_OUT[22] = and_11_out[22] ? s_r_ff_23_q : 1'bz;  // Controlled_Buffer controlled_buffer_30
  assign GPIO_OUT[23] = and_11_out[23] ? s_r_ff_24_q : 1'bz;  // Controlled_Buffer controlled_buffer_31
  assign GPIO_OUT[24] = and_11_out[24] ? s_r_ff_25_q : 1'bz;  // Controlled_Buffer controlled_buffer_32
  assign GPIO_OUT[25] = and_11_out[25] ? s_r_ff_26_q : 1'bz;  // Controlled_Buffer controlled_buffer_33
  assign GPIO_OUT[26] = and_11_out[26] ? s_r_ff_27_q : 1'bz;  // Controlled_Buffer controlled_buffer_34
  assign GPIO_OUT[27] = and_11_out[27] ? s_r_ff_28_q : 1'bz;  // Controlled_Buffer controlled_buffer_35
  assign GPIO_OUT[28] = and_11_out[28] ? s_r_ff_29_q : 1'bz;  // Controlled_Buffer controlled_buffer_36
  assign GPIO_OUT[29] = and_11_out[29] ? s_r_ff_30_q : 1'bz;  // Controlled_Buffer controlled_buffer_37
  assign GPIO_OUT[30] = and_11_out[30] ? s_r_ff_31_q : 1'bz;  // Controlled_Buffer controlled_buffer_38
  assign GPIO_OUT[31] = and_11_out[31] ? s_r_ff_32_q : 1'bz;  // Controlled_Buffer controlled_buffer_39
  assign GPIO_OUT[32] = and_11_out[32] ? s_r_ff_33_q : 1'bz;  // Controlled_Buffer controlled_buffer_40
  assign GPIO_OUT[33] = and_11_out[33] ? s_r_ff_34_q : 1'bz;  // Controlled_Buffer controlled_buffer_41
  assign GPIO_OUT[34] = and_11_out[34] ? s_r_ff_35_q : 1'bz;  // Controlled_Buffer controlled_buffer_42
  assign GPIO_OUT[35] = and_11_out[35] ? s_r_ff_36_q : 1'bz;  // Controlled_Buffer controlled_buffer_43
  assign GPIO_OUT[36] = and_11_out[36] ? s_r_ff_37_q : 1'bz;  // Controlled_Buffer controlled_buffer_44
  assign GPIO_OUT[37] = and_11_out[37] ? s_r_ff_38_q : 1'bz;  // Controlled_Buffer controlled_buffer_45
  assign GPIO_OUT[38] = and_11_out[38] ? s_r_ff_39_q : 1'bz;  // Controlled_Buffer controlled_buffer_46
  assign GPIO_OUT[39] = and_11_out[39] ? s_r_ff_40_q : 1'bz;  // Controlled_Buffer controlled_buffer_47
  assign GPIO_OUT[40] = and_11_out[40] ? s_r_ff_41_q : 1'bz;  // Controlled_Buffer controlled_buffer_48
  assign GPIO_OUT[41] = and_11_out[41] ? s_r_ff_42_q : 1'bz;  // Controlled_Buffer controlled_buffer_49
  assign GPIO_OUT[42] = and_11_out[42] ? s_r_ff_43_q : 1'bz;  // Controlled_Buffer controlled_buffer_50
  assign GPIO_OUT[43] = and_11_out[43] ? s_r_ff_44_q : 1'bz;  // Controlled_Buffer controlled_buffer_51
  assign GPIO_OUT[44] = and_11_out[44] ? s_r_ff_45_q : 1'bz;  // Controlled_Buffer controlled_buffer_52
  assign GPIO_OUT[45] = and_11_out[45] ? s_r_ff_46_q : 1'bz;  // Controlled_Buffer controlled_buffer_53
  assign GPIO_OUT[46] = and_11_out[46] ? s_r_ff_47_q : 1'bz;  // Controlled_Buffer controlled_buffer_54
  assign GPIO_OUT[47] = and_11_out[47] ? s_r_ff_48_q : 1'bz;  // Controlled_Buffer controlled_buffer_55
  assign GPIO_OUT[48] = and_11_out[48] ? s_r_ff_49_q : 1'bz;  // Controlled_Buffer controlled_buffer_56
  assign GPIO_OUT[49] = and_11_out[49] ? s_r_ff_50_q : 1'bz;  // Controlled_Buffer controlled_buffer_57
  assign GPIO_OUT[50] = and_11_out[50] ? s_r_ff_51_q : 1'bz;  // Controlled_Buffer controlled_buffer_58
  assign GPIO_OUT[51] = and_11_out[51] ? s_r_ff_52_q : 1'bz;  // Controlled_Buffer controlled_buffer_59
  assign GPIO_OUT[52] = and_11_out[52] ? s_r_ff_53_q : 1'bz;  // Controlled_Buffer controlled_buffer_60
  assign GPIO_OUT[53] = and_11_out[53] ? s_r_ff_54_q : 1'bz;  // Controlled_Buffer controlled_buffer_61
  assign GPIO_OUT[2] = and_119_out[2] ? SDA_GPIO : 1'bz;  // Controlled_Buffer controlled_buffer_62
  assign GPIO_OUT[3] = and_119_out[3] ? SCL_GPIO : 1'bz;  // Controlled_Buffer controlled_buffer_63
  and and_121 (GPIO_DRIVE[2], and_119_out[2], SDA_DRIVE);
  and and_122 (GPIO_DRIVE[3], and_119_out[3], SCL_DRIVE);
  assign GPIO_SDA = and_119_out[2] ? GPIO_IN[2] : 1'bz;  // Controlled_Buffer controlled_buffer_64
  assign GPIO_SCL = and_119_out[3] ? GPIO_IN[3] : 1'bz;  // Controlled_Buffer controlled_buffer_65
  Register #(.width(1)) register_1 (.D(GPIO_IN[0]), .en(and_65_out[0]), .clk(CLK), .Q(register_1_q[0]));  // open: clr
  Register #(.width(1)) register_2 (.D(GPIO_IN[1]), .en(and_65_out[1]), .clk(CLK), .Q(register_1_q[1]));  // open: clr
  Register #(.width(1)) register_3 (.D(GPIO_IN[2]), .en(and_65_out[2]), .clk(CLK), .Q(register_1_q[2]));  // open: clr
  Register #(.width(1)) register_4 (.D(GPIO_IN[3]), .en(and_65_out[3]), .clk(CLK), .Q(register_1_q[3]));  // open: clr
  Register #(.width(1)) register_5 (.D(GPIO_IN[4]), .en(and_65_out[4]), .clk(CLK), .Q(register_1_q[4]));  // open: clr
  Register #(.width(1)) register_6 (.D(GPIO_IN[5]), .en(and_65_out[5]), .clk(CLK), .Q(register_1_q[5]));  // open: clr
  Register #(.width(1)) register_7 (.D(GPIO_IN[6]), .en(and_65_out[6]), .clk(CLK), .Q(register_1_q[6]));  // open: clr
  Register #(.width(1)) register_8 (.D(GPIO_IN[7]), .en(and_65_out[7]), .clk(CLK), .Q(register_1_q[7]));  // open: clr
  Register #(.width(1)) register_9 (.D(GPIO_IN[8]), .en(and_65_out[8]), .clk(CLK), .Q(register_1_q[8]));  // open: clr
  Register #(.width(1)) register_10 (.D(GPIO_IN[9]), .en(and_65_out[9]), .clk(CLK), .Q(register_1_q[9]));  // open: clr
  Register #(.width(1)) register_11 (
    .D(GPIO_IN[10]), .en(and_65_out[10]), .clk(CLK), .Q(register_1_q[10]));  // open: clr
  Register #(.width(1)) register_12 (
    .D(GPIO_IN[11]), .en(and_65_out[11]), .clk(CLK), .Q(register_1_q[11]));  // open: clr
  Register #(.width(1)) register_13 (
    .D(GPIO_IN[12]), .en(and_65_out[12]), .clk(CLK), .Q(register_1_q[12]));  // open: clr
  Register #(.width(1)) register_14 (
    .D(GPIO_IN[13]), .en(and_65_out[13]), .clk(CLK), .Q(register_1_q[13]));  // open: clr
  Register #(.width(1)) register_15 (
    .D(GPIO_IN[14]), .en(and_65_out[14]), .clk(CLK), .Q(register_1_q[14]));  // open: clr
  Register #(.width(1)) register_16 (
    .D(GPIO_IN[15]), .en(and_65_out[15]), .clk(CLK), .Q(register_1_q[15]));  // open: clr
  Register #(.width(1)) register_17 (
    .D(GPIO_IN[16]), .en(and_65_out[16]), .clk(CLK), .Q(register_1_q[16]));  // open: clr
  Register #(.width(1)) register_18 (
    .D(GPIO_IN[17]), .en(and_65_out[17]), .clk(CLK), .Q(register_1_q[17]));  // open: clr
  Register #(.width(1)) register_19 (
    .D(GPIO_IN[18]), .en(and_65_out[18]), .clk(CLK), .Q(register_1_q[18]));  // open: clr
  Register #(.width(1)) register_20 (
    .D(GPIO_IN[19]), .en(and_65_out[19]), .clk(CLK), .Q(register_1_q[19]));  // open: clr
  Register #(.width(1)) register_21 (
    .D(GPIO_IN[20]), .en(and_65_out[20]), .clk(CLK), .Q(register_1_q[20]));  // open: clr
  Register #(.width(1)) register_22 (
    .D(GPIO_IN[21]), .en(and_65_out[21]), .clk(CLK), .Q(register_1_q[21]));  // open: clr
  Register #(.width(1)) register_23 (
    .D(GPIO_IN[22]), .en(and_65_out[22]), .clk(CLK), .Q(register_1_q[22]));  // open: clr
  Register #(.width(1)) register_24 (
    .D(GPIO_IN[23]), .en(and_65_out[23]), .clk(CLK), .Q(register_1_q[23]));  // open: clr
  Register #(.width(1)) register_25 (
    .D(GPIO_IN[24]), .en(and_65_out[24]), .clk(CLK), .Q(register_1_q[24]));  // open: clr
  Register #(.width(1)) register_26 (
    .D(GPIO_IN[25]), .en(and_65_out[25]), .clk(CLK), .Q(register_1_q[25]));  // open: clr
  Register #(.width(1)) register_27 (
    .D(GPIO_IN[26]), .en(and_65_out[26]), .clk(CLK), .Q(register_1_q[26]));  // open: clr
  Register #(.width(1)) register_28 (
    .D(GPIO_IN[27]), .en(and_65_out[27]), .clk(CLK), .Q(register_1_q[27]));  // open: clr
  Register #(.width(1)) register_29 (
    .D(GPIO_IN[28]), .en(and_65_out[28]), .clk(CLK), .Q(register_1_q[28]));  // open: clr
  Register #(.width(1)) register_30 (
    .D(GPIO_IN[29]), .en(and_65_out[29]), .clk(CLK), .Q(register_1_q[29]));  // open: clr
  Register #(.width(1)) register_31 (
    .D(GPIO_IN[30]), .en(and_65_out[30]), .clk(CLK), .Q(register_1_q[30]));  // open: clr
  Register #(.width(1)) register_32 (
    .D(GPIO_IN[31]), .en(and_65_out[31]), .clk(CLK), .Q(register_1_q[31]));  // open: clr
  Register #(.width(1)) register_33 (
    .D(GPIO_IN[32]), .en(and_65_out[32]), .clk(CLK), .Q(register_33_q[0]));  // open: clr
  Register #(.width(1)) register_34 (
    .D(GPIO_IN[33]), .en(and_65_out[33]), .clk(CLK), .Q(register_33_q[1]));  // open: clr
  Register #(.width(1)) register_35 (
    .D(GPIO_IN[34]), .en(and_65_out[34]), .clk(CLK), .Q(register_33_q[2]));  // open: clr
  Register #(.width(1)) register_36 (
    .D(GPIO_IN[35]), .en(and_65_out[35]), .clk(CLK), .Q(register_33_q[3]));  // open: clr
  Register #(.width(1)) register_37 (
    .D(GPIO_IN[36]), .en(and_65_out[36]), .clk(CLK), .Q(register_33_q[4]));  // open: clr
  Register #(.width(1)) register_38 (
    .D(GPIO_IN[37]), .en(and_65_out[37]), .clk(CLK), .Q(register_33_q[5]));  // open: clr
  Register #(.width(1)) register_39 (
    .D(GPIO_IN[38]), .en(and_65_out[38]), .clk(CLK), .Q(register_33_q[6]));  // open: clr
  Register #(.width(1)) register_40 (
    .D(GPIO_IN[39]), .en(and_65_out[39]), .clk(CLK), .Q(register_33_q[7]));  // open: clr
  Register #(.width(1)) register_41 (
    .D(GPIO_IN[40]), .en(and_65_out[40]), .clk(CLK), .Q(register_33_q[8]));  // open: clr
  Register #(.width(1)) register_42 (
    .D(GPIO_IN[41]), .en(and_65_out[41]), .clk(CLK), .Q(register_33_q[9]));  // open: clr
  Register #(.width(1)) register_43 (
    .D(GPIO_IN[42]), .en(and_65_out[42]), .clk(CLK), .Q(register_33_q[10]));  // open: clr
  Register #(.width(1)) register_44 (
    .D(GPIO_IN[43]), .en(and_65_out[43]), .clk(CLK), .Q(register_33_q[11]));  // open: clr
  Register #(.width(1)) register_45 (
    .D(GPIO_IN[44]), .en(and_65_out[44]), .clk(CLK), .Q(register_33_q[12]));  // open: clr
  Register #(.width(1)) register_46 (
    .D(GPIO_IN[45]), .en(and_65_out[45]), .clk(CLK), .Q(register_33_q[13]));  // open: clr
  Register #(.width(1)) register_47 (
    .D(GPIO_IN[46]), .en(and_65_out[46]), .clk(CLK), .Q(register_33_q[14]));  // open: clr
  Register #(.width(1)) register_48 (
    .D(GPIO_IN[47]), .en(and_65_out[47]), .clk(CLK), .Q(register_33_q[15]));  // open: clr
  Register #(.width(1)) register_49 (
    .D(GPIO_IN[48]), .en(and_65_out[48]), .clk(CLK), .Q(register_33_q[16]));  // open: clr
  Register #(.width(1)) register_50 (
    .D(GPIO_IN[49]), .en(and_65_out[49]), .clk(CLK), .Q(register_33_q[17]));  // open: clr
  Register #(.width(1)) register_51 (
    .D(GPIO_IN[50]), .en(and_65_out[50]), .clk(CLK), .Q(register_33_q[18]));  // open: clr
  Register #(.width(1)) register_52 (
    .D(GPIO_IN[51]), .en(and_65_out[51]), .clk(CLK), .Q(register_33_q[19]));  // open: clr
  Register #(.width(1)) register_53 (
    .D(GPIO_IN[52]), .en(and_65_out[52]), .clk(CLK), .Q(register_33_q[20]));  // open: clr
  Register #(.width(1)) register_54 (
    .D(GPIO_IN[53]), .en(and_65_out[53]), .clk(CLK), .Q(register_33_q[21]));  // open: clr
  assign controlled_buffer_1_out = comparator_11_eq ? register_1_q : 32'bz;  // Controlled_Buffer controlled_buffer_66
  assign controlled_buffer_1_out = comparator_12_eq ? {{10{1'b0}}, register_33_q} : 32'bz;  // Controlled_Buffer controlled_buffer_67
  assign DATA_OUT = {{32{1'b0}}, controlled_buffer_1_out};  // Bit_Extender bit_extender_1
endmodule

module InsAddrAlignment (
  input  [63:0] ADDR,
  output ALIGNED,
  output NOT_ALIGNED
);

  Comparator #(.mode("unsigned"), .width(2)) comparator_1 (.a(2'b00), .b(ADDR[1:0]), .eq(ALIGNED));  // open: gt, lt
  not not_1 (NOT_ALIGNED, ALIGNED);
endmodule

module InsAddrRange (
  input  [63:0] ADDR,
  output IN_RANGE,
  output OUT_OF_RANGE
);

  Comparator #(.mode("unsigned"), .width(40)) comparator_1 (
    .a({40{1'b0}}), .b(ADDR[63:24]), .eq(IN_RANGE));  // open: gt, lt
  not not_1 (OUT_OF_RANGE, IN_RANGE);
endmodule
module ControlUnit (
  input  [31:0] INS,
  input  [3:0] FLAGS,
  output insB,
  output insBL,
  output insBR,
  output insCBZ,
  output insCBNZ,
  output insBCOND,
  output insSTUR,
  output insLDUR,
  output insAND,
  output insORR,
  output insEOR,
  output insADD,
  output insSUB,
  output insANDI,
  output insORRI,
  output insEORI,
  output insADDI,
  output insSUBI,
  output insANDS,
  output insADDS,
  output insSUBS,
  output insANDIS,
  output insADDIS,
  output insSUBIS,
  output insLSL,
  output insLSR,
  output insMOVK,
  output insMOVZ,
  output insMOVN,
  output insLSLV,
  output insLSRV,
  output insMUL,
  output insUMULH,
  output insSMULH,
  output insUDIV,
  output insSDIV,
  output insADR,
  output insNOT_IMPLEMENTED,
  output [1:0] AccessSize,
  output RdSP,
  output RnSP,
  output [5:0] Shamt,
  output B,
  output BL,
  output BR,
  output CBZ,
  output CBNZ,
  output MOVK,
  output MOVZ,
  output MOVN,
  output ADR,
  output BCOND_TRUE,
  output Reg2Loc,
  output RegWrite,
  output MemRead,
  output MemWrite,
  output ALUSrc,
  output MemtoReg,
  output [2:0] ImmSel,
  output [3:0] ALUop,
  output SetFlags
);

  wire and_1_out, and_2_out, decoder_1_out0, decoder_1_out1, decoder_1_out2, decoder_1_out3, decoder_1_out4,
       decoder_1_out5, decoder_1_out6, decoder_1_out7, decoder_1_out8, decoder_1_out9, decoder_1_out10,
       decoder_1_out11, decoder_1_out12, decoder_1_out13, decoder_1_out14, gADDop_out, gALUimm_out,
       gANDop_out, gBRAddr_out, gCONDBRAddr_out, gDTAddr_out, gEORop_out, gEQ_out, gGE_out, gGT_out, gHI_out,
       gHS_out, gLE_out, gLO_out, gLogicalImm_out, gLS_out, gLT_out, gMI_out, gMOVImm_out, gNE_out,
       gORop_out, gPASSBop_out, gPL_out, gSUBop_out, gVC_out, gVS_out, or_1_out, or_2_out, or_3_out,
       or_4_out, or_5_out, or_6_out, xnor_1_out, xnor_2_out, xor_1_out, xor_2_out;
  wire [5:0] subtractor_1_out;

  Subtractor #(.width(6)) subtractor_1 (
    .a({6{1'b1}}), .b(INS[15:10]), .out(subtractor_1_out), .bin(1'b0));  // open: bout
  Decoder #(.select(4)) decoder_1 (
    .out0(decoder_1_out0), .out1(decoder_1_out1), .out2(decoder_1_out2), .out3(decoder_1_out3),
    .out4(decoder_1_out4), .out5(decoder_1_out5), .out6(decoder_1_out6), .out7(decoder_1_out7),
    .out8(decoder_1_out8), .out9(decoder_1_out9), .out10(decoder_1_out10), .out11(decoder_1_out11),
    .out12(decoder_1_out12), .out13(decoder_1_out13), .out14(decoder_1_out14), .sel(INS[3:0]), .en(insBCOND));  // open: out15
  and gB (B, ~INS[31], ~INS[30], ~INS[29], INS[28], ~INS[27], INS[26]);  // AND_Gate
  and gBL (BL, INS[31], ~INS[30], ~INS[29], INS[28], ~INS[27], INS[26]);  // AND_Gate
  and gBR (BR, INS[31], INS[30], ~INS[29], INS[28], ~INS[27], INS[26], INS[25], ~INS[24], ~INS[23], ~INS[22], ~INS[21]);  // AND_Gate
  and gCBZ (CBZ, INS[31], ~INS[30], INS[29], INS[28], ~INS[27], INS[26], ~INS[25], ~INS[24]);  // AND_Gate
  and gCBNZ (CBNZ, INS[31], ~INS[30], INS[29], INS[28], ~INS[27], INS[26], ~INS[25], INS[24]);  // AND_Gate
  and gBCOND (insBCOND, ~INS[31], INS[30], ~INS[29], INS[28], ~INS[27], INS[26], ~INS[25], ~INS[24]);  // AND_Gate
  and gSTUR (insSTUR, INS[29], INS[28], INS[27], ~INS[26], ~INS[25], ~INS[24], ~INS[23], ~INS[22], ~INS[21]);  // AND_Gate
  and gLDUR (insLDUR, INS[29], INS[28], INS[27], ~INS[26], ~INS[25], ~INS[24], ~INS[23], INS[22], ~INS[21]);  // AND_Gate
  and gAND (insAND, INS[31], ~INS[30], ~INS[29], ~INS[28], INS[27], ~INS[26], INS[25], ~INS[24], ~INS[23], ~INS[22], ~INS[21]);  // AND_Gate
  and gORR (insORR, INS[31], ~INS[30], INS[29], ~INS[28], INS[27], ~INS[26], INS[25], ~INS[24], ~INS[23], ~INS[22], ~INS[21]);  // AND_Gate
  and gEOR (insEOR, INS[31], INS[30], ~INS[29], ~INS[28], INS[27], ~INS[26], INS[25], ~INS[24], ~INS[23], ~INS[22], ~INS[21]);  // AND_Gate
  and gADD (insADD, INS[31], ~INS[30], ~INS[29], ~INS[28], INS[27], ~INS[26], INS[25], INS[24], ~INS[23], ~INS[22]);  // AND_Gate
  and gSUB (insSUB, INS[31], INS[30], ~INS[29], ~INS[28], INS[27], ~INS[26], INS[25], INS[24], ~INS[23], ~INS[22]);  // AND_Gate
  and gANDI (insANDI, INS[31], ~INS[30], ~INS[29], INS[28], ~INS[27], ~INS[26], INS[25], ~INS[24], ~INS[23]);  // AND_Gate
  and gORRI (insORRI, INS[31], ~INS[30], INS[29], INS[28], ~INS[27], ~INS[26], INS[25], ~INS[24], ~INS[23]);  // AND_Gate
  and gEORI (insEORI, INS[31], INS[30], ~INS[29], INS[28], ~INS[27], ~INS[26], INS[25], ~INS[24], ~INS[23]);  // AND_Gate
  and gADDI (insADDI, INS[31], ~INS[30], ~INS[29], INS[28], ~INS[27], ~INS[26], ~INS[25], INS[24], ~INS[23], ~INS[22]);  // AND_Gate
  and gSUBI (insSUBI, INS[31], INS[30], ~INS[29], INS[28], ~INS[27], ~INS[26], ~INS[25], INS[24], ~INS[23], ~INS[22]);  // AND_Gate
  and gANDS (insANDS, INS[31], INS[30], INS[29], ~INS[28], INS[27], ~INS[26], INS[25], ~INS[24], ~INS[23], ~INS[22], ~INS[21]);  // AND_Gate
  and gADDS (insADDS, INS[31], ~INS[30], INS[29], ~INS[28], INS[27], ~INS[26], INS[25], INS[24], ~INS[23], ~INS[22]);  // AND_Gate
  and gSUBS (insSUBS, INS[31], INS[30], INS[29], ~INS[28], INS[27], ~INS[26], INS[25], INS[24], ~INS[23], ~INS[22]);  // AND_Gate
  and gANDIS (insANDIS, INS[31], INS[30], INS[29], INS[28], ~INS[27], ~INS[26], INS[25], ~INS[24], ~INS[23]);  // AND_Gate
  and gADDIS (insADDIS, INS[31], ~INS[30], INS[29], INS[28], ~INS[27], ~INS[26], ~INS[25], INS[24], ~INS[23], ~INS[22]);  // AND_Gate
  and gSUBIS (insSUBIS, INS[31], INS[30], INS[29], INS[28], ~INS[27], ~INS[26], ~INS[25], INS[24], ~INS[23], ~INS[22]);  // AND_Gate
  and gLSL (insLSL, INS[31], INS[30], ~INS[29], INS[28], ~INS[27], ~INS[26], INS[25], INS[24], ~INS[23], INS[22], ~insLSR);  // AND_Gate
  and gLSR (insLSR, INS[31], INS[30], ~INS[29], INS[28], ~INS[27], ~INS[26], INS[25], INS[24], ~INS[23], INS[22], INS[15], INS[14], INS[13], INS[12], INS[11], INS[10]);  // AND_Gate
  and gMOVK (insMOVK, INS[31], INS[30], INS[29], INS[28], ~INS[27], ~INS[26], INS[25], ~INS[24], INS[23]);  // AND_Gate
  and gMOVZ (insMOVZ, INS[31], INS[30], ~INS[29], INS[28], ~INS[27], ~INS[26], INS[25], ~INS[24], INS[23]);  // AND_Gate
  and gMOVN (insMOVN, INS[31], ~INS[30], ~INS[29], INS[28], ~INS[27], ~INS[26], INS[25], ~INS[24], INS[23]);  // AND_Gate
  and gLSLV (insLSLV, INS[31], ~INS[30], ~INS[29], INS[28], INS[27], ~INS[26], INS[25], ~INS[24], INS[23], INS[22], ~INS[21], ~INS[15], ~INS[14], INS[13], ~INS[12], ~INS[11], ~INS[10]);  // AND_Gate
  and gLSRV (insLSRV, INS[31], ~INS[30], ~INS[29], INS[28], INS[27], ~INS[26], INS[25], ~INS[24], INS[23], INS[22], ~INS[21], ~INS[15], ~INS[14], INS[13], ~INS[12], ~INS[11], INS[10]);  // AND_Gate
  and gMUL (insMUL, INS[31], ~INS[30], ~INS[29], INS[28], INS[27], ~INS[26], INS[25], INS[24], ~INS[23], ~INS[22], ~INS[21], ~INS[15], INS[14], INS[13], INS[12], INS[11], INS[10]);  // AND_Gate
  and gUMULH (insUMULH, INS[31], ~INS[30], ~INS[29], INS[28], INS[27], ~INS[26], INS[25], INS[24], INS[23], INS[22], ~INS[21]);  // AND_Gate
  and gSMULH (insSMULH, INS[31], ~INS[30], ~INS[29], INS[28], INS[27], ~INS[26], INS[25], INS[24], ~INS[23], INS[22], ~INS[21]);  // AND_Gate
  and UDIV (insUDIV, INS[31], ~INS[30], ~INS[29], INS[28], INS[27], ~INS[26], INS[25], ~INS[24], INS[23], INS[22], ~INS[21], ~INS[15], ~INS[14], ~INS[13], ~INS[12], INS[11], INS[10]);  // AND_Gate
  and gSDIV (insSDIV, INS[31], ~INS[30], ~INS[29], INS[28], INS[27], ~INS[26], INS[25], ~INS[24], INS[23], INS[22], ~INS[21], ~INS[15], ~INS[14], ~INS[13], ~INS[12], INS[11], ~INS[10]);  // AND_Gate
  and gADR (ADR, ~INS[31], ~INS[30], ~INS[29], INS[28], ~INS[27], ~INS[26], ~INS[25], ~INS[24]);  // AND_Gate
  nor nor_1 (insNOT_IMPLEMENTED, B, BL, BR, CBZ, CBNZ, insBCOND, insSTUR, insLDUR, insAND, insORR, insEOR, insADD, insSUB, insANDI, insORRI, insEORI, insADDI, insSUBI, insANDS, insADDS, insSUBS, insANDIS, insADDIS, insSUBIS, insLSL, insLSR, insMOVK, insMOVZ, insMOVN, insLSLV, insLSRV, insMUL, insUMULH, insSMULH, insUDIV, insSDIV, ADR);
  or or_1 (or_1_out, insSTUR, insLDUR);
  assign AccessSize = or_1_out ? INS[31:30] : 2'bz;  // Controlled_Buffer controlled_buffer_1
  and and_1 (and_1_out, INS[21], or_2_out);
  or or_2 (or_2_out, insADD, insSUB);
  and and_2 (and_2_out, INS[21], or_3_out);
  or or_3 (or_3_out, insADDS, insSUBS);
  assign Shamt = insLSL ? subtractor_1_out : 6'bz;  // Controlled_Buffer controlled_buffer_2
  assign Shamt = insLSR ? INS[21:16] : 6'bz;  // Controlled_Buffer controlled_buffer_3
  or or_4 (or_4_out, insMOVK, insMOVZ, insMOVN);
  assign Shamt = or_4_out ? {INS[22:21], 4'b0000} : 6'bz;  // Controlled_Buffer controlled_buffer_4
  and gEQ (gEQ_out, decoder_1_out0, FLAGS[0]);
  and gNE (gNE_out, decoder_1_out1, ~FLAGS[0]);  // AND_Gate
  and gHS (gHS_out, decoder_1_out2, FLAGS[2]);
  and gLO (gLO_out, decoder_1_out3, ~FLAGS[2]);  // AND_Gate
  and gMI (gMI_out, decoder_1_out4, FLAGS[1]);
  and gPL (gPL_out, decoder_1_out5, ~FLAGS[1]);  // AND_Gate
  and gVS (gVS_out, decoder_1_out6, FLAGS[3]);
  and gVC (gVC_out, decoder_1_out7, ~FLAGS[3]);  // AND_Gate
  and gHI (gHI_out, decoder_1_out8, ~FLAGS[0], FLAGS[2]);  // AND_Gate
  or or_5 (or_5_out, FLAGS[0], ~FLAGS[2]);  // OR_Gate
  xnor xnor_1 (xnor_1_out, FLAGS[1], FLAGS[3]);
  xor xor_1 (xor_1_out, FLAGS[1], FLAGS[3]);
  xnor xnor_2 (xnor_2_out, FLAGS[1], FLAGS[3]);
  or or_6 (or_6_out, FLAGS[0], xor_2_out);
  xor xor_2 (xor_2_out, FLAGS[1], FLAGS[3]);
  or or_7 (Reg2Loc, CBZ, CBNZ, insSTUR, insMOVK);
  or or_8 (RegWrite, BL, insLDUR, insAND, insORR, insEOR, insADD, insSUB, insANDI, insORRI, insEORI, insADDI, insSUBI, insANDS, insADDS, insSUBS, insANDIS, insADDIS, insSUBIS, insLSL, insLSR, insMOVK, insMOVZ, insMOVN, insLSLV, insLSRV, insMUL, insUMULH, insSMULH, insUDIV, insSDIV, ADR);
  or or_9 (ALUSrc, insSTUR, insLDUR, insANDI, insORRI, insEORI, insADDI, insSUBI, insANDIS, insADDIS, insSUBIS, insMOVK, insMOVZ, insMOVN);
  or gALUimm (gALUimm_out, insADDI, insSUBI, insADDIS, insSUBIS);
  or gDTAddr (gDTAddr_out, insSTUR, insLDUR);
  or gBRAddr (gBRAddr_out, B, BL);
  or gCONDBRAddr (gCONDBRAddr_out, CBZ, CBNZ, insBCOND, ADR);
  or gMOVImm (gMOVImm_out, insMOVK, insMOVZ, insMOVN);
  or gLogicalImm (gLogicalImm_out, insANDI, insORRI, insEORI, insANDIS);
  or gANDop (gANDop_out, insAND, insANDI, insANDS, insANDIS);
  or gORop (gORop_out, insORR, insORRI);
  or gEORop (gEORop_out, insEOR, insEORI);
  or gADDop (gADDop_out, insSTUR, insLDUR, insADD, insADDI, insADDS, insADDIS);
  or gSUBop (gSUBop_out, insSUB, insSUBI, insSUBS, insSUBIS);
  or gPASSBop (gPASSBop_out, CBZ, CBNZ, insMOVK, insMOVZ, insMOVN);
  or or_10 (SetFlags, insANDS, insADDS, insSUBS, insANDIS, insADDIS, insSUBIS);
  or or_11 (RdSP, and_1_out, insANDI, insORRI, insEORI, insADDI, insSUBI);
  or or_12 (RnSP, and_1_out, and_2_out, insSTUR, insLDUR, insADDI, insSUBI, insADDIS, insSUBIS);
  and gLS (gLS_out, decoder_1_out9, or_5_out);
  and gGE (gGE_out, decoder_1_out10, xnor_1_out);
  and gLT (gLT_out, decoder_1_out11, xor_1_out);
  and gGT (gGT_out, decoder_1_out12, ~FLAGS[0], xnor_2_out);  // AND_Gate
  and gLE (gLE_out, decoder_1_out13, or_6_out);
  Priority_Encoder priority_encoder_1 (
    .in0(gALUimm_out), .in1(gDTAddr_out), .in2(gBRAddr_out), .in3(gCONDBRAddr_out), .in4(gMOVImm_out),
    .in5(gLogicalImm_out), .out(ImmSel), .en_in(1'b1));  // open: in6, in7, gs, en_out
  Priority_Encoder #(.select(4)) priority_encoder_2 (
    .in0(gANDop_out), .in1(gORop_out), .in2(gEORop_out), .in3(gADDop_out), .in4(gSUBop_out), .in5(insLSL),
    .in6(insLSR), .in7(insLSLV), .in8(insLSRV), .in9(insMUL), .in10(insUMULH), .in11(insSMULH),
    .in12(insUDIV), .in13(insSDIV), .in14(gPASSBop_out), .out(ALUop), .en_in(1'b1));  // open: in15, gs, en_out
  or or_13 (BCOND_TRUE, gEQ_out, gNE_out, gHS_out, gLO_out, gMI_out, gPL_out, gVS_out, gVC_out, gHI_out, gLS_out, gGE_out, gLT_out, gGT_out, gLE_out, decoder_1_out14);

  assign insADR = ADR;
  assign insB = B;
  assign insBL = BL;
  assign insBR = BR;
  assign insCBNZ = CBNZ;
  assign insCBZ = CBZ;
  assign MemRead = insLDUR;
  assign MemtoReg = insLDUR;
  assign MemWrite = insSTUR;
  assign MOVK = insMOVK;
  assign MOVN = insMOVN;
  assign MOVZ = insMOVZ;
endmodule

module ImmediateExtend (
  input  [2:0] CTRL,
  input  [31:0] INS,
  output ZERO_EXTEND,
  output SIGN_EXTEND,
  output IMM12,
  output IMM9,
  output IMM26,
  output IMM19,
  output IMM16,
  output IMM13,
  output [63:0] IMMEDIATE,
  output [63:0] EXTENDED1,
  output [63:0] EXTENDED2,
  output [63:0] EXTENDED3
);

  wire [63:0] bit_extender_1_out, bit_extender_2_out, bit_extender_3_out, bit_extender_4_out,
       bit_extender_5_out, bitmaskimmediate_1_out_2;

  assign bit_extender_1_out = {{52{1'b0}}, INS[21:10]};  // Bit_Extender bit_extender_1
  assign bit_extender_2_out = {{55{INS[20]}}, INS[20:12]};  // Bit_Extender bit_extender_2
  assign bit_extender_3_out = {{38{INS[25]}}, INS[25:0]};  // Bit_Extender bit_extender_3
  assign bit_extender_4_out = {{45{INS[23]}}, INS[23:5]};  // Bit_Extender bit_extender_4
  assign bit_extender_5_out = {{48{1'b0}}, INS[20:5]};  // Bit_Extender bit_extender_5
  BitmaskImmediate bitmaskimmediate_1 (.out_2(bitmaskimmediate_1_out_2), .in_1(INS[22:10]));
  Decoder #(.enable("false"), .select(3)) decoder_1 (
    .out0(IMM12), .out1(IMM9), .out2(IMM26), .out3(IMM19), .out4(IMM16), .out5(IMM13), .sel(CTRL));  // open: out6, out7
  Multiplexer #(.enable("false"), .select(3), .width(64)) multiplexer_1 (
    .in0(bit_extender_1_out), .in1(bit_extender_2_out), .in2(bit_extender_3_out), .in3(bit_extender_4_out),
    .in4(bit_extender_5_out), .in5(bitmaskimmediate_1_out_2), .out(EXTENDED1), .sel(CTRL));  // open: in6, in7
  or or_1 (ZERO_EXTEND, IMM12, IMM16);
  or or_2 (SIGN_EXTEND, IMM9, IMM26, IMM19);

  assign EXTENDED2 = EXTENDED1;
  assign EXTENDED3 = EXTENDED1;
  assign IMMEDIATE = EXTENDED1;
endmodule

module RegisterFile (
  input  [4:0] READ_ADDR1,
  input  [4:0] READ_ADDR2,
  input  [4:0] WRITE_ADDR,
  input  [63:0] WRITE_DATA,
  input  WRITE_ENABLE,
  input  CLOCK,
  input  WRITE_USE_SP,
  input  READ1_USE_SP,
  output [63:0] RD11,
  output [63:0] RD12,
  output [63:0] RD13,
  output [4:0] RA1,
  output [63:0] RD21,
  output [63:0] WD1,
  output [4:0] RA2,
  output [63:0] RD22,
  output [63:0] WD2,
  output [63:0] RD23,
  output [4:0] WA,
  output [63:0] WD3,
  output [63:0] READ_DATA1,
  output [63:0] READ_DATA2,
  output WE
);

  wire and_1_out, and_2_out, and_3_out, decoder_1_out0, decoder_1_out1, decoder_1_out2, decoder_1_out3,
       decoder_1_out4, decoder_1_out5, decoder_1_out6, decoder_1_out7, decoder_1_out8, decoder_1_out9,
       decoder_1_out10, decoder_1_out11, decoder_1_out12, decoder_1_out13, decoder_1_out14, decoder_1_out15,
       decoder_1_out16, decoder_1_out17, decoder_1_out18, decoder_1_out19, decoder_1_out20, decoder_1_out21,
       decoder_1_out22, decoder_1_out23, decoder_1_out24, decoder_1_out25, decoder_1_out26, decoder_1_out27,
       decoder_1_out28, decoder_1_out29, decoder_1_out30, decoder_1_out31, decoder_2_out0, decoder_2_out1,
       decoder_2_out2, decoder_2_out3, decoder_2_out4, decoder_2_out5, decoder_2_out6, decoder_2_out7,
       decoder_2_out8, decoder_2_out9, decoder_2_out10, decoder_2_out11, decoder_2_out12, decoder_2_out13,
       decoder_2_out14, decoder_2_out15, decoder_2_out16, decoder_2_out17, decoder_2_out18, decoder_2_out19,
       decoder_2_out20, decoder_2_out21, decoder_2_out22, decoder_2_out23, decoder_2_out24, decoder_2_out25,
       decoder_2_out26, decoder_2_out27, decoder_2_out28, decoder_2_out29, decoder_2_out30, decoder_2_out31,
       decoder_3_out0, decoder_3_out1, decoder_3_out2, decoder_3_out3, decoder_3_out4, decoder_3_out5,
       decoder_3_out6, decoder_3_out7, decoder_3_out8, decoder_3_out9, decoder_3_out10, decoder_3_out11,
       decoder_3_out12, decoder_3_out13, decoder_3_out14, decoder_3_out15, decoder_3_out16, decoder_3_out17,
       decoder_3_out18, decoder_3_out19, decoder_3_out20, decoder_3_out21, decoder_3_out22, decoder_3_out23,
       decoder_3_out24, decoder_3_out25, decoder_3_out26, decoder_3_out27, decoder_3_out28, decoder_3_out29,
       decoder_3_out30, decoder_3_out31;
  wire [63:0] SP_q, X0_q, X1_q, X2_q, X3_q, X4_q, X5_q, X6_q, X7_q, X8_q, X9_q, X10_q, X11_q, X12_q, X13_q,
       X14_q, X15_q, X16_q, X17_q, X18_q, X19_q, X20_q, X21_q, X22_q, X23_q, X24_q, X25_q, X26_q, X27_q,
       X28_q, X29_q, X30_q;

  Decoder #(.select(5)) decoder_1 (
    .out0(decoder_1_out0), .out1(decoder_1_out1), .out2(decoder_1_out2), .out3(decoder_1_out3),
    .out4(decoder_1_out4), .out5(decoder_1_out5), .out6(decoder_1_out6), .out7(decoder_1_out7),
    .out8(decoder_1_out8), .out9(decoder_1_out9), .out10(decoder_1_out10), .out11(decoder_1_out11),
    .out12(decoder_1_out12), .out13(decoder_1_out13), .out14(decoder_1_out14), .out15(decoder_1_out15),
    .out16(decoder_1_out16), .out17(decoder_1_out17), .out18(decoder_1_out18), .out19(decoder_1_out19),
    .out20(decoder_1_out20), .out21(decoder_1_out21), .out22(decoder_1_out22), .out23(decoder_1_out23),
    .out24(decoder_1_out24), .out25(decoder_1_out25), .out26(decoder_1_out26), .out27(decoder_1_out27),
    .out28(decoder_1_out28), .out29(decoder_1_out29), .out30(decoder_1_out30), .out31(decoder_1_out31),
    .sel(WRITE_ADDR), .en(WRITE_ENABLE));
  Decoder #(.enable("false"), .select(5)) decoder_2 (
    .out0(decoder_2_out0), .out1(decoder_2_out1), .out2(decoder_2_out2), .out3(decoder_2_out3),
    .out4(decoder_2_out4), .out5(decoder_2_out5), .out6(decoder_2_out6), .out7(decoder_2_out7),
    .out8(decoder_2_out8), .out9(decoder_2_out9), .out10(decoder_2_out10), .out11(decoder_2_out11),
    .out12(decoder_2_out12), .out13(decoder_2_out13), .out14(decoder_2_out14), .out15(decoder_2_out15),
    .out16(decoder_2_out16), .out17(decoder_2_out17), .out18(decoder_2_out18), .out19(decoder_2_out19),
    .out20(decoder_2_out20), .out21(decoder_2_out21), .out22(decoder_2_out22), .out23(decoder_2_out23),
    .out24(decoder_2_out24), .out25(decoder_2_out25), .out26(decoder_2_out26), .out27(decoder_2_out27),
    .out28(decoder_2_out28), .out29(decoder_2_out29), .out30(decoder_2_out30), .out31(decoder_2_out31),
    .sel(READ_ADDR1));
  Decoder #(.enable("false"), .select(5)) decoder_3 (
    .out0(decoder_3_out0), .out1(decoder_3_out1), .out2(decoder_3_out2), .out3(decoder_3_out3),
    .out4(decoder_3_out4), .out5(decoder_3_out5), .out6(decoder_3_out6), .out7(decoder_3_out7),
    .out8(decoder_3_out8), .out9(decoder_3_out9), .out10(decoder_3_out10), .out11(decoder_3_out11),
    .out12(decoder_3_out12), .out13(decoder_3_out13), .out14(decoder_3_out14), .out15(decoder_3_out15),
    .out16(decoder_3_out16), .out17(decoder_3_out17), .out18(decoder_3_out18), .out19(decoder_3_out19),
    .out20(decoder_3_out20), .out21(decoder_3_out21), .out22(decoder_3_out22), .out23(decoder_3_out23),
    .out24(decoder_3_out24), .out25(decoder_3_out25), .out26(decoder_3_out26), .out27(decoder_3_out27),
    .out28(decoder_3_out28), .out29(decoder_3_out29), .out30(decoder_3_out30), .out31(decoder_3_out31),
    .sel(READ_ADDR2));
  Register #(.width(64)) X0 (.D(WRITE_DATA), .en(decoder_1_out0), .clk(CLOCK), .Q(X0_q));  // open: clr
  Register #(.width(64)) X1 (.D(WRITE_DATA), .en(decoder_1_out1), .clk(CLOCK), .Q(X1_q));  // open: clr
  Register #(.width(64)) X2 (.D(WRITE_DATA), .en(decoder_1_out2), .clk(CLOCK), .Q(X2_q));  // open: clr
  Register #(.width(64)) X3 (.D(WRITE_DATA), .en(decoder_1_out3), .clk(CLOCK), .Q(X3_q));  // open: clr
  Register #(.width(64)) X4 (.D(WRITE_DATA), .en(decoder_1_out4), .clk(CLOCK), .Q(X4_q));  // open: clr
  Register #(.width(64)) X5 (.D(WRITE_DATA), .en(decoder_1_out5), .clk(CLOCK), .Q(X5_q));  // open: clr
  Register #(.width(64)) X6 (.D(WRITE_DATA), .en(decoder_1_out6), .clk(CLOCK), .Q(X6_q));  // open: clr
  Register #(.width(64)) X7 (.D(WRITE_DATA), .en(decoder_1_out7), .clk(CLOCK), .Q(X7_q));  // open: clr
  Register #(.width(64)) X8 (.D(WRITE_DATA), .en(decoder_1_out8), .clk(CLOCK), .Q(X8_q));  // open: clr
  Register #(.width(64)) X9 (.D(WRITE_DATA), .en(decoder_1_out9), .clk(CLOCK), .Q(X9_q));  // open: clr
  Register #(.width(64)) X10 (.D(WRITE_DATA), .en(decoder_1_out10), .clk(CLOCK), .Q(X10_q));  // open: clr
  Register #(.width(64)) X11 (.D(WRITE_DATA), .en(decoder_1_out11), .clk(CLOCK), .Q(X11_q));  // open: clr
  Register #(.width(64)) X12 (.D(WRITE_DATA), .en(decoder_1_out12), .clk(CLOCK), .Q(X12_q));  // open: clr
  Register #(.width(64)) X13 (.D(WRITE_DATA), .en(decoder_1_out13), .clk(CLOCK), .Q(X13_q));  // open: clr
  Register #(.width(64)) X14 (.D(WRITE_DATA), .en(decoder_1_out14), .clk(CLOCK), .Q(X14_q));  // open: clr
  Register #(.width(64)) X15 (.D(WRITE_DATA), .en(decoder_1_out15), .clk(CLOCK), .Q(X15_q));  // open: clr
  Register #(.width(64)) X16 (.D(WRITE_DATA), .en(decoder_1_out16), .clk(CLOCK), .Q(X16_q));  // open: clr
  Register #(.width(64)) X17 (.D(WRITE_DATA), .en(decoder_1_out17), .clk(CLOCK), .Q(X17_q));  // open: clr
  Register #(.width(64)) X18 (.D(WRITE_DATA), .en(decoder_1_out18), .clk(CLOCK), .Q(X18_q));  // open: clr
  Register #(.width(64)) X19 (.D(WRITE_DATA), .en(decoder_1_out19), .clk(CLOCK), .Q(X19_q));  // open: clr
  Register #(.width(64)) X20 (.D(WRITE_DATA), .en(decoder_1_out20), .clk(CLOCK), .Q(X20_q));  // open: clr
  Register #(.width(64)) X21 (.D(WRITE_DATA), .en(decoder_1_out21), .clk(CLOCK), .Q(X21_q));  // open: clr
  Register #(.width(64)) X22 (.D(WRITE_DATA), .en(decoder_1_out22), .clk(CLOCK), .Q(X22_q));  // open: clr
  Register #(.width(64)) X23 (.D(WRITE_DATA), .en(decoder_1_out23), .clk(CLOCK), .Q(X23_q));  // open: clr
  Register #(.width(64)) X24 (.D(WRITE_DATA), .en(decoder_1_out24), .clk(CLOCK), .Q(X24_q));  // open: clr
  Register #(.width(64)) X25 (.D(WRITE_DATA), .en(decoder_1_out25), .clk(CLOCK), .Q(X25_q));  // open: clr
  Register #(.width(64)) X26 (.D(WRITE_DATA), .en(decoder_1_out26), .clk(CLOCK), .Q(X26_q));  // open: clr
  Register #(.width(64)) X27 (.D(WRITE_DATA), .en(decoder_1_out27), .clk(CLOCK), .Q(X27_q));  // open: clr
  Register #(.width(64)) X28 (.D(WRITE_DATA), .en(decoder_1_out28), .clk(CLOCK), .Q(X28_q));  // open: clr
  Register #(.width(64)) X29 (.D(WRITE_DATA), .en(decoder_1_out29), .clk(CLOCK), .Q(X29_q));  // open: clr
  Register #(.width(64)) X30 (.D(WRITE_DATA), .en(decoder_1_out30), .clk(CLOCK), .Q(X30_q));  // open: clr
  Register #(.width(64)) SP (.D(WRITE_DATA), .en(and_1_out), .clk(CLOCK), .Q(SP_q));  // open: clr
  and and_1 (and_1_out, WRITE_USE_SP, decoder_1_out31);
  and and_2 (and_2_out, READ1_USE_SP, decoder_2_out31);
  assign RD11 = decoder_2_out0 ? X0_q : 64'bz;  // Controlled_Buffer controlled_buffer_1
  assign RD11 = decoder_2_out1 ? X1_q : 64'bz;  // Controlled_Buffer controlled_buffer_2
  assign RD11 = decoder_2_out2 ? X2_q : 64'bz;  // Controlled_Buffer controlled_buffer_3
  assign RD11 = decoder_2_out3 ? X3_q : 64'bz;  // Controlled_Buffer controlled_buffer_4
  assign RD11 = decoder_2_out4 ? X4_q : 64'bz;  // Controlled_Buffer controlled_buffer_5
  assign RD11 = decoder_2_out5 ? X5_q : 64'bz;  // Controlled_Buffer controlled_buffer_6
  assign RD11 = decoder_2_out6 ? X6_q : 64'bz;  // Controlled_Buffer controlled_buffer_7
  assign RD11 = decoder_2_out7 ? X7_q : 64'bz;  // Controlled_Buffer controlled_buffer_8
  assign RD11 = decoder_2_out8 ? X8_q : 64'bz;  // Controlled_Buffer controlled_buffer_9
  assign RD11 = decoder_2_out9 ? X9_q : 64'bz;  // Controlled_Buffer controlled_buffer_10
  assign RD11 = decoder_2_out10 ? X10_q : 64'bz;  // Controlled_Buffer controlled_buffer_11
  assign RD11 = decoder_2_out11 ? X11_q : 64'bz;  // Controlled_Buffer controlled_buffer_12
  assign RD11 = decoder_2_out12 ? X12_q : 64'bz;  // Controlled_Buffer controlled_buffer_13
  assign RD11 = decoder_2_out13 ? X13_q : 64'bz;  // Controlled_Buffer controlled_buffer_14
  assign RD11 = decoder_2_out14 ? X14_q : 64'bz;  // Controlled_Buffer controlled_buffer_15
  assign RD11 = decoder_2_out15 ? X15_q : 64'bz;  // Controlled_Buffer controlled_buffer_16
  assign RD11 = decoder_2_out16 ? X16_q : 64'bz;  // Controlled_Buffer controlled_buffer_17
  assign RD11 = decoder_2_out17 ? X17_q : 64'bz;  // Controlled_Buffer controlled_buffer_18
  assign RD11 = decoder_2_out18 ? X18_q : 64'bz;  // Controlled_Buffer controlled_buffer_19
  assign RD11 = decoder_2_out19 ? X19_q : 64'bz;  // Controlled_Buffer controlled_buffer_20
  assign RD11 = decoder_2_out20 ? X20_q : 64'bz;  // Controlled_Buffer controlled_buffer_21
  assign RD11 = decoder_2_out21 ? X21_q : 64'bz;  // Controlled_Buffer controlled_buffer_22
  assign RD11 = decoder_2_out22 ? X22_q : 64'bz;  // Controlled_Buffer controlled_buffer_23
  assign RD11 = decoder_2_out23 ? X23_q : 64'bz;  // Controlled_Buffer controlled_buffer_24
  assign RD11 = decoder_2_out24 ? X24_q : 64'bz;  // Controlled_Buffer controlled_buffer_25
  assign RD11 = decoder_2_out25 ? X25_q : 64'bz;  // Controlled_Buffer controlled_buffer_26
  assign RD11 = decoder_2_out26 ? X26_q : 64'bz;  // Controlled_Buffer controlled_buffer_27
  assign RD11 = decoder_2_out27 ? X27_q : 64'bz;  // Controlled_Buffer controlled_buffer_28
  assign RD11 = decoder_2_out28 ? X28_q : 64'bz;  // Controlled_Buffer controlled_buffer_29
  assign RD11 = decoder_2_out29 ? X29_q : 64'bz;  // Controlled_Buffer controlled_buffer_30
  assign RD11 = decoder_2_out30 ? X30_q : 64'bz;  // Controlled_Buffer controlled_buffer_31
  assign RD11 = and_2_out ? SP_q : 64'bz;  // Controlled_Buffer controlled_buffer_32
  assign RD11 = and_3_out ? {64{1'b0}} : 64'bz;  // Controlled_Buffer controlled_buffer_33
  and and_3 (and_3_out, ~READ1_USE_SP, decoder_2_out31);  // AND_Gate
  assign RD21 = decoder_3_out0 ? X0_q : 64'bz;  // Controlled_Buffer controlled_buffer_34
  assign RD21 = decoder_3_out1 ? X1_q : 64'bz;  // Controlled_Buffer controlled_buffer_35
  assign RD21 = decoder_3_out2 ? X2_q : 64'bz;  // Controlled_Buffer controlled_buffer_36
  assign RD21 = decoder_3_out3 ? X3_q : 64'bz;  // Controlled_Buffer controlled_buffer_37
  assign RD21 = decoder_3_out4 ? X4_q : 64'bz;  // Controlled_Buffer controlled_buffer_38
  assign RD21 = decoder_3_out5 ? X5_q : 64'bz;  // Controlled_Buffer controlled_buffer_39
  assign RD21 = decoder_3_out6 ? X6_q : 64'bz;  // Controlled_Buffer controlled_buffer_40
  assign RD21 = decoder_3_out7 ? X7_q : 64'bz;  // Controlled_Buffer controlled_buffer_41
  assign RD21 = decoder_3_out8 ? X8_q : 64'bz;  // Controlled_Buffer controlled_buffer_42
  assign RD21 = decoder_3_out9 ? X9_q : 64'bz;  // Controlled_Buffer controlled_buffer_43
  assign RD21 = decoder_3_out10 ? X10_q : 64'bz;  // Controlled_Buffer controlled_buffer_44
  assign RD21 = decoder_3_out11 ? X11_q : 64'bz;  // Controlled_Buffer controlled_buffer_45
  assign RD21 = decoder_3_out12 ? X12_q : 64'bz;  // Controlled_Buffer controlled_buffer_46
  assign RD21 = decoder_3_out13 ? X13_q : 64'bz;  // Controlled_Buffer controlled_buffer_47
  assign RD21 = decoder_3_out14 ? X14_q : 64'bz;  // Controlled_Buffer controlled_buffer_48
  assign RD21 = decoder_3_out15 ? X15_q : 64'bz;  // Controlled_Buffer controlled_buffer_49
  assign RD21 = decoder_3_out16 ? X16_q : 64'bz;  // Controlled_Buffer controlled_buffer_50
  assign RD21 = decoder_3_out17 ? X17_q : 64'bz;  // Controlled_Buffer controlled_buffer_51
  assign RD21 = decoder_3_out18 ? X18_q : 64'bz;  // Controlled_Buffer controlled_buffer_52
  assign RD21 = decoder_3_out19 ? X19_q : 64'bz;  // Controlled_Buffer controlled_buffer_53
  assign RD21 = decoder_3_out20 ? X20_q : 64'bz;  // Controlled_Buffer controlled_buffer_54
  assign RD21 = decoder_3_out21 ? X21_q : 64'bz;  // Controlled_Buffer controlled_buffer_55
  assign RD21 = decoder_3_out22 ? X22_q : 64'bz;  // Controlled_Buffer controlled_buffer_56
  assign RD21 = decoder_3_out23 ? X23_q : 64'bz;  // Controlled_Buffer controlled_buffer_57
  assign RD21 = decoder_3_out24 ? X24_q : 64'bz;  // Controlled_Buffer controlled_buffer_58
  assign RD21 = decoder_3_out25 ? X25_q : 64'bz;  // Controlled_Buffer controlled_buffer_59
  assign RD21 = decoder_3_out26 ? X26_q : 64'bz;  // Controlled_Buffer controlled_buffer_60
  assign RD21 = decoder_3_out27 ? X27_q : 64'bz;  // Controlled_Buffer controlled_buffer_61
  assign RD21 = decoder_3_out28 ? X28_q : 64'bz;  // Controlled_Buffer controlled_buffer_62
  assign RD21 = decoder_3_out29 ? X29_q : 64'bz;  // Controlled_Buffer controlled_buffer_63
  assign RD21 = decoder_3_out30 ? X30_q : 64'bz;  // Controlled_Buffer controlled_buffer_64
  assign RD21 = decoder_3_out31 ? {64{1'b0}} : 64'bz;  // Controlled_Buffer controlled_buffer_65

  assign RA1 = READ_ADDR1;
  assign RA2 = READ_ADDR2;
  assign RD12 = RD11;
  assign RD13 = RD11;
  assign RD22 = RD21;
  assign RD23 = RD21;
  assign READ_DATA1 = RD11;
  assign READ_DATA2 = RD21;
  assign WA = WRITE_ADDR;
  assign WD1 = WRITE_DATA;
  assign WD2 = WRITE_DATA;
  assign WD3 = WRITE_DATA;
  assign WE = WRITE_ENABLE;
endmodule

module ArithmeticLogicUnit (
  input  [5:0] SHIFT_AMOUNT,
  input  [63:0] OPERAND1,
  input  [63:0] OPERAND2,
  input  [3:0] ALU_OP,
  output [5:0] SHAMT,
  output [63:0] O11,
  output [63:0] O12,
  output [63:0] O13,
  output [63:0] O21,
  output [63:0] O22,
  output [63:0] O23,
  output pAND,
  output pOR,
  output pEOR,
  output pADD,
  output pSUB,
  output pLSL,
  output pLSR,
  output pLSLV,
  output pLSRV,
  output pMUL,
  output pUMULH,
  output pSMULH,
  output UDIV,
  output SDIV,
  output pPASS_B,
  output [63:0] R1,
  output [63:0] R2,
  output [63:0] R3,
  output [63:0] RESULT,
  output ZERO,
  output Z,
  output N,
  output [3:0] FLAGS,
  output C,
  output V
);

  wire adder_1_cout, adder_2_cout, adder_3_cout, adder_4_cout, and_2_out, and_3_out, and_4_out, and_5_out,
       xor_2_out, xor_3_out;
  wire [63:0] adder_1_out, adder_2_out, and_1_out, bit_extender_1_out, divider_1_out, divider_2_out,
       multiplier_1_cout, multiplier_1_out, multiplier_2_cout, not_1_out, not_2_out, or_1_out, shifter_1_out,
       shifter_2_out, shifter_3_out, shifter_4_out, xor_1_out;

  assign not_1_out = ~OPERAND2;  // NOT_Gate not_1, 64 bits wide
  assign not_2_out = ~OPERAND2;  // NOT_Gate not_2, 64 bits wide
  Adder #(.width(64)) adder_1 (.a(OPERAND1), .b(OPERAND2), .out(adder_1_out), .cin(1'b0), .cout(adder_1_cout));
  Adder #(.width(64)) adder_2 (.a(OPERAND1), .b(not_1_out), .out(adder_2_out), .cin(1'b1), .cout(adder_2_cout));
  Shifter #(.width(64)) shifter_1 (.in(OPERAND1), .\dist (SHIFT_AMOUNT), .out(shifter_1_out));
  Shifter #(.shift("lr"), .width(64)) shifter_2 (.in(OPERAND1), .\dist (SHIFT_AMOUNT), .out(shifter_2_out));
  Shifter #(.width(64)) shifter_3 (.in(OPERAND1), .\dist (OPERAND2[5:0]), .out(shifter_3_out));
  Shifter #(.shift("lr"), .width(64)) shifter_4 (.in(OPERAND1), .\dist (OPERAND2[5:0]), .out(shifter_4_out));
  Multiplier #(.width(64)) multiplier_1 (
    .a(OPERAND1), .b(OPERAND2), .out(multiplier_1_out), .cin({64{1'b0}}), .cout(multiplier_1_cout));
  Multiplier #(.mode("twosComplement"), .width(64)) multiplier_2 (
    .a(OPERAND1), .b(OPERAND2), .cin({64{1'b0}}), .cout(multiplier_2_cout));  // open: out
  Divider #(.width(64)) divider_1 (.a(OPERAND1), .b(OPERAND2), .out(divider_1_out), .upper({64{1'b0}}));  // open: rem
  assign bit_extender_1_out = {{63{OPERAND1[63]}}, OPERAND1[63]};  // Bit_Extender bit_extender_1
  Divider #(.mode("twosComplement"), .width(64)) divider_2 (
    .a(OPERAND1), .b(OPERAND2), .out(divider_2_out), .upper(bit_extender_1_out));  // open: rem
  Adder #(.width(63)) adder_3 (.a(OPERAND1[62:0]), .b(OPERAND2[62:0]), .cin(1'b0), .cout(adder_3_cout));  // open: out
  Adder #(.width(63)) adder_4 (.a(OPERAND1[62:0]), .b(not_2_out[62:0]), .cin(1'b1), .cout(adder_4_cout));  // open: out
  assign and_1_out = OPERAND1 & OPERAND2;  // AND_Gate and_1, 64 bits wide
  assign or_1_out = OPERAND1 | OPERAND2;  // OR_Gate or_1, 64 bits wide
  assign xor_1_out = OPERAND1 ^ OPERAND2;  // XOR_Gate xor_1, 64 bits wide
  Multiplexer #(.enable("false"), .select(4), .width(64)) multiplexer_1 (
    .in0(and_1_out), .in1(or_1_out), .in2(xor_1_out), .in3(adder_1_out), .in4(adder_2_out),
    .in5(shifter_1_out), .in6(shifter_2_out), .in7(shifter_3_out), .in8(shifter_4_out),
    .in9(multiplier_1_out), .in10(multiplier_1_cout), .in11(multiplier_2_cout), .in12(divider_1_out),
    .in13(divider_2_out), .in14(OPERAND2), .out(R1), .sel(ALU_OP));  // open: in15
  Decoder #(.enable("false"), .select(4)) decoder_1 (
    .out0(pAND), .out1(pOR), .out2(pEOR), .out3(pADD), .out4(pSUB), .out5(pLSL), .out6(pLSR), .out7(pLSLV),
    .out8(pLSRV), .out9(pMUL), .out10(pUMULH), .out11(pSMULH), .out12(UDIV), .out13(SDIV), .out14(pPASS_B),
    .sel(ALU_OP));  // open: out15
  xor xor_2 (xor_2_out, adder_1_cout, adder_3_cout);
  xor xor_3 (xor_3_out, adder_2_cout, adder_4_cout);
  and and_2 (and_2_out, pADD, adder_1_cout);
  and and_3 (and_3_out, pSUB, adder_2_cout);
  and and_4 (and_4_out, pADD, xor_2_out);
  and and_5 (and_5_out, pSUB, xor_3_out);
  or or_2 (C, and_2_out, and_3_out);
  or or_3 (FLAGS[3], and_4_out, and_5_out);
  Comparator #(.width(64)) comparator_1 (.a(R1), .b({64{1'b0}}), .eq(FLAGS[0]), .lt(FLAGS[1]));  // open: gt

  assign FLAGS[2] = C;
  assign N = FLAGS[1];
  assign O11 = OPERAND1;
  assign O12 = OPERAND1;
  assign O13 = OPERAND1;
  assign O21 = OPERAND2;
  assign O22 = OPERAND2;
  assign O23 = OPERAND2;
  assign R2 = R1;
  assign R3 = R1;
  assign RESULT = R1;
  assign SHAMT = SHIFT_AMOUNT;
  assign V = FLAGS[3];
  assign Z = FLAGS[0];
  assign ZERO = FLAGS[0];
endmodule

module MemoryController (
  input  [63:0] DATA_IN,
  input  [63:0] ADDRESS,
  input  MEM_READ,
  input  MEM_WRITE,
  input  [1:0] ACCESS_SIZE,
  output [63:0] DATA_OUT,
  output DATA_MEMORY_ACCESS,
  output PERIPHERAL_ACCESS,
  output ADDRESS_OUT_OF_RANGE,
  output [23:0] DATA_MEMORY_ADDRESS,
  output DATA_MEMORY_READ,
  output R,
  output DATA_MEMORY_WRITE,
  output W,
  output [63:0] ACCESS_MASK,
  output A0,
  output A1,
  output [7:0] DATA_MEMORY_BYTE_ENABLE,
  output A3,
  output A2,
  output GPIO_ACCESS,
  output [7:0] GPIO_ADDRESS,
  output BSC1_ACCESS,
  output [7:0] BSC1_ADDRESS,
  output PERIPHERAL_ADDRESS_NOT_ALIGNED,
  output PERIPHERAL_ACCESS_SIZE_INVALID,
  output GPIO_READ,
  output GPIO_WRITE,
  output BSC1_READ,
  output BSC1_WRITE,
  output PERIPHERAL_NOT_IMPLEMENTED
);

  wire and_4_out, comparator_1_eq, comparator_2_eq, comparator_3_eq, comparator_3_gt, comparator_4_gt,
       comparator_6_eq, comparator_6_gt, comparator_7_lt, comparator_8_eq, comparator_8_gt, comparator_9_lt,
       comparator_10_eq, comparator_11_eq, or_1_out, or_2_out, or_3_out, or_4_out, or_5_out;
  wire [63:0] multiplexer_1_out;

  or or_1 (or_1_out, MEM_READ, MEM_WRITE);
  Comparator #(.mode("unsigned"), .width(40)) comparator_1 (
    .a({40{1'b0}}), .b(ADDRESS[63:24]), .eq(comparator_1_eq));  // open: gt, lt
  Comparator #(.mode("unsigned"), .width(40)) comparator_2 (
    .a(40'h3f), .b(ADDRESS[63:24]), .eq(comparator_2_eq));  // open: gt, lt
  Comparator #(.mode("unsigned"), .width(2)) comparator_3 (
    .a(ACCESS_SIZE), .b(2'b00), .gt(comparator_3_gt), .eq(comparator_3_eq));  // open: lt
  Comparator #(.mode("unsigned"), .width(2)) comparator_4 (
    .a(ACCESS_SIZE), .b(2'b01), .gt(comparator_4_gt), .eq(A1));  // open: lt
  Comparator #(.mode("unsigned"), .width(2)) comparator_5 (.a(ACCESS_SIZE), .b(2'b10), .gt(A3), .eq(A2));  // open: lt
  or or_2 (or_2_out, comparator_6_gt, comparator_6_eq);
  Comparator #(.mode("unsigned"), .width(24)) comparator_6 (
    .a(ADDRESS[23:0]), .b(24'h200000), .gt(comparator_6_gt), .eq(comparator_6_eq));  // open: lt
  Comparator #(.mode("unsigned"), .width(24)) comparator_7 (
    .a(ADDRESS[23:0]), .b(24'h2000b4), .lt(comparator_7_lt));  // open: gt, eq
  or or_3 (or_3_out, comparator_8_gt, comparator_8_eq);
  Comparator #(.mode("unsigned"), .width(24)) comparator_8 (
    .a(ADDRESS[23:0]), .b(24'h804000), .gt(comparator_8_gt), .eq(comparator_8_eq));  // open: lt
  Comparator #(.mode("unsigned"), .width(24)) comparator_9 (
    .a(ADDRESS[23:0]), .b(24'h80401f), .lt(comparator_9_lt));  // open: gt, eq
  Comparator #(.mode("unsigned"), .width(2)) comparator_10 (
    .a(ADDRESS[1:0]), .b(2'b00), .eq(comparator_10_eq));  // open: gt, lt
  Comparator #(.mode("unsigned"), .width(2)) comparator_11 (
    .a(ACCESS_SIZE), .b(2'b10), .eq(comparator_11_eq));  // open: gt, lt
  and and_1 (DATA_MEMORY_ACCESS, or_1_out, comparator_1_eq);
  and and_2 (PERIPHERAL_ACCESS, or_1_out, comparator_2_eq);
  and and_3 (ADDRESS_OUT_OF_RANGE, or_1_out, ~comparator_1_eq, ~comparator_2_eq);  // AND_Gate
  and and_4 (and_4_out, comparator_10_eq, comparator_11_eq);
  assign DATA_MEMORY_ADDRESS = DATA_MEMORY_ACCESS ? ADDRESS[23:0] : 24'bz;  // Controlled_Buffer controlled_buffer_1
  and and_5 (DATA_MEMORY_READ, DATA_MEMORY_ACCESS, MEM_READ);
  and and_6 (DATA_MEMORY_WRITE, DATA_MEMORY_ACCESS, MEM_WRITE);
  and and_7 (DATA_MEMORY_BYTE_ENABLE[1], comparator_3_gt, DATA_MEMORY_ACCESS);
  and and_8 (DATA_MEMORY_BYTE_ENABLE[3], comparator_4_gt, DATA_MEMORY_ACCESS);
  and and_9 (DATA_MEMORY_BYTE_ENABLE[7], A3, DATA_MEMORY_ACCESS);
  and and_10 (GPIO_ACCESS, PERIPHERAL_ACCESS, or_2_out, comparator_7_lt);
  and and_11 (BSC1_ACCESS, PERIPHERAL_ACCESS, or_3_out, comparator_9_lt);
  Multiplexer #(.enable("false"), .select(2), .width(64)) multiplexer_1 (
    .in0(64'hff), .in1(64'hffff), .in2(64'hffffffff), .in3({64{1'b1}}), .out(multiplexer_1_out),
    .sel(ACCESS_SIZE));
  and and_12 (A0, comparator_3_eq, DATA_MEMORY_ACCESS);
  assign GPIO_ADDRESS = GPIO_ACCESS ? ADDRESS[7:0] : 8'bz;  // Controlled_Buffer controlled_buffer_2
  assign BSC1_ADDRESS = BSC1_ACCESS ? ADDRESS[7:0] : 8'bz;  // Controlled_Buffer controlled_buffer_3
  or or_4 (or_4_out, GPIO_ACCESS, BSC1_ACCESS);
  or or_5 (or_5_out, GPIO_ACCESS, BSC1_ACCESS);
  and and_13 (GPIO_READ, GPIO_ACCESS, and_4_out, MEM_READ);
  and and_14 (GPIO_WRITE, GPIO_ACCESS, and_4_out, MEM_WRITE);
  and and_15 (BSC1_READ, BSC1_ACCESS, and_4_out, MEM_READ);
  and and_16 (BSC1_WRITE, BSC1_ACCESS, and_4_out, MEM_WRITE);
  and and_17 (PERIPHERAL_NOT_IMPLEMENTED, PERIPHERAL_ACCESS, ~GPIO_ACCESS, ~BSC1_ACCESS);  // AND_Gate
  Multiplexer #(.enable("false"), .width(64)) multiplexer_2 (
    .in0({64{1'b0}}), .in1(multiplexer_1_out), .out(ACCESS_MASK), .sel(or_1_out));
  and and_18 (PERIPHERAL_ADDRESS_NOT_ALIGNED, or_4_out, ~comparator_10_eq);  // AND_Gate
  and and_19 (PERIPHERAL_ACCESS_SIZE_INVALID, or_5_out, ~comparator_11_eq);  // AND_Gate

  assign {DATA_MEMORY_BYTE_ENABLE[6:4], DATA_MEMORY_BYTE_ENABLE[2], DATA_MEMORY_BYTE_ENABLE[0]} = {{3{DATA_MEMORY_BYTE_ENABLE[7]}}, DATA_MEMORY_BYTE_ENABLE[3], DATA_MEMORY_ACCESS};
  assign DATA_OUT = DATA_IN;
  assign R = MEM_READ;
  assign W = MEM_WRITE;
endmodule

module BitmaskImmediate (
  input  [12:0] in_1,
  output [63:0] out_2
);

  wire g2_out, g4_out, g8_out, g16_out, g32_out;
  wire [1:0] shifter_1_out, subtractor_1_out;
  wire [3:0] shifter_2_out, subtractor_2_out;
  wire [7:0] shifter_3_out, subtractor_3_out;
  wire [15:0] shifter_4_out, subtractor_4_out;
  wire [31:0] shifter_5_out, subtractor_5_out;
  wire [63:0] shifter_6_out, shifter_12_out, subtractor_6_out;
  wire [63:32] shifter_11_out;
  wire [63:48] shifter_10_out;
  wire [63:56] shifter_9_out;
  wire [63:60] shifter_8_out;
  wire [63:62] shifter_7_out;

  and g2 (g2_out, ~in_1[12], in_1[5], in_1[4], in_1[3], in_1[2], in_1[1]);  // AND_Gate
  and g4 (g4_out, ~in_1[12], in_1[5], in_1[4], in_1[3], in_1[2]);  // AND_Gate
  and g8 (g8_out, ~in_1[12], in_1[5], in_1[4], in_1[3]);  // AND_Gate
  and g16 (g16_out, ~in_1[12], in_1[5], in_1[4]);  // AND_Gate
  and g32 (g32_out, ~in_1[12], in_1[5]);  // AND_Gate
  Shifter #(.width(2)) shifter_1 (.in(2'b10), .\dist (in_1[0]), .out(shifter_1_out));
  Shifter #(.width(4)) shifter_2 (.in(4'b0010), .\dist (in_1[1:0]), .out(shifter_2_out));
  Shifter shifter_3 (.in(8'h2), .\dist (in_1[2:0]), .out(shifter_3_out));
  Shifter #(.width(16)) shifter_4 (.in(16'h2), .\dist (in_1[3:0]), .out(shifter_4_out));
  Shifter #(.width(32)) shifter_5 (.in(32'h2), .\dist (in_1[4:0]), .out(shifter_5_out));
  Shifter #(.width(64)) shifter_6 (.in(64'h2), .\dist (in_1[5:0]), .out(shifter_6_out));
  Subtractor #(.width(2)) subtractor_1 (.a(shifter_1_out), .b(2'b01), .out(subtractor_1_out));  // open: bin, bout
  Subtractor #(.width(4)) subtractor_2 (.a(shifter_2_out), .b(4'b0001), .out(subtractor_2_out));  // open: bin, bout
  Subtractor subtractor_3 (.a(shifter_3_out), .b(8'h1), .out(subtractor_3_out));  // open: bin, bout
  Subtractor #(.width(16)) subtractor_4 (.a(shifter_4_out), .b(16'h1), .out(subtractor_4_out));  // open: bin, bout
  Subtractor #(.width(32)) subtractor_5 (.a(shifter_5_out), .b(32'h1), .out(subtractor_5_out));  // open: bin, bout
  Subtractor #(.width(64)) subtractor_6 (.a(shifter_6_out), .b(64'h1), .out(subtractor_6_out));  // open: bin, bout
  Shifter #(.shift("rr"), .width(2)) shifter_7 (.in(subtractor_1_out), .\dist (in_1[6]), .out(shifter_7_out));
  Shifter #(.shift("rr"), .width(4)) shifter_8 (.in(subtractor_2_out), .\dist (in_1[7:6]), .out(shifter_8_out));
  Shifter #(.shift("rr")) shifter_9 (.in(subtractor_3_out), .\dist (in_1[8:6]), .out(shifter_9_out));
  Shifter #(.shift("rr"), .width(16)) shifter_10 (.in(subtractor_4_out), .\dist (in_1[9:6]), .out(shifter_10_out));
  Shifter #(.shift("rr"), .width(32)) shifter_11 (.in(subtractor_5_out), .\dist (in_1[10:6]), .out(shifter_11_out));
  Shifter #(.shift("rr"), .width(64)) shifter_12 (.in(subtractor_6_out), .\dist (in_1[11:6]), .out(shifter_12_out));
  assign out_2 = g32_out ? {shifter_11_out, shifter_11_out} : 64'bz;  // Controlled_Buffer controlled_buffer_1
  assign out_2 = in_1[12] ? shifter_12_out : 64'bz;  // Controlled_Buffer controlled_buffer_2
  assign out_2 = g2_out ? {shifter_7_out, shifter_7_out, shifter_7_out, shifter_7_out, shifter_7_out, shifter_7_out, shifter_7_out, shifter_7_out, shifter_7_out, shifter_7_out, shifter_7_out, shifter_7_out, shifter_7_out, shifter_7_out, shifter_7_out, shifter_7_out, shifter_7_out, shifter_7_out, shifter_7_out, shifter_7_out, shifter_7_out, shifter_7_out, shifter_7_out, shifter_7_out, shifter_7_out, shifter_7_out, shifter_7_out, shifter_7_out, shifter_7_out, shifter_7_out, shifter_7_out, shifter_7_out} : 64'bz;  // Controlled_Buffer controlled_buffer_3
  assign out_2 = g4_out ? {shifter_8_out, shifter_8_out, shifter_8_out, shifter_8_out, shifter_8_out, shifter_8_out, shifter_8_out, shifter_8_out, shifter_8_out, shifter_8_out, shifter_8_out, shifter_8_out, shifter_8_out, shifter_8_out, shifter_8_out, shifter_8_out} : 64'bz;  // Controlled_Buffer controlled_buffer_4
  assign out_2 = g8_out ? {shifter_9_out, shifter_9_out, shifter_9_out, shifter_9_out, shifter_9_out, shifter_9_out, shifter_9_out, shifter_9_out} : 64'bz;  // Controlled_Buffer controlled_buffer_5
  assign out_2 = g16_out ? {shifter_10_out, shifter_10_out, shifter_10_out, shifter_10_out} : 64'bz;  // Controlled_Buffer controlled_buffer_6
endmodule

module WideImmediate (
  input  MOVK,
  input  MOVZ,
  input  MOVN,
  input  [63:0] REG_DATA,
  input  [5:0] SHAMT,
  input  [63:0] IMM_IN,
  output [63:0] IMM_OUT
);

  wire and_2_out;
  wire [63:0] and_1_out, or_1_out, shifter_1_out, shifter_2_out;

  Shifter #(.shift("rl"), .width(64)) shifter_1 (.in(64'hffffffffffff0000), .\dist (SHAMT), .out(shifter_1_out));
  Shifter #(.width(64)) shifter_2 (.in(IMM_IN), .\dist (SHAMT), .out(shifter_2_out));
  assign and_1_out = REG_DATA & shifter_1_out;  // AND_Gate and_1, 64 bits wide
  and and_2 (and_2_out, ~MOVK, ~MOVZ, ~MOVN);  // AND_Gate
  assign or_1_out = and_1_out | shifter_2_out;  // OR_Gate or_1, 64 bits wide
  assign IMM_OUT = MOVK ? or_1_out : 64'bz;  // Controlled_Buffer controlled_buffer_1
  assign IMM_OUT = MOVZ ? shifter_2_out : 64'bz;  // Controlled_Buffer controlled_buffer_2
  assign IMM_OUT = MOVN ? ~shifter_2_out : 64'bz;  // Controlled_Inverter controlled_inverter_1
  assign IMM_OUT = and_2_out ? IMM_IN : 64'bz;  // Controlled_Buffer controlled_buffer_3
endmodule

module I2C_master (
  input  [63:0] DATA_IN,
  input  WRITE,
  input  [7:0] ADDR,
  input  CLK,
  input  SCL_IN,
  input  SDA_IN,
  output [63:0] DATA_OUT,
  output SDA_OUT,
  output SDA_PULLDOWN,
  output SCL_OUT,
  output SCL_PULLDOWN
);

  wire A0_q, A1_q, A2_q, A3_q, A4_q, A5_q, A6_q, and_1_out, and_2_out, and_3_out, and_4_out, and_5_out,
       and_6_out, and_7_out, and_8_out, and_9_out, and_10_out, and_11_out, and_12_out, and_13_out,
       and_14_out, and_15_out, and_16_out, and_17_out, and_18_out, and_19_out, and_20_out, and_21_out,
       and_22_out, and_23_out, and_24_out, B0_q, comparator_1_eq, comparator_2_eq, comparator_3_eq,
       comparator_4_eq, comparator_5_eq, comparator_6_eq, comparator_7_eq, comparator_7_gt, comparator_8_gt,
       comparator_9_lt, comparator_10_gt, comparator_11_lt, D0_q, D1_q, D2_q, D3_q, D4_q, D5_q, D6_q, D7_q,
       d_ff_1_q, d_ff_2_q, d_ff_3_q, d_ff_4_q, gBUSY_out, gFAIL_out, gIDLE_out, gNACK_out, gSCL_HIGH_out,
       gSDA_NEGEDGE_out, gSDA_POSEDGE_out, gSEND_out, gSEND_POSEDGE_out, gSTART_CND_out, gSTOP_CND_out,
       gSUCCESS_out, gTRY_START_out, gTRY_STOP_out, gWAIT_START_out, multiplexer_1_out, multiplexer_2_out,
       multiplexer_3_out, multiplexer_4_out, multiplexer_5_out, multiplexer_6_out, multiplexer_7_out,
       multiplexer_8_out, multiplexer_9_out, multiplexer_10_out, multiplexer_11_out, multiplexer_12_out,
       multiplexer_13_out, multiplexer_14_out, multiplexer_15_out, multiplexer_16_out, multiplexer_17_out,
       not_1_out, or_1_out, or_2_out, or_3_out, or_4_out, or_5_out, or_6_out, or_7_out, or_8_out, or_9_out,
       or_10_out, or_11_out, priority_encoder_1_gs, RW0_q;
  wire [1:1] S_DONE_q;
  wire [2:0] MASTER_STATE_q, priority_encoder_1_out;
  wire [6:0] A_ADDR_q, adder_1_out, MASTER_COUNTER_q;
  wire [7:0] C_READ_q, FIFO_DATA_q;
  wire [31:0] controlled_buffer_1_out, DLEN_q;

  Comparator comparator_1 (.a(ADDR), .b({8{1'b0}}), .eq(comparator_1_eq));  // open: gt, lt
  Comparator comparator_2 (.a(ADDR), .b(8'h4), .eq(comparator_2_eq));  // open: gt, lt
  Comparator comparator_3 (.a(ADDR), .b(8'h8), .eq(comparator_3_eq));  // open: gt, lt
  Comparator comparator_4 (.a(ADDR), .b(8'hc), .eq(comparator_4_eq));  // open: gt, lt
  Comparator comparator_5 (.a(ADDR), .b(8'h10), .eq(comparator_5_eq));  // open: gt, lt
  Register #(.trigger("high"), .width(1)) C_ST (
    .D(DATA_IN[7]), .en(and_1_out), .clk(CLK), .Q(C_READ_q[7]), .clr(d_ff_1_q));
  and and_1 (and_1_out, comparator_1_eq, WRITE);
  D_Flip_Flop d_ff_1 (.D(and_1_out), .clk(CLK), .Q(d_ff_1_q));  // open: Qn, preset, reset
  Register #(.width(1)) C_READ (.D(DATA_IN[0]), .en(and_2_out), .clk(CLK), .Q(C_READ_q[0]));  // open: clr
  and and_2 (and_2_out, comparator_1_eq, WRITE);
  Register #(.trigger("high"), .width(1)) S_DONE (.D(gSUCCESS_out), .clk(CLK), .Q(S_DONE_q[1]));  // open: en, clr
  Register #(.width(32)) DLEN (.D(DATA_IN[31:0]), .en(and_3_out), .clk(CLK), .Q(DLEN_q));  // open: clr
  and and_3 (and_3_out, comparator_3_eq, WRITE);
  Register #(.width(7)) A_ADDR (.D(DATA_IN[6:0]), .en(and_4_out), .clk(CLK), .Q(A_ADDR_q));  // open: clr
  and and_4 (and_4_out, comparator_4_eq, WRITE);
  Register FIFO_DATA (.D(DATA_IN[7:0]), .en(and_5_out), .clk(CLK), .Q(FIFO_DATA_q));  // open: clr
  and and_5 (and_5_out, comparator_5_eq, WRITE);
  and and_6 (and_6_out, comparator_2_eq, WRITE, DATA_IN[1]);
  assign controlled_buffer_1_out = comparator_3_eq ? DLEN_q : 32'bz;  // Controlled_Buffer controlled_buffer_1
  assign controlled_buffer_1_out = comparator_1_eq ? {{24{1'b0}}, C_READ_q[7], {6{1'b0}}, C_READ_q[0]} : 32'bz;  // Controlled_Buffer controlled_buffer_2
  assign controlled_buffer_1_out = comparator_2_eq ? {{30{1'b0}}, S_DONE_q[1], 1'b0} : 32'bz;  // Controlled_Buffer controlled_buffer_3
  assign controlled_buffer_1_out = comparator_4_eq ? {{25{1'b0}}, A_ADDR_q} : 32'bz;  // Controlled_Buffer controlled_buffer_4
  assign controlled_buffer_1_out = comparator_5_eq ? {{24{1'b0}}, FIFO_DATA_q} : 32'bz;  // Controlled_Buffer controlled_buffer_5
  assign DATA_OUT = {{32{1'b0}}, controlled_buffer_1_out};  // Bit_Extender bit_extender_1
  D_Flip_Flop d_ff_2 (.clk(CLK), .D(SCL_IN), .Q(d_ff_2_q));  // open: Qn, preset, reset
  D_Flip_Flop d_ff_3 (.clk(CLK), .D(SDA_IN), .Q(d_ff_3_q));  // open: Qn, preset, reset
  D_Flip_Flop d_ff_4 (.clk(CLK), .D(C_READ_q[7]), .Q(d_ff_4_q));  // open: Qn, preset, reset
  and gSCL_HIGH (gSCL_HIGH_out, SCL_IN, d_ff_2_q);
  and gSDA_POSEDGE (gSDA_POSEDGE_out, SDA_IN, ~d_ff_3_q);  // AND_Gate
  and gSDA_NEGEDGE (gSDA_NEGEDGE_out, ~SDA_IN, d_ff_3_q);  // AND_Gate
  and gSEND_POSEDGE (gSEND_POSEDGE_out, C_READ_q[7], ~d_ff_4_q);  // AND_Gate
  Register #(.width(3)) MASTER_STATE (
    .D(priority_encoder_1_out), .en(priority_encoder_1_gs), .clk(CLK), .Q(MASTER_STATE_q), .clr(and_6_out));
  Register #(.width(7)) MASTER_COUNTER (
    .D(adder_1_out), .en(or_3_out), .clk(CLK), .Q({MASTER_COUNTER_q[6:2], SCL_OUT, MASTER_COUNTER_q[0]}),
    .clr(or_1_out));
  or or_1 (or_1_out, gSTART_CND_out, and_6_out);
  and gNACK (gNACK_out, gSCL_HIGH_out, SDA_IN);
  and gSTOP_CND (gSTOP_CND_out, gSCL_HIGH_out, gSDA_POSEDGE_out);
  and gSTART_CND (gSTART_CND_out, gSCL_HIGH_out, gSDA_NEGEDGE_out);
  not not_1 (not_1_out, gSEND_POSEDGE_out);
  Multiplexer #(.enable("false")) multiplexer_1 (
    .in0(FIFO_DATA_q[0]), .in1(1'b0), .out(multiplexer_1_out), .sel(not_1_out));
  Register #(.width(1)) D0 (.D(multiplexer_1_out), .en(or_11_out), .Q(D0_q), .clk(CLK), .clr(and_6_out));
  Multiplexer #(.enable("false")) multiplexer_2 (
    .in0(C_READ_q[0]), .in1(D7_q), .out(multiplexer_2_out), .sel(not_1_out));
  Register #(.width(1)) RW0 (.D(multiplexer_2_out), .en(or_11_out), .Q(RW0_q), .clk(CLK), .clr(and_6_out));
  Adder #(.width(7)) adder_1 (
    .a({MASTER_COUNTER_q[6:2], SCL_OUT, MASTER_COUNTER_q[0]}), .b(7'b0000001), .out(adder_1_out));  // open: cin, cout
  Comparator #(.mode("unsigned"), .width(6)) comparator_6 (
    .a({MASTER_COUNTER_q[6:2], SCL_OUT}), .b(6'b010001), .eq(comparator_6_eq));  // open: gt, lt
  Comparator #(.mode("unsigned"), .width(6)) comparator_7 (
    .a({MASTER_COUNTER_q[6:2], SCL_OUT}), .b(6'b100011), .gt(comparator_7_gt), .eq(comparator_7_eq));  // open: lt
  Comparator #(.mode("unsigned"), .width(7)) comparator_8 (
    .a({MASTER_COUNTER_q[6:2], SCL_OUT, MASTER_COUNTER_q[0]}), .b(7'b0100000), .gt(comparator_8_gt));  // open: eq, lt
  Comparator #(.mode("unsigned"), .width(7)) comparator_9 (
    .a({MASTER_COUNTER_q[6:2], SCL_OUT, MASTER_COUNTER_q[0]}), .b(7'b0100101), .lt(comparator_9_lt));  // open: gt, eq
  Comparator #(.mode("unsigned"), .width(7)) comparator_10 (
    .a({MASTER_COUNTER_q[6:2], SCL_OUT, MASTER_COUNTER_q[0]}), .b(7'b1000100), .gt(comparator_10_gt));  // open: eq, lt
  Comparator #(.mode("unsigned"), .width(7)) comparator_11 (
    .a({MASTER_COUNTER_q[6:2], SCL_OUT, MASTER_COUNTER_q[0]}), .b(7'b1001001), .lt(comparator_11_lt));  // open: gt, eq
  Multiplexer #(.enable("false")) multiplexer_3 (
    .in0(FIFO_DATA_q[1]), .in1(D0_q), .out(multiplexer_3_out), .sel(not_1_out));
  Register #(.width(1)) D1 (.D(multiplexer_3_out), .en(or_11_out), .Q(D1_q), .clk(CLK), .clr(and_6_out));
  Multiplexer #(.enable("false")) multiplexer_4 (
    .in0(A_ADDR_q[0]), .in1(RW0_q), .out(multiplexer_4_out), .sel(not_1_out));
  Register #(.width(1)) A0 (.D(multiplexer_4_out), .en(or_11_out), .Q(A0_q), .clk(CLK), .clr(and_6_out));
  and gIDLE (gIDLE_out, ~MASTER_STATE_q[0], ~MASTER_STATE_q[1], ~MASTER_STATE_q[2]);  // AND_Gate
  and gBUSY (gBUSY_out, MASTER_STATE_q[0], ~MASTER_STATE_q[1], ~MASTER_STATE_q[2]);  // AND_Gate
  and gWAIT_START (gWAIT_START_out, ~MASTER_STATE_q[0], MASTER_STATE_q[1], ~MASTER_STATE_q[2]);  // AND_Gate
  and gTRY_START (gTRY_START_out, MASTER_STATE_q[0], MASTER_STATE_q[1], ~MASTER_STATE_q[2]);  // AND_Gate
  and gSEND (gSEND_out, ~MASTER_STATE_q[0], ~MASTER_STATE_q[1], MASTER_STATE_q[2]);  // AND_Gate
  and gTRY_STOP (gTRY_STOP_out, MASTER_STATE_q[0], ~MASTER_STATE_q[1], MASTER_STATE_q[2]);  // AND_Gate
  and gSUCCESS (gSUCCESS_out, ~MASTER_STATE_q[0], MASTER_STATE_q[1], MASTER_STATE_q[2]);  // AND_Gate
  and gFAIL (gFAIL_out, MASTER_STATE_q[0], MASTER_STATE_q[1], MASTER_STATE_q[2]);
  and and_7 (and_7_out, comparator_8_gt, comparator_9_lt);
  and and_8 (and_8_out, comparator_10_gt, comparator_11_lt);
  Multiplexer #(.enable("false")) multiplexer_5 (
    .in0(FIFO_DATA_q[2]), .in1(D1_q), .out(multiplexer_5_out), .sel(not_1_out));
  Multiplexer #(.enable("false")) multiplexer_6 (
    .in0(A_ADDR_q[1]), .in1(A0_q), .out(multiplexer_6_out), .sel(not_1_out));
  or or_2 (or_2_out, and_7_out, and_8_out);
  Multiplexer #(.enable("false")) multiplexer_7 (
    .in0(FIFO_DATA_q[3]), .in1(D2_q), .out(multiplexer_7_out), .sel(not_1_out));
  Register #(.width(1)) D2 (.D(multiplexer_5_out), .en(or_11_out), .Q(D2_q), .clk(CLK), .clr(and_6_out));
  Multiplexer #(.enable("false")) multiplexer_8 (
    .in0(A_ADDR_q[2]), .in1(A1_q), .out(multiplexer_8_out), .sel(not_1_out));
  Register #(.width(1)) A1 (.D(multiplexer_6_out), .en(or_11_out), .Q(A1_q), .clk(CLK), .clr(and_6_out));
  or or_3 (or_3_out, gTRY_START_out, gSEND_out, gTRY_STOP_out);
  and and_9 (and_9_out, gBUSY_out, gSTOP_CND_out, ~gSEND_POSEDGE_out);  // AND_Gate
  and and_10 (and_10_out, gIDLE_out, gSTART_CND_out, ~gSEND_POSEDGE_out);  // AND_Gate
  or or_4 (or_4_out, gIDLE_out, gSUCCESS_out, gFAIL_out);
  and and_11 (and_11_out, gBUSY_out, ~gSTOP_CND_out, gSEND_POSEDGE_out);  // AND_Gate
  or or_5 (or_5_out, gIDLE_out, gSUCCESS_out, gFAIL_out);
  and and_12 (and_12_out, gWAIT_START_out, gSTOP_CND_out, gSEND_POSEDGE_out);
  and and_13 (and_13_out, gTRY_START_out, gSTART_CND_out);
  and and_14 (and_14_out, gSEND_out, comparator_7_gt);
  and and_15 (and_15_out, gTRY_STOP_out, gSTOP_CND_out);
  and and_16 (and_16_out, gSEND_out, comparator_6_eq, gNACK_out);
  and and_17 (and_17_out, gSEND_out, comparator_7_eq, gNACK_out);
  or or_6 (or_6_out, gTRY_START_out, gSEND_out, gTRY_STOP_out);
  or or_7 (or_7_out, gSEND_out, gTRY_STOP_out);
  Multiplexer #(.enable("false")) multiplexer_9 (
    .in0(FIFO_DATA_q[4]), .in1(D3_q), .out(multiplexer_9_out), .sel(not_1_out));
  Register #(.width(1)) D3 (.D(multiplexer_7_out), .en(or_11_out), .Q(D3_q), .clk(CLK), .clr(and_6_out));
  Multiplexer #(.enable("false")) multiplexer_10 (
    .in0(A_ADDR_q[3]), .in1(A2_q), .out(multiplexer_10_out), .sel(not_1_out));
  Register #(.width(1)) A2 (.D(multiplexer_8_out), .en(or_11_out), .Q(A2_q), .clk(CLK), .clr(and_6_out));
  and and_18 (and_18_out, or_4_out, gSTART_CND_out, gSEND_POSEDGE_out);
  or or_8 (or_8_out, and_18_out, and_11_out);
  and and_19 (and_19_out, or_5_out, ~gSTART_CND_out, gSEND_POSEDGE_out);  // AND_Gate
  or or_9 (or_9_out, and_19_out, and_12_out);
  or or_10 (or_10_out, and_16_out, and_17_out);
  and and_20 (and_20_out, or_6_out, ~or_2_out);  // AND_Gate
  and and_21 (and_21_out, or_7_out, ~or_2_out);  // AND_Gate
  Multiplexer #(.enable("false")) multiplexer_11 (
    .in0(FIFO_DATA_q[5]), .in1(D4_q), .out(multiplexer_11_out), .sel(not_1_out));
  Register #(.width(1)) D4 (.D(multiplexer_9_out), .en(or_11_out), .Q(D4_q), .clk(CLK), .clr(and_6_out));
  Multiplexer #(.enable("false")) multiplexer_12 (
    .in0(A_ADDR_q[4]), .in1(A3_q), .out(multiplexer_12_out), .sel(not_1_out));
  Register #(.width(1)) A3 (.D(multiplexer_10_out), .en(or_11_out), .Q(A3_q), .clk(CLK), .clr(and_6_out));
  and and_22 (and_22_out, and_21_out, ~SCL_OUT, ~MASTER_COUNTER_q[0]);  // AND_Gate
  and and_23 (and_23_out, gTRY_STOP_out, SCL_OUT, MASTER_COUNTER_q[0]);
  Multiplexer #(.enable("false")) multiplexer_13 (
    .in0(FIFO_DATA_q[6]), .in1(D5_q), .out(multiplexer_13_out), .sel(not_1_out));
  Register #(.width(1)) D5 (.D(multiplexer_11_out), .en(or_11_out), .Q(D5_q), .clk(CLK), .clr(and_6_out));
  Multiplexer #(.enable("false")) multiplexer_14 (
    .in0(A_ADDR_q[5]), .in1(A4_q), .out(multiplexer_14_out), .sel(not_1_out));
  Register #(.width(1)) A4 (.D(multiplexer_12_out), .en(or_11_out), .Q(A4_q), .clk(CLK), .clr(and_6_out));
  or or_11 (or_11_out, gSEND_POSEDGE_out, and_22_out);
  Register #(.width(1)) D6 (.D(multiplexer_13_out), .en(or_11_out), .Q(D6_q), .clk(CLK), .clr(and_6_out));
  Register #(.width(1)) A5 (.D(multiplexer_14_out), .en(or_11_out), .Q(A5_q), .clk(CLK), .clr(and_6_out));
  Priority_Encoder priority_encoder_1 (
    .in0(and_9_out), .in1(and_10_out), .in2(or_8_out), .in3(or_9_out), .in4(and_13_out), .in5(and_14_out),
    .in6(and_15_out), .in7(or_10_out), .out(priority_encoder_1_out), .gs(priority_encoder_1_gs));  // open: en_in, en_out
  Multiplexer #(.enable("false")) multiplexer_15 (
    .in0(FIFO_DATA_q[7]), .in1(D6_q), .out(multiplexer_15_out), .sel(not_1_out));
  Register #(.width(1)) D7 (.D(multiplexer_15_out), .en(or_11_out), .Q(D7_q), .clk(CLK), .clr(and_6_out));
  Multiplexer #(.enable("false")) multiplexer_16 (
    .in0(A_ADDR_q[6]), .in1(A5_q), .out(multiplexer_16_out), .sel(not_1_out));
  Register #(.width(1)) A6 (.D(multiplexer_16_out), .en(or_11_out), .Q(A6_q), .clk(CLK), .clr(and_6_out));
  Multiplexer #(.enable("false")) multiplexer_17 (.in0(1'b0), .in1(A6_q), .out(multiplexer_17_out), .sel(not_1_out));
  Register #(.width(1)) B0 (.D(multiplexer_17_out), .en(or_11_out), .Q(B0_q), .clk(CLK), .clr(and_6_out));
  and and_24 (and_24_out, gSEND_out, ~or_2_out, B0_q);  // AND_Gate
  or or_12 (SDA_OUT, and_23_out, and_24_out);
  and and_25 (SDA_PULLDOWN, ~SDA_OUT, and_20_out);  // AND_Gate
  and and_26 (SCL_PULLDOWN, ~SCL_OUT, or_7_out);  // AND_Gate

  // Notes on the sheet:
  //   START
  //   DATA
  //   ADDRESS
  //   READ
  //   Within ACK window
  //   Bus now available
  //   Bus now busy
  //   Bus now busy, received start
  //   Bus busy, received start
  //   Bus available, received start
  //   Bus now available, received start
  //   Started transmission
  //   Data sent
  //   Stopped transmission
  //   Drive the SCL during transmission
  //   Received NACK
  //   Drive the SDA during transmission except for ACK window
endmodule

module PCF8574 (
  input  SDA_IN,
  input  SCL,
  output SDA_OUT,
  output SDA_PULLDOWN,
  output [7:0] DATA_OUT
);

  wire and_1_out, and_2_out, and_3_out, and_4_out, and_5_out, and_6_out, and_7_out, and_8_out, and_9_out,
       clock_1_out, comparator_1_eq, comparator_2_eq, comparator_3_eq, FAIL_out, gACK_ADDR_out,
       gACK_DATA_out, gIGNORE_out, gRECEIVE_ADDR_out, gRECEIVE_DATA_out, IDLE_out, not_1_out, or_1_out,
       or_2_out, or_3_out, or_4_out, or_5_out, or_6_out, or_7_out, priority_encoder_1_gs, register_1_q,
       SCL_HIGH_out, SCL_NEGEDGE_out, SDA_NEGEDGE_out, SDA_POSEDGE_out, sSCL_q, sSDA_q, START_CND_out,
       STOP_CND_out, SUCCESS_out;
  wire [2:0] priority_encoder_1_out, SLAVE_STATE_q;
  wire [4:0] adder_1_out, SLAVE_COUNTER_q;
  wire [7:0] S0_q;

  Clock clock_1 (.out(clock_1_out));
  D_Flip_Flop sSCL (.clk(clock_1_out), .D(SCL), .Q(sSCL_q));  // open: Qn, preset, reset
  D_Flip_Flop sSDA (.clk(clock_1_out), .D(SDA_IN), .Q(sSDA_q));  // open: Qn, preset, reset
  and SCL_NEGEDGE (SCL_NEGEDGE_out, ~SCL, sSCL_q);  // AND_Gate
  and SCL_HIGH (SCL_HIGH_out, SCL, sSCL_q);
  and STOP_CND (STOP_CND_out, SCL_HIGH_out, SDA_POSEDGE_out);
  and SDA_POSEDGE (SDA_POSEDGE_out, SDA_IN, ~sSDA_q);  // AND_Gate
  and START_CND (START_CND_out, SCL_HIGH_out, SDA_NEGEDGE_out);
  and SDA_NEGEDGE (SDA_NEGEDGE_out, ~SDA_IN, sSDA_q);  // AND_Gate
  Register #(.width(1)) S0 (.D(SDA_IN), .en(or_6_out), .Q(S0_q[0]), .clk(SCL), .clr(IDLE_out));
  Register #(.width(1)) S1 (.D(S0_q[0]), .en(or_6_out), .Q(S0_q[1]), .clk(SCL), .clr(IDLE_out));
  Register #(.width(1)) S2 (.D(S0_q[1]), .en(or_6_out), .Q(S0_q[2]), .clk(SCL), .clr(IDLE_out));
  Register #(.width(5)) SLAVE_COUNTER (.D(adder_1_out), .en(or_2_out), .clk(SCL), .Q(SLAVE_COUNTER_q), .clr(or_1_out));
  Register #(.width(1)) S3 (.D(S0_q[2]), .en(or_6_out), .Q(S0_q[3]), .clk(SCL), .clr(IDLE_out));
  Register #(.width(3)) SLAVE_STATE (
    .D(priority_encoder_1_out), .en(priority_encoder_1_gs), .clk(clock_1_out), .Q(SLAVE_STATE_q));  // open: clr
  Register #(.width(1)) S4 (.D(S0_q[3]), .en(or_6_out), .Q(S0_q[4]), .clk(SCL), .clr(IDLE_out));
  Register #(.width(1)) S5 (.D(S0_q[4]), .en(or_6_out), .Q(S0_q[5]), .clk(SCL), .clr(IDLE_out));
  Adder #(.width(5)) adder_1 (.a(SLAVE_COUNTER_q), .b(5'b00001), .out(adder_1_out));  // open: cin, cout
  Comparator #(.mode("unsigned"), .width(5)) comparator_1 (
    .a(SLAVE_COUNTER_q), .b(5'b01001), .eq(comparator_1_eq));  // open: gt, lt
  Comparator #(.mode("unsigned"), .width(5)) comparator_2 (
    .a(SLAVE_COUNTER_q), .b(5'b01000), .eq(comparator_2_eq));  // open: gt, lt
  Register #(.width(1)) S6 (.D(S0_q[5]), .en(or_6_out), .Q(S0_q[6]), .clk(SCL), .clr(IDLE_out));
  or or_1 (or_1_out, IDLE_out, comparator_1_eq, START_CND_out);
  Register #(.width(1)) S7 (.D(S0_q[6]), .en(or_6_out), .Q(S0_q[7]), .clk(SCL), .clr(IDLE_out));
  and IDLE (IDLE_out, ~SLAVE_STATE_q[0], ~SLAVE_STATE_q[1], ~SLAVE_STATE_q[2]);  // AND_Gate
  and gRECEIVE_ADDR (gRECEIVE_ADDR_out, SLAVE_STATE_q[0], ~SLAVE_STATE_q[1], ~SLAVE_STATE_q[2]);  // AND_Gate
  and gACK_ADDR (gACK_ADDR_out, ~SLAVE_STATE_q[0], SLAVE_STATE_q[1], ~SLAVE_STATE_q[2]);  // AND_Gate
  and gRECEIVE_DATA (gRECEIVE_DATA_out, SLAVE_STATE_q[0], SLAVE_STATE_q[1], ~SLAVE_STATE_q[2]);  // AND_Gate
  and gACK_DATA (gACK_DATA_out, ~SLAVE_STATE_q[0], ~SLAVE_STATE_q[1], SLAVE_STATE_q[2]);  // AND_Gate
  and SUCCESS (SUCCESS_out, SLAVE_STATE_q[0], ~SLAVE_STATE_q[1], SLAVE_STATE_q[2]);  // AND_Gate
  and FAIL (FAIL_out, ~SLAVE_STATE_q[0], SLAVE_STATE_q[1], SLAVE_STATE_q[2]);  // AND_Gate
  and gIGNORE (gIGNORE_out, SLAVE_STATE_q[0], SLAVE_STATE_q[1], SLAVE_STATE_q[2]);
  Comparator #(.mode("unsigned"), .width(7)) comparator_3 (
    .a(S0_q[7:1]), .b(7'b0100111), .eq(comparator_3_eq));  // open: gt, lt
  not not_1 (not_1_out, S0_q[0]);
  and and_1 (and_1_out, comparator_3_eq, not_1_out);
  or or_2 (or_2_out, gRECEIVE_ADDR_out, gACK_ADDR_out, gRECEIVE_DATA_out, gACK_DATA_out);
  and and_2 (and_2_out, gIGNORE_out, STOP_CND_out);
  or or_3 (or_3_out, IDLE_out, gRECEIVE_ADDR_out, gACK_ADDR_out, gRECEIVE_DATA_out, gACK_DATA_out, SUCCESS_out, FAIL_out);
  and and_3 (and_3_out, gRECEIVE_ADDR_out, comparator_2_eq, and_1_out);
  or or_4 (or_4_out, gACK_ADDR_out, gACK_DATA_out);
  and and_4 (and_4_out, gRECEIVE_DATA_out, comparator_2_eq);
  or or_5 (or_5_out, gRECEIVE_DATA_out, gACK_DATA_out);
  and and_5 (and_5_out, gRECEIVE_ADDR_out, comparator_2_eq, ~and_1_out);  // AND_Gate
  or or_6 (or_6_out, gRECEIVE_ADDR_out, gRECEIVE_DATA_out);
  or or_7 (or_7_out, gACK_ADDR_out, gACK_DATA_out);
  and and_6 (and_6_out, gACK_DATA_out, comparator_2_eq);
  and and_7 (and_7_out, or_3_out, START_CND_out);
  and and_8 (and_8_out, or_4_out, register_1_q);
  and and_9 (and_9_out, or_5_out, STOP_CND_out);
  Register #(.trigger("falling"), .width(1)) register_1 (.D(or_7_out), .clk(SCL), .Q(register_1_q));  // open: en, clr
  Register #(.trigger("falling")) DATA_REG (.D(S0_q), .en(and_6_out), .clk(SCL), .Q(DATA_OUT));  // open: clr
  Priority_Encoder priority_encoder_1 (
    .in0(and_2_out), .in1(and_7_out), .in2(and_3_out), .in3(and_8_out), .in4(and_4_out), .in5(and_9_out),
    .in7(and_5_out), .out(priority_encoder_1_out), .gs(priority_encoder_1_gs));  // open: in6, en_in, en_out
  and and_10 (SDA_PULLDOWN, ~1'b0, register_1_q);  // AND_Gate

  assign SDA_OUT = 1'b0;

  // Notes on the sheet:
  //   I2C SLAVE
  //   Only support read
  //   Ignored transmission ended
  //   Start listening for address
  //   Address matches
  //   ACK sent
  //   Data received
  //   Stopped receiving
  //   Ignore different address
endmodule

module HD44780 (
  input  BL,
  input  D7,
  input  D6,
  input  D5,
  input  D4,
  input  D3,
  input  D2,
  input  D1,
  input  D0,
  input  E,
  input  RW,
  input  RS,
  output [7:0] out_13,
  output [7:0] out_14,
  output [7:0] out_15,
  output [7:0] out_16,
  output [7:0] out_17,
  output [7:0] out_18,
  output [7:0] out_19,
  output [7:0] out_20,
  output [7:0] out_21,
  output [7:0] out_22,
  output [7:0] out_23,
  output [7:0] out_24,
  output [7:0] out_25,
  output [7:0] out_26,
  output [7:0] out_27,
  output [7:0] out_28,
  output [7:0] out_29,
  output [7:0] out_30,
  output [7:0] out_31,
  output [7:0] out_32,
  output [7:0] out_33,
  output [7:0] out_34,
  output [7:0] out_35,
  output [7:0] out_36,
  output [7:0] out_37,
  output [7:0] out_38,
  output [7:0] out_39,
  output [7:0] out_40,
  output [7:0] out_41,
  output [7:0] out_42,
  output [7:0] out_43,
  output [7:0] out_44,
  output [7:0] out_45,
  output [7:0] out_46,
  output [7:0] out_47,
  output [7:0] out_48,
  output [7:0] out_49,
  output [7:0] out_50,
  output [7:0] out_51,
  output [7:0] out_52,
  output [7:0] out_53,
  output [7:0] out_54,
  output [7:0] out_55,
  output [7:0] out_56,
  output [7:0] out_57,
  output [7:0] out_58,
  output [7:0] out_59,
  output [7:0] out_60,
  output [7:0] out_61,
  output [7:0] out_62,
  output [7:0] out_63,
  output [7:0] out_64,
  output [7:0] out_65,
  output [7:0] out_66,
  output [7:0] out_67,
  output [7:0] out_68,
  output [7:0] out_69,
  output [7:0] out_70,
  output [7:0] out_71,
  output [7:0] out_72,
  output [7:0] out_73,
  output [7:0] out_74,
  output [7:0] out_75,
  output [7:0] out_76,
  output [7:0] out_77,
  output [7:0] out_78,
  output [7:0] out_79,
  output [7:0] out_80,
  output [7:0] out_81,
  output [7:0] out_82,
  output [7:0] out_83,
  output [7:0] out_84,
  output [7:0] out_85,
  output [7:0] out_86,
  output [7:0] out_87,
  output [7:0] out_88,
  output [7:0] out_89,
  output [7:0] out_90,
  output [7:0] out_91,
  output [7:0] out_92,
  output [7:0] out_93,
  output [7:0] out_94,
  output [7:0] out_95,
  output [7:0] out_96,
  output [7:0] out_97,
  output [7:0] out_98,
  output [7:0] out_99,
  output [7:0] out_100,
  output [7:0] out_101,
  output [7:0] out_102,
  output [7:0] out_103,
  output [7:0] out_104,
  output [7:0] out_105,
  output [7:0] out_106,
  output [7:0] out_107,
  output [7:0] out_108,
  output [7:0] out_109,
  output [7:0] out_110,
  output [7:0] out_111,
  output [7:0] out_112,
  output [7:0] out_113,
  output [7:0] out_114,
  output [7:0] out_115,
  output [7:0] out_116,
  output [7:0] out_117,
  output [7:0] out_118,
  output [7:0] out_119,
  output [7:0] out_120,
  output [7:0] out_121,
  output [7:0] out_122,
  output [7:0] out_123,
  output [7:0] out_124,
  output [7:0] out_125,
  output [7:0] out_126,
  output [7:0] out_127,
  output [7:0] out_128,
  output [7:0] out_129,
  output [7:0] out_130,
  output [7:0] out_131,
  output [7:0] out_132,
  output [7:0] out_133,
  output [7:0] out_134,
  output [7:0] out_135,
  output [7:0] out_136,
  output [7:0] out_137,
  output [7:0] out_138,
  output [7:0] out_139,
  output [7:0] out_140,
  output [7:0] out_141,
  output [7:0] out_142,
  output [7:0] out_143,
  output [7:0] out_144,
  output [7:0] out_145,
  output [7:0] out_146,
  output [7:0] out_147,
  output [7:0] out_148,
  output [7:0] out_149,
  output [7:0] out_150,
  output [7:0] out_151,
  output [7:0] out_152,
  output [7:0] out_153,
  output [7:0] out_154,
  output [7:0] out_155,
  output [7:0] out_156,
  output [7:0] out_157,
  output [7:0] out_158,
  output [7:0] out_159,
  output [7:0] out_160,
  output [7:0] out_161,
  output [7:0] out_162,
  output [7:0] out_163,
  output [7:0] out_164,
  output [7:0] out_165,
  output [7:0] out_166,
  output [7:0] out_167,
  output [7:0] out_168,
  output [7:0] out_169,
  output [7:0] out_170,
  output [7:0] out_171,
  output [7:0] out_172,
  output [7:0] out_173,
  output [7:0] out_174,
  output [7:0] out_175,
  output [7:0] out_176,
  output [7:0] out_177,
  output [7:0] out_178,
  output [7:0] out_179,
  output [7:0] out_180,
  output [7:0] out_181,
  output [7:0] out_182,
  output [7:0] out_183,
  output [7:0] out_184,
  output [7:0] out_185,
  output [7:0] out_186,
  output [7:0] out_187,
  output [7:0] out_188,
  output [7:0] out_189,
  output [7:0] out_190,
  output [7:0] out_191,
  output [7:0] out_192,
  output [7:0] out_193,
  output [7:0] out_194,
  output [7:0] out_195,
  output [7:0] out_196,
  output [7:0] out_197,
  output [7:0] out_198,
  output [7:0] out_199,
  output [7:0] out_200,
  output [7:0] out_201,
  output [7:0] out_202,
  output [7:0] out_203,
  output [7:0] out_204,
  output [7:0] out_205,
  output [7:0] out_206,
  output [7:0] out_207,
  output [7:0] out_208,
  output [7:0] out_209,
  output [7:0] out_210,
  output [7:0] out_211,
  output [7:0] out_212,
  output [7:0] out_213,
  output [7:0] out_214,
  output [7:0] out_215,
  output [7:0] out_216,
  output [7:0] out_217,
  output [7:0] out_218,
  output [7:0] out_219,
  output [7:0] out_220,
  output [7:0] out_221,
  output [7:0] out_222,
  output [7:0] out_223,
  output [7:0] out_224,
  output [7:0] out_225,
  output [7:0] out_226,
  output [7:0] out_227,
  output [7:0] out_228,
  output [7:0] out_229,
  output [7:0] out_230,
  output [7:0] out_231,
  output [7:0] out_232,
  output [7:0] out_233,
  output [7:0] out_234,
  output [7:0] out_235,
  output [7:0] out_236,
  output [7:0] out_237,
  output [7:0] out_238,
  output [7:0] out_239,
  output [7:0] out_240,
  output [7:0] out_241,
  output [7:0] out_242,
  output [7:0] out_243,
  output [7:0] out_244,
  output [7:0] out_245,
  output [7:0] out_246,
  output [7:0] out_247,
  output [7:0] out_248,
  output [7:0] out_249,
  output [7:0] out_250,
  output [7:0] out_251,
  output [7:0] out_252,
  output [7:0] out_253,
  output [7:0] out_254,
  output [7:0] out_255,
  output [7:0] out_256,
  output [7:0] out_257,
  output [7:0] out_258,
  output [7:0] out_259,
  output [7:0] out_260,
  output [7:0] out_261,
  output [7:0] out_262,
  output [7:0] out_263,
  output [7:0] out_264,
  output [7:0] out_265,
  output [7:0] out_266,
  output [7:0] out_267,
  output [7:0] out_268,
  output [7:0] out_269,
  output [7:0] out_270,
  output [7:0] out_271,
  output [7:0] out_272,
  output [7:0] out_273,
  output [7:0] out_274,
  output [7:0] out_275,
  output [7:0] out_276,
  output [7:0] out_277,
  output [7:0] out_278,
  output [7:0] out_279,
  output [7:0] out_280,
  output [7:0] out_281,
  output [7:0] out_282,
  output [7:0] out_283,
  output [7:0] out_284,
  output [7:0] out_285,
  output [7:0] out_286,
  output [7:0] out_287,
  output [7:0] out_288,
  output [7:0] out_289,
  output [7:0] out_290,
  output [7:0] out_291,
  output [7:0] out_292,
  output [7:0] out_293,
  output [7:0] out_294,
  output [7:0] out_295,
  output [7:0] out_296,
  output [7:0] out_297,
  output [7:0] out_298,
  output [7:0] out_299,
  output [7:0] out_300,
  output [7:0] out_301,
  output [7:0] out_302,
  output [7:0] out_303,
  output [7:0] out_304,
  output [7:0] out_305,
  output [7:0] out_306,
  output [7:0] out_307,
  output [7:0] out_308,
  output [7:0] out_309,
  output [7:0] out_310,
  output [7:0] out_311,
  output [7:0] out_312,
  output [7:0] out_313,
  output [7:0] out_314,
  output [7:0] out_315,
  output [7:0] out_316,
  output [7:0] out_317,
  output [7:0] out_318,
  output [7:0] out_319,
  output [7:0] out_320,
  output [7:0] out_321,
  output [7:0] out_322,
  output [7:0] out_323,
  output [7:0] out_324,
  output [7:0] out_325,
  output [7:0] out_326,
  output [7:0] out_327,
  output [7:0] out_328,
  output [7:0] out_329,
  output [7:0] out_330,
  output [7:0] out_331,
  output [7:0] out_332,
  output [7:0] out_333,
  output [7:0] out_334,
  output [7:0] out_335,
  output [7:0] out_336,
  output [7:0] out_337,
  output [7:0] out_338,
  output [7:0] out_339,
  output [7:0] out_340,
  output [7:0] out_341,
  output [7:0] out_342,
  output [7:0] out_343,
  output [7:0] out_344,
  output [7:0] out_345,
  output [7:0] out_346,
  output [7:0] out_347,
  output [7:0] out_348,
  output [7:0] out_349,
  output [7:0] out_350,
  output [7:0] out_351,
  output [7:0] out_352,
  output [7:0] out_353,
  output [7:0] out_354,
  output [7:0] out_355,
  output [7:0] out_356,
  output [7:0] out_357,
  output [7:0] out_358,
  output [7:0] out_359,
  output [7:0] out_360,
  output [7:0] out_361,
  output [7:0] out_362,
  output [7:0] out_363,
  output [7:0] out_364,
  output [7:0] out_365,
  output [7:0] out_366,
  output [7:0] out_367,
  output [7:0] out_368,
  output [7:0] out_369,
  output [7:0] out_370,
  output [7:0] out_371,
  output [7:0] out_372,
  output [7:0] out_373,
  output [7:0] out_374,
  output [7:0] out_375,
  output [7:0] out_376,
  output [7:0] out_377,
  output [7:0] out_378,
  output [7:0] out_379,
  output [7:0] out_380,
  output [7:0] out_381,
  output [7:0] out_382,
  output [7:0] out_383,
  output [7:0] out_384,
  output [7:0] out_385,
  output [7:0] out_386,
  output [7:0] out_387,
  output [7:0] out_388,
  output [7:0] out_389,
  output [7:0] out_390,
  output [7:0] out_391,
  output [7:0] out_392,
  output [7:0] out_393,
  output [7:0] out_394,
  output [7:0] out_395,
  output [7:0] out_396,
  output [7:0] out_397,
  output [7:0] out_398,
  output [7:0] out_399,
  output [7:0] out_400,
  output [7:0] out_401,
  output [7:0] out_402,
  output [7:0] out_403,
  output [7:0] out_404,
  output [7:0] out_405,
  output [7:0] out_406,
  output [7:0] out_407,
  output [7:0] out_408,
  output [7:0] out_409,
  output [7:0] out_410,
  output [7:0] out_411,
  output [7:0] out_412
);

  wire and_1_out, comparator_1_eq, d_ff_1_q, decoder_1_out0, decoder_1_out1, decoder_1_out2, decoder_1_out3,
       decoder_2_out0, decoder_2_out1, decoder_2_out2, decoder_2_out3, decoder_2_out4, decoder_2_out5,
       decoder_2_out6, decoder_2_out7, decoder_2_out8, decoder_2_out9, decoder_2_out10, decoder_2_out11,
       decoder_2_out12, decoder_2_out13, decoder_2_out14, decoder_2_out15, decoder_2_out16, decoder_2_out17,
       decoder_2_out18, decoder_2_out19, decoder_3_out0, decoder_3_out1, decoder_3_out2, decoder_3_out3,
       decoder_3_out4, decoder_3_out5, decoder_3_out6, decoder_3_out7, decoder_3_out8, decoder_3_out9,
       decoder_3_out10, decoder_3_out11, decoder_3_out12, decoder_3_out13, decoder_3_out14, decoder_3_out15,
       decoder_3_out16, decoder_3_out17, decoder_3_out18, decoder_3_out19, decoder_4_out0, decoder_4_out1,
       decoder_4_out2, decoder_4_out3, decoder_4_out4, decoder_4_out5, decoder_4_out6, decoder_4_out7,
       decoder_4_out8, decoder_4_out9, decoder_4_out10, decoder_4_out11, decoder_4_out12, decoder_4_out13,
       decoder_4_out14, decoder_4_out15, decoder_4_out16, decoder_4_out17, decoder_4_out18, decoder_4_out19,
       decoder_5_out0, decoder_5_out1, decoder_5_out2, decoder_5_out3, decoder_5_out4, decoder_5_out5,
       decoder_5_out6, decoder_5_out7, decoder_5_out8, decoder_5_out9, decoder_5_out10, decoder_5_out11,
       decoder_5_out12, decoder_5_out13, decoder_5_out14, decoder_5_out15, decoder_5_out16, decoder_5_out17,
       decoder_5_out18, decoder_5_out19, not_1_out, undriven, undriven_2, undriven_3, undriven_4;
  wire [1:0] adder_2_out, ADDR_ROW_q, multiplexer_2_out;
  wire [3:0] register_1_q;
  wire [4:0] adder_1_out, ADDR_COLUMN_q, multiplexer_1_out;
  wire [39:0] rom_1_data;

  D_Flip_Flop d_ff_1 (.D(not_1_out), .clk(E), .Q(d_ff_1_q));  // open: Qn, preset, reset
  Register #(.width(4)) register_1 (.D({D7, D6, D5, D4}), .en(RS), .clk(E), .Q(register_1_q));  // open: clr
  not not_1 (not_1_out, d_ff_1_q);
  Register #(.width(5)) ADDR_COLUMN (.D(multiplexer_1_out), .en(and_1_out), .clk(E), .Q(ADDR_COLUMN_q));  // open: clr
  Multiplexer #(.enable("false"), .width(5)) multiplexer_1 (
    .in0(adder_1_out), .in1({5{1'b0}}), .out(multiplexer_1_out), .sel(comparator_1_eq));
  Register #(.width(2)) ADDR_ROW (.D(multiplexer_2_out), .en(and_1_out), .clk(E), .Q(ADDR_ROW_q));  // open: clr
  Multiplexer #(.enable("false"), .width(2)) multiplexer_2 (
    .in0(ADDR_ROW_q), .in1(adder_2_out), .out(multiplexer_2_out), .sel(comparator_1_eq));
  and and_1 (and_1_out, d_ff_1_q, RS);
  ROM #(.dataWidth(40)) rom_1 (.addr({register_1_q, D7, D6, D5, D4}), .data(rom_1_data));
  Adder #(.width(5)) adder_1 (.a(5'b00001), .b(ADDR_COLUMN_q), .out(adder_1_out));  // open: cin, cout
  Comparator #(.width(5)) comparator_1 (.a(ADDR_COLUMN_q), .b(5'b10011), .eq(comparator_1_eq));  // open: gt, lt
  Adder #(.width(2)) adder_2 (.a(2'b01), .b(ADDR_ROW_q), .out(adder_2_out));  // open: cin, cout
  Decoder #(.select(2)) decoder_1 (
    .out0(decoder_1_out0), .out1(decoder_1_out1), .out2(decoder_1_out2), .out3(decoder_1_out3),
    .sel(ADDR_ROW_q), .en(d_ff_1_q));
  Register #(.width(40)) register_2 (
    .D(rom_1_data), .en(decoder_2_out0), .clk(E), .Q({out_93, out_73, out_53, out_33, out_13}), .clr(undriven));
  Register #(.width(40)) register_3 (
    .D(rom_1_data), .en(decoder_3_out0), .clk(E), .Q({out_193, out_173, out_153, out_133, out_113}),
    .clr(undriven_2));
  Register #(.width(40)) register_4 (
    .D(rom_1_data), .en(decoder_4_out0), .clk(E), .Q({out_293, out_273, out_253, out_233, out_213}),
    .clr(undriven_3));
  Register #(.width(40)) register_5 (
    .D(rom_1_data), .en(decoder_5_out0), .clk(E), .Q({out_393, out_373, out_353, out_333, out_313}),
    .clr(undriven_4));
  Register #(.width(40)) register_6 (
    .D(rom_1_data), .en(decoder_2_out1), .clk(E), .Q({out_94, out_74, out_54, out_34, out_14}), .clr(undriven));
  Register #(.width(40)) register_7 (
    .D(rom_1_data), .en(decoder_3_out1), .clk(E), .Q({out_194, out_174, out_154, out_134, out_114}),
    .clr(undriven_2));
  Register #(.width(40)) register_8 (
    .D(rom_1_data), .en(decoder_4_out1), .clk(E), .Q({out_294, out_274, out_254, out_234, out_214}),
    .clr(undriven_3));
  Register #(.width(40)) register_9 (
    .D(rom_1_data), .en(decoder_5_out1), .clk(E), .Q({out_394, out_374, out_354, out_334, out_314}),
    .clr(undriven_4));
  Register #(.width(40)) register_10 (
    .D(rom_1_data), .en(decoder_2_out2), .clk(E), .Q({out_95, out_75, out_55, out_35, out_15}), .clr(undriven));
  Register #(.width(40)) register_11 (
    .D(rom_1_data), .en(decoder_3_out2), .clk(E), .Q({out_195, out_175, out_155, out_135, out_115}),
    .clr(undriven_2));
  Register #(.width(40)) register_12 (
    .D(rom_1_data), .en(decoder_4_out2), .clk(E), .Q({out_295, out_275, out_255, out_235, out_215}),
    .clr(undriven_3));
  Register #(.width(40)) register_13 (
    .D(rom_1_data), .en(decoder_5_out2), .clk(E), .Q({out_395, out_375, out_355, out_335, out_315}),
    .clr(undriven_4));
  Register #(.width(40)) register_14 (
    .D(rom_1_data), .en(decoder_2_out3), .clk(E), .Q({out_96, out_76, out_56, out_36, out_16}), .clr(undriven));
  Register #(.width(40)) register_15 (
    .D(rom_1_data), .en(decoder_3_out3), .clk(E), .Q({out_196, out_176, out_156, out_136, out_116}),
    .clr(undriven_2));
  Register #(.width(40)) register_16 (
    .D(rom_1_data), .en(decoder_4_out3), .clk(E), .Q({out_296, out_276, out_256, out_236, out_216}),
    .clr(undriven_3));
  Register #(.width(40)) register_17 (
    .D(rom_1_data), .en(decoder_5_out3), .clk(E), .Q({out_396, out_376, out_356, out_336, out_316}),
    .clr(undriven_4));
  Register #(.width(40)) register_18 (
    .D(rom_1_data), .en(decoder_2_out4), .clk(E), .Q({out_97, out_77, out_57, out_37, out_17}), .clr(undriven));
  Register #(.width(40)) register_19 (
    .D(rom_1_data), .en(decoder_3_out4), .clk(E), .Q({out_197, out_177, out_157, out_137, out_117}),
    .clr(undriven_2));
  Register #(.width(40)) register_20 (
    .D(rom_1_data), .en(decoder_4_out4), .clk(E), .Q({out_297, out_277, out_257, out_237, out_217}),
    .clr(undriven_3));
  Register #(.width(40)) register_21 (
    .D(rom_1_data), .en(decoder_5_out4), .clk(E), .Q({out_397, out_377, out_357, out_337, out_317}),
    .clr(undriven_4));
  Register #(.width(40)) register_22 (
    .D(rom_1_data), .en(decoder_2_out5), .clk(E), .Q({out_98, out_78, out_58, out_38, out_18}), .clr(undriven));
  Register #(.width(40)) register_23 (
    .D(rom_1_data), .en(decoder_3_out5), .clk(E), .Q({out_198, out_178, out_158, out_138, out_118}),
    .clr(undriven_2));
  Register #(.width(40)) register_24 (
    .D(rom_1_data), .en(decoder_4_out5), .clk(E), .Q({out_298, out_278, out_258, out_238, out_218}),
    .clr(undriven_3));
  Register #(.width(40)) register_25 (
    .D(rom_1_data), .en(decoder_5_out5), .clk(E), .Q({out_398, out_378, out_358, out_338, out_318}),
    .clr(undriven_4));
  Register #(.width(40)) register_26 (
    .D(rom_1_data), .en(decoder_2_out6), .clk(E), .Q({out_99, out_79, out_59, out_39, out_19}), .clr(undriven));
  Register #(.width(40)) register_27 (
    .D(rom_1_data), .en(decoder_3_out6), .clk(E), .Q({out_199, out_179, out_159, out_139, out_119}),
    .clr(undriven_2));
  Register #(.width(40)) register_28 (
    .D(rom_1_data), .en(decoder_4_out6), .clk(E), .Q({out_299, out_279, out_259, out_239, out_219}),
    .clr(undriven_3));
  Register #(.width(40)) register_29 (
    .D(rom_1_data), .en(decoder_5_out6), .clk(E), .Q({out_399, out_379, out_359, out_339, out_319}),
    .clr(undriven_4));
  Register #(.width(40)) register_30 (
    .D(rom_1_data), .en(decoder_2_out7), .clk(E), .Q({out_100, out_80, out_60, out_40, out_20}),
    .clr(undriven));
  Register #(.width(40)) register_31 (
    .D(rom_1_data), .en(decoder_3_out7), .clk(E), .Q({out_200, out_180, out_160, out_140, out_120}),
    .clr(undriven_2));
  Register #(.width(40)) register_32 (
    .D(rom_1_data), .en(decoder_4_out7), .clk(E), .Q({out_300, out_280, out_260, out_240, out_220}),
    .clr(undriven_3));
  Register #(.width(40)) register_33 (
    .D(rom_1_data), .en(decoder_5_out7), .clk(E), .Q({out_400, out_380, out_360, out_340, out_320}),
    .clr(undriven_4));
  Register #(.width(40)) register_34 (
    .D(rom_1_data), .en(decoder_2_out8), .clk(E), .Q({out_101, out_81, out_61, out_41, out_21}),
    .clr(undriven));
  Register #(.width(40)) register_35 (
    .D(rom_1_data), .en(decoder_3_out8), .clk(E), .Q({out_201, out_181, out_161, out_141, out_121}),
    .clr(undriven_2));
  Register #(.width(40)) register_36 (
    .D(rom_1_data), .en(decoder_4_out8), .clk(E), .Q({out_301, out_281, out_261, out_241, out_221}),
    .clr(undriven_3));
  Register #(.width(40)) register_37 (
    .D(rom_1_data), .en(decoder_5_out8), .clk(E), .Q({out_401, out_381, out_361, out_341, out_321}),
    .clr(undriven_4));
  Decoder #(.select(5)) decoder_2 (
    .out0(decoder_2_out0), .out1(decoder_2_out1), .out2(decoder_2_out2), .out3(decoder_2_out3),
    .out4(decoder_2_out4), .out5(decoder_2_out5), .out6(decoder_2_out6), .out7(decoder_2_out7),
    .out8(decoder_2_out8), .out9(decoder_2_out9), .out10(decoder_2_out10), .out11(decoder_2_out11),
    .out12(decoder_2_out12), .out13(decoder_2_out13), .out14(decoder_2_out14), .out15(decoder_2_out15),
    .out16(decoder_2_out16), .out17(decoder_2_out17), .out18(decoder_2_out18), .out19(decoder_2_out19),
    .sel(ADDR_COLUMN_q), .en(decoder_1_out0));  // open: out20, out21, out22, out23, out24, out25, out26, out27, out28, out29, out30, out31
  Register #(.width(40)) register_38 (
    .D(rom_1_data), .en(decoder_2_out9), .clk(E), .Q({out_102, out_82, out_62, out_42, out_22}),
    .clr(undriven));
  Decoder #(.select(5)) decoder_3 (
    .out0(decoder_3_out0), .out1(decoder_3_out1), .out2(decoder_3_out2), .out3(decoder_3_out3),
    .out4(decoder_3_out4), .out5(decoder_3_out5), .out6(decoder_3_out6), .out7(decoder_3_out7),
    .out8(decoder_3_out8), .out9(decoder_3_out9), .out10(decoder_3_out10), .out11(decoder_3_out11),
    .out12(decoder_3_out12), .out13(decoder_3_out13), .out14(decoder_3_out14), .out15(decoder_3_out15),
    .out16(decoder_3_out16), .out17(decoder_3_out17), .out18(decoder_3_out18), .out19(decoder_3_out19),
    .sel(ADDR_COLUMN_q), .en(decoder_1_out1));  // open: out20, out21, out22, out23, out24, out25, out26, out27, out28, out29, out30, out31
  Register #(.width(40)) register_39 (
    .D(rom_1_data), .en(decoder_3_out9), .clk(E), .Q({out_202, out_182, out_162, out_142, out_122}),
    .clr(undriven_2));
  Decoder #(.select(5)) decoder_4 (
    .out0(decoder_4_out0), .out1(decoder_4_out1), .out2(decoder_4_out2), .out3(decoder_4_out3),
    .out4(decoder_4_out4), .out5(decoder_4_out5), .out6(decoder_4_out6), .out7(decoder_4_out7),
    .out8(decoder_4_out8), .out9(decoder_4_out9), .out10(decoder_4_out10), .out11(decoder_4_out11),
    .out12(decoder_4_out12), .out13(decoder_4_out13), .out14(decoder_4_out14), .out15(decoder_4_out15),
    .out16(decoder_4_out16), .out17(decoder_4_out17), .out18(decoder_4_out18), .out19(decoder_4_out19),
    .sel(ADDR_COLUMN_q), .en(decoder_1_out2));  // open: out20, out21, out22, out23, out24, out25, out26, out27, out28, out29, out30, out31
  Register #(.width(40)) register_40 (
    .D(rom_1_data), .en(decoder_4_out9), .clk(E), .Q({out_302, out_282, out_262, out_242, out_222}),
    .clr(undriven_3));
  Decoder #(.select(5)) decoder_5 (
    .out0(decoder_5_out0), .out1(decoder_5_out1), .out2(decoder_5_out2), .out3(decoder_5_out3),
    .out4(decoder_5_out4), .out5(decoder_5_out5), .out6(decoder_5_out6), .out7(decoder_5_out7),
    .out8(decoder_5_out8), .out9(decoder_5_out9), .out10(decoder_5_out10), .out11(decoder_5_out11),
    .out12(decoder_5_out12), .out13(decoder_5_out13), .out14(decoder_5_out14), .out15(decoder_5_out15),
    .out16(decoder_5_out16), .out17(decoder_5_out17), .out18(decoder_5_out18), .out19(decoder_5_out19),
    .sel(ADDR_COLUMN_q), .en(decoder_1_out3));  // open: out20, out21, out22, out23, out24, out25, out26, out27, out28, out29, out30, out31
  Register #(.width(40)) register_41 (
    .D(rom_1_data), .en(decoder_5_out9), .clk(E), .Q({out_402, out_382, out_362, out_342, out_322}),
    .clr(undriven_4));
  Register #(.width(40)) register_42 (
    .D(rom_1_data), .en(decoder_2_out10), .clk(E), .Q({out_103, out_83, out_63, out_43, out_23}),
    .clr(undriven));
  Register #(.width(40)) register_43 (
    .D(rom_1_data), .en(decoder_3_out10), .clk(E), .Q({out_203, out_183, out_163, out_143, out_123}),
    .clr(undriven_2));
  Register #(.width(40)) register_44 (
    .D(rom_1_data), .en(decoder_4_out10), .clk(E), .Q({out_303, out_283, out_263, out_243, out_223}),
    .clr(undriven_3));
  Register #(.width(40)) register_45 (
    .D(rom_1_data), .en(decoder_5_out10), .clk(E), .Q({out_403, out_383, out_363, out_343, out_323}),
    .clr(undriven_4));
  Register #(.width(40)) register_46 (
    .D(rom_1_data), .en(decoder_2_out11), .clk(E), .Q({out_104, out_84, out_64, out_44, out_24}),
    .clr(undriven));
  Register #(.width(40)) register_47 (
    .D(rom_1_data), .en(decoder_3_out11), .clk(E), .Q({out_204, out_184, out_164, out_144, out_124}),
    .clr(undriven_2));
  Register #(.width(40)) register_48 (
    .D(rom_1_data), .en(decoder_4_out11), .clk(E), .Q({out_304, out_284, out_264, out_244, out_224}),
    .clr(undriven_3));
  Register #(.width(40)) register_49 (
    .D(rom_1_data), .en(decoder_5_out11), .clk(E), .Q({out_404, out_384, out_364, out_344, out_324}),
    .clr(undriven_4));
  Register #(.width(40)) register_50 (
    .D(rom_1_data), .en(decoder_2_out12), .clk(E), .Q({out_105, out_85, out_65, out_45, out_25}),
    .clr(undriven));
  Register #(.width(40)) register_51 (
    .D(rom_1_data), .en(decoder_3_out12), .clk(E), .Q({out_205, out_185, out_165, out_145, out_125}),
    .clr(undriven_2));
  Register #(.width(40)) register_52 (
    .D(rom_1_data), .en(decoder_4_out12), .clk(E), .Q({out_305, out_285, out_265, out_245, out_225}),
    .clr(undriven_3));
  Register #(.width(40)) register_53 (
    .D(rom_1_data), .en(decoder_5_out12), .clk(E), .Q({out_405, out_385, out_365, out_345, out_325}),
    .clr(undriven_4));
  Register #(.width(40)) register_54 (
    .D(rom_1_data), .en(decoder_2_out13), .clk(E), .Q({out_106, out_86, out_66, out_46, out_26}),
    .clr(undriven));
  Register #(.width(40)) register_55 (
    .D(rom_1_data), .en(decoder_3_out13), .clk(E), .Q({out_206, out_186, out_166, out_146, out_126}),
    .clr(undriven_2));
  Register #(.width(40)) register_56 (
    .D(rom_1_data), .en(decoder_4_out13), .clk(E), .Q({out_306, out_286, out_266, out_246, out_226}),
    .clr(undriven_3));
  Register #(.width(40)) register_57 (
    .D(rom_1_data), .en(decoder_5_out13), .clk(E), .Q({out_406, out_386, out_366, out_346, out_326}),
    .clr(undriven_4));
  Register #(.width(40)) register_58 (
    .D(rom_1_data), .en(decoder_2_out14), .clk(E), .Q({out_107, out_87, out_67, out_47, out_27}),
    .clr(undriven));
  Register #(.width(40)) register_59 (
    .D(rom_1_data), .en(decoder_3_out14), .clk(E), .Q({out_207, out_187, out_167, out_147, out_127}),
    .clr(undriven_2));
  Register #(.width(40)) register_60 (
    .D(rom_1_data), .en(decoder_4_out14), .clk(E), .Q({out_307, out_287, out_267, out_247, out_227}),
    .clr(undriven_3));
  Register #(.width(40)) register_61 (
    .D(rom_1_data), .en(decoder_5_out14), .clk(E), .Q({out_407, out_387, out_367, out_347, out_327}),
    .clr(undriven_4));
  Register #(.width(40)) register_62 (
    .D(rom_1_data), .en(decoder_2_out15), .clk(E), .Q({out_108, out_88, out_68, out_48, out_28}),
    .clr(undriven));
  Register #(.width(40)) register_63 (
    .D(rom_1_data), .en(decoder_3_out15), .clk(E), .Q({out_208, out_188, out_168, out_148, out_128}),
    .clr(undriven_2));
  Register #(.width(40)) register_64 (
    .D(rom_1_data), .en(decoder_4_out15), .clk(E), .Q({out_308, out_288, out_268, out_248, out_228}),
    .clr(undriven_3));
  Register #(.width(40)) register_65 (
    .D(rom_1_data), .en(decoder_5_out15), .clk(E), .Q({out_408, out_388, out_368, out_348, out_328}),
    .clr(undriven_4));
  Register #(.width(40)) register_66 (
    .D(rom_1_data), .en(decoder_2_out16), .clk(E), .Q({out_109, out_89, out_69, out_49, out_29}),
    .clr(undriven));
  Register #(.width(40)) register_67 (
    .D(rom_1_data), .en(decoder_3_out16), .clk(E), .Q({out_209, out_189, out_169, out_149, out_129}),
    .clr(undriven_2));
  Register #(.width(40)) register_68 (
    .D(rom_1_data), .en(decoder_4_out16), .clk(E), .Q({out_309, out_289, out_269, out_249, out_229}),
    .clr(undriven_3));
  Register #(.width(40)) register_69 (
    .D(rom_1_data), .en(decoder_5_out16), .clk(E), .Q({out_409, out_389, out_369, out_349, out_329}),
    .clr(undriven_4));
  Register #(.width(40)) register_70 (
    .D(rom_1_data), .en(decoder_2_out17), .clk(E), .Q({out_110, out_90, out_70, out_50, out_30}),
    .clr(undriven));
  Register #(.width(40)) register_71 (
    .D(rom_1_data), .en(decoder_3_out17), .clk(E), .Q({out_210, out_190, out_170, out_150, out_130}),
    .clr(undriven_2));
  Register #(.width(40)) register_72 (
    .D(rom_1_data), .en(decoder_4_out17), .clk(E), .Q({out_310, out_290, out_270, out_250, out_230}),
    .clr(undriven_3));
  Register #(.width(40)) register_73 (
    .D(rom_1_data), .en(decoder_5_out17), .clk(E), .Q({out_410, out_390, out_370, out_350, out_330}),
    .clr(undriven_4));
  Register #(.width(40)) register_74 (
    .D(rom_1_data), .en(decoder_2_out18), .clk(E), .Q({out_111, out_91, out_71, out_51, out_31}),
    .clr(undriven));
  Register #(.width(40)) register_75 (
    .D(rom_1_data), .en(decoder_3_out18), .clk(E), .Q({out_211, out_191, out_171, out_151, out_131}),
    .clr(undriven_2));
  Register #(.width(40)) register_76 (
    .D(rom_1_data), .en(decoder_4_out18), .clk(E), .Q({out_311, out_291, out_271, out_251, out_231}),
    .clr(undriven_3));
  Register #(.width(40)) register_77 (
    .D(rom_1_data), .en(decoder_5_out18), .clk(E), .Q({out_411, out_391, out_371, out_351, out_331}),
    .clr(undriven_4));
  Register #(.width(40)) register_78 (
    .D(rom_1_data), .en(decoder_2_out19), .clk(E), .Q({out_112, out_92, out_72, out_52, out_32}),
    .clr(undriven));
  Register #(.width(40)) register_79 (
    .D(rom_1_data), .en(decoder_3_out19), .clk(E), .Q({out_212, out_192, out_172, out_152, out_132}),
    .clr(undriven_2));
  Register #(.width(40)) register_80 (
    .D(rom_1_data), .en(decoder_4_out19), .clk(E), .Q({out_312, out_292, out_272, out_252, out_232}),
    .clr(undriven_3));
  Register #(.width(40)) register_81 (
    .D(rom_1_data), .en(decoder_5_out19), .clk(E), .Q({out_412, out_392, out_372, out_352, out_332}),
    .clr(undriven_4));

  // Notes on the sheet:
  //   contents of rom_1 (hex, n*v repeats v):
  //   33*0 fa0000 e000e000 28fe28fe28 4854fe5424 462610c8c4 a44aa926c c0a000 824438 3844820000 28107c1028
  //   10107c1010 c0a00 1010101010 60600 4020100804 7ca2928a7c 2fe4200 6292928a06 6c92928284 8fe482818
  //   9ca2a2a2e4 c9292523c c0a0908e80 6c9292926c 7894929260 6c6c00 6c6a00 82442810 2828282828 1028448200
  //   60908a8000 7c829e924c 3e4888483e 6c929292fe 448282827c 38448282fe 92929292fe 80909090fe 5e9282827c
  //   fe101010fe 82fe8200 80fc820204 82442810fe 2020202fe fe403040fe fe081020fe 7c8282827c 60909090fe
  //   7a848a827c 62949890fe 4c92929264 8080fe8080 fc020202fc f8040204f8 fc021c02fc c6281028c6 e0100e10e0
  //   c2a2928a86 8282fe00 408102000 fe828200 2040804020 202020202 20408000 1e2a2a2a04 1c222212fe 42222221c
  //   fe1222221c 182a2a2a1c 4080907e10 3c2a2a2a10 1e202010fe 2be1200 bc220204 221408fe 2fe8200 1e201e203e
  //   1e2020103e 1c2222221c 102828283e 3e18282810 102020103e 42a2a2a12 40222fc20 3e0402023c 3804020438
  //   3c020c023c 2214081422 3c0a0a0a30 22322a2622 826c1000 fe0000 106c8200 1008101008
endmodule
