// Logisim project combinational_multiplier.circ as structural Verilog: 1 circuit, main circuit main
module main (
  input  A0,
  input  A1,
  input  A2,
  input  B0,
  input  B1,
  input  B2,
  output C0,
  output C1,
  output C2,
  output C3,
  output C4,
  output C5
);

  wire g1_out, g2_out, g3_out, g4_out, g5_out, g6_out, g7_out, g8_out, g10_out, g11_out, g12_out, g13_out,
       g14_out, g15_out, g16_out, g18_out, g19_out, g20_out, g21_out, g23_out, g24_out, g25_out, g26_out,
       g28_out;

  and g0 (C0, A0, B0);
  and g1 (g1_out, A0, B1);
  and g2 (g2_out, A0, B2);
  and g3 (g3_out, A1, B0);
  and g4 (g4_out, A1, B1);
  and g5 (g5_out, A1, B2);
  and g6 (g6_out, A2, B0);
  and g7 (g7_out, A2, B1);
  and g8 (g8_out, A2, B2);
  xor g9 (C1, g3_out, g1_out);
  and g10 (g10_out, g1_out, g3_out);
  xor g11 (g11_out, g2_out, g4_out);
  and g12 (g12_out, g2_out, g4_out);
  xor g13 (g13_out, g5_out, g7_out);
  and g14 (g14_out, g5_out, g7_out);
  xor g17 (C2, g6_out, g15_out);
  xor g15 (g15_out, g11_out, g10_out);
  and g18 (g18_out, g15_out, g6_out);
  and g16 (g16_out, g10_out, g11_out);
  or g19 (g19_out, g16_out, g12_out);
  xor g20 (g20_out, g19_out, g13_out);
  and g21 (g21_out, g19_out, g13_out);
  xor g22 (C3, g18_out, g20_out);
  and g23 (g23_out, g18_out, g20_out);
  or g24 (g24_out, g21_out, g14_out);
  xor g25 (g25_out, g24_out, g8_out);
  and g26 (g26_out, g24_out, g8_out);
  xor g27 (C4, g23_out, g25_out);
  and g28 (g28_out, g23_out, g25_out);
  or g29 (C5, g28_out, g26_out);
endmodule
