// Logisim project ins_memory.circ as structural Verilog: 1 circuit, main circuit main
module main (
  output [1:0] SEL_OP,
  output USE_R_SRC2,
  output [3:0] D_IN,
  output [1:0] SEL_R_SRC1,
  output [1:0] SEL_R_SRC2,
  output [1:0] SEL_R_DST
);

  wire CLK_out, decoder_1_out0, decoder_1_out1, decoder_1_out2, decoder_1_out3, Reset_out;
  wire [3:0] adder_1_out, adder_2_out, and_1_out, multiplexer_1_out, multiplexer_2_out, multiplexer_3_out,
       multiplexer_4_out, or_1_out, PC_q, REG0_q, REG1_q, REG2_q, REG3_q, xor_1_out;

  Register #(.width(4)) PC (.D(adder_1_out), .en(1'b1), .clk(CLK_out), .Q(PC_q), .clr(Reset_out));
  Clock CLK (.out(CLK_out));
  Button Reset (.out(Reset_out));
  Adder #(.width(4)) adder_1 (.a(4'b0001), .b(PC_q), .out(adder_1_out), .cin(1'b0));  // open: cout
  ROM #(.addrWidth(4), .dataWidth(13)) INSTRUCTION_MEMORY (
    .addr(PC_q), .data({SEL_R_DST, SEL_R_SRC2, SEL_R_SRC1, D_IN, USE_R_SRC2, SEL_OP}));
  Decoder #(.select(2)) decoder_1 (
    .out0(decoder_1_out0), .out1(decoder_1_out1), .out2(decoder_1_out2), .out3(decoder_1_out3),
    .sel(SEL_R_DST), .en(1'b1));
  Register #(.width(4)) REG0 (.D(multiplexer_4_out), .en(decoder_1_out0), .clk(CLK_out), .Q(REG0_q), .clr(Reset_out));
  Register #(.width(4)) REG1 (.D(multiplexer_4_out), .en(decoder_1_out1), .clk(CLK_out), .Q(REG1_q), .clr(Reset_out));
  Register #(.width(4)) REG2 (.D(multiplexer_4_out), .en(decoder_1_out2), .clk(CLK_out), .Q(REG2_q), .clr(Reset_out));
  Register #(.width(4)) REG3 (.D(multiplexer_4_out), .en(decoder_1_out3), .clk(CLK_out), .Q(REG3_q), .clr(Reset_out));
  Multiplexer #(.enable("false"), .select(2), .width(4)) multiplexer_1 (
    .in0(REG0_q), .in1(REG1_q), .in2(REG2_q), .in3(REG3_q), .out(multiplexer_1_out), .sel(SEL_R_SRC1));
  Multiplexer #(.enable("false"), .select(2), .width(4)) multiplexer_2 (
    .in0(REG0_q), .in1(REG1_q), .in2(REG2_q), .in3(REG3_q), .out(multiplexer_2_out), .sel(SEL_R_SRC2));
  Multiplexer #(.enable("false"), .width(4)) multiplexer_3 (
    .in0(D_IN), .in1(multiplexer_2_out), .out(multiplexer_3_out), .sel(USE_R_SRC2));
  assign and_1_out = multiplexer_1_out & multiplexer_3_out;  // AND_Gate and_1, 4 bits wide
  assign or_1_out = multiplexer_1_out | multiplexer_3_out;  // OR_Gate or_1, 4 bits wide
  assign xor_1_out = multiplexer_1_out ^ multiplexer_3_out;  // XOR_Gate xor_1, 4 bits wide
  Adder #(.width(4)) adder_2 (
    .a(multiplexer_1_out), .b(multiplexer_3_out), .out(adder_2_out), .cin(1'b0));  // open: cout
  Multiplexer #(.enable("false"), .select(2), .width(4)) multiplexer_4 (
    .in0(and_1_out), .in1(or_1_out), .in2(xor_1_out), .in3(adder_2_out), .out(multiplexer_4_out), .sel(SEL_OP));
endmodule
