// Logisim project mux4.circ as structural Verilog: 1 circuit, main circuit main
module main (
  input  in_1,
  input  in_2,
  input  in_3,
  input  in_4,
  input  in_5,
  input  in_6,
  input  in_7,
  input  in_8,
  input  in_9,
  input  in_10,
  input  in_11,
  input  in_12,
  output out_13,
  output out_14
);

  wire and_1_out, and_2_out, and_3_out, and_4_out, and_5_out, and_6_out, and_7_out, and_8_out, and_9_out,
       and_10_out, and_11_out, and_12_out, not_1_out, not_2_out, not_3_out, not_4_out;

  not not_1 (not_1_out, in_9);
  not not_2 (not_2_out, in_11);
  assign out_13 = and_1_out ? in_1 : 1'bz;  // Controlled_Buffer controlled_buffer_1
  assign out_13 = and_2_out ? in_3 : 1'bz;  // Controlled_Buffer controlled_buffer_2
  and and_1 (and_1_out, not_1_out, not_2_out);
  and and_2 (and_2_out, not_1_out, in_11);
  assign out_13 = and_3_out ? in_5 : 1'bz;  // Controlled_Buffer controlled_buffer_3
  assign out_13 = and_4_out ? in_7 : 1'bz;  // Controlled_Buffer controlled_buffer_4
  and and_3 (and_3_out, in_9, not_2_out);
  and and_4 (and_4_out, in_9, in_11);
  and and_5 (and_5_out, in_2, and_6_out);
  and and_6 (and_6_out, not_3_out, not_4_out);
  and and_7 (and_7_out, not_3_out, in_12);
  not not_3 (not_3_out, in_10);
  not not_4 (not_4_out, in_12);
  and and_8 (and_8_out, in_4, and_7_out);
  and and_9 (and_9_out, in_6, and_10_out);
  and and_10 (and_10_out, in_10, not_4_out);
  and and_11 (and_11_out, in_10, in_12);
  and and_12 (and_12_out, in_8, and_11_out);
  or or_1 (out_14, and_5_out, and_8_out, and_9_out, and_12_out);

  // Notes on the sheet:
  //   If we want to select among four options,
  //    we need two select bits, enumerating all four possibilities
  //   Here is the same circuit using AND and OR gates
endmodule
