// Logisim project pipeline.circ as structural Verilog: 17 circuits, main circuit main
module main (
);

  wire and_1_out, and_2_out, clock_1_out, cmp0_1_out_2, ctrlunit_1_alusrc, ctrlunit_1_b, ctrlunit_1_cbnz,
       ctrlunit_1_cbz, ctrlunit_1_memread, ctrlunit_1_memtoreg, ctrlunit_1_memwrite, ctrlunit_1_reg2loc,
       ctrlunit_1_regwrite, ex_mem_1_out_11, ex_mem_1_out_12, ex_mem_1_out_14, ex_mem_1_out_15,
       id_ex_1_out_17, id_ex_1_out_18, id_ex_1_out_20, id_ex_1_out_21, id_ex_1_out_22, mem_wb_1_out_8,
       mem_wb_1_out_9, or_1_out, Reset_out;
  wire [1:0] ctrlunit_1_accesssize, ex_mem_1_out_13, fwdunit_1_fwdrm, fwdunit_1_fwdrn, id_ex_1_out_19;
  wire [2:0] ctrlunit_1_immsel;
  wire [3:0] ctrlunit_1_aluop, id_ex_1_out_23;
  wire [4:0] ex_mem_1_out_18, id_ex_1_out_27, id_ex_1_out_28, id_ex_1_out_29, if_id_1_out_12, if_id_1_out_13,
       if_id_1_out_14, mem_wb_1_out_12, multiplexer_2_out;
  wire [10:0] if_id_1_out_11;
  wire [11:0] id_ex_1_out_30, if_id_1_out_16;
  wire [31:0] if_id_1_out_15, insmem_1_inst;
  wire [63:0] add64b_1_out_3, add64b_2_out_3, alu_1_result, datamem_1_rddata, ex_mem_1_out_16,
       ex_mem_1_out_17, id_ex_1_out_24, id_ex_1_out_25, id_ex_1_out_26, if_id_1_out_10, immextend_1_out_3,
       mem_wb_1_out_10, mem_wb_1_out_11, multiplexer_1_out, multiplexer_3_out, multiplexer_4_out,
       multiplexer_5_out, multiplexer_6_out, pcreg_1_out_4, regs_1_rddata0, regs_1_rddata1,
       shiftleft2_1_out_2;

  Multiplexer #(.enable("false"), .width(64)) multiplexer_1 (
    .in0(add64b_1_out_3), .in1(add64b_2_out_3), .out(multiplexer_1_out), .sel(or_1_out));
  Clock clock_1 (.out(clock_1_out));
  Button Reset (.out(Reset_out));
  PCReg pcreg_1 (.out_4(pcreg_1_out_4), .in_1(multiplexer_1_out), .in_2(clock_1_out), .in_3(Reset_out));
  Add64b add64b_1 (.out_3(add64b_1_out_3), .in_1(64'h4), .in_2(pcreg_1_out_4));
  InsMem insmem_1 (.Inst(insmem_1_inst), .Addr(pcreg_1_out_4));
  IF_ID if_id_1 (
    .out_16(if_id_1_out_16), .out_10(if_id_1_out_10), .out_11(if_id_1_out_11), .out_12(if_id_1_out_12),
    .out_13(if_id_1_out_13), .out_14(if_id_1_out_14), .out_15(if_id_1_out_15), .in_7(insmem_1_inst[21:10]),
    .in_6(insmem_1_inst), .in_1(pcreg_1_out_4), .in_2(insmem_1_inst[31:21]), .in_3(insmem_1_inst[9:5]),
    .in_4(insmem_1_inst[20:16]), .in_5(insmem_1_inst[4:0]), .in_8(clock_1_out), .in_9(Reset_out));
  CtrlUnit ctrlunit_1 (
    .B(ctrlunit_1_b), .CBZ(ctrlunit_1_cbz), .CBNZ(ctrlunit_1_cbnz), .Reg2Loc(ctrlunit_1_reg2loc),
    .RegWrite(ctrlunit_1_regwrite), .MemRead(ctrlunit_1_memread), .MemWrite(ctrlunit_1_memwrite),
    .ALUSrc(ctrlunit_1_alusrc), .MemtoReg(ctrlunit_1_memtoreg), .ALUop(ctrlunit_1_aluop),
    .ImmSel(ctrlunit_1_immsel), .AccessSize(ctrlunit_1_accesssize), .opcode(if_id_1_out_11));
  Multiplexer #(.enable("false"), .width(5)) multiplexer_2 (
    .in0(if_id_1_out_13), .in1(if_id_1_out_14), .out(multiplexer_2_out), .sel(ctrlunit_1_reg2loc));
  ImmExtend immextend_1 (.out_3(immextend_1_out_3), .in_1(if_id_1_out_15), .ExtCtrl(ctrlunit_1_immsel));
  Cmp0 cmp0_1 (.out_2(cmp0_1_out_2), .in_1(regs_1_rddata1));
  Regs regs_1 (
    .RdData0(regs_1_rddata0), .RdData1(regs_1_rddata1), .WrAddr(mem_wb_1_out_12), .WrData(multiplexer_6_out),
    .RegWrite(mem_wb_1_out_9), .CLK(clock_1_out), .RdAddr0(if_id_1_out_12), .RdAddr1(multiplexer_2_out));
  Add64b add64b_2 (.out_3(add64b_2_out_3), .in_1(if_id_1_out_10), .in_2(shiftleft2_1_out_2));
  ShiftLeft2 shiftleft2_1 (.out_2(shiftleft2_1_out_2), .in_1(immextend_1_out_3));
  or or_1 (or_1_out, ctrlunit_1_b, and_1_out, and_2_out);
  and and_1 (and_1_out, ctrlunit_1_cbz, cmp0_1_out_2);
  and and_2 (and_2_out, ctrlunit_1_cbnz, ~cmp0_1_out_2);  // AND_Gate
  ID_EX id_ex_1 (
    .out_25(id_ex_1_out_25), .out_26(id_ex_1_out_26), .out_27(id_ex_1_out_27), .out_28(id_ex_1_out_28),
    .out_29(id_ex_1_out_29), .out_18(id_ex_1_out_18), .out_30(id_ex_1_out_30), .out_19(id_ex_1_out_19),
    .out_20(id_ex_1_out_20), .out_21(id_ex_1_out_21), .out_22(id_ex_1_out_22), .out_17(id_ex_1_out_17),
    .out_23(id_ex_1_out_23), .out_24(id_ex_1_out_24), .in_13(if_id_1_out_14), .in_14(if_id_1_out_16),
    .in_9(regs_1_rddata1), .in_10(immextend_1_out_3), .in_11(if_id_1_out_12), .in_12(multiplexer_2_out),
    .in_2(ctrlunit_1_regwrite), .in_3(ctrlunit_1_accesssize), .in_4(ctrlunit_1_memread),
    .in_5(ctrlunit_1_memwrite), .in_6(ctrlunit_1_alusrc), .in_1(ctrlunit_1_memtoreg),
    .in_7(ctrlunit_1_aluop), .in_8(regs_1_rddata0), .in_15(clock_1_out), .in_16(Reset_out));
  Multiplexer #(.enable("false"), .select(2), .width(64)) multiplexer_3 (
    .in0(id_ex_1_out_24), .in1(ex_mem_1_out_16), .in2(multiplexer_6_out), .out(multiplexer_3_out),
    .sel(fwdunit_1_fwdrn));  // open: in3
  Multiplexer #(.enable("false"), .select(2), .width(64)) multiplexer_4 (
    .in0(id_ex_1_out_25), .in1(ex_mem_1_out_16), .in2(multiplexer_6_out), .out(multiplexer_4_out),
    .sel(fwdunit_1_fwdrm));  // open: in3
  Multiplexer #(.enable("false"), .width(64)) multiplexer_5 (
    .in0(multiplexer_4_out), .in1(id_ex_1_out_26), .out(multiplexer_5_out), .sel(id_ex_1_out_22));
  FwdUnit fwdunit_1 (
    .FwdRn(fwdunit_1_fwdrn), .FwdRm(fwdunit_1_fwdrm), .Rn(id_ex_1_out_27), .EX_MEM_Rd(ex_mem_1_out_18),
    .EX_MEM_RegWrite(ex_mem_1_out_12), .MEM_WB_Rd(mem_wb_1_out_12), .MEM_WB_RegWrite(mem_wb_1_out_9),
    .Rm(id_ex_1_out_28));
  EX_MEM ex_mem_1 (
    .out_12(ex_mem_1_out_12), .out_13(ex_mem_1_out_13), .out_14(ex_mem_1_out_14), .out_15(ex_mem_1_out_15),
    .out_16(ex_mem_1_out_16), .out_11(ex_mem_1_out_11), .out_17(ex_mem_1_out_17), .out_18(ex_mem_1_out_18),
    .in_8(id_ex_1_out_29), .in_2(id_ex_1_out_18), .in_3(id_ex_1_out_19), .in_4(id_ex_1_out_20),
    .in_5(id_ex_1_out_21), .in_6(alu_1_result), .in_1(id_ex_1_out_17), .in_7(multiplexer_4_out),
    .in_9(clock_1_out), .in_10(Reset_out));
  ALU alu_1 (
    .Result(alu_1_result), .shamt(id_ex_1_out_30), .A(multiplexer_3_out), .B(multiplexer_5_out),
    .op(id_ex_1_out_23));  // open: Overflow, Negative, Carry, Zero
  DataMem datamem_1 (
    .RdData(datamem_1_rddata), .Addr(ex_mem_1_out_16), .Size(ex_mem_1_out_13), .MemWrite(ex_mem_1_out_15),
    .MemRead(ex_mem_1_out_14), .CLK(clock_1_out), .WrData(ex_mem_1_out_17));
  MEM_WB mem_wb_1 (
    .out_8(mem_wb_1_out_8), .out_9(mem_wb_1_out_9), .out_10(mem_wb_1_out_10), .out_11(mem_wb_1_out_11),
    .out_12(mem_wb_1_out_12), .in_5(ex_mem_1_out_18), .in_1(ex_mem_1_out_11), .in_2(ex_mem_1_out_12),
    .in_3(ex_mem_1_out_16), .in_4(datamem_1_rddata), .in_6(clock_1_out), .in_7(Reset_out));
  Multiplexer #(.enable("false"), .width(64)) multiplexer_6 (
    .in0(mem_wb_1_out_10), .in1(mem_wb_1_out_11), .out(multiplexer_6_out), .sel(mem_wb_1_out_8));
endmodule

module ALU1b (
  input  cin,
  input  a,
  input  b,
  input  [3:0] op,
  output s,
  output cout
);

  wire adder_1_out, and_1_out, multiplexer_1_out, multiplexer_2_out, not_1_out, not_2_out, or_1_out;

  not not_1 (not_1_out, a);
  not not_2 (not_2_out, b);
  Multiplexer #(.enable("false")) multiplexer_1 (.in0(a), .in1(not_1_out), .out(multiplexer_1_out), .sel(op[3]));
  Multiplexer #(.enable("false")) multiplexer_2 (.in0(b), .in1(not_2_out), .out(multiplexer_2_out), .sel(op[2]));
  and and_1 (and_1_out, multiplexer_1_out, multiplexer_2_out);
  or or_1 (or_1_out, multiplexer_1_out, multiplexer_2_out);
  Adder #(.width(1)) adder_1 (.a(multiplexer_1_out), .b(multiplexer_2_out), .out(adder_1_out), .cin(cin), .cout(cout));
  Multiplexer #(.enable("false"), .select(2)) multiplexer_3 (
    .in0(and_1_out), .in1(or_1_out), .in2(adder_1_out), .in3(b), .out(s), .sel(op[1:0]));
endmodule

module ALU (
  input  [11:0] shamt,
  input  [63:0] A,
  input  [3:0] op,
  input  [63:0] B,
  output [63:0] Result,
  output Zero,
  output Overflow,
  output Negative,
  output Carry
);

  wire alu1b_1_cout, alu1b_2_cout, alu1b_3_cout, alu1b_4_cout, alu1b_5_cout, alu1b_6_cout, alu1b_7_cout,
       alu1b_8_cout, alu1b_9_cout, alu1b_10_cout, alu1b_11_cout, alu1b_12_cout, alu1b_13_cout, alu1b_14_cout,
       alu1b_15_cout, alu1b_16_cout, alu1b_17_cout, alu1b_18_cout, alu1b_19_cout, alu1b_20_cout,
       alu1b_21_cout, alu1b_22_cout, alu1b_23_cout, alu1b_24_cout, alu1b_25_cout, alu1b_26_cout,
       alu1b_27_cout, alu1b_28_cout, alu1b_29_cout, alu1b_30_cout, alu1b_31_cout, alu1b_32_cout,
       alu1b_33_cout, alu1b_34_cout, alu1b_35_cout, alu1b_36_cout, alu1b_37_cout, alu1b_38_cout,
       alu1b_39_cout, alu1b_40_cout, alu1b_41_cout, alu1b_42_cout, alu1b_43_cout, alu1b_44_cout,
       alu1b_45_cout, alu1b_46_cout, alu1b_47_cout, alu1b_48_cout, alu1b_49_cout, alu1b_50_cout,
       alu1b_51_cout, alu1b_52_cout, alu1b_53_cout, alu1b_54_cout, alu1b_55_cout, alu1b_56_cout,
       alu1b_57_cout, alu1b_58_cout, alu1b_59_cout, alu1b_60_cout, alu1b_61_cout, alu1b_62_cout,
       alu1b_63_cout, and_1_out, and_2_out, and_3_out, nor_1_out, nor_2_out, or_1_out;
  wire [5:0] subtractor_1_out;
  wire [62:0] alu1b_1_s;
  wire [63:0] multiplexer_1_out, multiplexer_2_out, shifter_1_out, shifter_2_out, xor_1_out;

  assign xor_1_out = B ^ A;  // XOR_Gate xor_1, 64 bits wide
  Subtractor #(.width(6)) subtractor_1 (.a({6{1'b1}}), .b(shamt[5:0]), .out(subtractor_1_out));  // open: bin, bout
  and and_1 (and_1_out, shamt[0], shamt[1], shamt[2], shamt[3], shamt[4], shamt[5]);
  Shifter #(.width(64)) shifter_1 (.in(A), .\dist (subtractor_1_out), .out(shifter_1_out));
  Shifter #(.shift("lr"), .width(64)) shifter_2 (.in(A), .\dist (shamt[11:6]), .out(shifter_2_out));
  Multiplexer #(.enable("false"), .width(64)) multiplexer_1 (
    .in0(shifter_1_out), .in1(shifter_2_out), .out(multiplexer_1_out), .sel(and_1_out));
  ALU1b alu1b_1 (.cout(alu1b_1_cout), .s(alu1b_1_s[0]), .a(A[0]), .b(B[0]), .op(op), .cin(op[2]));
  ALU1b alu1b_2 (.cout(alu1b_2_cout), .s(alu1b_1_s[1]), .a(A[1]), .b(B[1]), .op(op), .cin(alu1b_1_cout));
  ALU1b alu1b_3 (.cout(alu1b_3_cout), .s(alu1b_1_s[2]), .a(A[2]), .b(B[2]), .op(op), .cin(alu1b_2_cout));
  ALU1b alu1b_4 (.cout(alu1b_4_cout), .s(alu1b_1_s[3]), .a(A[3]), .b(B[3]), .op(op), .cin(alu1b_3_cout));
  ALU1b alu1b_5 (.cout(alu1b_5_cout), .s(alu1b_1_s[4]), .a(A[4]), .b(B[4]), .op(op), .cin(alu1b_4_cout));
  ALU1b alu1b_6 (.cout(alu1b_6_cout), .s(alu1b_1_s[5]), .a(A[5]), .b(B[5]), .op(op), .cin(alu1b_5_cout));
  ALU1b alu1b_7 (.cout(alu1b_7_cout), .s(alu1b_1_s[6]), .a(A[6]), .b(B[6]), .op(op), .cin(alu1b_6_cout));
  ALU1b alu1b_8 (.cout(alu1b_8_cout), .s(alu1b_1_s[7]), .a(A[7]), .b(B[7]), .op(op), .cin(alu1b_7_cout));
  ALU1b alu1b_9 (.cout(alu1b_9_cout), .s(alu1b_1_s[8]), .a(A[8]), .b(B[8]), .op(op), .cin(alu1b_8_cout));
  ALU1b alu1b_10 (.cout(alu1b_10_cout), .s(alu1b_1_s[9]), .a(A[9]), .b(B[9]), .op(op), .cin(alu1b_9_cout));
  ALU1b alu1b_11 (.cout(alu1b_11_cout), .s(alu1b_1_s[10]), .a(A[10]), .b(B[10]), .op(op), .cin(alu1b_10_cout));
  ALU1b alu1b_12 (.cout(alu1b_12_cout), .s(alu1b_1_s[11]), .a(A[11]), .b(B[11]), .op(op), .cin(alu1b_11_cout));
  ALU1b alu1b_13 (.cout(alu1b_13_cout), .s(alu1b_1_s[12]), .a(A[12]), .b(B[12]), .op(op), .cin(alu1b_12_cout));
  ALU1b alu1b_14 (.cout(alu1b_14_cout), .s(alu1b_1_s[13]), .a(A[13]), .b(B[13]), .op(op), .cin(alu1b_13_cout));
  ALU1b alu1b_15 (.cout(alu1b_15_cout), .s(alu1b_1_s[14]), .a(A[14]), .b(B[14]), .op(op), .cin(alu1b_14_cout));
  ALU1b alu1b_16 (.cout(alu1b_16_cout), .s(alu1b_1_s[15]), .a(A[15]), .b(B[15]), .op(op), .cin(alu1b_15_cout));
  ALU1b alu1b_17 (.cout(alu1b_17_cout), .s(alu1b_1_s[16]), .a(A[16]), .b(B[16]), .op(op), .cin(alu1b_16_cout));
  ALU1b alu1b_18 (.cout(alu1b_18_cout), .s(alu1b_1_s[17]), .a(A[17]), .b(B[17]), .op(op), .cin(alu1b_17_cout));
  ALU1b alu1b_19 (.cout(alu1b_19_cout), .s(alu1b_1_s[18]), .a(A[18]), .b(B[18]), .op(op), .cin(alu1b_18_cout));
  ALU1b alu1b_20 (.cout(alu1b_20_cout), .s(alu1b_1_s[19]), .a(A[19]), .b(B[19]), .op(op), .cin(alu1b_19_cout));
  ALU1b alu1b_21 (.cout(alu1b_21_cout), .s(alu1b_1_s[20]), .a(A[20]), .b(B[20]), .op(op), .cin(alu1b_20_cout));
  ALU1b alu1b_22 (.cout(alu1b_22_cout), .s(alu1b_1_s[21]), .a(A[21]), .b(B[21]), .op(op), .cin(alu1b_21_cout));
  ALU1b alu1b_23 (.cout(alu1b_23_cout), .s(alu1b_1_s[22]), .a(A[22]), .b(B[22]), .op(op), .cin(alu1b_22_cout));
  ALU1b alu1b_24 (.cout(alu1b_24_cout), .s(alu1b_1_s[23]), .a(A[23]), .b(B[23]), .op(op), .cin(alu1b_23_cout));
  ALU1b alu1b_25 (.cout(alu1b_25_cout), .s(alu1b_1_s[24]), .a(A[24]), .b(B[24]), .op(op), .cin(alu1b_24_cout));
  ALU1b alu1b_26 (.cout(alu1b_26_cout), .s(alu1b_1_s[25]), .a(A[25]), .b(B[25]), .op(op), .cin(alu1b_25_cout));
  ALU1b alu1b_27 (.cout(alu1b_27_cout), .s(alu1b_1_s[26]), .a(A[26]), .b(B[26]), .op(op), .cin(alu1b_26_cout));
  ALU1b alu1b_28 (.cout(alu1b_28_cout), .s(alu1b_1_s[27]), .a(A[27]), .b(B[27]), .op(op), .cin(alu1b_27_cout));
  ALU1b alu1b_29 (.cout(alu1b_29_cout), .s(alu1b_1_s[28]), .a(A[28]), .b(B[28]), .op(op), .cin(alu1b_28_cout));
  ALU1b alu1b_30 (.cout(alu1b_30_cout), .s(alu1b_1_s[29]), .a(A[29]), .b(B[29]), .op(op), .cin(alu1b_29_cout));
  ALU1b alu1b_31 (.cout(alu1b_31_cout), .s(alu1b_1_s[30]), .a(A[30]), .b(B[30]), .op(op), .cin(alu1b_30_cout));
  ALU1b alu1b_32 (.cout(alu1b_32_cout), .s(alu1b_1_s[31]), .a(A[31]), .b(B[31]), .op(op), .cin(alu1b_31_cout));
  ALU1b alu1b_33 (.cout(alu1b_33_cout), .s(alu1b_1_s[32]), .a(A[32]), .b(B[32]), .op(op), .cin(alu1b_32_cout));
  ALU1b alu1b_34 (.cout(alu1b_34_cout), .s(alu1b_1_s[33]), .a(A[33]), .b(B[33]), .op(op), .cin(alu1b_33_cout));
  ALU1b alu1b_35 (.cout(alu1b_35_cout), .s(alu1b_1_s[34]), .a(A[34]), .b(B[34]), .op(op), .cin(alu1b_34_cout));
  ALU1b alu1b_36 (.cout(alu1b_36_cout), .s(alu1b_1_s[35]), .a(A[35]), .b(B[35]), .op(op), .cin(alu1b_35_cout));
  ALU1b alu1b_37 (.cout(alu1b_37_cout), .s(alu1b_1_s[36]), .a(A[36]), .b(B[36]), .op(op), .cin(alu1b_36_cout));
  ALU1b alu1b_38 (.cout(alu1b_38_cout), .s(alu1b_1_s[37]), .a(A[37]), .b(B[37]), .op(op), .cin(alu1b_37_cout));
  ALU1b alu1b_39 (.cout(alu1b_39_cout), .s(alu1b_1_s[38]), .a(A[38]), .b(B[38]), .op(op), .cin(alu1b_38_cout));
  ALU1b alu1b_40 (.cout(alu1b_40_cout), .s(alu1b_1_s[39]), .a(A[39]), .b(B[39]), .op(op), .cin(alu1b_39_cout));
  ALU1b alu1b_41 (.cout(alu1b_41_cout), .s(alu1b_1_s[40]), .a(A[40]), .b(B[40]), .op(op), .cin(alu1b_40_cout));
  ALU1b alu1b_42 (.cout(alu1b_42_cout), .s(alu1b_1_s[41]), .a(A[41]), .b(B[41]), .op(op), .cin(alu1b_41_cout));
  ALU1b alu1b_43 (.cout(alu1b_43_cout), .s(alu1b_1_s[42]), .a(A[42]), .b(B[42]), .op(op), .cin(alu1b_42_cout));
  ALU1b alu1b_44 (.cout(alu1b_44_cout), .s(alu1b_1_s[43]), .a(A[43]), .b(B[43]), .op(op), .cin(alu1b_43_cout));
  ALU1b alu1b_45 (.cout(alu1b_45_cout), .s(alu1b_1_s[44]), .a(A[44]), .b(B[44]), .op(op), .cin(alu1b_44_cout));
  ALU1b alu1b_46 (.cout(alu1b_46_cout), .s(alu1b_1_s[45]), .a(A[45]), .b(B[45]), .op(op), .cin(alu1b_45_cout));
  ALU1b alu1b_47 (.cout(alu1b_47_cout), .s(alu1b_1_s[46]), .a(A[46]), .b(B[46]), .op(op), .cin(alu1b_46_cout));
  ALU1b alu1b_48 (.cout(alu1b_48_cout), .s(alu1b_1_s[47]), .a(A[47]), .b(B[47]), .op(op), .cin(alu1b_47_cout));
  ALU1b alu1b_49 (.cout(alu1b_49_cout), .s(alu1b_1_s[48]), .a(A[48]), .b(B[48]), .op(op), .cin(alu1b_48_cout));
  ALU1b alu1b_50 (.cout(alu1b_50_cout), .s(alu1b_1_s[49]), .a(A[49]), .b(B[49]), .op(op), .cin(alu1b_49_cout));
  ALU1b alu1b_51 (.cout(alu1b_51_cout), .s(alu1b_1_s[50]), .a(A[50]), .b(B[50]), .op(op), .cin(alu1b_50_cout));
  ALU1b alu1b_52 (.cout(alu1b_52_cout), .s(alu1b_1_s[51]), .a(A[51]), .b(B[51]), .op(op), .cin(alu1b_51_cout));
  ALU1b alu1b_53 (.cout(alu1b_53_cout), .s(alu1b_1_s[52]), .a(A[52]), .b(B[52]), .op(op), .cin(alu1b_52_cout));
  ALU1b alu1b_54 (.cout(alu1b_54_cout), .s(alu1b_1_s[53]), .a(A[53]), .b(B[53]), .op(op), .cin(alu1b_53_cout));
  ALU1b alu1b_55 (.cout(alu1b_55_cout), .s(alu1b_1_s[54]), .a(A[54]), .b(B[54]), .op(op), .cin(alu1b_54_cout));
  ALU1b alu1b_56 (.cout(alu1b_56_cout), .s(alu1b_1_s[55]), .a(A[55]), .b(B[55]), .op(op), .cin(alu1b_55_cout));
  ALU1b alu1b_57 (.cout(alu1b_57_cout), .s(alu1b_1_s[56]), .a(A[56]), .b(B[56]), .op(op), .cin(alu1b_56_cout));
  ALU1b alu1b_58 (.cout(alu1b_58_cout), .s(alu1b_1_s[57]), .a(A[57]), .b(B[57]), .op(op), .cin(alu1b_57_cout));
  ALU1b alu1b_59 (.cout(alu1b_59_cout), .s(alu1b_1_s[58]), .a(A[58]), .b(B[58]), .op(op), .cin(alu1b_58_cout));
  ALU1b alu1b_60 (.cout(alu1b_60_cout), .s(alu1b_1_s[59]), .a(A[59]), .b(B[59]), .op(op), .cin(alu1b_59_cout));
  ALU1b alu1b_61 (.cout(alu1b_61_cout), .s(alu1b_1_s[60]), .a(A[60]), .b(B[60]), .op(op), .cin(alu1b_60_cout));
  ALU1b alu1b_62 (.cout(alu1b_62_cout), .s(alu1b_1_s[61]), .a(A[61]), .b(B[61]), .op(op), .cin(alu1b_61_cout));
  ALU1b alu1b_63 (.cout(alu1b_63_cout), .s(alu1b_1_s[62]), .a(A[62]), .b(B[62]), .op(op), .cin(alu1b_62_cout));
  ALU1b alu1b_64 (.cout(Carry), .s(Negative), .a(A[63]), .b(B[63]), .op(op), .cin(alu1b_63_cout));
  and and_2 (and_2_out, ~op[0], op[1], op[2], op[3]);  // AND_Gate
  and and_3 (and_3_out, op[0], op[1], op[2], op[3]);
  Multiplexer #(.enable("false"), .width(64)) multiplexer_2 (
    .in0(multiplexer_1_out), .in1(xor_1_out), .out(multiplexer_2_out), .sel(and_2_out));
  or or_1 (or_1_out, and_2_out, and_3_out);
  nor nor_1 (nor_1_out, alu1b_1_s[0], alu1b_1_s[1], alu1b_1_s[2], alu1b_1_s[3], alu1b_1_s[4], alu1b_1_s[5], alu1b_1_s[6], alu1b_1_s[7], alu1b_1_s[8], alu1b_1_s[9], alu1b_1_s[10], alu1b_1_s[11], alu1b_1_s[12], alu1b_1_s[13], alu1b_1_s[14], alu1b_1_s[15], alu1b_1_s[16], alu1b_1_s[17], alu1b_1_s[18], alu1b_1_s[19], alu1b_1_s[20], alu1b_1_s[21], alu1b_1_s[22], alu1b_1_s[23], alu1b_1_s[24], alu1b_1_s[25], alu1b_1_s[26], alu1b_1_s[27], alu1b_1_s[28], alu1b_1_s[29], alu1b_1_s[30], alu1b_1_s[31]);
  nor nor_2 (nor_2_out, alu1b_1_s[32], alu1b_1_s[33], alu1b_1_s[34], alu1b_1_s[35], alu1b_1_s[36], alu1b_1_s[37], alu1b_1_s[38], alu1b_1_s[39], alu1b_1_s[40], alu1b_1_s[41], alu1b_1_s[42], alu1b_1_s[43], alu1b_1_s[44], alu1b_1_s[45], alu1b_1_s[46], alu1b_1_s[47], alu1b_1_s[48], alu1b_1_s[49], alu1b_1_s[50], alu1b_1_s[51], alu1b_1_s[52], alu1b_1_s[53], alu1b_1_s[54], alu1b_1_s[55], alu1b_1_s[56], alu1b_1_s[57], alu1b_1_s[58], alu1b_1_s[59], alu1b_1_s[60], alu1b_1_s[61], alu1b_1_s[62], Negative);
  xor xor_2 (Overflow, alu1b_63_cout, Carry);
  and and_4 (Zero, nor_1_out, nor_2_out);
  Multiplexer #(.enable("false"), .width(64)) multiplexer_3 (
    .in0({Negative, alu1b_1_s}), .in1(multiplexer_2_out), .out(Result), .sel(or_1_out));
endmodule

module InsMem (
  input  [63:0] Addr,
  output [31:0] Inst
);

  ROM #(.addrWidth(24), .dataWidth(32)) rom_1 (.addr(Addr[25:2]), .data(Inst));

  // Notes on the sheet:
  //   contents of rom_1 (hex, n*v repeats v):
  //   cb000000 910fc800 d36cac00 b8400001 cb020042 91001c42 d36eb442 cb030063 d1000463 ca030042 8a020021
  //   cb040084 91000484 d36eb484 aa040021 b8000001 cb0500a5 910004a5 d37ae4a5 b801c005 cb0600c6 910004c6
  //   d37ef4c6 d10004c6 b5ffffe6 b8028005 cb0600c6 910004c6 d37ef4c6 d10004c6 b5ffffe6 17fffff4
endmodule

module DataMem (
  input  [63:0] Addr,
  input  MemWrite,
  input  MemRead,
  input  CLK,
  input  [1:0] Size,
  input  [63:0] WrData,
  output [63:0] RdData
);

  wire and_1_out, and_2_out, and_3_out, decoder_1_out1, decoder_1_out2, decoder_1_out3, nor_1_out, nor_2_out,
       or_1_out, or_2_out;

  Decoder #(.enable("false"), .select(2)) decoder_1 (
    .out1(decoder_1_out1), .out2(decoder_1_out2), .out3(decoder_1_out3), .sel(Size));  // open: out0
  nor nor_1 (nor_1_out, Addr[33], Addr[24], Addr[25], Addr[26], Addr[27], Addr[28], Addr[29], Addr[30], Addr[31], Addr[32], Addr[34], Addr[35], Addr[36], Addr[37], Addr[38], Addr[39], Addr[40], Addr[41], Addr[42], Addr[43]);
  and and_1 (and_1_out, nor_1_out, nor_2_out);
  nor nor_2 (nor_2_out, Addr[44], Addr[45], Addr[46], Addr[47], Addr[48], Addr[49], Addr[50], Addr[51], Addr[52], Addr[53], Addr[55], Addr[56], Addr[57], Addr[58], Addr[59], Addr[60], Addr[61], Addr[62], Addr[63], Addr[54]);
  or or_1 (or_1_out, decoder_1_out2, decoder_1_out3);
  and and_2 (and_2_out, and_1_out, MemWrite);
  and and_3 (and_3_out, and_1_out, MemRead);
  or or_2 (or_2_out, decoder_1_out1, or_1_out);
  RAM #(.addrWidth(24), .byteenables("byteEnables"), .dataWidth(64)) ram_1 (
    .addr(Addr[23:0]), .we(and_2_out), .oe(and_3_out), .clk(CLK), .din(WrData), .dout(RdData),
    .be7(decoder_1_out3), .be6(decoder_1_out3), .be5(decoder_1_out3), .be4(decoder_1_out3), .be3(or_1_out),
    .be2(or_1_out), .be1(or_2_out), .be0(1'b1));
endmodule

module ImmExtend (
  input  [31:0] in_1,
  input  [2:0] ExtCtrl,
  output [63:0] out_3
);

  wire [63:0] bit_extender_1_out, bit_extender_2_out, bit_extender_3_out, bit_extender_4_out,
       bit_extender_5_out;

  assign bit_extender_1_out = {{52{1'b0}}, in_1[21:10]};  // Bit_Extender bit_extender_1
  assign bit_extender_2_out = {{55{in_1[20]}}, in_1[20:12]};  // Bit_Extender bit_extender_2
  assign bit_extender_3_out = {{38{in_1[25]}}, in_1[25:0]};  // Bit_Extender bit_extender_3
  assign bit_extender_4_out = {{45{in_1[23]}}, in_1[23:5]};  // Bit_Extender bit_extender_4
  assign bit_extender_5_out = {{48{1'b0}}, in_1[20:5]};  // Bit_Extender bit_extender_5
  Multiplexer #(.enable("false"), .select(3), .width(64)) multiplexer_1 (
    .in0(bit_extender_1_out), .in1(bit_extender_2_out), .in2(bit_extender_3_out), .in3(bit_extender_4_out),
    .in4(bit_extender_5_out), .out(out_3), .sel(ExtCtrl));  // open: in5, in6, in7
endmodule

module CtrlUnit (
  input  [10:0] opcode,
  output B,
  output CBZ,
  output CBNZ,
  output Reg2Loc,
  output RegWrite,
  output MemRead,
  output MemWrite,
  output ALUSrc,
  output MemtoReg,
  output [2:0] ImmSel,
  output [3:0] ALUop,
  output [1:0] AccessSize
);

  wire gADD_out, gADDI_out, gADDop_out, gALUimm_out, gAND_out, gANDI_out, gANDop_out, gCONDBRAddr_out,
       gDTAddr_out, gDWORD_out, gEOR_out, gEORI_out, gEORop_out, gLDUR_out, gLDURW_out, gLS_out, gORop_out,
       gORR_out, gORRI_out, gPASSBop_out, gSTUR_out, gSTURW_out, gSUB_out, gSUBI_out, gSUBop_out, gWORD_out;

  and gB (B, ~opcode[10], ~opcode[9], ~opcode[8], opcode[7], ~opcode[6], opcode[5]);  // AND_Gate
  and gCBZ (CBZ, opcode[10], ~opcode[9], opcode[8], opcode[7], ~opcode[6], opcode[5], ~opcode[4], ~opcode[3]);  // AND_Gate
  and gCBNZ (CBNZ, opcode[10], ~opcode[9], opcode[8], opcode[7], ~opcode[6], opcode[5], ~opcode[4], opcode[3]);  // AND_Gate
  and gSTUR (gSTUR_out, opcode[10], opcode[9], opcode[8], opcode[7], opcode[6], ~opcode[5], ~opcode[4], ~opcode[3], ~opcode[2], ~opcode[1], ~opcode[0]);  // AND_Gate
  and gLDUR (gLDUR_out, opcode[10], opcode[9], opcode[8], opcode[7], opcode[6], ~opcode[5], ~opcode[4], ~opcode[3], ~opcode[2], opcode[1], ~opcode[0]);  // AND_Gate
  and gSTURW (gSTURW_out, opcode[10], ~opcode[9], opcode[8], opcode[7], opcode[6], ~opcode[5], ~opcode[4], ~opcode[3], ~opcode[2], ~opcode[1], ~opcode[0]);  // AND_Gate
  and gLDURW (gLDURW_out, opcode[10], ~opcode[9], opcode[8], opcode[7], opcode[6], ~opcode[5], ~opcode[4], ~opcode[3], ~opcode[2], opcode[1], ~opcode[0]);  // AND_Gate
  and gAND (gAND_out, opcode[10], ~opcode[9], ~opcode[8], ~opcode[7], opcode[6], ~opcode[5], opcode[4], ~opcode[3], ~opcode[2], ~opcode[1], ~opcode[0]);  // AND_Gate
  and gORR (gORR_out, opcode[10], ~opcode[9], opcode[8], ~opcode[7], opcode[6], ~opcode[5], opcode[4], ~opcode[3], ~opcode[2], ~opcode[1], ~opcode[0]);  // AND_Gate
  and gEOR (gEOR_out, opcode[10], opcode[9], ~opcode[8], ~opcode[7], opcode[6], ~opcode[5], opcode[4], ~opcode[3], ~opcode[2], ~opcode[1], ~opcode[0]);  // AND_Gate
  and gADD (gADD_out, opcode[10], ~opcode[9], ~opcode[8], ~opcode[7], opcode[6], ~opcode[5], opcode[4], opcode[3], ~opcode[2], ~opcode[1], ~opcode[0]);  // AND_Gate
  and gSUB (gSUB_out, opcode[10], opcode[9], ~opcode[8], ~opcode[7], opcode[6], ~opcode[5], opcode[4], opcode[3], ~opcode[2], ~opcode[1], ~opcode[0]);  // AND_Gate
  and gANDI (gANDI_out, opcode[10], ~opcode[9], ~opcode[8], opcode[7], ~opcode[6], ~opcode[5], opcode[4], ~opcode[3], ~opcode[2], ~opcode[1]);  // AND_Gate
  and gORRI (gORRI_out, opcode[10], ~opcode[9], opcode[8], opcode[7], ~opcode[6], ~opcode[5], opcode[4], ~opcode[3], ~opcode[2], ~opcode[1]);  // AND_Gate
  and gEORI (gEORI_out, opcode[10], opcode[9], ~opcode[8], opcode[7], ~opcode[6], ~opcode[5], opcode[4], ~opcode[3], ~opcode[2], ~opcode[1]);  // AND_Gate
  and gADDI (gADDI_out, opcode[10], ~opcode[9], ~opcode[8], opcode[7], ~opcode[6], ~opcode[5], ~opcode[4], opcode[3], ~opcode[2], ~opcode[1]);  // AND_Gate
  and gSUBI (gSUBI_out, opcode[10], opcode[9], ~opcode[8], opcode[7], ~opcode[6], ~opcode[5], ~opcode[4], opcode[3], ~opcode[2], ~opcode[1]);  // AND_Gate
  and gLS (gLS_out, opcode[10], opcode[9], ~opcode[8], opcode[7], ~opcode[6], ~opcode[5], opcode[4], opcode[3], ~opcode[2], opcode[1]);  // AND_Gate
  or or_1 (Reg2Loc, CBZ, CBNZ, gSTUR_out, gSTURW_out);
  or or_2 (RegWrite, gLDUR_out, gLDURW_out, gAND_out, gORR_out, gEOR_out, gADD_out, gSUB_out, gANDI_out, gORRI_out, gEORI_out, gADDI_out, gSUBI_out, gLS_out);
  or or_3 (MemRead, gLDUR_out, gLDURW_out);
  or or_4 (MemWrite, gSTUR_out, gSTURW_out);
  or or_5 (ALUSrc, gSTUR_out, gLDUR_out, gSTURW_out, gLDURW_out, gANDI_out, gORRI_out, gEORI_out, gADDI_out, gSUBI_out);
  or or_6 (MemtoReg, gLDUR_out, gLDURW_out);
  or gALUimm (gALUimm_out, gANDI_out, gORRI_out, gEORI_out, gADDI_out, gSUBI_out);
  or gDTAddr (gDTAddr_out, gSTUR_out, gLDUR_out, gSTURW_out, gLDURW_out);
  or gCONDBRAddr (gCONDBRAddr_out, CBZ, CBNZ);
  or gANDop (gANDop_out, gAND_out, gANDI_out);
  or gORop (gORop_out, gORR_out, gORRI_out);
  or gADDop (gADDop_out, gSTUR_out, gLDUR_out, gSTURW_out, gLDURW_out, gADD_out, gADDI_out);
  or gPASSBop (gPASSBop_out, CBZ, CBNZ);
  or gSUBop (gSUBop_out, gSUB_out, gSUBI_out);
  or gEORop (gEORop_out, gEOR_out, gEORI_out);
  or gWORD (gWORD_out, gSTURW_out, gLDURW_out);
  or gDWORD (gDWORD_out, gSTUR_out, gLDUR_out);
  Priority_Encoder priority_encoder_1 (
    .in0(gALUimm_out), .in1(gDTAddr_out), .in2(B), .in3(gCONDBRAddr_out), .out(ImmSel), .en_in(1'b1));  // open: in4, in5, in6, in7, gs, en_out
  Priority_Encoder #(.select(4)) priority_encoder_2 (
    .in0(gANDop_out), .in1(gORop_out), .in2(gADDop_out), .in3(gPASSBop_out), .in6(gSUBop_out),
    .in14(gEORop_out), .in15(gLS_out), .out(ALUop), .en_in(1'b1));  // open: in4, in5, in7, in8, in9, in10, in11, in12, in13, gs, en_out
  Priority_Encoder #(.select(2)) priority_encoder_3 (
    .in2(gWORD_out), .in3(gDWORD_out), .out(AccessSize), .en_in(1'b1));  // open: in0, in1, gs, en_out
endmodule

module ShiftLeft2 (
  input  [63:0] in_1,
  output [63:0] out_2
);


  assign out_2 = {in_1[61:0], 2'b00};
endmodule

module PCReg (
  input  [63:0] in_1,
  input  in_2,
  input  in_3,
  output [63:0] out_4
);

  Register #(.width(64)) PC (.D(in_1), .en(1'b1), .clk(in_2), .Q(out_4), .clr(in_3));
endmodule

module Add64b (
  input  [63:0] in_1,
  input  [63:0] in_2,
  output [63:0] out_3
);

  wire adder_1_cout;

  Adder #(.width(32)) adder_1 (.a(in_1[31:0]), .b(in_2[31:0]), .out(out_3[31:0]), .cin(1'b0), .cout(adder_1_cout));
  Adder #(.width(32)) adder_2 (.a(in_1[63:32]), .b(in_2[63:32]), .out(out_3[63:32]), .cin(adder_1_cout));  // open: cout
endmodule

module Regs (
  input  [4:0] RdAddr0,
  input  [4:0] RdAddr1,
  input  [4:0] WrAddr,
  input  [63:0] WrData,
  input  RegWrite,
  input  CLK,
  output [63:0] RdData0,
  output [63:0] RdData1
);

  wire decoder_1_out0, decoder_1_out1, decoder_1_out2, decoder_1_out3, decoder_1_out4, decoder_1_out5,
       decoder_1_out6, decoder_1_out7, decoder_1_out8, decoder_1_out9, decoder_1_out10, decoder_1_out11,
       decoder_1_out12, decoder_1_out13, decoder_1_out14, decoder_1_out15, decoder_1_out16, decoder_1_out17,
       decoder_1_out18, decoder_1_out19, decoder_1_out20, decoder_1_out21, decoder_1_out22, decoder_1_out23,
       decoder_1_out24, decoder_1_out25, decoder_1_out26, decoder_1_out27, decoder_1_out28, decoder_1_out29,
       decoder_1_out30, decoder_2_out0, decoder_2_out1, decoder_2_out2, decoder_2_out3, decoder_2_out4,
       decoder_2_out5, decoder_2_out6, decoder_2_out7, decoder_2_out8, decoder_2_out9, decoder_2_out10,
       decoder_2_out11, decoder_2_out12, decoder_2_out13, decoder_2_out14, decoder_2_out15, decoder_2_out16,
       decoder_2_out17, decoder_2_out18, decoder_2_out19, decoder_2_out20, decoder_2_out21, decoder_2_out22,
       decoder_2_out23, decoder_2_out24, decoder_2_out25, decoder_2_out26, decoder_2_out27, decoder_2_out28,
       decoder_2_out29, decoder_2_out30, decoder_2_out31, decoder_3_out0, decoder_3_out1, decoder_3_out2,
       decoder_3_out3, decoder_3_out4, decoder_3_out5, decoder_3_out6, decoder_3_out7, decoder_3_out8,
       decoder_3_out9, decoder_3_out10, decoder_3_out11, decoder_3_out12, decoder_3_out13, decoder_3_out14,
       decoder_3_out15, decoder_3_out16, decoder_3_out17, decoder_3_out18, decoder_3_out19, decoder_3_out20,
       decoder_3_out21, decoder_3_out22, decoder_3_out23, decoder_3_out24, decoder_3_out25, decoder_3_out26,
       decoder_3_out27, decoder_3_out28, decoder_3_out29, decoder_3_out30, decoder_3_out31;
  wire [63:0] X00_q, X01_q, X02_q, X03_q, X04_q, X05_q, X06_q, X07_q, X08_q, X09_q, X10_q, X11_q, X12_q,
       X13_q, X14_q, X15_q, X16_q, X17_q, X18_q, X19_q, X20_q, X21_q, X22_q, X23_q, X24_q, X25_q, X26_q,
       X27_q, X28_q, X29_q, X30_q;

  Decoder #(.select(5)) decoder_1 (
    .out0(decoder_1_out0), .out1(decoder_1_out1), .out2(decoder_1_out2), .out3(decoder_1_out3),
    .out4(decoder_1_out4), .out5(decoder_1_out5), .out6(decoder_1_out6), .out7(decoder_1_out7),
    .out8(decoder_1_out8), .out9(decoder_1_out9), .out10(decoder_1_out10), .out11(decoder_1_out11),
    .out12(decoder_1_out12), .out13(decoder_1_out13), .out14(decoder_1_out14), .out15(decoder_1_out15),
    .out16(decoder_1_out16), .out17(decoder_1_out17), .out18(decoder_1_out18), .out19(decoder_1_out19),
    .out20(decoder_1_out20), .out21(decoder_1_out21), .out22(decoder_1_out22), .out23(decoder_1_out23),
    .out24(decoder_1_out24), .out25(decoder_1_out25), .out26(decoder_1_out26), .out27(decoder_1_out27),
    .out28(decoder_1_out28), .out29(decoder_1_out29), .out30(decoder_1_out30), .sel(WrAddr), .en(RegWrite));  // open: out31
  Decoder #(.enable("false"), .select(5)) decoder_2 (
    .out0(decoder_2_out0), .out1(decoder_2_out1), .out2(decoder_2_out2), .out3(decoder_2_out3),
    .out4(decoder_2_out4), .out5(decoder_2_out5), .out6(decoder_2_out6), .out7(decoder_2_out7),
    .out8(decoder_2_out8), .out9(decoder_2_out9), .out10(decoder_2_out10), .out11(decoder_2_out11),
    .out12(decoder_2_out12), .out13(decoder_2_out13), .out14(decoder_2_out14), .out15(decoder_2_out15),
    .out16(decoder_2_out16), .out17(decoder_2_out17), .out18(decoder_2_out18), .out19(decoder_2_out19),
    .out20(decoder_2_out20), .out21(decoder_2_out21), .out22(decoder_2_out22), .out23(decoder_2_out23),
    .out24(decoder_2_out24), .out25(decoder_2_out25), .out26(decoder_2_out26), .out27(decoder_2_out27),
    .out28(decoder_2_out28), .out29(decoder_2_out29), .out30(decoder_2_out30), .out31(decoder_2_out31),
    .sel(RdAddr1));
  Decoder #(.enable("false"), .select(5)) decoder_3 (
    .out0(decoder_3_out0), .out1(decoder_3_out1), .out2(decoder_3_out2), .out3(decoder_3_out3),
    .out4(decoder_3_out4), .out5(decoder_3_out5), .out6(decoder_3_out6), .out7(decoder_3_out7),
    .out8(decoder_3_out8), .out9(decoder_3_out9), .out10(decoder_3_out10), .out11(decoder_3_out11),
    .out12(decoder_3_out12), .out13(decoder_3_out13), .out14(decoder_3_out14), .out15(decoder_3_out15),
    .out16(decoder_3_out16), .out17(decoder_3_out17), .out18(decoder_3_out18), .out19(decoder_3_out19),
    .out20(decoder_3_out20), .out21(decoder_3_out21), .out22(decoder_3_out22), .out23(decoder_3_out23),
    .out24(decoder_3_out24), .out25(decoder_3_out25), .out26(decoder_3_out26), .out27(decoder_3_out27),
    .out28(decoder_3_out28), .out29(decoder_3_out29), .out30(decoder_3_out30), .out31(decoder_3_out31),
    .sel(RdAddr0));
  Register #(.width(64)) X00 (.D(WrData), .en(decoder_1_out0), .clk(CLK), .Q(X00_q));  // open: clr
  Register #(.width(64)) X01 (.D(WrData), .en(decoder_1_out1), .clk(CLK), .Q(X01_q));  // open: clr
  Register #(.width(64)) X02 (.D(WrData), .en(decoder_1_out2), .clk(CLK), .Q(X02_q));  // open: clr
  Register #(.width(64)) X03 (.D(WrData), .en(decoder_1_out3), .clk(CLK), .Q(X03_q));  // open: clr
  Register #(.width(64)) X04 (.D(WrData), .en(decoder_1_out4), .clk(CLK), .Q(X04_q));  // open: clr
  Register #(.width(64)) X05 (.D(WrData), .en(decoder_1_out5), .clk(CLK), .Q(X05_q));  // open: clr
  Register #(.width(64)) X06 (.D(WrData), .en(decoder_1_out6), .clk(CLK), .Q(X06_q));  // open: clr
  Register #(.width(64)) X07 (.D(WrData), .en(decoder_1_out7), .clk(CLK), .Q(X07_q));  // open: clr
  Register #(.width(64)) X08 (.D(WrData), .en(decoder_1_out8), .clk(CLK), .Q(X08_q));  // open: clr
  Register #(.width(64)) X09 (.D(WrData), .en(decoder_1_out9), .clk(CLK), .Q(X09_q));  // open: clr
  Register #(.width(64)) X10 (.D(WrData), .en(decoder_1_out10), .clk(CLK), .Q(X10_q));  // open: clr
  Register #(.width(64)) X11 (.D(WrData), .en(decoder_1_out11), .clk(CLK), .Q(X11_q));  // open: clr
  Register #(.width(64)) X12 (.D(WrData), .en(decoder_1_out12), .clk(CLK), .Q(X12_q));  // open: clr
  Register #(.width(64)) X13 (.D(WrData), .en(decoder_1_out13), .clk(CLK), .Q(X13_q));  // open: clr
  Register #(.width(64)) X14 (.D(WrData), .en(decoder_1_out14), .clk(CLK), .Q(X14_q));  // open: clr
  Register #(.width(64)) X15 (.D(WrData), .en(decoder_1_out15), .clk(CLK), .Q(X15_q));  // open: clr
  Register #(.width(64)) X16 (.D(WrData), .en(decoder_1_out16), .clk(CLK), .Q(X16_q));  // open: clr
  Register #(.width(64)) X17 (.D(WrData), .en(decoder_1_out17), .clk(CLK), .Q(X17_q));  // open: clr
  Register #(.width(64)) X18 (.D(WrData), .en(decoder_1_out18), .clk(CLK), .Q(X18_q));  // open: clr
  Register #(.width(64)) X19 (.D(WrData), .en(decoder_1_out19), .clk(CLK), .Q(X19_q));  // open: clr
  Register #(.width(64)) X20 (.D(WrData), .en(decoder_1_out20), .clk(CLK), .Q(X20_q));  // open: clr
  Register #(.width(64)) X21 (.D(WrData), .en(decoder_1_out21), .clk(CLK), .Q(X21_q));  // open: clr
  Register #(.width(64)) X22 (.D(WrData), .en(decoder_1_out22), .clk(CLK), .Q(X22_q));  // open: clr
  Register #(.width(64)) X23 (.D(WrData), .en(decoder_1_out23), .clk(CLK), .Q(X23_q));  // open: clr
  Register #(.width(64)) X24 (.D(WrData), .en(decoder_1_out24), .clk(CLK), .Q(X24_q));  // open: clr
  Register #(.width(64)) X25 (.D(WrData), .en(decoder_1_out25), .clk(CLK), .Q(X25_q));  // open: clr
  Register #(.width(64)) X26 (.D(WrData), .en(decoder_1_out26), .clk(CLK), .Q(X26_q));  // open: clr
  Register #(.width(64)) X27 (.D(WrData), .en(decoder_1_out27), .clk(CLK), .Q(X27_q));  // open: clr
  Register #(.width(64)) X28 (.D(WrData), .en(decoder_1_out28), .clk(CLK), .Q(X28_q));  // open: clr
  Register #(.width(64)) X29 (.D(WrData), .en(decoder_1_out29), .clk(CLK), .Q(X29_q));  // open: clr
  Register #(.width(64)) X30 (.D(WrData), .en(decoder_1_out30), .clk(CLK), .Q(X30_q));  // open: clr
  assign RdData0 = decoder_3_out0 ? X00_q : 64'bz;  // Controlled_Buffer controlled_buffer_1
  assign RdData0 = decoder_3_out1 ? X01_q : 64'bz;  // Controlled_Buffer controlled_buffer_2
  assign RdData0 = decoder_3_out2 ? X02_q : 64'bz;  // Controlled_Buffer controlled_buffer_3
  assign RdData0 = decoder_3_out3 ? X03_q : 64'bz;  // Controlled_Buffer controlled_buffer_4
  assign RdData0 = decoder_3_out4 ? X04_q : 64'bz;  // Controlled_Buffer controlled_buffer_5
  assign RdData0 = decoder_3_out5 ? X05_q : 64'bz;  // Controlled_Buffer controlled_buffer_6
  assign RdData0 = decoder_3_out6 ? X06_q : 64'bz;  // Controlled_Buffer controlled_buffer_7
  assign RdData0 = decoder_3_out7 ? X07_q : 64'bz;  // Controlled_Buffer controlled_buffer_8
  assign RdData0 = decoder_3_out8 ? X08_q : 64'bz;  // Controlled_Buffer controlled_buffer_9
  assign RdData0 = decoder_3_out9 ? X09_q : 64'bz;  // Controlled_Buffer controlled_buffer_10
  assign RdData0 = decoder_3_out10 ? X10_q : 64'bz;  // Controlled_Buffer controlled_buffer_11
  assign RdData0 = decoder_3_out11 ? X11_q : 64'bz;  // Controlled_Buffer controlled_buffer_12
  assign RdData0 = decoder_3_out12 ? X12_q : 64'bz;  // Controlled_Buffer controlled_buffer_13
  assign RdData0 = decoder_3_out13 ? X13_q : 64'bz;  // Controlled_Buffer controlled_buffer_14
  assign RdData0 = decoder_3_out14 ? X14_q : 64'bz;  // Controlled_Buffer controlled_buffer_15
  assign RdData0 = decoder_3_out15 ? X15_q : 64'bz;  // Controlled_Buffer controlled_buffer_16
  assign RdData0 = decoder_3_out16 ? X16_q : 64'bz;  // Controlled_Buffer controlled_buffer_17
  assign RdData0 = decoder_3_out17 ? X17_q : 64'bz;  // Controlled_Buffer controlled_buffer_18
  assign RdData0 = decoder_3_out18 ? X18_q : 64'bz;  // Controlled_Buffer controlled_buffer_19
  assign RdData0 = decoder_3_out19 ? X19_q : 64'bz;  // Controlled_Buffer controlled_buffer_20
  assign RdData0 = decoder_3_out20 ? X20_q : 64'bz;  // Controlled_Buffer controlled_buffer_21
  assign RdData0 = decoder_3_out21 ? X21_q : 64'bz;  // Controlled_Buffer controlled_buffer_22
  assign RdData0 = decoder_3_out22 ? X22_q : 64'bz;  // Controlled_Buffer controlled_buffer_23
  assign RdData0 = decoder_3_out23 ? X23_q : 64'bz;  // Controlled_Buffer controlled_buffer_24
  assign RdData0 = decoder_3_out24 ? X24_q : 64'bz;  // Controlled_Buffer controlled_buffer_25
  assign RdData0 = decoder_3_out25 ? X25_q : 64'bz;  // Controlled_Buffer controlled_buffer_26
  assign RdData0 = decoder_3_out26 ? X26_q : 64'bz;  // Controlled_Buffer controlled_buffer_27
  assign RdData0 = decoder_3_out27 ? X27_q : 64'bz;  // Controlled_Buffer controlled_buffer_28
  assign RdData0 = decoder_3_out28 ? X28_q : 64'bz;  // Controlled_Buffer controlled_buffer_29
  assign RdData0 = decoder_3_out29 ? X29_q : 64'bz;  // Controlled_Buffer controlled_buffer_30
  assign RdData0 = decoder_3_out30 ? X30_q : 64'bz;  // Controlled_Buffer controlled_buffer_31
  assign RdData0 = decoder_3_out31 ? {64{1'b0}} : 64'bz;  // Controlled_Buffer controlled_buffer_32
  assign RdData1 = decoder_2_out0 ? X00_q : 64'bz;  // Controlled_Buffer controlled_buffer_33
  assign RdData1 = decoder_2_out1 ? X01_q : 64'bz;  // Controlled_Buffer controlled_buffer_34
  assign RdData1 = decoder_2_out2 ? X02_q : 64'bz;  // Controlled_Buffer controlled_buffer_35
  assign RdData1 = decoder_2_out3 ? X03_q : 64'bz;  // Controlled_Buffer controlled_buffer_36
  assign RdData1 = decoder_2_out4 ? X04_q : 64'bz;  // Controlled_Buffer controlled_buffer_37
  assign RdData1 = decoder_2_out5 ? X05_q : 64'bz;  // Controlled_Buffer controlled_buffer_38
  assign RdData1 = decoder_2_out6 ? X06_q : 64'bz;  // Controlled_Buffer controlled_buffer_39
  assign RdData1 = decoder_2_out7 ? X07_q : 64'bz;  // Controlled_Buffer controlled_buffer_40
  assign RdData1 = decoder_2_out8 ? X08_q : 64'bz;  // Controlled_Buffer controlled_buffer_41
  assign RdData1 = decoder_2_out9 ? X09_q : 64'bz;  // Controlled_Buffer controlled_buffer_42
  assign RdData1 = decoder_2_out10 ? X10_q : 64'bz;  // Controlled_Buffer controlled_buffer_43
  assign RdData1 = decoder_2_out11 ? X11_q : 64'bz;  // Controlled_Buffer controlled_buffer_44
  assign RdData1 = decoder_2_out12 ? X12_q : 64'bz;  // Controlled_Buffer controlled_buffer_45
  assign RdData1 = decoder_2_out13 ? X13_q : 64'bz;  // Controlled_Buffer controlled_buffer_46
  assign RdData1 = decoder_2_out14 ? X14_q : 64'bz;  // Controlled_Buffer controlled_buffer_47
  assign RdData1 = decoder_2_out15 ? X15_q : 64'bz;  // Controlled_Buffer controlled_buffer_48
  assign RdData1 = decoder_2_out16 ? X16_q : 64'bz;  // Controlled_Buffer controlled_buffer_49
  assign RdData1 = decoder_2_out17 ? X17_q : 64'bz;  // Controlled_Buffer controlled_buffer_50
  assign RdData1 = decoder_2_out18 ? X18_q : 64'bz;  // Controlled_Buffer controlled_buffer_51
  assign RdData1 = decoder_2_out19 ? X19_q : 64'bz;  // Controlled_Buffer controlled_buffer_52
  assign RdData1 = decoder_2_out20 ? X20_q : 64'bz;  // Controlled_Buffer controlled_buffer_53
  assign RdData1 = decoder_2_out21 ? X21_q : 64'bz;  // Controlled_Buffer controlled_buffer_54
  assign RdData1 = decoder_2_out22 ? X22_q : 64'bz;  // Controlled_Buffer controlled_buffer_55
  assign RdData1 = decoder_2_out23 ? X23_q : 64'bz;  // Controlled_Buffer controlled_buffer_56
  assign RdData1 = decoder_2_out24 ? X24_q : 64'bz;  // Controlled_Buffer controlled_buffer_57
  assign RdData1 = decoder_2_out25 ? X25_q : 64'bz;  // Controlled_Buffer controlled_buffer_58
  assign RdData1 = decoder_2_out26 ? X26_q : 64'bz;  // Controlled_Buffer controlled_buffer_59
  assign RdData1 = decoder_2_out27 ? X27_q : 64'bz;  // Controlled_Buffer controlled_buffer_60
  assign RdData1 = decoder_2_out28 ? X28_q : 64'bz;  // Controlled_Buffer controlled_buffer_61
  assign RdData1 = decoder_2_out29 ? X29_q : 64'bz;  // Controlled_Buffer controlled_buffer_62
  assign RdData1 = decoder_2_out30 ? X30_q : 64'bz;  // Controlled_Buffer controlled_buffer_63
  assign RdData1 = decoder_2_out31 ? {64{1'b0}} : 64'bz;  // Controlled_Buffer controlled_buffer_64
endmodule

module IF_ID (
  input  [63:0] in_1,
  input  [10:0] in_2,
  input  [4:0] in_3,
  input  [4:0] in_4,
  input  [4:0] in_5,
  input  [31:0] in_6,
  input  [11:0] in_7,
  input  in_8,
  input  in_9,
  output [63:0] out_10,
  output [10:0] out_11,
  output [4:0] out_12,
  output [4:0] out_13,
  output [4:0] out_14,
  output [31:0] out_15,
  output [11:0] out_16
);

  Register #(.width(64)) IF_ID_PC (.D(in_1), .en(1'b1), .clk(in_8), .Q(out_10), .clr(in_9));
  Register #(.width(11)) IF_ID_opcode (.D(in_2), .en(1'b1), .clk(in_8), .Q(out_11), .clr(in_9));
  Register #(.width(5)) IF_ID_Rn (.D(in_3), .en(1'b1), .clk(in_8), .Q(out_12), .clr(in_9));
  Register #(.width(5)) IF_ID_Rm (.D(in_4), .en(1'b1), .clk(in_8), .Q(out_13), .clr(in_9));
  Register #(.width(5)) IF_ID_Rd (.D(in_5), .en(1'b1), .clk(in_8), .Q(out_14), .clr(in_9));
  Register #(.width(32)) IF_ID_imm (.D(in_6), .en(1'b1), .clk(in_8), .Q(out_15), .clr(in_9));
  Register #(.width(12)) IF_ID_shamt (.D(in_7), .en(1'b1), .clk(in_8), .Q(out_16), .clr(in_9));
endmodule

module Cmp0 (
  input  [63:0] in_1,
  output out_2
);

  wire nor_1_out, nor_2_out;

  nor nor_1 (nor_1_out, in_1[0], in_1[1], in_1[2], in_1[3], in_1[4], in_1[5], in_1[6], in_1[7], in_1[8], in_1[9], in_1[10], in_1[11], in_1[12], in_1[13], in_1[14], in_1[15], in_1[16], in_1[17], in_1[18], in_1[19], in_1[20], in_1[21], in_1[22], in_1[23], in_1[24], in_1[25], in_1[26], in_1[27], in_1[28], in_1[29], in_1[30], in_1[31]);
  nor nor_2 (nor_2_out, in_1[32], in_1[33], in_1[34], in_1[35], in_1[36], in_1[37], in_1[38], in_1[39], in_1[40], in_1[41], in_1[42], in_1[43], in_1[44], in_1[45], in_1[46], in_1[47], in_1[48], in_1[49], in_1[50], in_1[51], in_1[52], in_1[53], in_1[54], in_1[55], in_1[56], in_1[57], in_1[58], in_1[59], in_1[60], in_1[61], in_1[62], in_1[63]);
  and and_1 (out_2, nor_1_out, nor_2_out);
endmodule

module ID_EX (
  input  in_1,
  input  in_2,
  input  [1:0] in_3,
  input  in_4,
  input  in_5,
  input  in_6,
  input  [3:0] in_7,
  input  [63:0] in_8,
  input  [63:0] in_9,
  input  [63:0] in_10,
  input  [4:0] in_11,
  input  [4:0] in_12,
  input  [4:0] in_13,
  input  [11:0] in_14,
  input  in_15,
  input  in_16,
  output out_17,
  output out_18,
  output [1:0] out_19,
  output out_20,
  output out_21,
  output out_22,
  output [3:0] out_23,
  output [63:0] out_24,
  output [63:0] out_25,
  output [63:0] out_26,
  output [4:0] out_27,
  output [4:0] out_28,
  output [4:0] out_29,
  output [11:0] out_30
);

  Register #(.width(1)) ID_EX_MemtoReg (.D(in_1), .en(1'b1), .clk(in_15), .Q(out_17), .clr(in_16));
  Register #(.width(1)) ID_EX_RegWrite (.D(in_2), .en(1'b1), .clk(in_15), .Q(out_18), .clr(in_16));
  Register #(.width(2)) ID_EX_AccessSize (.D(in_3), .en(1'b1), .clk(in_15), .Q(out_19), .clr(in_16));
  Register #(.width(1)) ID_EX_MemRead (.D(in_4), .en(1'b1), .clk(in_15), .Q(out_20), .clr(in_16));
  Register #(.width(1)) ID_EX_MemWrite (.D(in_5), .en(1'b1), .clk(in_15), .Q(out_21), .clr(in_16));
  Register #(.width(1)) ID_EX_ALUSrc (.D(in_6), .en(1'b1), .clk(in_15), .Q(out_22), .clr(in_16));
  Register #(.width(4)) ID_EX_ALUop (.D(in_7), .en(1'b1), .clk(in_15), .Q(out_23), .clr(in_16));
  Register #(.width(64)) ID_EX_Reg0 (.D(in_8), .en(1'b1), .clk(in_15), .Q(out_24), .clr(in_16));
  Register #(.width(64)) ID_EX_Reg1 (.D(in_9), .en(1'b1), .clk(in_15), .Q(out_25), .clr(in_16));
  Register #(.width(64)) ID_EX_imm (.D(in_10), .en(1'b1), .clk(in_15), .Q(out_26), .clr(in_16));
  Register #(.width(5)) ID_EX_Rn (.D(in_11), .en(1'b1), .clk(in_15), .Q(out_27), .clr(in_16));
  Register #(.width(5)) ID_EX_Rm (.D(in_12), .en(1'b1), .clk(in_15), .Q(out_28), .clr(in_16));
  Register #(.width(5)) ID_EX_Rd (.D(in_13), .en(1'b1), .clk(in_15), .Q(out_29), .clr(in_16));
  Register #(.width(12)) ID_EX_shamt (.D(in_14), .en(1'b1), .clk(in_15), .Q(out_30), .clr(in_16));
endmodule

module EX_MEM (
  input  in_1,
  input  in_2,
  input  [1:0] in_3,
  input  in_4,
  input  in_5,
  input  [63:0] in_6,
  input  [63:0] in_7,
  input  [4:0] in_8,
  input  in_9,
  input  in_10,
  output out_11,
  output out_12,
  output [1:0] out_13,
  output out_14,
  output out_15,
  output [63:0] out_16,
  output [63:0] out_17,
  output [4:0] out_18
);

  Register #(.width(1)) EX_MEM_MemtoReg (.D(in_1), .en(1'b1), .clk(in_9), .Q(out_11), .clr(in_10));
  Register #(.width(1)) EX_MEM_RegWrite (.D(in_2), .en(1'b1), .clk(in_9), .Q(out_12), .clr(in_10));
  Register #(.width(2)) EX_MEM_AccessSize (.D(in_3), .en(1'b1), .clk(in_9), .Q(out_13), .clr(in_10));
  Register #(.width(1)) EX_MEM_MemRead (.D(in_4), .en(1'b1), .clk(in_9), .Q(out_14), .clr(in_10));
  Register #(.width(1)) EX_MEM_MemWrite (.D(in_5), .en(1'b1), .clk(in_9), .Q(out_15), .clr(in_10));
  Register #(.width(64)) EX_MEM_ALUResult (.D(in_6), .en(1'b1), .clk(in_9), .Q(out_16), .clr(in_10));
  Register #(.width(64)) EX_MEM_Reg1 (.D(in_7), .en(1'b1), .clk(in_9), .Q(out_17), .clr(in_10));
  Register #(.width(5)) EX_MEM_Rd (.D(in_8), .en(1'b1), .clk(in_9), .Q(out_18), .clr(in_10));
endmodule

module MEM_WB (
  input  in_1,
  input  in_2,
  input  [63:0] in_3,
  input  [63:0] in_4,
  input  [4:0] in_5,
  input  in_6,
  input  in_7,
  output out_8,
  output out_9,
  output [63:0] out_10,
  output [63:0] out_11,
  output [4:0] out_12
);

  Register #(.width(1)) MEM_WB_MemtoReg (.D(in_1), .en(1'b1), .clk(in_6), .Q(out_8), .clr(in_7));
  Register #(.width(1)) MEM_WB_RegWrite (.D(in_2), .en(1'b1), .clk(in_6), .Q(out_9), .clr(in_7));
  Register #(.width(64)) MEM_WB_ALUResult (.D(in_3), .en(1'b1), .clk(in_6), .Q(out_10), .clr(in_7));
  Register #(.width(64)) MEM_WB_MemData (.D(in_4), .en(1'b1), .clk(in_6), .Q(out_11), .clr(in_7));
  Register #(.width(5)) MEM_WB_Rd (.D(in_5), .en(1'b1), .clk(in_6), .Q(out_12), .clr(in_7));
endmodule

module FwdUnit (
  input  [4:0] Rn,
  input  [4:0] EX_MEM_Rd,
  input  EX_MEM_RegWrite,
  input  [4:0] MEM_WB_Rd,
  input  MEM_WB_RegWrite,
  input  [4:0] Rm,
  output [1:0] FwdRn,
  output [1:0] FwdRm
);

  wire and_1_out, and_2_out, and_3_out, and_4_out, and_5_out, and_6_out, and_7_out, and_8_out, and_9_out,
       and_10_out, and_11_out, and_12_out, and_13_out, and_14_out, and_15_out, and_16_out;
  wire [4:0] xnor_1_out, xnor_2_out, xnor_3_out, xnor_4_out;

  assign xnor_1_out = ~(Rn ^ EX_MEM_Rd);  // XNOR_Gate xnor_1, 5 bits wide
  assign xnor_2_out = ~(Rn ^ MEM_WB_Rd);  // XNOR_Gate xnor_2, 5 bits wide
  assign xnor_3_out = ~(EX_MEM_Rd ^ Rm);  // XNOR_Gate xnor_3, 5 bits wide
  assign xnor_4_out = ~(MEM_WB_Rd ^ Rm);  // XNOR_Gate xnor_4, 5 bits wide
  and and_1 (and_1_out, xnor_1_out[0], xnor_1_out[1], xnor_1_out[2], xnor_1_out[3], xnor_1_out[4]);
  and and_2 (and_2_out, xnor_2_out[0], xnor_2_out[1], xnor_2_out[2], xnor_2_out[3], xnor_2_out[4]);
  and and_3 (and_3_out, EX_MEM_Rd[0], EX_MEM_Rd[1], EX_MEM_Rd[2], EX_MEM_Rd[3], EX_MEM_Rd[4]);
  and and_4 (and_4_out, ~and_3_out, EX_MEM_RegWrite);  // AND_Gate
  and and_5 (and_5_out, MEM_WB_Rd[0], MEM_WB_Rd[1], MEM_WB_Rd[2], MEM_WB_Rd[3], MEM_WB_Rd[4]);
  and and_6 (and_6_out, ~and_5_out, MEM_WB_RegWrite);  // AND_Gate
  and and_7 (and_7_out, xnor_3_out[0], xnor_3_out[1], xnor_3_out[2], xnor_3_out[3], xnor_3_out[4]);
  and and_8 (and_8_out, xnor_4_out[0], xnor_4_out[1], xnor_4_out[2], xnor_4_out[3], xnor_4_out[4]);
  and and_9 (and_9_out, and_1_out, and_4_out);
  and and_10 (and_10_out, and_2_out, and_6_out);
  and and_11 (and_11_out, and_4_out, and_7_out);
  and and_12 (and_12_out, and_6_out, and_8_out);
  and and_13 (and_13_out, ~and_9_out, ~and_10_out);  // AND_Gate
  and and_14 (and_14_out, ~and_9_out, and_10_out);  // AND_Gate
  and and_15 (and_15_out, ~and_11_out, ~and_12_out);  // AND_Gate
  and and_16 (and_16_out, ~and_11_out, and_12_out);  // AND_Gate
  Priority_Encoder #(.select(2)) priority_encoder_1 (
    .in0(and_13_out), .in1(and_9_out), .in2(and_14_out), .out(FwdRn), .en_in(1'b1));  // open: in3, gs, en_out
  Priority_Encoder #(.select(2)) priority_encoder_2 (
    .in0(and_15_out), .in1(and_11_out), .in2(and_16_out), .out(FwdRm), .en_in(1'b1));  // open: in3, gs, en_out
endmodule
