// Logisim project pipelined_multiplier.circ as structural Verilog: 1 circuit, main circuit main
module main (
  input  A0,
  input  A1,
  input  A2,
  input  B0,
  input  B1,
  input  B2,
  output C0,
  output C1,
  output C2,
  output C3,
  output C4,
  output C5
);

  wire CLK_out, d0_q, d1_q, d2_q, d3_q, d4_q, d5_q, d6_q, d7_q, d8_q, d13_q, d14_q, d15_q, g0_out, g1_out,
       g2_out, g3_out, g4_out, g5_out, g6_out, g7_out, g8_out, g9_out, g10_out, g11_out, g12_out, g13_out,
       g14_out, g15_out, g16_out, g17_out, g18_out, g19_out, g20_out, g21_out, g22_out, g23_out, g24_out,
       g25_out, g26_out, g28_out;

  Clock CLK (.out(CLK_out));
  and g0 (g0_out, A0, B0);
  and g1 (g1_out, A0, B1);
  and g2 (g2_out, A0, B2);
  and g3 (g3_out, A1, B0);
  and g4 (g4_out, A1, B1);
  and g5 (g5_out, A1, B2);
  and g6 (g6_out, A2, B0);
  and g7 (g7_out, A2, B1);
  and g8 (g8_out, A2, B2);
  xor g9 (g9_out, g1_out, g3_out);
  and g10 (g10_out, g1_out, g3_out);
  xor g11 (g11_out, g2_out, g4_out);
  and g12 (g12_out, g2_out, g4_out);
  xor g13 (g13_out, g5_out, g7_out);
  and g14 (g14_out, g5_out, g7_out);
  D_Flip_Flop d0 (.D(g0_out), .clk(CLK_out), .Q(d0_q));  // open: Qn, preset, reset
  D_Flip_Flop d1 (.D(g9_out), .clk(CLK_out), .Q(d1_q));  // open: Qn, preset, reset
  D_Flip_Flop d2 (.D(g15_out), .clk(CLK_out), .Q(d2_q));  // open: Qn, preset, reset
  xor g15 (g15_out, g11_out, g10_out);
  D_Flip_Flop d3 (.D(g16_out), .clk(CLK_out), .Q(d3_q));  // open: Qn, preset, reset
  and g16 (g16_out, g10_out, g11_out);
  D_Flip_Flop d4 (.D(g12_out), .clk(CLK_out), .Q(d4_q));  // open: Qn, preset, reset
  D_Flip_Flop d5 (.D(g13_out), .clk(CLK_out), .Q(d5_q));  // open: Qn, preset, reset
  D_Flip_Flop d6 (.D(g6_out), .clk(CLK_out), .Q(d6_q));  // open: Qn, preset, reset
  D_Flip_Flop d7 (.D(g14_out), .clk(CLK_out), .Q(d7_q));  // open: Qn, preset, reset
  D_Flip_Flop d8 (.D(g8_out), .clk(CLK_out), .Q(d8_q));  // open: Qn, preset, reset
  xor g17 (g17_out, d2_q, d6_q);
  and g18 (g18_out, d2_q, d6_q);
  or g19 (g19_out, d3_q, d4_q);
  xor g20 (g20_out, g19_out, d5_q);
  and g21 (g21_out, g19_out, d5_q);
  D_Flip_Flop d9 (.D(d0_q), .clk(CLK_out), .Q(C0));  // open: Qn, preset, reset
  D_Flip_Flop d10 (.D(d1_q), .clk(CLK_out), .Q(C1));  // open: Qn, preset, reset
  D_Flip_Flop d11 (.D(g17_out), .clk(CLK_out), .Q(C2));  // open: Qn, preset, reset
  D_Flip_Flop d12 (.D(g22_out), .clk(CLK_out), .Q(C3));  // open: Qn, preset, reset
  xor g22 (g22_out, g18_out, g20_out);
  and g23 (g23_out, g18_out, g20_out);
  D_Flip_Flop d13 (.D(g23_out), .clk(CLK_out), .Q(d13_q));  // open: Qn, preset, reset
  D_Flip_Flop d14 (.D(g24_out), .clk(CLK_out), .Q(d14_q));  // open: Qn, preset, reset
  or g24 (g24_out, g21_out, d7_q);
  D_Flip_Flop d15 (.D(d8_q), .clk(CLK_out), .Q(d15_q));  // open: Qn, preset, reset
  xor g25 (g25_out, d14_q, d15_q);
  and g26 (g26_out, d14_q, d15_q);
  xor g27 (C4, d13_q, g25_out);
  and g28 (g28_out, d13_q, g25_out);
  or g29 (C5, g28_out, g26_out);
endmodule
