// Logisim project propagation.circ as structural Verilog: 1 circuit, main circuit main
module main (
  input  En
);

  wire and_1_out, and_2_out, and_3_out, and_4_out, CLK_out, d_ff_1_q, d_ff_2_q, d_ff_3_q, d_ff_4_q, d_ff_5_q,
       xor_1_out, xor_2_out, xor_3_out, xor_4_out, xor_5_out;

  D_Flip_Flop d_ff_1 (.D(xor_1_out), .clk(CLK_out), .Q(d_ff_1_q));  // open: Qn, preset, reset
  Clock CLK (.out(CLK_out));
  D_Flip_Flop d_ff_2 (.D(xor_2_out), .clk(CLK_out), .Q(d_ff_2_q));  // open: Qn, preset, reset
  D_Flip_Flop d_ff_3 (.D(xor_3_out), .clk(CLK_out), .Q(d_ff_3_q));  // open: Qn, preset, reset
  D_Flip_Flop d_ff_4 (.D(xor_4_out), .clk(CLK_out), .Q(d_ff_4_q));  // open: Qn, preset, reset
  D_Flip_Flop d_ff_5 (.D(xor_5_out), .clk(CLK_out), .Q(d_ff_5_q));  // open: Qn, preset, reset
  xor xor_1 (xor_1_out, d_ff_1_q, En);
  and and_1 (and_1_out, d_ff_1_q, En);
  xor xor_2 (xor_2_out, d_ff_2_q, and_1_out);
  and and_2 (and_2_out, d_ff_2_q, and_1_out);
  xor xor_3 (xor_3_out, d_ff_3_q, and_2_out);
  and and_3 (and_3_out, d_ff_3_q, and_2_out);
  xor xor_4 (xor_4_out, d_ff_4_q, and_3_out);
  and and_4 (and_4_out, d_ff_4_q, and_3_out);
  xor xor_5 (xor_5_out, d_ff_5_q, and_4_out);
endmodule
