// Logisim project sequential.circ as structural Verilog: 1 circuit, main circuit main
module main (
  input  in_1,
  input  in_2,
  output out_3
);

  wire d_ff_1_q, d_ff_2_q, not_1_out, not_2_out, not_3_out, xor_1_out, xor_2_out;

  not not_1 (not_1_out, in_2);
  D_Flip_Flop #(.trigger("high")) d_ff_1 (.D(in_1), .clk(not_1_out), .Q(d_ff_1_q));  // open: Qn, preset, reset
  xor xor_1 (xor_1_out, in_2, in_1);
  D_Flip_Flop #(.trigger("high")) d_ff_2 (.D(d_ff_1_q), .clk(not_2_out), .Q(d_ff_2_q));  // open: Qn, preset, reset
  not not_2 (not_2_out, xor_1_out);
  xor xor_2 (xor_2_out, xor_1_out, d_ff_1_q);
  D_Flip_Flop #(.trigger("high")) d_ff_3 (.D(d_ff_2_q), .clk(not_3_out), .Q(out_3));  // open: Qn, preset, reset
  not not_3 (not_3_out, xor_2_out);
endmodule
