// Logisim project store_data_memory.circ as structural Verilog: 1 circuit, main circuit main
module main (
  output [1:0] SEL_OP,
  output USE_R_SRC2,
  output [3:0] D_IN,
  output [1:0] SEL_R_SRC1,
  output [1:0] SEL_R_SRC2,
  output [1:0] SEL_R_DST,
  output BRANCH,
  output BRANCH_IF_ZERO,
  output LOAD_FROM_MEMORY,
  output STORE_TO_MEMORY
);

  wire and_1_out, and_3_out, CLK_out, comparator_1_eq, decoder_1_out0, decoder_1_out1, decoder_1_out2,
       decoder_1_out3, or_1_out, Reset_out;
  wire [3:0] adder_1_out, adder_2_out, adder_3_out, and_2_out, multiplexer_1_out, multiplexer_2_out,
       multiplexer_3_out, multiplexer_4_out, multiplexer_5_out, multiplexer_6_out, or_2_out, PC_q,
       ram_1_dout, REG0_q, REG1_q, REG2_q, REG3_q, xor_1_out;

  Register #(.width(4)) PC (.D(multiplexer_4_out), .en(1'b1), .clk(CLK_out), .Q(PC_q), .clr(Reset_out));
  Clock CLK (.out(CLK_out));
  Button Reset (.out(Reset_out));
  ROM #(.addrWidth(4), .dataWidth(17)) INSTRUCTION_MEMORY (
    .addr(PC_q),
    .data({STORE_TO_MEMORY, LOAD_FROM_MEMORY, BRANCH_IF_ZERO, BRANCH, SEL_R_DST, SEL_R_SRC2, SEL_R_SRC1, D_IN, USE_R_SRC2, SEL_OP}));
  Adder #(.width(4)) adder_1 (.a(4'b0001), .b(PC_q), .out(adder_1_out), .cin(1'b0));  // open: cout
  and and_1 (and_1_out, ~STORE_TO_MEMORY, ~BRANCH_IF_ZERO, ~BRANCH);  // AND_Gate
  Decoder #(.select(2)) decoder_1 (
    .out0(decoder_1_out0), .out1(decoder_1_out1), .out2(decoder_1_out2), .out3(decoder_1_out3),
    .sel(SEL_R_DST), .en(and_1_out));
  Adder #(.width(4)) adder_2 (.a(PC_q), .b(D_IN), .out(adder_2_out), .cin(1'b0));  // open: cout
  Register #(.width(4)) REG0 (.D(multiplexer_6_out), .en(decoder_1_out0), .clk(CLK_out), .Q(REG0_q), .clr(Reset_out));
  Register #(.width(4)) REG1 (.D(multiplexer_6_out), .en(decoder_1_out1), .clk(CLK_out), .Q(REG1_q), .clr(Reset_out));
  Register #(.width(4)) REG2 (.D(multiplexer_6_out), .en(decoder_1_out2), .clk(CLK_out), .Q(REG2_q), .clr(Reset_out));
  Register #(.width(4)) REG3 (.D(multiplexer_6_out), .en(decoder_1_out3), .clk(CLK_out), .Q(REG3_q), .clr(Reset_out));
  Multiplexer #(.enable("false"), .select(2), .width(4)) multiplexer_1 (
    .in0(REG0_q), .in1(REG1_q), .in2(REG2_q), .in3(REG3_q), .out(multiplexer_1_out), .sel(SEL_R_SRC1));
  Multiplexer #(.enable("false"), .select(2), .width(4)) multiplexer_2 (
    .in0(REG0_q), .in1(REG1_q), .in2(REG2_q), .in3(REG3_q), .out(multiplexer_2_out), .sel(SEL_R_SRC2));
  Multiplexer #(.enable("false"), .width(4)) multiplexer_3 (
    .in0(D_IN), .in1(multiplexer_2_out), .out(multiplexer_3_out), .sel(USE_R_SRC2));
  Multiplexer #(.enable("false"), .width(4)) multiplexer_4 (
    .in0(adder_1_out), .in1(adder_2_out), .out(multiplexer_4_out), .sel(or_1_out));
  or or_1 (or_1_out, BRANCH, and_3_out);
  Comparator #(.mode("unsigned"), .width(4)) comparator_1 (
    .a(4'b0000), .b(multiplexer_1_out), .eq(comparator_1_eq));  // open: gt, lt
  assign and_2_out = multiplexer_1_out & multiplexer_3_out;  // AND_Gate and_2, 4 bits wide
  assign or_2_out = multiplexer_1_out | multiplexer_3_out;  // OR_Gate or_2, 4 bits wide
  assign xor_1_out = multiplexer_1_out ^ multiplexer_3_out;  // XOR_Gate xor_1, 4 bits wide
  Adder #(.width(4)) adder_3 (
    .a(multiplexer_1_out), .b(multiplexer_3_out), .out(adder_3_out), .cin(1'b0));  // open: cout
  RAM #(.addrWidth(4), .asyncread("true"), .dataWidth(4)) ram_1 (
    .addr(multiplexer_1_out), .we(STORE_TO_MEMORY), .oe(LOAD_FROM_MEMORY), .clk(CLK_out),
    .din(multiplexer_2_out), .dout(ram_1_dout));
  and and_3 (and_3_out, BRANCH_IF_ZERO, comparator_1_eq);
  Multiplexer #(.enable("false"), .select(2), .width(4)) multiplexer_5 (
    .in0(and_2_out), .in1(or_2_out), .in2(xor_1_out), .in3(adder_3_out), .out(multiplexer_5_out), .sel(SEL_OP));
  Multiplexer #(.enable("false"), .width(4)) multiplexer_6 (
    .in0(multiplexer_5_out), .in1(ram_1_dout), .out(multiplexer_6_out), .sel(LOAD_FROM_MEMORY));

  // Notes on the sheet:
  //   contents of INSTRUCTION_MEMORY (hex, n*v repeats v):
  //   2018 9*0 2078
endmodule
