// Logisim project sync.circ as structural Verilog: 1 circuit, main circuit main
module main (
  input  En,
  input  RST,
  output C0,
  output C1,
  output C2,
  output C3
);

  wire and_1_out, and_2_out, CLK_out;

  Clock CLK (.out(CLK_out));
  T_Flip_Flop t_ff_1 (.T(En), .clk(CLK_out), .Q(C0), .reset(RST));  // open: Qn, preset
  T_Flip_Flop t_ff_2 (.T(C0), .clk(CLK_out), .Q(C1), .reset(RST));  // open: Qn, preset
  and and_1 (and_1_out, C1, C0);
  T_Flip_Flop t_ff_3 (.T(and_1_out), .clk(CLK_out), .Q(C2), .reset(RST));  // open: Qn, preset
  T_Flip_Flop t_ff_4 (.T(and_2_out), .clk(CLK_out), .Q(C3), .reset(RST));  // open: Qn, preset
  and and_2 (and_2_out, and_1_out, C2);
endmodule
