// Logisim project tristate_mux.circ as structural Verilog: 1 circuit, main circuit main
module main (
  input  in_1,
  input  in_2,
  input  in_3,
  input  in_4,
  input  in_5,
  input  in_6,
  input  in_7,
  input  in_8,
  input  in_9,
  input  in_10,
  input  in_11,
  input  in_12,
  input  in_13,
  input  in_14,
  input  in_15,
  input  in_16,
  input  in_17,
  input  in_18,
  input  in_19,
  input  in_20,
  input  in_21,
  input  in_22,
  input  in_23,
  input  in_24,
  input  in_25,
  output out_26,
  output out_27,
  output out_28,
  output out_29,
  output out_30,
  output out_31,
  output out_32,
  output out_33,
  output out_34,
  output out_35,
  output out_36
);

  wire and_4_out, and_5_out, and_6_out, and_7_out, and_8_out, not_1_out, not_2_out, not_3_out, or_1_out,
       or_2_out, or_3_out, undriven, undriven_2;

  // AND_Gate and_1 has open pins: out=out_27
  and and_2 (out_28, undriven, undriven_2);
  and and_3 (out_29, in_2, in_3);
  nor nor_1 (out_30, in_4, in_5);
  assign out_32 = in_7 ? in_6 : 1'bz;  // Controlled_Buffer controlled_buffer_1
  assign out_33 = not_1_out ? in_8 : 1'bz;  // Controlled_Buffer controlled_buffer_2
  not not_1 (not_1_out, in_9);
  and and_4 (and_4_out, in_10, in_11);
  or or_1 (or_1_out, in_12, in_13);
  and and_5 (and_5_out, in_16, in_17);
  or or_2 (or_2_out, in_18, in_19);
  not not_2 (not_2_out, in_20);
  and and_6 (and_6_out, in_21, in_22);
  or or_3 (or_3_out, in_23, in_24);
  not not_3 (not_3_out, in_25);
  assign out_34 = in_14 ? and_4_out : 1'bz;  // Controlled_Buffer controlled_buffer_3
  assign out_34 = in_15 ? or_1_out : 1'bz;  // Controlled_Buffer controlled_buffer_4
  assign out_35 = not_2_out ? and_5_out : 1'bz;  // Controlled_Buffer controlled_buffer_5
  assign out_35 = in_20 ? or_2_out : 1'bz;  // Controlled_Buffer controlled_buffer_6
  and and_7 (and_7_out, and_6_out, not_3_out);
  and and_8 (and_8_out, or_3_out, in_25);
  or or_4 (out_36, and_7_out, and_8_out);

  // Notes on the sheet:
  //   This is an output pin.
  //   This is an input pin. It is currently LOW (or 0).
  //   The AND gate drives this output pin. 
  //   This output is configured to have three states: 
  //   driven LOW, driven HIGH, or not driven (floating)
  //   If their outputs are same, it might be okay.
  //   But if they are different, it is a serious issue.
  //   We need a way to enable only one buffer at a time.
  //   We can change that by clicking on it with the Poke tool.
  //   Since nothing drives it, it is shown as U (unknown or floating).
  //   Since its inputs are not connected, it shows E (for error).
  //   The wires that are not driven by anything
  //    are shown in blue.
  //   The wires and inputs that are LOW 
  //   are shown in dark green.
  //   The wires and inputs that are HIGH
  //   are shown in light green.
  //   to select when the output should be driven.
  //   The control input is LOW, so it is not driven.
  //   When the buffer is enabled,
  //   Use the poke tool to change these values
  //   and see what happens.
  //   If both are set to 1, then both the AND gate and the OR gate drive the output.
  //   When multiple drivers drive a wire this way, it is called a (bus) contention.
  //   By having a single bit selection, we can ensure that.
  //   This is one way to implement a multiplexer.
  //   We can use a Controlled (a.k.a. Tristate) buffer
  //   the output is driven to the level of the input.
  //   If we want to have an output that is driven 
  //   by different subcircuits at different times,
  //   we can construct a circuit like this.
  //   We can also implement it 
  //   with AND and OR gates.
endmodule
